// Logisim project cpu21-riscv -8-17.circ as structural Verilog: 29 circuits, main circuit ◇单周期RISC-V
module \单周期RISC_V  (
  input  IR1,
  input  IR2,
  input  IR3,
  output RegWrite,
  output MemWrite,
  output [31:0] PC,
  output [31:0] IR,
  output [31:0] RDin,
  output [31:0] MDin,
  output [31:0] LedData
);

  wire alu_1_out_6, and_1_out, and_3_out, and_4_out, and_5_out, B, blt, CLK, clock_1_out, comparator_1_eq,
       comparator_1_lt, d_ff_1_q, ecall, Go, halt, IR1_t, IR2_t, IR3_t, IRA, IRB, IRC, jal, jalr, lb,
       nand_1_out, not_1_out, not_2_out, or_5_out, riscv_probe_1_p2, RST, S_type, tunnel, W1, W2, W3,
       \单周期硬布线控制器_1_alu_src , \单周期硬布线控制器_1_beq , \单周期硬布线控制器_1_bne , \单周期硬布线控制器_1_memtoreg ;
  wire [0:0] or_1_out;
  wire [3:0] \单周期硬布线控制器_1_alu_op ;
  wire [4:0] multiplexer_2_out, multiplexer_3_out;
  wire [7:0] multiplexer_10_out, multiplexer_10_out_2, multiplexer_10_out_3, multiplexer_10_out_4,
       multiplexer_11_out;
  wire [11:0] shifter_1_out;
  wire [12:0] CNT_num;
  wire [15:0] \总周期数 ;
  wire [19:0] shifter_2_out;
  wire [31:0] adder_1_out, adder_2_out, adder_3_out, adder_4_out, alu_res, bit_extender_1_out,
       bit_extender_2_out, bit_extender_3_out, bit_extender_4_out, bit_extender_5_out, multiplexer_1_out,
       multiplexer_4_out, multiplexer_5_out, multiplexer_6_out, multiplexer_8_out, multiplexer_9_out,
       ram_1_data, regifile_1_r1;

  Button \u_继续运行  (.out(Go));
  Button _1 (.out(IRA));
  Button _2 (.out(IRB));
  Button _3 (.out(IRC));
  LED #(.active("true")) led_1 (.in(W1));
  LED #(.active("true")) led_2 (.in(W2));
  LED #(.active("true")) led_3 (.in(W3));
  and and_1 (and_1_out, ~tunnel, ecall);  // AND_Gate
  Multiplexer #(.select(2), .width(32), .disabled("Z"), .enable("false")) multiplexer_1 (
    .in0(adder_1_out), .in1(multiplexer_8_out), .in2(alu_res), .out(multiplexer_1_out),
    .sel({jalr, or_1_out[0]}));  // open: in3
  or or_1 (or_1_out[0], jal, B);
  Hex_Digit_Display hex_digit_display_1 (.value(LedData[31:28]));  // open: dp
  and and_2 (halt, ~Go, and_1_out);  // AND_Gate
  Register #(.width(32), .trigger("rising"), .Select("low")) u_PC (
    .D(multiplexer_1_out), .en(not_1_out), .Q(PC), .clk(CLK), .clr(RST));
  not not_1 (not_1_out, halt);
  Hex_Digit_Display hex_digit_display_2 (.value(LedData[23:20]));  // open: dp
  Hex_Digit_Display hex_digit_display_3 (.value(LedData[27:24]));  // open: dp
  Adder #(.width(32)) adder_1 (.a(PC), .b(32'h4), .out(adder_1_out));  // open: cin, cout
  Hex_Digit_Display hex_digit_display_4 (.value(LedData[15:12]));  // open: dp
  Hex_Digit_Display hex_digit_display_5 (.value(LedData[19:16]));  // open: dp
  // RiscV_Probe riscv_probe_1: pin names not known; wires that end beside it: IR, riscv_probe_1_p2
  Hex_Digit_Display hex_digit_display_6 (.value(LedData[7:4]));  // open: dp
  Hex_Digit_Display hex_digit_display_7 (.value(LedData[11:8]));  // open: dp
  // Probe on \总周期数 
  ROM #(.addrWidth(10), .dataWidth(32), .Select("high")) rom_1 (.addr(PC[11:2]), .data(IR));
  Hex_Digit_Display hex_digit_display_8 (.value(LedData[3:0]));  // open: dp
  \单周期硬布线控制器  \u_单周期硬布线控制器_1  (
    .Funct({IR[30], IR[25], IR[14:12]}), .OP(IR[6:2]), .ALU_OP(\单周期硬布线控制器_1_alu_op ),
    .MemToReg(\单周期硬布线控制器_1_memtoreg ), .MemWrite(MemWrite), .ALU_SRC(\单周期硬布线控制器_1_alu_src ),
    .RegWrite(RegWrite), .ecall(ecall), .S_type(S_type), .Jalr(jalr), .Beq(\单周期硬布线控制器_1_beq ), .JAL(jal),
    .Bne(\单周期硬布线控制器_1_bne ), .in_3(IR[21]), .uret(riscv_probe_1_p2), .lb(lb), .blt(blt));  // open: CSRRSI, CSRRCI
  Multiplexer #(.select(1), .width(5), .disabled("Z"), .enable("false")) multiplexer_2 (
    .in0(IR[19:15]), .in1(5'b10001), .out(multiplexer_2_out), .sel(ecall));
  Multiplexer #(.select(1), .width(5), .disabled("Z"), .enable("false")) multiplexer_3 (
    .in0(IR[24:20]), .in1(5'b01010), .out(multiplexer_3_out), .sel(ecall));
  or or_2 (IR1_t, IR1, IRA);
  assign bit_extender_1_out = {{20{IR[31]}}, IR[31:20]};  // Bit_Extender bit_extender_1
  assign bit_extender_2_out = {{20{IR[31]}}, {IR[31:25], IR[11:7]}};  // Bit_Extender bit_extender_2
  Shifter #(.width(12), .shift("ll")) shifter_1 (
    .in({IR[31], IR[7], IR[30:25], IR[11:8]}), .\dist (4'b0001), .out(shifter_1_out));
  Shifter #(.width(20), .shift("ll")) shifter_2 (
    .in({IR[31], IR[19:12], IR[20], IR[30:21]}), .\dist (5'b00001), .out(shifter_2_out));
  or or_3 (IR2_t, IR2, IRB);
  Regifile regifile_1 (
    .Din(RDin), .Clk(CLK), .R1(regifile_1_r1), .R2(MDin), .WE(RegWrite), .W_num(IR[11:7]),
    .R1_num(multiplexer_2_out), .R2_num(multiplexer_3_out));
  Multiplexer #(.select(1), .width(32), .disabled("Z"), .enable("false")) multiplexer_4 (
    .in0(bit_extender_1_out), .in1(bit_extender_2_out), .out(multiplexer_4_out), .sel(S_type));
  assign bit_extender_3_out = {{20{shifter_1_out[11]}}, shifter_1_out};  // Bit_Extender bit_extender_3
  assign bit_extender_4_out = {{12{shifter_2_out[19]}}, shifter_2_out};  // Bit_Extender bit_extender_4
  Multiplexer #(.select(1), .width(32), .disabled("Z"), .enable("false")) multiplexer_5 (
    .in0(multiplexer_4_out), .in1(32'h22), .out(multiplexer_5_out), .sel(ecall));
  or or_4 (IR3_t, IR3, IRC);
  Multiplexer #(.select(1), .width(32), .disabled("Z"), .enable("false")) multiplexer_6 (
    .in0(MDin), .in1(multiplexer_5_out), .out(multiplexer_6_out), .sel(\单周期硬布线控制器_1_alu_src ));
  Adder #(.width(32)) adder_2 (.a(PC), .b(bit_extender_3_out), .out(adder_2_out));  // open: cin, cout
  Adder #(.width(32)) adder_3 (.a(PC), .b(bit_extender_4_out), .out(adder_3_out));  // open: cin, cout
  Multiplexer #(.select(1), .width(32), .disabled("Z"), .enable("false")) multiplexer_7 (
    .in0(multiplexer_9_out), .in1(adder_4_out), .out(RDin), .sel(or_5_out));
  or or_5 (or_5_out, jalr, jal);
  Multiplexer #(.select(1), .width(32), .disabled("Z"), .enable("false")) multiplexer_8 (
    .in0(adder_2_out), .in1(adder_3_out), .out(multiplexer_8_out), .sel(jal));
  ALU alu_1 (
    .X(regifile_1_r1), .Y(multiplexer_6_out), .AluOP(\单周期硬布线控制器_1_alu_op ), .Equal(tunnel), .Result(alu_res),
    .out_6(alu_1_out_6));  // open: Result_2, out_4
  Adder #(.width(32)) adder_4 (.a(32'h4), .b(PC), .out(adder_4_out));  // open: cin, cout
  and and_3 (and_3_out, \单周期硬布线控制器_1_beq , tunnel);
  and and_4 (and_4_out, \单周期硬布线控制器_1_bne , ~tunnel);  // AND_Gate
  and and_5 (and_5_out, blt, alu_1_out_6);
  or or_6 (B, and_3_out, and_4_out, and_5_out);
  RAM #(.addrWidth(10), .dataWidth(32), .bus("separate"), .Select("high")) ram_1 (
    .addr(alu_res[11:2]), .din(MDin), .data(ram_1_data), .str(MemWrite), .clk(CLK));  // open: sel, ld, clr
  Multiplexer #(.select(1), .width(32), .disabled("Z"), .enable("false")) multiplexer_9 (
    .in0({multiplexer_10_out_4, multiplexer_10_out_3, multiplexer_10_out_2, multiplexer_10_out}),
    .in1(bit_extender_5_out), .out(multiplexer_9_out), .sel(lb));
  Register #(.width(32), .trigger("rising"), .Select("low")) register_1 (
    .D(MDin), .en(ecall), .Q(LedData), .clk(CLK));  // open: clr
  D_Flip_Flop #(.trigger("high"), .Pre_Clr_Positions("LEGACY"), .NegatePresetClear("false"), .enable("true"), .NewFFLayout("false")) d_ff_1 (.Q(d_ff_1_q));  // open: clk, D, Qn, preset, en, reset
  // Probe on 13'h28
  Multiplexer #(.select(1), .width(32), .disabled("Z"), .enable("false")) multiplexer_10 (
    .in0(alu_res), .in1(ram_1_data),
    .out({multiplexer_10_out_4, multiplexer_10_out_3, multiplexer_10_out_2, multiplexer_10_out}),
    .sel(\单周期硬布线控制器_1_memtoreg ));
  Multiplexer #(.select(2), .width(8), .disabled("Z"), .enable("false")) multiplexer_11 (
    .in0(multiplexer_10_out), .in1(multiplexer_10_out_2), .in2(multiplexer_10_out_3),
    .in3(multiplexer_10_out_4), .out(multiplexer_11_out), .sel(alu_res[1:0]));
  assign bit_extender_5_out = {{24{multiplexer_11_out[7]}}, multiplexer_11_out};  // Bit_Extender bit_extender_5
  Comparator #(.width(13), .mode("twosComplement")) comparator_1 (
    .a(CNT_num), .b(13'h28), .eq(comparator_1_eq), .lt(comparator_1_lt));  // open: gt
  Clock #(.highDuration(1), .lowDuration(1)) clock_1 (.out(clock_1_out));
  not not_2 (not_2_out, halt);
  Counter #(.width(13), .max('h1fff), .ongoal("stay"), .trigger("rising"), .behavior("old")) counter_1 (
    .count(comparator_1_lt), .Q(CNT_num), .clk(clock_1_out));  // open: load, D, carry, clr, preset
  Counter #(.width(16), .max('hffff), .ongoal("stay"), .trigger("rising"), .behavior("new")) counter_2 (
    .count(not_2_out), .Q(\总周期数 ), .clk(CLK));  // open: load, D, carry, clr, preset, down
  nand nand_1 (nand_1_out, d_ff_1_q, comparator_1_eq);
  assign CLK = nand_1_out ? clock_1_out : 1'bz;  // Controlled_Buffer controlled_buffer_1
  Pull_Resistor #(.pull(1)) pull_resistor_1 (.node(CLK));

  // Other names for the same wires on the sheet: R2data[31:0] = MDin

  // Notes on the sheet:
  //   中断源
  //   中断等待指示
  //   数码管输出应该用寄存器锁存，否则显示数据只能一闪而过
  //   数码管输出
  //   指令探针
  //   指令存储器
  //   指令字
  //   contents of rom_1 (hex, n*v repeats v):
  //   100493 100006f 100493 200913 300993 100006f 100493 200913 300993 100006f 100493 200913 300993
  //   100006f 100493 200913 300993 3b8000ef 100413 100493 1f49493 900533 2200893 73 24d493 48463 fedff06f
  //   900533 2200893 73 100493 249493 900533 2200893 73 48463 fedff06f 100493 1f49493 900533 2200893 73
  //   4034d493 900533 2200893 73 4044d493 900533 2200893 73 4044d493 900533 2200893 73 4044d493 900533
  //   2200893 73 4044d493 900533 2200893 73 4044d493 900533 2200893 73 4044d493 900533 2200893 73 4044d493
  //   900533 2200893 73 100413 1f41993 41f9d993 433 c00913 300b13 140413 f47413 800293 100313 499993
  //   89e9b3 1300533 2200893 73 406282b3 fe0294e3 140413 f00f93 1f47433 1c41413 800293 100313 49d993
  //   89e9b3 1300533 2200893 73 406282b3 fe0294e3 1c45413 406b0b33 b0463 f95ff06f 2b3 fff2c293 829293
  //   ff2e293 500533 2200893 73 fff00413 493 84a023 140413 448493 84a023 140413 448493 84a023 140413
  //   448493 84a023 140413 448493 84a023 140413 448493 84a023 140413 448493 84a023 140413 448493 84a023
  //   140413 448493 84a023 140413 448493 84a023 140413 448493 84a023 140413 448493 84a023 140413 448493
  //   84a023 140413 448493 84a023 140413 448493 84a023 140413 448493 84a023 140413 448493 140413 433
  //   3c00493 42983 4aa03 149a2b3 28663 134a023 1442023 ffc48493 fe9412e3 800533 2200893 73 440413 3c00493
  //   fc9416e3 3200893 73 100293 300313 800493 849493 7648493 900533 2200893 73 800e13 5494b3 6494b3
  //   900533 2200893 73 fffe0e13 fe0e14e3 a00893 73 fff00293 313 1900413 841413 9700493 940533 2200893 73
  //   5484b3 494b313 fe0306e3 a00893 73 313 1000e13 8400493 849493 8348493 400913 891913 490913 849493
  //   8248493 849493 8148493 891913 490913 891913 490913 932023 12484b3 430313 fffe0e13 fe0e18e3 2000e13
  //   313 30483 900533 2200893 73 130313 fffe0e13 fe0e14e3 a00893 73 ff100493 900533 2200893 73 148493
  //   fe04c8e3 a00893 73 413 140413 800533 2200893 73 240413 800533 2200893 73 340413 800533 2200893 73
  //   440413 800533 2200893 73 540413 800533 2200893 73 640413 800533 2200893 73 740413 800533 2200893 73
  //   840413 800533 2200893 2200893 73 8067
  //   JAL
  //   JALR
  //   URET
  //   I jalr
  //   sw
  //   Beq
  //   Bne
  //   MemToReg
  //   MemWrite
  //   AluOP
  //   AluSrcB
  //   RegWrite
  //   B
  //   jal
  //   为方便自动评测，需要输出PC，IR，寄存器堆写如数据RDin
  //   RAM写使能MemWrite、RAM写入数据MDin等信号
  //   数据存储器
  //   控制位
  //   暂停节拍，不能为0
  //   戳工具置1进入计数暂停模式，ctrl+k时钟自动运行到对应节拍暂停
  //   ctrl+k关闭时钟连续运行，将控制位置零，进入单步调试模式调试
  //   用这个时钟源需要去掉电路中的其他时钟源
  //   可计数暂停的时钟源
endmodule

// 单周期硬布线控制器
module \单周期硬布线控制器  (
  input  [4:0] OP,
  input  [4:0] Funct,
  input  in_3,
  output [3:0] ALU_OP,
  output uret,
  output MemToReg,
  output ecall,
  output MemWrite,
  output ALU_SRC,
  output RegWrite,
  output S_type,
  output Beq,
  output Bne,
  output Jalr,
  output JAL,
  output lb,
  output blt,
  output CSRRSI,
  output CSRRCI
);

  wire \控制信号自动生成_1_ecall ;

  \运算控制器自动生成  \u_运算控制器自动生成_1  (
    .OP2(OP[0]), .OP3(OP[1]), .OP4(OP[2]), .OP5(OP[3]), .OP6(OP[4]), .F12(Funct[0]), .F13(Funct[1]),
    .F14(Funct[2]), .F25(Funct[3]), .F30(Funct[4]), .S0(ALU_OP[0]), .S1(ALU_OP[1]), .S2(ALU_OP[2]),
    .S3(ALU_OP[3]));
  \控制信号自动生成  \u_控制信号自动生成_1  (
    .OP2(OP[0]), .OP3(OP[1]), .MemToReg(MemToReg), .OP4(OP[2]), .OP5(OP[3]), .OP6(OP[4]), .F12(Funct[0]),
    .CSRRSI(CSRRSI), .F13(Funct[1]), .F14(Funct[2]), .CSRRCI(CSRRCI), .F25(Funct[3]), .F30(Funct[4]),
    .MemWrite(MemWrite), .ALU_SRC(ALU_SRC), .RegWrite(RegWrite), .ecall(\控制信号自动生成_1_ecall ), .S_Type(S_type),
    .BEQ(Beq), .BNE(Bne), .JALR(Jalr), .JAL(JAL), .lb(lb), .blt(blt));
  and and_1 (uret, in_3, \控制信号自动生成_1_ecall );
  and and_2 (ecall, ~in_3, \控制信号自动生成_1_ecall );  // AND_Gate

  // Other names for the same wires on the sheet: IR21 = in_3; OP_CODE[4:0] = OP

  // Notes on the sheet:
  //   运算器控制器，根据指令生成运算器功能选择信号
  //   控制信号生成，产生数据通路需要的其他控制信号
endmodule

// 运算器控制器
module \运算控制器自动生成  (
  input  OP2,
  input  OP3,
  input  OP4,
  input  OP5,
  input  OP6,
  input  F12,
  input  F13,
  input  F14,
  input  F25,
  input  F30,
  output S0,
  output S1,
  output S2,
  output S3
);

  wire and_1_out, and_2_out, and_3_out, and_4_out, and_5_out, and_6_out, and_7_out, and_8_out, and_9_out,
       and_10_out, and_11_out, and_12_out, and_13_out, and_14_out, and_15_out, and_16_out, and_17_out,
       and_18_out, and_19_out, and_20_out, and_21_out, and_22_out, and_23_out, and_24_out, and_25_out,
       and_26_out, and_27_out, and_28_out, and_29_out, and_30_out, and_31_out, and_32_out, and_33_out,
       and_34_out, and_35_out, and_36_out, and_37_out, and_38_out, and_39_out, and_40_out, and_41_out,
       and_42_out, and_43_out, and_44_out, and_45_out, and_46_out, and_47_out, and_48_out, not_1_out,
       not_2_out, not_3_out, not_4_out, not_5_out, not_6_out, not_7_out, not_8_out, not_9_out, not_10_out,
       not_11_out, not_12_out, not_13_out, not_14_out, not_15_out, not_16_out, not_17_out, not_18_out,
       not_19_out, not_20_out, not_21_out, not_22_out, not_23_out, not_24_out, not_25_out, not_26_out,
       not_27_out, not_28_out, not_29_out, not_30_out, not_31_out, not_32_out, not_33_out, not_34_out,
       not_35_out, not_36_out, not_37_out, not_38_out, not_39_out, not_40_out, not_41_out, not_42_out,
       not_43_out, not_44_out, not_45_out, not_46_out, not_47_out, not_48_out, not_49_out, not_50_out,
       not_51_out, not_52_out, not_53_out, not_54_out, not_55_out, not_56_out, not_57_out, not_58_out,
       not_59_out, not_60_out, not_61_out, not_62_out, not_63_out, not_64_out, not_65_out, not_66_out,
       not_67_out, not_68_out, not_69_out, not_70_out, not_71_out, not_72_out, not_73_out, not_74_out,
       not_75_out, not_76_out, not_77_out, not_78_out, not_79_out, not_80_out, not_81_out, not_82_out,
       not_83_out, not_84_out, not_85_out, not_86_out, not_87_out, not_88_out, not_89_out, not_90_out,
       not_91_out, not_92_out, not_93_out, not_94_out, not_95_out, not_96_out, not_97_out, not_98_out,
       not_99_out, not_100_out, not_101_out, not_102_out, not_103_out, not_104_out, not_105_out, not_106_out,
       not_107_out, not_108_out, not_109_out, not_110_out, not_111_out, not_112_out, not_113_out,
       not_114_out, not_115_out, not_116_out, not_117_out, not_118_out, not_119_out, not_120_out,
       not_121_out, not_122_out, not_123_out, not_124_out, not_125_out, not_126_out, not_127_out,
       not_128_out, not_129_out, not_130_out, not_131_out, not_132_out, not_133_out, not_134_out,
       not_135_out, not_136_out, not_137_out, not_138_out, not_139_out, not_140_out, not_141_out,
       not_142_out, not_143_out, not_144_out, not_145_out, not_146_out, not_147_out, not_148_out,
       not_149_out, not_150_out, not_151_out, not_152_out, not_153_out, not_154_out, not_155_out,
       not_156_out, not_157_out, not_158_out, not_159_out, not_160_out, not_161_out, not_162_out,
       not_163_out, not_164_out, not_165_out, not_166_out, not_167_out, not_168_out, not_169_out,
       not_170_out, not_171_out, not_172_out, not_173_out, not_174_out, not_175_out, not_176_out,
       not_177_out, not_178_out, not_179_out, not_180_out, not_181_out, not_182_out, not_183_out,
       not_184_out, not_185_out, not_186_out, not_187_out, not_188_out, not_189_out, not_190_out,
       not_191_out, not_192_out, not_193_out, not_194_out, not_195_out, not_196_out, not_197_out,
       not_198_out, not_199_out, not_200_out, not_201_out, not_202_out, not_203_out, not_204_out,
       not_205_out, not_206_out, not_207_out, not_208_out, not_209_out, not_210_out, not_211_out,
       not_212_out, not_213_out, not_214_out, not_215_out, not_216_out, not_217_out, not_218_out,
       not_219_out, not_220_out, not_221_out, not_222_out, not_223_out, not_224_out, not_225_out,
       not_226_out, not_227_out, not_228_out, not_229_out, not_230_out, not_231_out, not_232_out,
       not_233_out, not_234_out, not_235_out, not_236_out, not_237_out, not_238_out, not_239_out,
       not_240_out, not_241_out, not_242_out, not_243_out, not_244_out, not_245_out, not_246_out,
       not_247_out, not_248_out, not_249_out, not_250_out, not_251_out, not_252_out, not_253_out,
       not_254_out, not_255_out, not_256_out, not_257_out, not_258_out, not_259_out, not_260_out,
       not_261_out, not_262_out, not_263_out, not_264_out, not_265_out, not_266_out, not_267_out,
       not_268_out, not_269_out, not_270_out, not_271_out, not_272_out, not_273_out, not_274_out,
       not_275_out, not_276_out, not_277_out, not_278_out, not_279_out, not_280_out, not_281_out,
       not_282_out, not_283_out, not_284_out, not_285_out, not_286_out, not_287_out, not_288_out, not_289_out;

  not not_1 (not_1_out, F30);
  not not_2 (not_2_out, F25);
  not not_3 (not_3_out, F14);
  not not_4 (not_4_out, F13);
  not not_5 (not_5_out, F12);
  not not_6 (not_6_out, OP6);
  not not_7 (not_7_out, OP3);
  not not_8 (not_8_out, OP2);
  not not_9 (not_9_out, F30);
  not not_10 (not_10_out, F25);
  not not_11 (not_11_out, OP6);
  not not_12 (not_12_out, OP3);
  not not_13 (not_13_out, OP2);
  not not_14 (not_14_out, F30);
  not not_15 (not_15_out, F25);
  not not_16 (not_16_out, F14);
  not not_17 (not_17_out, F12);
  not not_18 (not_18_out, OP6);
  not not_19 (not_19_out, OP3);
  not not_20 (not_20_out, OP2);
  not not_21 (not_21_out, F14);
  not not_22 (not_22_out, F13);
  not not_23 (not_23_out, F12);
  not not_24 (not_24_out, OP6);
  not not_25 (not_25_out, OP5);
  not not_26 (not_26_out, OP3);
  not not_27 (not_27_out, OP2);
  not not_28 (not_28_out, OP6);
  not not_29 (not_29_out, OP5);
  not not_30 (not_30_out, OP3);
  not not_31 (not_31_out, OP2);
  not not_32 (not_32_out, F13);
  not not_33 (not_33_out, F12);
  not not_34 (not_34_out, OP6);
  not not_35 (not_35_out, OP5);
  not not_36 (not_36_out, OP3);
  not not_37 (not_37_out, OP2);
  not not_38 (not_38_out, F14);
  not not_39 (not_39_out, F12);
  not not_40 (not_40_out, OP6);
  not not_41 (not_41_out, OP5);
  not not_42 (not_42_out, OP3);
  not not_43 (not_43_out, OP2);
  not not_44 (not_44_out, F25);
  not not_45 (not_45_out, F13);
  not not_46 (not_46_out, OP6);
  not not_47 (not_47_out, OP5);
  not not_48 (not_48_out, OP3);
  not not_49 (not_49_out, OP2);
  not not_50 (not_50_out, F14);
  not not_51 (not_51_out, F12);
  not not_52 (not_52_out, OP6);
  not not_53 (not_53_out, OP5);
  not not_54 (not_54_out, OP4);
  not not_55 (not_55_out, OP3);
  not not_56 (not_56_out, OP2);
  not not_57 (not_57_out, F14);
  not not_58 (not_58_out, F12);
  not not_59 (not_59_out, OP6);
  not not_60 (not_60_out, OP4);
  not not_61 (not_61_out, OP3);
  not not_62 (not_62_out, OP2);
  not not_63 (not_63_out, F30);
  not not_64 (not_64_out, F25);
  not not_65 (not_65_out, F14);
  not not_66 (not_66_out, F13);
  not not_67 (not_67_out, F12);
  not not_68 (not_68_out, OP3);
  not not_69 (not_69_out, OP2);
  not not_70 (not_70_out, F14);
  not not_71 (not_71_out, F13);
  not not_72 (not_72_out, F12);
  not not_73 (not_73_out, OP4);
  not not_74 (not_74_out, OP3);
  not not_75 (not_75_out, OP2);
  not not_76 (not_76_out, F14);
  not not_77 (not_77_out, F13);
  not not_78 (not_78_out, OP4);
  not not_79 (not_79_out, OP3);
  not not_80 (not_80_out, OP2);
  not not_81 (not_81_out, F14);
  not not_82 (not_82_out, F13);
  not not_83 (not_83_out, F12);
  not not_84 (not_84_out, OP4);
  not not_85 (not_85_out, OP3);
  not not_86 (not_86_out, F14);
  not not_87 (not_87_out, F13);
  not not_88 (not_88_out, F12);
  not not_89 (not_89_out, OP6);
  not not_90 (not_90_out, OP5);
  not not_91 (not_91_out, OP4);
  not not_92 (not_92_out, OP3);
  not not_93 (not_93_out, OP2);
  not not_94 (not_94_out, F13);
  not not_95 (not_95_out, F12);
  not not_96 (not_96_out, OP4);
  not not_97 (not_97_out, OP3);
  not not_98 (not_98_out, OP2);
  not not_99 (not_99_out, F25);
  not not_100 (not_100_out, F14);
  not not_101 (not_101_out, F13);
  not not_102 (not_102_out, F12);
  not not_103 (not_103_out, OP6);
  not not_104 (not_104_out, OP3);
  not not_105 (not_105_out, OP2);
  not not_106 (not_106_out, F30);
  not not_107 (not_107_out, F25);
  not not_108 (not_108_out, OP6);
  not not_109 (not_109_out, OP3);
  not not_110 (not_110_out, OP2);
  not not_111 (not_111_out, F30);
  not not_112 (not_112_out, F25);
  not not_113 (not_113_out, F14);
  not not_114 (not_114_out, F12);
  not not_115 (not_115_out, OP6);
  not not_116 (not_116_out, OP3);
  not not_117 (not_117_out, OP2);
  not not_118 (not_118_out, OP6);
  not not_119 (not_119_out, OP5);
  not not_120 (not_120_out, OP3);
  not not_121 (not_121_out, OP2);
  not not_122 (not_122_out, F14);
  not not_123 (not_123_out, F12);
  not not_124 (not_124_out, OP6);
  not not_125 (not_125_out, OP5);
  not not_126 (not_126_out, OP3);
  not not_127 (not_127_out, OP2);
  not not_128 (not_128_out, F30);
  not not_129 (not_129_out, F25);
  not not_130 (not_130_out, F13);
  not not_131 (not_131_out, OP6);
  not not_132 (not_132_out, OP5);
  not not_133 (not_133_out, OP3);
  not not_134 (not_134_out, OP2);
  not not_135 (not_135_out, F30);
  not not_136 (not_136_out, F25);
  not not_137 (not_137_out, F14);
  not not_138 (not_138_out, F13);
  not not_139 (not_139_out, F12);
  not not_140 (not_140_out, OP3);
  not not_141 (not_141_out, OP2);
  not not_142 (not_142_out, F14);
  not not_143 (not_143_out, F13);
  not not_144 (not_144_out, F12);
  not not_145 (not_145_out, OP4);
  not not_146 (not_146_out, OP3);
  not not_147 (not_147_out, OP2);
  not not_148 (not_148_out, F14);
  not not_149 (not_149_out, F13);
  not not_150 (not_150_out, OP4);
  not not_151 (not_151_out, OP3);
  not not_152 (not_152_out, OP2);
  not not_153 (not_153_out, F13);
  not not_154 (not_154_out, F12);
  not not_155 (not_155_out, OP4);
  not not_156 (not_156_out, OP3);
  not not_157 (not_157_out, OP2);
  not not_158 (not_158_out, F30);
  not not_159 (not_159_out, F25);
  not not_160 (not_160_out, F14);
  not not_161 (not_161_out, F13);
  not not_162 (not_162_out, F12);
  not not_163 (not_163_out, OP6);
  not not_164 (not_164_out, OP3);
  not not_165 (not_165_out, OP2);
  not not_166 (not_166_out, F25);
  not not_167 (not_167_out, F14);
  not not_168 (not_168_out, F13);
  not not_169 (not_169_out, F12);
  not not_170 (not_170_out, OP6);
  not not_171 (not_171_out, OP3);
  not not_172 (not_172_out, OP2);
  not not_173 (not_173_out, F30);
  not not_174 (not_174_out, F25);
  not not_175 (not_175_out, OP6);
  not not_176 (not_176_out, OP3);
  not not_177 (not_177_out, OP2);
  not not_178 (not_178_out, F30);
  not not_179 (not_179_out, F25);
  not not_180 (not_180_out, F14);
  not not_181 (not_181_out, OP6);
  not not_182 (not_182_out, OP3);
  not not_183 (not_183_out, OP2);
  not not_184 (not_184_out, F14);
  not not_185 (not_185_out, F13);
  not not_186 (not_186_out, F12);
  not not_187 (not_187_out, OP6);
  not not_188 (not_188_out, OP5);
  not not_189 (not_189_out, OP3);
  not not_190 (not_190_out, OP2);
  not not_191 (not_191_out, OP6);
  not not_192 (not_192_out, OP5);
  not not_193 (not_193_out, OP3);
  not not_194 (not_194_out, OP2);
  not not_195 (not_195_out, F14);
  not not_196 (not_196_out, F12);
  not not_197 (not_197_out, OP6);
  not not_198 (not_198_out, OP5);
  not not_199 (not_199_out, OP4);
  not not_200 (not_200_out, OP3);
  not not_201 (not_201_out, OP2);
  not not_202 (not_202_out, F14);
  not not_203 (not_203_out, F12);
  not not_204 (not_204_out, OP6);
  not not_205 (not_205_out, OP4);
  not not_206 (not_206_out, OP3);
  not not_207 (not_207_out, OP2);
  not not_208 (not_208_out, F14);
  not not_209 (not_209_out, F13);
  not not_210 (not_210_out, F12);
  not not_211 (not_211_out, OP4);
  not not_212 (not_212_out, OP3);
  not not_213 (not_213_out, F14);
  not not_214 (not_214_out, OP6);
  not not_215 (not_215_out, OP5);
  not not_216 (not_216_out, OP3);
  not not_217 (not_217_out, OP2);
  not not_218 (not_218_out, F14);
  not not_219 (not_219_out, F13);
  not not_220 (not_220_out, F12);
  not not_221 (not_221_out, OP6);
  not not_222 (not_222_out, OP5);
  not not_223 (not_223_out, OP4);
  not not_224 (not_224_out, OP3);
  not not_225 (not_225_out, OP2);
  not not_226 (not_226_out, F30);
  not not_227 (not_227_out, F25);
  not not_228 (not_228_out, F12);
  not not_229 (not_229_out, OP6);
  not not_230 (not_230_out, OP3);
  not not_231 (not_231_out, OP2);
  not not_232 (not_232_out, F30);
  not not_233 (not_233_out, F25);
  not not_234 (not_234_out, F14);
  not not_235 (not_235_out, F12);
  not not_236 (not_236_out, OP6);
  not not_237 (not_237_out, OP3);
  not not_238 (not_238_out, OP2);
  not not_239 (not_239_out, F30);
  not not_240 (not_240_out, F25);
  not not_241 (not_241_out, F14);
  not not_242 (not_242_out, OP6);
  not not_243 (not_243_out, OP3);
  not not_244 (not_244_out, OP2);
  not not_245 (not_245_out, F12);
  not not_246 (not_246_out, OP6);
  not not_247 (not_247_out, OP5);
  not not_248 (not_248_out, OP3);
  not not_249 (not_249_out, OP2);
  not not_250 (not_250_out, F13);
  not not_251 (not_251_out, F12);
  not not_252 (not_252_out, OP6);
  not not_253 (not_253_out, OP5);
  not not_254 (not_254_out, OP3);
  not not_255 (not_255_out, OP2);
  not not_256 (not_256_out, F14);
  not not_257 (not_257_out, F12);
  not not_258 (not_258_out, OP6);
  not not_259 (not_259_out, OP5);
  not not_260 (not_260_out, OP3);
  not not_261 (not_261_out, OP2);
  not not_262 (not_262_out, F30);
  not not_263 (not_263_out, F25);
  not not_264 (not_264_out, F14);
  not not_265 (not_265_out, F13);
  not not_266 (not_266_out, F12);
  not not_267 (not_267_out, OP3);
  not not_268 (not_268_out, OP2);
  not not_269 (not_269_out, F14);
  not not_270 (not_270_out, F13);
  not not_271 (not_271_out, F12);
  not not_272 (not_272_out, OP4);
  not not_273 (not_273_out, OP3);
  not not_274 (not_274_out, OP2);
  not not_275 (not_275_out, F14);
  not not_276 (not_276_out, F13);
  not not_277 (not_277_out, OP4);
  not not_278 (not_278_out, OP3);
  not not_279 (not_279_out, OP2);
  not not_280 (not_280_out, F14);
  not not_281 (not_281_out, OP6);
  not not_282 (not_282_out, OP5);
  not not_283 (not_283_out, OP3);
  not not_284 (not_284_out, OP2);
  not not_285 (not_285_out, F13);
  not not_286 (not_286_out, F12);
  not not_287 (not_287_out, OP4);
  not not_288 (not_288_out, OP3);
  not not_289 (not_289_out, OP2);
  and and_1 (and_1_out, not_1_out, not_2_out, not_3_out, not_4_out, not_5_out, not_6_out, OP5, OP4, not_7_out, not_8_out);
  and and_2 (and_2_out, not_9_out, not_10_out, F14, F13, F12, not_11_out, OP5, OP4, not_12_out, not_13_out);
  and and_3 (and_3_out, not_14_out, not_15_out, not_16_out, F13, not_17_out, not_18_out, OP5, OP4, not_19_out, not_20_out);
  and and_4 (and_4_out, not_21_out, not_22_out, not_23_out, not_24_out, not_25_out, OP4, not_26_out, not_27_out);
  and and_5 (and_5_out, F14, F13, F12, not_28_out, not_29_out, OP4, not_30_out, not_31_out);
  and and_6 (and_6_out, F14, not_32_out, not_33_out, not_34_out, not_35_out, OP4, not_36_out, not_37_out);
  and and_7 (and_7_out, not_38_out, F13, not_39_out, not_40_out, not_41_out, OP4, not_42_out, not_43_out);
  and and_8 (and_8_out, F30, not_44_out, F14, not_45_out, F12, not_46_out, not_47_out, OP4, not_48_out, not_49_out);
  and and_9 (and_9_out, not_50_out, F13, not_51_out, not_52_out, not_53_out, not_54_out, not_55_out, not_56_out);
  and and_10 (and_10_out, not_57_out, F13, not_58_out, not_59_out, OP5, not_60_out, not_61_out, not_62_out);
  and and_11 (and_11_out, not_63_out, not_64_out, not_65_out, not_66_out, not_67_out, OP6, OP5, OP4, not_68_out, not_69_out);
  and and_12 (and_12_out, not_70_out, not_71_out, not_72_out, OP6, OP5, not_73_out, not_74_out, not_75_out);
  and and_13 (and_13_out, not_76_out, not_77_out, F12, OP6, OP5, not_78_out, not_79_out, not_80_out);
  and and_14 (and_14_out, not_81_out, not_82_out, not_83_out, OP6, OP5, not_84_out, not_85_out, OP2);
  and and_15 (and_15_out, not_86_out, not_87_out, not_88_out, not_89_out, not_90_out, not_91_out, not_92_out, not_93_out);
  and and_16 (and_16_out, F14, not_94_out, not_95_out, OP6, OP5, not_96_out, not_97_out, not_98_out);
  and and_17 (and_17_out, F30, not_99_out, not_100_out, not_101_out, not_102_out, not_103_out, OP5, OP4, not_104_out, not_105_out);
  and and_18 (and_18_out, not_106_out, not_107_out, F14, F13, F12, not_108_out, OP5, OP4, not_109_out, not_110_out);
  and and_19 (and_19_out, not_111_out, not_112_out, not_113_out, F13, not_114_out, not_115_out, OP5, OP4, not_116_out, not_117_out);
  and and_20 (and_20_out, F14, F13, F12, not_118_out, not_119_out, OP4, not_120_out, not_121_out);
  and and_21 (and_21_out, not_122_out, F13, not_123_out, not_124_out, not_125_out, OP4, not_126_out, not_127_out);
  and and_22 (and_22_out, not_128_out, not_129_out, F14, not_130_out, F12, not_131_out, not_132_out, OP4, not_133_out, not_134_out);
  and and_23 (and_23_out, not_135_out, not_136_out, not_137_out, not_138_out, not_139_out, OP6, OP5, OP4, not_140_out, not_141_out);
  and and_24 (and_24_out, not_142_out, not_143_out, not_144_out, OP6, OP5, not_145_out, not_146_out, not_147_out);
  and and_25 (and_25_out, not_148_out, not_149_out, F12, OP6, OP5, not_150_out, not_151_out, not_152_out);
  and and_26 (and_26_out, F14, not_153_out, not_154_out, OP6, OP5, not_155_out, not_156_out, not_157_out);
  and and_27 (and_27_out, not_158_out, not_159_out, not_160_out, not_161_out, not_162_out, not_163_out, OP5, OP4, not_164_out, not_165_out);
  and and_28 (and_28_out, F30, not_166_out, not_167_out, not_168_out, not_169_out, not_170_out, OP5, OP4, not_171_out, not_172_out);
  and and_29 (and_29_out, not_173_out, not_174_out, F14, F13, F12, not_175_out, OP5, OP4, not_176_out, not_177_out);
  and and_30 (and_30_out, not_178_out, not_179_out, not_180_out, F13, F12, not_181_out, OP5, OP4, not_182_out, not_183_out);
  and and_31 (and_31_out, not_184_out, not_185_out, not_186_out, not_187_out, not_188_out, OP4, not_189_out, not_190_out);
  and and_32 (and_32_out, F14, F13, F12, not_191_out, not_192_out, OP4, not_193_out, not_194_out);
  and and_33 (and_33_out, not_195_out, F13, not_196_out, not_197_out, not_198_out, not_199_out, not_200_out, not_201_out);
  and and_34 (and_34_out, not_202_out, F13, not_203_out, not_204_out, OP5, not_205_out, not_206_out, not_207_out);
  and and_35 (and_35_out, not_208_out, not_209_out, not_210_out, OP6, OP5, not_211_out, not_212_out, OP2);
  and and_36 (and_36_out, not_213_out, F13, F12, not_214_out, not_215_out, OP4, not_216_out, not_217_out);
  and and_37 (and_37_out, not_218_out, not_219_out, not_220_out, not_221_out, not_222_out, not_223_out, not_224_out, not_225_out);
  and and_38 (and_38_out, not_226_out, not_227_out, F14, F13, not_228_out, not_229_out, OP5, OP4, not_230_out, not_231_out);
  and and_39 (and_39_out, not_232_out, not_233_out, not_234_out, F13, not_235_out, not_236_out, OP5, OP4, not_237_out, not_238_out);
  and and_40 (and_40_out, not_239_out, not_240_out, not_241_out, F13, F12, not_242_out, OP5, OP4, not_243_out, not_244_out);
  and and_41 (and_41_out, F14, F13, not_245_out, not_246_out, not_247_out, OP4, not_248_out, not_249_out);
  and and_42 (and_42_out, F14, not_250_out, not_251_out, not_252_out, not_253_out, OP4, not_254_out, not_255_out);
  and and_43 (and_43_out, not_256_out, F13, not_257_out, not_258_out, not_259_out, OP4, not_260_out, not_261_out);
  and and_44 (and_44_out, not_262_out, not_263_out, not_264_out, not_265_out, not_266_out, OP6, OP5, OP4, not_267_out, not_268_out);
  and and_45 (and_45_out, not_269_out, not_270_out, not_271_out, OP6, OP5, not_272_out, not_273_out, not_274_out);
  and and_46 (and_46_out, not_275_out, not_276_out, F12, OP6, OP5, not_277_out, not_278_out, not_279_out);
  and and_47 (and_47_out, not_280_out, F13, F12, not_281_out, not_282_out, OP4, not_283_out, not_284_out);
  and and_48 (and_48_out, F14, not_285_out, not_286_out, OP6, OP5, not_287_out, not_288_out, not_289_out);
  or or_1 (S0, and_1_out, and_2_out, and_3_out, and_4_out, and_5_out, and_6_out, and_7_out, and_8_out, and_9_out, and_10_out, and_11_out, and_12_out, and_13_out, and_14_out, and_15_out, and_16_out);
  or or_2 (S1, and_17_out, and_18_out, and_19_out, and_20_out, and_21_out, and_22_out, and_23_out, and_24_out, and_25_out, and_26_out);
  or or_3 (S2, and_27_out, and_28_out, and_29_out, and_30_out, and_31_out, and_32_out, and_33_out, and_34_out, and_35_out, and_36_out, and_37_out);
  or or_4 (S3, and_38_out, and_39_out, and_40_out, and_41_out, and_42_out, and_43_out, and_44_out, and_45_out, and_46_out, and_47_out, and_48_out);
endmodule

// 控制信号生成
module \控制信号自动生成  (
  input  OP2,
  input  OP3,
  input  OP4,
  input  OP5,
  input  OP6,
  input  F12,
  input  F13,
  input  F14,
  input  F25,
  input  F30,
  output MemToReg,
  output CSRRSI,
  output CSRRCI,
  output MemWrite,
  output ALU_SRC,
  output RegWrite,
  output ecall,
  output S_Type,
  output BEQ,
  output BNE,
  output JALR,
  output JAL,
  output lb,
  output blt
);

  wire and_5_out, and_6_out, and_7_out, and_8_out, and_9_out, and_10_out, and_11_out, and_12_out, and_13_out,
       and_14_out, and_15_out, and_16_out, and_17_out, and_18_out, and_19_out, and_20_out, and_21_out,
       not_1_out, not_2_out, not_3_out, not_4_out, not_5_out, not_6_out, not_7_out, not_8_out, not_9_out,
       not_10_out, not_11_out, not_12_out, not_13_out, not_14_out, not_15_out, not_16_out, not_17_out,
       not_18_out, not_19_out, not_20_out, not_21_out, not_22_out, not_23_out, not_24_out, not_25_out,
       not_26_out, not_27_out, not_28_out, not_29_out, not_30_out, not_31_out, not_32_out, not_33_out,
       not_34_out, not_35_out, not_36_out, not_37_out, not_38_out, not_39_out, not_40_out, not_41_out,
       not_42_out, not_43_out, not_44_out, not_45_out, not_46_out, not_47_out, not_48_out, not_49_out,
       not_50_out, not_51_out, not_52_out, not_53_out, not_54_out, not_55_out, not_56_out, not_57_out,
       not_58_out, not_59_out, not_60_out, not_61_out, not_62_out, not_63_out, not_64_out, not_65_out,
       not_66_out, not_67_out, not_68_out, not_69_out, not_70_out, not_71_out, not_72_out, not_73_out,
       not_74_out, not_75_out, not_76_out, not_77_out, not_78_out, not_79_out, not_80_out, not_81_out,
       not_82_out, not_83_out, not_84_out, not_85_out, not_86_out, not_87_out, not_88_out, not_89_out,
       not_90_out, not_91_out, not_92_out, not_93_out, not_94_out, not_95_out, not_96_out, not_97_out,
       not_98_out, not_99_out, not_100_out, not_101_out, not_102_out, not_103_out, not_104_out, not_105_out,
       not_106_out, not_107_out, not_108_out, not_109_out, not_110_out, not_111_out, not_112_out,
       not_113_out, not_114_out, not_115_out, not_116_out, not_117_out, not_118_out, not_119_out,
       not_120_out, not_121_out, not_122_out, not_123_out, not_124_out, not_125_out, not_126_out,
       not_127_out, not_128_out, not_129_out, not_130_out, not_131_out, not_132_out, not_133_out,
       not_134_out, not_135_out, not_136_out, not_137_out, not_138_out, not_139_out, not_140_out,
       not_141_out, not_142_out, not_143_out, not_144_out, not_145_out, not_146_out, not_147_out, not_148_out;

  not not_1 (not_1_out, OP2);
  not not_2 (not_2_out, OP3);
  not not_3 (not_3_out, OP4);
  not not_4 (not_4_out, OP5);
  not not_5 (not_5_out, OP6);
  not not_6 (not_6_out, F12);
  not not_7 (not_7_out, F14);
  not not_8 (not_8_out, F12);
  not not_9 (not_9_out, OP3);
  not not_10 (not_10_out, OP2);
  not not_11 (not_11_out, OP3);
  not not_12 (not_12_out, OP2);
  not not_13 (not_13_out, OP2);
  not not_14 (not_14_out, OP3);
  not not_15 (not_15_out, OP4);
  not not_16 (not_16_out, OP6);
  not not_17 (not_17_out, F12);
  not not_18 (not_18_out, F14);
  not not_19 (not_19_out, OP2);
  not not_20 (not_20_out, OP3);
  not not_21 (not_21_out, OP5);
  not not_22 (not_22_out, OP6);
  not not_23 (not_23_out, F12);
  not not_24 (not_24_out, F14);
  not not_25 (not_25_out, OP2);
  not not_26 (not_26_out, OP3);
  not not_27 (not_27_out, OP4);
  not not_28 (not_28_out, OP6);
  not not_29 (not_29_out, F12);
  not not_30 (not_30_out, F14);
  not not_31 (not_31_out, OP2);
  not not_32 (not_32_out, OP3);
  not not_33 (not_33_out, OP5);
  not not_34 (not_34_out, OP6);
  not not_35 (not_35_out, F12);
  not not_36 (not_36_out, OP2);
  not not_37 (not_37_out, OP3);
  not not_38 (not_38_out, OP5);
  not not_39 (not_39_out, OP6);
  not not_40 (not_40_out, F25);
  not not_41 (not_41_out, F30);
  not not_42 (not_42_out, OP2);
  not not_43 (not_43_out, OP3);
  not not_44 (not_44_out, OP5);
  not not_45 (not_45_out, OP6);
  not not_46 (not_46_out, F25);
  not not_47 (not_47_out, OP2);
  not not_48 (not_48_out, OP3);
  not not_49 (not_49_out, OP5);
  not not_50 (not_50_out, OP6);
  not not_51 (not_51_out, OP2);
  not not_52 (not_52_out, OP3);
  not not_53 (not_53_out, F12);
  not not_54 (not_54_out, F13);
  not not_55 (not_55_out, F14);
  not not_56 (not_56_out, F25);
  not not_57 (not_57_out, F30);
  not not_58 (not_58_out, OP3);
  not not_59 (not_59_out, OP4);
  not not_60 (not_60_out, F12);
  not not_61 (not_61_out, F13);
  not not_62 (not_62_out, F14);
  not not_63 (not_63_out, OP2);
  not not_64 (not_64_out, OP3);
  not not_65 (not_65_out, OP5);
  not not_66 (not_66_out, OP6);
  not not_67 (not_67_out, F12);
  not not_68 (not_68_out, F14);
  not not_69 (not_69_out, OP2);
  not not_70 (not_70_out, OP3);
  not not_71 (not_71_out, OP5);
  not not_72 (not_72_out, OP6);
  not not_73 (not_73_out, F12);
  not not_74 (not_74_out, OP2);
  not not_75 (not_75_out, OP3);
  not not_76 (not_76_out, OP6);
  not not_77 (not_77_out, F12);
  not not_78 (not_78_out, F13);
  not not_79 (not_79_out, F14);
  not not_80 (not_80_out, F25);
  not not_81 (not_81_out, OP2);
  not not_82 (not_82_out, OP3);
  not not_83 (not_83_out, OP6);
  not not_84 (not_84_out, F14);
  not not_85 (not_85_out, F25);
  not not_86 (not_86_out, F30);
  not not_87 (not_87_out, OP2);
  not not_88 (not_88_out, OP3);
  not not_89 (not_89_out, OP5);
  not not_90 (not_90_out, OP6);
  not not_91 (not_91_out, F25);
  not not_92 (not_92_out, OP2);
  not not_93 (not_93_out, OP3);
  not not_94 (not_94_out, OP5);
  not not_95 (not_95_out, OP6);
  not not_96 (not_96_out, OP2);
  not not_97 (not_97_out, OP3);
  not not_98 (not_98_out, OP6);
  not not_99 (not_99_out, F25);
  not not_100 (not_100_out, F30);
  not not_101 (not_101_out, OP4);
  not not_102 (not_102_out, F12);
  not not_103 (not_103_out, F13);
  not not_104 (not_104_out, F14);
  not not_105 (not_105_out, OP4);
  not not_106 (not_106_out, OP2);
  not not_107 (not_107_out, OP3);
  not not_108 (not_108_out, F12);
  not not_109 (not_109_out, F13);
  not not_110 (not_110_out, F14);
  not not_111 (not_111_out, F25);
  not not_112 (not_112_out, F30);
  not not_113 (not_113_out, OP2);
  not not_114 (not_114_out, OP3);
  not not_115 (not_115_out, OP4);
  not not_116 (not_116_out, OP6);
  not not_117 (not_117_out, F12);
  not not_118 (not_118_out, F14);
  not not_119 (not_119_out, OP2);
  not not_120 (not_120_out, OP3);
  not not_121 (not_121_out, OP4);
  not not_122 (not_122_out, F12);
  not not_123 (not_123_out, F13);
  not not_124 (not_124_out, F14);
  not not_125 (not_125_out, OP2);
  not not_126 (not_126_out, OP3);
  not not_127 (not_127_out, OP4);
  not not_128 (not_128_out, F13);
  not not_129 (not_129_out, F14);
  not not_130 (not_130_out, OP3);
  not not_131 (not_131_out, OP4);
  not not_132 (not_132_out, F12);
  not not_133 (not_133_out, F13);
  not not_134 (not_134_out, F14);
  not not_135 (not_135_out, OP4);
  not not_136 (not_136_out, OP2);
  not not_137 (not_137_out, OP3);
  not not_138 (not_138_out, OP4);
  not not_139 (not_139_out, OP5);
  not not_140 (not_140_out, OP6);
  not not_141 (not_141_out, F12);
  not not_142 (not_142_out, F13);
  not not_143 (not_143_out, F14);
  not not_144 (not_144_out, OP2);
  not not_145 (not_145_out, OP3);
  not not_146 (not_146_out, OP4);
  not not_147 (not_147_out, F12);
  not not_148 (not_148_out, F13);
  and and_1 (MemToReg, not_1_out, not_2_out, not_3_out, not_4_out, not_5_out, not_6_out, not_7_out);
  and and_2 (CSRRSI, F14, F13, not_8_out, OP6, OP5, OP4, not_9_out, not_10_out);
  and and_3 (CSRRCI, F14, F13, F12, OP6, OP5, OP4, not_11_out, not_12_out);
  and and_4 (MemWrite, not_13_out, not_14_out, not_15_out, OP5, not_16_out, not_17_out, F13, not_18_out);
  and and_5 (and_5_out, not_19_out, not_20_out, not_21_out, not_22_out, not_23_out, not_24_out);
  and and_6 (and_6_out, not_25_out, not_26_out, not_27_out, not_28_out, not_29_out, F13, not_30_out);
  and and_7 (and_7_out, not_31_out, not_32_out, OP4, not_33_out, not_34_out, not_35_out);
  and and_8 (and_8_out, not_36_out, not_37_out, OP4, not_38_out, not_39_out, not_40_out, not_41_out);
  and and_9 (and_9_out, not_42_out, not_43_out, OP4, not_44_out, not_45_out, F14, not_46_out);
  and and_10 (and_10_out, not_47_out, not_48_out, OP4, not_49_out, not_50_out, F13);
  and and_11 (and_11_out, not_51_out, not_52_out, OP4, OP5, OP6, not_53_out, not_54_out, not_55_out, not_56_out, not_57_out);
  and and_12 (and_12_out, OP2, not_58_out, not_59_out, OP5, OP6, not_60_out, not_61_out, not_62_out);
  and and_13 (and_13_out, not_63_out, not_64_out, not_65_out, not_66_out, not_67_out, not_68_out);
  and and_14 (and_14_out, not_69_out, not_70_out, OP4, not_71_out, not_72_out, not_73_out);
  and and_15 (and_15_out, not_74_out, not_75_out, OP4, not_76_out, not_77_out, not_78_out, not_79_out, not_80_out);
  and and_16 (and_16_out, not_81_out, not_82_out, OP4, not_83_out, not_84_out, not_85_out, not_86_out);
  and and_17 (and_17_out, not_87_out, not_88_out, OP4, not_89_out, not_90_out, F14, not_91_out);
  and and_18 (and_18_out, not_92_out, not_93_out, OP4, not_94_out, not_95_out, F13);
  and and_19 (and_19_out, not_96_out, not_97_out, OP4, not_98_out, F13, not_99_out, not_100_out);
  and and_20 (and_20_out, OP2, not_101_out, OP5, OP6, not_102_out, not_103_out, not_104_out);
  and and_21 (and_21_out, OP2, OP3, not_105_out, OP5, OP6);
  and and_22 (ecall, not_106_out, not_107_out, OP4, OP5, OP6, not_108_out, not_109_out, not_110_out, not_111_out, not_112_out);
  and and_23 (S_Type, not_113_out, not_114_out, not_115_out, OP5, not_116_out, not_117_out, F13, not_118_out);
  and and_24 (BEQ, not_119_out, not_120_out, not_121_out, OP5, OP6, not_122_out, not_123_out, not_124_out);
  and and_25 (BNE, not_125_out, not_126_out, not_127_out, OP5, OP6, F12, not_128_out, not_129_out);
  and and_26 (JALR, OP2, not_130_out, not_131_out, OP5, OP6, not_132_out, not_133_out, not_134_out);
  and and_27 (JAL, OP2, OP3, not_135_out, OP5, OP6);
  and and_28 (lb, not_136_out, not_137_out, not_138_out, not_139_out, not_140_out, not_141_out, not_142_out, not_143_out);
  and and_29 (blt, not_144_out, not_145_out, not_146_out, OP5, OP6, not_147_out, not_148_out, F14);
  or or_1 (ALU_SRC, and_5_out, and_6_out, and_7_out, and_8_out, and_9_out, and_10_out, and_11_out, and_12_out);
  or or_2 (RegWrite, and_13_out, and_14_out, and_15_out, and_16_out, and_17_out, and_18_out, and_19_out, and_20_out, and_21_out);
endmodule

// ALU
module ALU (
  input  [31:0] X,
  input  [31:0] Y,
  input  [3:0] AluOP,
  output out_4,
  output Equal,
  output out_6,
  output [31:0] Result,
  output [31:0] Result_2
);

  wire [0:0] comparator_1_lt, comparator_2_lt;
  wire [31:0] adder_1_out, AND_out, divider_1_out, divider_1_rem, multiplier_1_cout, multiplier_1_out,
       NOR_out, OR_out, shifter_1_out, shifter_2_out, shifter_3_out, subtractor_1_out, XOR_out;

  assign AND_out = X & Y;  // AND_Gate AND, 32 bits wide
  assign OR_out = X | Y;  // OR_Gate OR, 32 bits wide
  Shifter #(.width(32), .shift("ll")) shifter_1 (.in(X), .\dist (Y[4:0]), .out(shifter_1_out));
  Shifter #(.width(32), .shift("ar")) shifter_2 (.in(X), .\dist (Y[4:0]), .out(shifter_2_out));
  Shifter #(.width(32), .shift("lr")) shifter_3 (.in(X), .\dist (Y[4:0]), .out(shifter_3_out));
  Multiplier #(.width(32)) multiplier_1 (.a(X), .b(Y), .out(multiplier_1_out), .cout(multiplier_1_cout));  // open: cin
  Divider #(.width(32)) divider_1 (.a(X), .b(Y), .out(divider_1_out), .rem(divider_1_rem));  // open: upper
  Adder #(.width(32)) adder_1 (.a(X), .b(Y), .out(adder_1_out));  // open: cin, cout
  Subtractor #(.width(32)) subtractor_1 (.a(X), .b(Y), .out(subtractor_1_out));  // open: bin, bout
  assign XOR_out = X ^ Y;  // XOR_Gate XOR, 32 bits wide
  assign NOR_out = ~(X | Y);  // NOR_Gate NOR, 32 bits wide
  Comparator #(.width(32), .mode("twosComplement")) comparator_1 (
    .a(X), .b(Y), .eq(Equal), .lt(comparator_1_lt[0]));  // open: gt
  Comparator #(.width(32), .mode("unsigned")) comparator_2 (.a(X), .b(Y), .lt(comparator_2_lt[0]));  // open: gt, eq
  Multiplexer #(.select(4), .width(32), .disabled("Z"), .enable("false")) multiplexer_1 (
    .in0(shifter_1_out), .in1(shifter_2_out), .in2(shifter_3_out), .in3(multiplier_1_out),
    .in4(divider_1_out), .in5(adder_1_out), .in6(subtractor_1_out), .in7(AND_out), .in8(OR_out),
    .in9(XOR_out), .in10(NOR_out), .in11({{31{1'b0}}, comparator_1_lt[0]}),
    .in12({{31{1'b0}}, comparator_2_lt[0]}), .in13({32{1'b0}}), .in14({32{1'b0}}), .in15({32{1'b0}}),
    .out(Result), .sel(AluOP));
  Multiplexer #(.select(4), .width(32), .disabled("Z"), .enable("false")) multiplexer_2 (
    .in0({32{1'b0}}), .in1({32{1'b0}}), .in2({32{1'b0}}), .in3(multiplier_1_cout), .in4(divider_1_rem),
    .in5({32{1'b0}}), .in6({32{1'b0}}), .in7({32{1'b0}}), .in8({32{1'b0}}), .in9({32{1'b0}}),
    .in10({32{1'b0}}), .in11({32{1'b0}}), .in12({32{1'b0}}), .in13({32{1'b0}}), .in14({32{1'b0}}),
    .in15({32{1'b0}}), .out(Result_2), .sel(AluOP));
  Multiplexer #(.select(4), .width(1), .disabled("Z"), .enable("false")) multiplexer_3 (
    .in0(1'b0), .in1(1'b0), .in2(1'b0), .in3(1'b0), .in4(1'b0), .in5(1'b0), .in6(1'b0), .in7(1'b0),
    .in8(1'b0), .in9(1'b0), .in10(1'b0), .in11(comparator_1_lt[0]), .in12(comparator_2_lt[0]), .in13(1'b0),
    .in14(1'b0), .in15(1'b0), .out(out_6), .sel(AluOP));
  not not_1 (out_4, out_6);

  // Other names for the same wires on the sheet: Result2[31:0] = Result_2; S[3:0] = AluOP; tunnel = out_6;
  //   tunnel_t = out_4

  // Notes on the sheet:
  //   不要改变此引脚区域内容，也不要改变ALU封装形式
  //   输入引脚
  //   输出引脚
endmodule

module Regifile (
  input  [31:0] Din,
  input  Clk,
  input  WE,
  input  [4:0] R1_num,
  input  [4:0] W_num,
  input  [4:0] R2_num,
  output [31:0] R1,
  output [31:0] R2
);

  // RegisterFile registerfile_1: pin names not known; wires that end beside it: Din, Clk, WE, W_num, R1_num, R2_num, R1, R2
endmodule

module \理想流水线  (
  output RegWrite,
  output MemWrite,
  output [31:0] IF_PC,
  output [31:0] ID_PC,
  output [31:0] EX_PC,
  output [31:0] M_PC,
  output [31:0] WB_PC,
  output [31:0] RDin,
  output [31:0] MDin,
  output [31:0] LedData
);

  wire alu_1_out_6, and_1_out, and_2_out, and_3_out, and_4_out, CLK, clock_1_out, comparator_1_eq,
       comparator_1_lt, comparator_2_eq, d_ff_1_q, en, EX_B, EX_ecall, EX_jal, EX_jalr, Go, halt, ID_ecall,
       IR1, IR2, IR3, nand_1_out, not_1_out, or_3_out, RST, W1, W2, W3, WB, WB_ecall, \单周期硬布线控制器_1_s_type ;
  wire [0:0] or_1_out;
  wire [3:0] \单周期硬布线控制器_1_alu_op ;
  wire [4:0] EX_W_num, MEM_W_num, mem_wb_1_ctrlsignal_2, multiplexer_2_out, multiplexer_3_out, WD_W_num;
  wire [7:0] ex_mem_1_ctrlsignal_2, multiplexer_10_out;
  wire [7:7] alu_1_equal;
  wire [11:0] \id_ex_理想_气泡_1_badd_2 , shifter_1_out;
  wire [12:0] CNT_num;
  wire [13:0] \单周期硬布线控制器_1_jal ;
  wire [13:2] \id_ex_理想_气泡_1_ctrlsignal_2 ;
  wire [14:0] multiplexer_6_out;
  wire [15:0] \LoadUse次数 , \总周期数 , \插入气泡数 , \无条件分支数 , \条件分支成功数 ;
  wire [19:0] \id_ex_理想_气泡_1_j_2 , shifter_2_out;
  wire [31:0] adder_1_out, adder_2_out, adder_3_out, adder_4_out, bit_extender_1_out, bit_extender_2_out,
       bit_extender_3_out, bit_extender_4_out, bit_extender_5_out, EX_ALU_res, EX_IR, ex_mem_1_alu_2,
       \id_ex_理想_气泡_1_a_2 , \id_ex_理想_气泡_1_imm_2 , ID_IR, IF_IR, MEM_IR, mem_wb_1_alu_2, mem_wb_1_md_2,
       multiplexer_1_out, multiplexer_4_out, multiplexer_5_out, multiplexer_7_out, multiplexer_8_out,
       multiplexer_9_out, multiplexer_11_out, R2data, ram_1_data, regifile_1_r1, regifile_1_r2, WB_IR;

  Button \u_总复位  (.out(RST));
  Button _1 (.out(IR1));
  Button _2 (.out(IR2));
  Button _3 (.out(IR3));
  // Probe on \总周期数 
  // Probe on \总周期数 
  Button \u_继续运行  (.out(Go));
  LED #(.active("true")) led_1 (.in(W1));
  LED #(.active("true")) led_2 (.in(W2));
  LED #(.active("true")) led_3 (.in(W3));
  Hex_Digit_Display hex_digit_display_1 (.value(LedData[31:28]));  // open: dp
  // Probe on IF_PC[19:0]
  // RiscV_Probe riscv_probe_1: pin names not known; wires that end beside it: IF_IR
  or or_1 (or_1_out[0], EX_jal, EX_B);
  Hex_Digit_Display hex_digit_display_2 (.value(LedData[23:20]));  // open: dp
  Hex_Digit_Display hex_digit_display_3 (.value(LedData[27:24]));  // open: dp
  // Probe on ID_PC[19:0]
  // RiscV_Probe riscv_probe_2: pin names not known; wires that end beside it: ID_IR
  not not_1 (not_1_out, halt);
  Multiplexer #(.select(2), .width(32), .disabled("Z"), .enable("false")) multiplexer_1 (
    .in0(adder_1_out), .in1(multiplexer_8_out), .in2(EX_ALU_res), .out(multiplexer_1_out),
    .sel({EX_jalr, or_1_out[0]}));  // open: in3
  Hex_Digit_Display hex_digit_display_4 (.value(LedData[15:12]));  // open: dp
  Hex_Digit_Display hex_digit_display_5 (.value(LedData[19:16]));  // open: dp
  Register #(.width(32), .trigger("rising"), .Select("low")) PC (
    .D(multiplexer_1_out), .en(not_1_out), .Q(IF_PC), .clk(CLK), .clr(RST));
  Hex_Digit_Display hex_digit_display_6 (.value(LedData[11:8]));  // open: dp
  Hex_Digit_Display hex_digit_display_7 (.value(LedData[7:4]));  // open: dp
  // Probe on EX_PC[19:0]
  // RiscV_Probe riscv_probe_3: pin names not known; wires that end beside it: EX_IR
  Adder #(.width(32)) adder_1 (.a(IF_PC), .b(32'h4), .out(adder_1_out));  // open: cin, cout
  Hex_Digit_Display hex_digit_display_8 (.value(LedData[3:0]));  // open: dp
  // Probe on \总周期数 
  // Probe on M_PC[19:0]
  // RiscV_Probe riscv_probe_4: pin names not known; wires that end beside it: MEM_IR
  ROM #(.addrWidth(10), .dataWidth(32), .Select("high")) rom_1 (.addr(IF_PC[11:2]), .data(IF_IR));
  IF_ID if_id_1 (.PC_2(ID_PC), .IR_2(ID_IR), .PC(IF_PC), .IR(IF_IR), .CLK(CLK), .CLR(RST), .en(en));
  // Probe on \总周期数 
  // Probe on \无条件分支数 
  // Probe on \条件分支成功数 
  // Probe on \插入气泡数 
  // Probe on \LoadUse次数 
  // Probe on IF_PC[11:0]
  // Probe on WB_PC[19:0]
  // RiscV_Probe riscv_probe_5: pin names not known; wires that end beside it: WB_IR
  // Probe on ID_PC[11:0]
  // Probe on EX_PC[11:0]
  \单周期硬布线控制器  \u_单周期硬布线控制器_1  (
    .Funct({ID_IR[30], ID_IR[25], ID_IR[14:12]}), .OP(ID_IR[6:2]), .ALU_OP(\单周期硬布线控制器_1_alu_op ),
    .MemToReg(\单周期硬布线控制器_1_jal [3]), .MemWrite(\单周期硬布线控制器_1_jal [4]), .ALU_SRC(\单周期硬布线控制器_1_jal [13]),
    .RegWrite(\单周期硬布线控制器_1_jal [2]), .ecall(ID_ecall), .S_type(\单周期硬布线控制器_1_s_type ),
    .Jalr(\单周期硬布线控制器_1_jal [1]), .Beq(\单周期硬布线控制器_1_jal [10]), .JAL(\单周期硬布线控制器_1_jal [0]),
    .Bne(\单周期硬布线控制器_1_jal [11]), .in_3(ID_IR[21]), .lb(\单周期硬布线控制器_1_jal [5]), .blt(\单周期硬布线控制器_1_jal [12]));  // open: uret, CSRRSI, CSRRCI
  Multiplexer #(.select(1), .width(5), .disabled("Z"), .enable("false")) multiplexer_2 (
    .in0(ID_IR[19:15]), .in1(5'b10001), .out(multiplexer_2_out), .sel(ID_ecall));
  Multiplexer #(.select(1), .width(5), .disabled("Z"), .enable("false")) multiplexer_3 (
    .in0(ID_IR[24:20]), .in1(5'b01010), .out(multiplexer_3_out), .sel(ID_ecall));
  assign bit_extender_1_out = {{20{1'b0}}, ID_IR[31:20]};  // Bit_Extender bit_extender_1
  assign bit_extender_2_out = {{20{1'b0}}, {ID_IR[31:25], ID_IR[11:7]}};  // Bit_Extender bit_extender_2
  // Probe on M_PC[11:0]
  D_Flip_Flop #(.trigger("high"), .Pre_Clr_Positions("LEGACY"), .NegatePresetClear("false"), .enable("true"), .NewFFLayout("false")) d_ff_1 (.Q(d_ff_1_q));  // open: clk, D, Qn, preset, en, reset
  // Probe on 13'h13
  Multiplexer #(.select(1), .width(32), .disabled("Z"), .enable("false")) multiplexer_4 (
    .in0(bit_extender_1_out), .in1(bit_extender_2_out), .out(multiplexer_4_out), .sel(\单周期硬布线控制器_1_s_type ));
  // Probe on WB_PC[11:0]
  Comparator #(.width(13), .mode("twosComplement")) comparator_1 (
    .a(CNT_num), .b(13'h13), .eq(comparator_1_eq), .lt(comparator_1_lt));  // open: gt
  Clock #(.highDuration(1), .lowDuration(1)) clock_1 (.out(clock_1_out));
  Multiplexer #(.select(1), .width(32), .disabled("Z"), .enable("false")) multiplexer_5 (
    .in0(multiplexer_4_out), .in1(32'h22), .out(multiplexer_5_out), .sel(ID_ecall));
  nand nand_1 (nand_1_out, d_ff_1_q, comparator_1_eq);
  Counter #(.width(13), .max('h1fff), .ongoal("stay"), .trigger("rising"), .behavior("old")) counter_1 (
    .count(comparator_1_lt), .Q(CNT_num), .clk(clock_1_out));  // open: load, D, carry, clr, preset
  Comparator #(.width(32), .mode("twosComplement")) comparator_2 (
    .a(ID_IR), .b({32{1'b0}}), .eq(comparator_2_eq));  // open: gt, lt
  Regifile regifile_1 (
    .Din(RDin), .Clk(CLK), .R1(regifile_1_r1), .R2(regifile_1_r2), .WE(RegWrite), .W_num(WD_W_num),
    .R1_num(multiplexer_2_out), .R2_num(multiplexer_3_out));
  assign CLK = nand_1_out ? clock_1_out : 1'bz;  // Controlled_Buffer controlled_buffer_1
  Multiplexer #(.select(1), .width(15), .disabled("Z"), .enable("false")) multiplexer_6 (
    .in0({ID_ecall, \单周期硬布线控制器_1_jal [13:10], \单周期硬布线控制器_1_alu_op , \单周期硬布线控制器_1_jal [5:0]}),
    .in1({15{1'b0}}), .out(multiplexer_6_out), .sel(comparator_2_eq));
  Pull_Resistor #(.pull(1)) pull_resistor_1 (.node(CLK));
  \ID_EX_理想_气泡  \id_ex_理想_气泡_1  (
    .CLK(CLK), .CLR(RST), .en(en), .PC(ID_PC), .imm(multiplexer_5_out), .IR(ID_IR),
    .ctrlSignal(multiplexer_6_out), .A(regifile_1_r1), .W_num(ID_IR[11:7]), .B(regifile_1_r2),
    .Badd({ID_IR[31], ID_IR[7], ID_IR[30:25], ID_IR[11:8]}),
    .J({ID_IR[31], ID_IR[19:12], ID_IR[20], ID_IR[30:21]}), .PC_2(EX_PC), .imm_2(\id_ex_理想_气泡_1_imm_2 ),
    .IR_2(EX_IR), .ctrlSignal_2({EX_ecall, \id_ex_理想_气泡_1_ctrlsignal_2 , EX_jalr, EX_jal}),
    .A_2(\id_ex_理想_气泡_1_a_2 ), .W_num_2(EX_W_num), .B_2(R2data), .Badd_2(\id_ex_理想_气泡_1_badd_2 ),
    .J_2(\id_ex_理想_气泡_1_j_2 ));
  Counter #(.width(16), .max('hffff), .ongoal("stay"), .trigger("rising"), .behavior("new")) counter_2 (
    .count(en), .Q(\总周期数 ), .clk(CLK));  // open: load, D, carry, clr, preset, down
  Multiplexer #(.select(1), .width(32), .disabled("Z"), .enable("false")) multiplexer_7 (
    .in0(R2data), .in1(\id_ex_理想_气泡_1_imm_2 ), .out(multiplexer_7_out), .sel(\id_ex_理想_气泡_1_ctrlsignal_2 [13]));
  assign bit_extender_3_out = {{20{shifter_1_out[11]}}, shifter_1_out};  // Bit_Extender bit_extender_3
  Shifter #(.width(12), .shift("ll")) shifter_1 (.in(\id_ex_理想_气泡_1_badd_2 ), .\dist (4'b0001), .out(shifter_1_out));
  Shifter #(.width(20), .shift("ll")) shifter_2 (.in(\id_ex_理想_气泡_1_j_2 ), .\dist (5'b00001), .out(shifter_2_out));
  assign bit_extender_4_out = {{12{shifter_2_out[19]}}, shifter_2_out};  // Bit_Extender bit_extender_4
  and and_1 (and_1_out, \id_ex_理想_气泡_1_ctrlsignal_2 [11], ~alu_1_equal[7]);  // AND_Gate
  and and_2 (and_2_out, \id_ex_理想_气泡_1_ctrlsignal_2 [10], alu_1_equal[7]);
  ALU alu_1 (
    .X(\id_ex_理想_气泡_1_a_2 ), .Y(multiplexer_7_out), .AluOP(\id_ex_理想_气泡_1_ctrlsignal_2 [9:6]),
    .Equal(alu_1_equal[7]), .Result(EX_ALU_res), .out_6(alu_1_out_6));  // open: Result_2, out_4
  and and_3 (and_3_out, \id_ex_理想_气泡_1_ctrlsignal_2 [12], alu_1_out_6);
  Adder #(.width(32)) adder_2 (.a(bit_extender_3_out), .b(EX_PC), .out(adder_2_out));  // open: cin, cout
  Adder #(.width(32)) adder_3 (.a(bit_extender_4_out), .b(EX_PC), .out(adder_3_out));  // open: cin, cout
  or or_2 (EX_B, and_3_out, and_1_out, and_2_out);
  Multiplexer #(.select(1), .width(32), .disabled("Z"), .enable("false")) multiplexer_8 (
    .in0(adder_2_out), .in1(adder_3_out), .out(multiplexer_8_out), .sel(EX_jal));
  EX_MEM ex_mem_1 (
    .PC_2(M_PC), .ctrlSignal_2({ex_mem_1_ctrlsignal_2[7:5], MemWrite, ex_mem_1_ctrlsignal_2[3:0]}),
    .IR_2(MEM_IR), .B_2(MDin), .ALU_2(ex_mem_1_alu_2), .PC(EX_PC),
    .ctrlSignal({alu_1_equal[7], EX_ecall, \id_ex_理想_气泡_1_ctrlsignal_2 [5:2], EX_jalr, EX_jal}), .IR(EX_IR),
    .B(R2data), .ALU(EX_ALU_res), .W_num_2(MEM_W_num), .W_num(EX_W_num), .CLK(CLK), .CLR(RST), .en(en));
  RAM #(.addrWidth(10), .dataWidth(32), .bus("separate"), .Select("high")) ram_1 (
    .addr(ex_mem_1_alu_2[11:2]), .din(MDin), .data(ram_1_data), .str(MemWrite), .clk(CLK));  // open: sel, ld, clr
  MEM_WB mem_wb_1 (
    .PC(M_PC), .ctrlSignal({ex_mem_1_ctrlsignal_2[7:5], ex_mem_1_ctrlsignal_2[3:0]}), .IR(MEM_IR),
    .ALU(ex_mem_1_alu_2), .MD(ram_1_data), .PC_2(WB_PC),
    .ctrlSignal_2({WB, WB_ecall, mem_wb_1_ctrlsignal_2[4:3], RegWrite, mem_wb_1_ctrlsignal_2[1:0]}),
    .IR_2(WB_IR), .ALU_2(mem_wb_1_alu_2), .MD_2(mem_wb_1_md_2), .W_num(MEM_W_num), .W_num_2(WD_W_num),
    .en(en), .CLR(RST), .CLK(CLK));
  Multiplexer #(.select(1), .width(32), .disabled("Z"), .enable("false")) multiplexer_9 (
    .in0(mem_wb_1_alu_2), .in1(mem_wb_1_md_2), .out(multiplexer_9_out), .sel(mem_wb_1_ctrlsignal_2[3]));
  Multiplexer #(.select(2), .width(8), .disabled("Z"), .enable("false")) multiplexer_10 (
    .in0(multiplexer_9_out[7:0]), .in1(multiplexer_9_out[15:8]), .in2(multiplexer_9_out[23:16]),
    .in3(multiplexer_9_out[31:24]), .out(multiplexer_10_out), .sel(mem_wb_1_alu_2[1:0]));
  Multiplexer #(.select(1), .width(32), .disabled("Z"), .enable("false")) multiplexer_11 (
    .in0(multiplexer_9_out), .in1(bit_extender_5_out), .out(multiplexer_11_out),
    .sel(mem_wb_1_ctrlsignal_2[4]));
  assign bit_extender_5_out = {{24{multiplexer_10_out[7]}}, multiplexer_10_out};  // Bit_Extender bit_extender_5
  and and_4 (and_4_out, ~WB, WB_ecall);  // AND_Gate
  Register #(.width(32), .trigger("rising"), .Select("low")) register_1 (
    .D(R2data), .en(WB_ecall), .Q(LedData), .clk(CLK));  // open: clr
  not not_2 (en, halt);
  and and_5 (halt, ~Go, and_4_out);  // AND_Gate
  Adder #(.width(32)) adder_4 (.a(32'h4), .b(WB_PC), .out(adder_4_out));  // open: cin, cout
  or or_3 (or_3_out, mem_wb_1_ctrlsignal_2[1], mem_wb_1_ctrlsignal_2[0]);
  Multiplexer #(.select(1), .width(32), .disabled("Z"), .enable("false")) multiplexer_12 (
    .in0(multiplexer_11_out), .in1(adder_4_out), .out(RDin), .sel(or_3_out));

  // Other names for the same wires on the sheet: ID_W_num[4:0] = ID_IR[11:7]; WB_RegWrite = RegWrite;
  //   MEM_PC[31:0] = M_PC

  // Notes on the sheet:
  //   中断源
  //   时空图监测，可删除
  //   中断等待指示
  //   数码管输出
  //   ID:jal 1;jalr 1;RegWrite 1;MemToReg 1;MemWrite 1;lb 1;ALUOP 4;Beq 1;Bne 1;Blt 1;AluSrc 1;ecall 1;
  //   MEM: ... = 1;
  //   指令存储器
  //   contents of rom_1 (hex, n*v repeats v):
  //   100493 100006f 100493 200913 300993 100006f 100493 200913 300993 100006f 100493 200913 300993
  //   100006f 100493 200913 300993 29c000ef 100413 100493 1f49493 900533 2200893 73 24d493 48463 fedff06f
  //   900533 2200893 73 100493 249493 900533 2200893 73 48463 fedff06f 100493 1f49493 900533 2200893 73
  //   4034d493 900533 2200893 73 4044d493 900533 2200893 73 4044d493 900533 2200893 73 4044d493 900533
  //   2200893 73 4044d493 900533 2200893 73 4044d493 900533 2200893 73 4044d493 900533 2200893 73 4044d493
  //   900533 2200893 73 100413 1f41993 41f9d993 433 c00913 300b13 140413 f47413 800293 100313 499993
  //   89e9b3 1300533 2200893 73 406282b3 fe0294e3 140413 f00f93 1f47433 1c41413 800293 100313 49d993
  //   89e9b3 1300533 2200893 73 406282b3 fe0294e3 1c45413 406b0b33 b0463 f95ff06f 2b3 fff2c293 829293
  //   ff2e293 500533 2200893 73 fff00413 493 84a023 140413 448493 84a023 140413 448493 84a023 140413
  //   448493 84a023 140413 448493 84a023 140413 448493 84a023 140413 448493 84a023 140413 448493 84a023
  //   140413 448493 84a023 140413 448493 84a023 140413 448493 84a023 140413 448493 84a023 140413 448493
  //   84a023 140413 448493 84a023 140413 448493 84a023 140413 448493 84a023 140413 448493 140413 433
  //   3c00493 42983 4aa03 149a2b3 28663 134a023 1442023 ffc48493 fe9412e3 800533 2200893 73 440413 3c00493
  //   fc9416e3 a00893 73 413 140413 800533 2200893 73 240413 800533 2200893 73 340413 800533 2200893 73
  //   440413 800533 2200893 73 540413 800533 2200893 73 640413 800533 2200893 73 740413 800533 2200893 73
  //   840413 800533 2200893 2200893 73 8067
  //   I jalr
  //   sw
  //   控制位
  //   B
  //   jal
  //   流水调试日志用
  //   暂停节拍，不能为0
  //   戳工具置1进入计数暂停模式，ctrl+k时钟自动运行到对应节拍暂停
  //   ctrl+k关闭时钟连续运行，将控制位置零，进入单步调试模式调试
  //   用这个时钟源需要去掉电路中的其他时钟源
  //   可计数暂停的时钟源
  //   为方便自动评测，需要输出流水线各段保存的PC值，注意是PC不是PC+4，另外ID段寄存器写入信息，Mem段内存写入信息也要输出
  //   数据存储器
endmodule

module \气泡流水线  (
  output RegWrite,
  output MemWrite,
  output [31:0] IF_PC,
  output [31:0] ID_PC,
  output [31:0] EX_PC,
  output [31:0] M_PC,
  output [31:0] WB_PC,
  output [31:0] RDin,
  output [31:0] MDin,
  output [31:0] LedData
);

  wire alu_1_out_6, and_1_out, and_2_out, and_3_out, and_4_out, and_5_out, and_6_out, and_7_out, and_8_out,
       and_9_out, branch, CLK, clock_1_out, comparator_1_eq, comparator_1_lt, comparator_2_eq, d_ff_1_q,
       DataHazzard, en, EX, EX_B, EX_ecall, EX_jal, EX_jalr, Go, halt, ID_ecall, IR1, IR2, IR3,
       multiplexer_8_out, multiplexer_10_out, multiplexer_11_out, nand_1_out, or_2_out, or_3_out, or_4_out,
       or_7_out, or_8_out, RST, W1, W2, W3, WB, WB_ecall, \单周期硬布线控制器_1_s_type ;
  wire [0:0] or_1_out;
  wire [4:0] EX_W_num, MEM_W_num, mem_wb_1_ctrlsignal_2, multiplexer_2_out, multiplexer_3_out, WD_W_num;
  wire [7:0] ex_mem_1_ctrlsignal_2, multiplexer_13_out;
  wire [11:0] \id_ex_理想_气泡_1_badd_2 , shifter_1_out;
  wire [12:0] CNT_num;
  wire [13:0] \单周期硬布线控制器_1_jal ;
  wire [13:2] \id_ex_理想_气泡_1_ctrlsignal_2 ;
  wire [14:0] multiplexer_6_out;
  wire [15:0] \LoadUse次数 , \总周期数 , \插入气泡数 , \无条件分支数 , \条件分支成功数 ;
  wire [19:0] \id_ex_理想_气泡_1_j_2 , shifter_2_out;
  wire [31:0] adder_1_out, adder_2_out, adder_3_out, adder_4_out, bit_extender_1_out, bit_extender_2_out,
       bit_extender_3_out, bit_extender_4_out, bit_extender_5_out, EX_ALU_res, EX_IR, ex_mem_1_alu_2,
       \id_ex_理想_气泡_1_a_2 , \id_ex_理想_气泡_1_imm_2 , ID_IR, IF_IR, MEM_IR, mem_wb_1_alu_2, mem_wb_1_md_2,
       multiplexer_1_out, multiplexer_4_out, multiplexer_5_out, multiplexer_7_out, multiplexer_9_out,
       multiplexer_12_out, multiplexer_14_out, R2data, ram_1_data, regifile_1_r1, regifile_1_r2, WB_IR;

  Button \u_总复位  (.out(RST));
  Button _1 (.out(IR1));
  Button _2 (.out(IR2));
  Button _3 (.out(IR3));
  // Probe on \总周期数 
  // Probe on \总周期数 
  Button \u_继续运行  (.out(Go));
  LED #(.active("true")) led_1 (.in(W1));
  LED #(.active("true")) led_2 (.in(W2));
  LED #(.active("true")) led_3 (.in(W3));
  Hex_Digit_Display hex_digit_display_1 (.value(LedData[31:28]));  // open: dp
  // Probe on IF_PC[19:0]
  // RiscV_Probe riscv_probe_1: pin names not known; wires that end beside it: IF_IR
  or or_1 (or_1_out[0], EX_jal, EX_B);
  Hex_Digit_Display hex_digit_display_2 (.value(LedData[27:24]));  // open: dp
  Hex_Digit_Display hex_digit_display_3 (.value(LedData[23:20]));  // open: dp
  // Probe on ID_PC[19:0]
  // RiscV_Probe riscv_probe_2: pin names not known; wires that end beside it: ID_IR
  and and_1 (and_1_out, ~DataHazzard, en);  // AND_Gate
  Multiplexer #(.select(2), .width(32), .disabled("Z"), .enable("false")) multiplexer_1 (
    .in0(adder_1_out), .in1(multiplexer_9_out), .in2(EX_ALU_res), .out(multiplexer_1_out),
    .sel({EX_jalr, or_1_out[0]}));  // open: in3
  Hex_Digit_Display hex_digit_display_4 (.value(LedData[19:16]));  // open: dp
  Hex_Digit_Display hex_digit_display_5 (.value(LedData[15:12]));  // open: dp
  Register #(.width(32), .trigger("rising"), .Select("low")) PC (
    .D(multiplexer_1_out), .en(and_1_out), .Q(IF_PC), .clk(CLK), .clr(RST));
  Hex_Digit_Display hex_digit_display_6 (.value(LedData[11:8]));  // open: dp
  Hex_Digit_Display hex_digit_display_7 (.value(LedData[7:4]));  // open: dp
  // Probe on EX_PC[19:0]
  // RiscV_Probe riscv_probe_3: pin names not known; wires that end beside it: EX_IR
  Adder #(.width(32)) adder_1 (.a(IF_PC), .b(32'h4), .out(adder_1_out));  // open: cin, cout
  Hex_Digit_Display hex_digit_display_8 (.value(LedData[3:0]));  // open: dp
  // Probe on \总周期数 
  // Probe on M_PC[19:0]
  // RiscV_Probe riscv_probe_4: pin names not known; wires that end beside it: MEM_IR
  or or_2 (or_2_out, RST, branch);
  ROM #(.addrWidth(10), .dataWidth(32), .Select("high")) rom_1 (.addr(IF_PC[11:2]), .data(IF_IR));
  IF_ID if_id_1 (.PC_2(ID_PC), .IR_2(ID_IR), .PC(IF_PC), .IR(IF_IR), .CLK(CLK), .CLR(or_2_out), .en(and_2_out));
  and and_2 (and_2_out, ~DataHazzard, en);  // AND_Gate
  // Probe on \总周期数 
  // Probe on \无条件分支数 
  // Probe on \条件分支成功数 
  // Probe on \插入气泡数 
  // Probe on \LoadUse次数 
  // Probe on IF_PC[11:0]
  // Probe on WB_PC[19:0]
  // RiscV_Probe riscv_probe_5: pin names not known; wires that end beside it: WB_IR
  // Probe on ID_PC[11:0]
  // Probe on EX_PC[11:0]
  \单周期硬布线控制器  \u_单周期硬布线控制器_1  (
    .Funct({ID_IR[30], ID_IR[25], ID_IR[14:12]}), .OP(ID_IR[6:2]), .ALU_OP(\单周期硬布线控制器_1_jal [9:6]),
    .MemToReg(\单周期硬布线控制器_1_jal [3]), .MemWrite(\单周期硬布线控制器_1_jal [4]), .ALU_SRC(\单周期硬布线控制器_1_jal [13]),
    .RegWrite(\单周期硬布线控制器_1_jal [2]), .ecall(ID_ecall), .S_type(\单周期硬布线控制器_1_s_type ),
    .Jalr(\单周期硬布线控制器_1_jal [1]), .Beq(\单周期硬布线控制器_1_jal [10]), .JAL(\单周期硬布线控制器_1_jal [0]),
    .Bne(\单周期硬布线控制器_1_jal [11]), .in_3(ID_IR[21]), .lb(\单周期硬布线控制器_1_jal [5]), .blt(\单周期硬布线控制器_1_jal [12]));  // open: uret, CSRRSI, CSRRCI
  Multiplexer #(.select(1), .width(5), .disabled("Z"), .enable("false")) multiplexer_2 (
    .in0(ID_IR[19:15]), .in1(5'b10001), .out(multiplexer_2_out), .sel(ID_ecall));
  Multiplexer #(.select(1), .width(5), .disabled("Z"), .enable("false")) multiplexer_3 (
    .in0(ID_IR[24:20]), .in1(5'b01010), .out(multiplexer_3_out), .sel(ID_ecall));
  assign bit_extender_1_out = {{20{ID_IR[31]}}, ID_IR[31:20]};  // Bit_Extender bit_extender_1
  assign bit_extender_2_out = {{20{ID_IR[31]}}, {ID_IR[31:25], ID_IR[11:7]}};  // Bit_Extender bit_extender_2
  // Probe on M_PC[11:0]
  D_Flip_Flop #(.trigger("high"), .Pre_Clr_Positions("LEGACY"), .NegatePresetClear("false"), .enable("true"), .NewFFLayout("false")) d_ff_1 (.Q(d_ff_1_q));  // open: clk, D, Qn, preset, en, reset
  // Probe on 13'h9
  Multiplexer #(.select(1), .width(32), .disabled("Z"), .enable("false")) multiplexer_4 (
    .in0(bit_extender_1_out), .in1(bit_extender_2_out), .out(multiplexer_4_out), .sel(\单周期硬布线控制器_1_s_type ));
  // Probe on WB_PC[11:0]
  Comparator #(.width(13), .mode("twosComplement")) comparator_1 (
    .a(CNT_num), .b(13'h9), .eq(comparator_1_eq), .lt(comparator_1_lt));  // open: gt
  Clock #(.highDuration(1), .lowDuration(1)) clock_1 (.out(clock_1_out));
  Multiplexer #(.select(1), .width(32), .disabled("Z"), .enable("false")) multiplexer_5 (
    .in0(multiplexer_4_out), .in1(32'h22), .out(multiplexer_5_out), .sel(ID_ecall));
  nand nand_1 (nand_1_out, d_ff_1_q, comparator_1_eq);
  Counter #(.width(13), .max('h1fff), .ongoal("stay"), .trigger("rising"), .behavior("old")) counter_1 (
    .count(comparator_1_lt), .Q(CNT_num), .clk(clock_1_out));  // open: load, D, carry, clr, preset
  Regifile regifile_1 (
    .Din(RDin), .Clk(CLK), .R1(regifile_1_r1), .R2(regifile_1_r2), .WE(RegWrite), .W_num(WD_W_num),
    .R1_num(multiplexer_2_out), .R2_num(multiplexer_3_out));
  assign CLK = nand_1_out ? clock_1_out : 1'bz;  // Controlled_Buffer controlled_buffer_1
  \数据相关检测逻辑  \u_数据相关检测逻辑_1  (
    .op_code(ID_IR[6:2]), .Funct({ID_IR[30], ID_IR[25], ID_IR[14:12]}), .R1_num(multiplexer_2_out),
    .R2_num(multiplexer_3_out), .EX_RegWrite(\id_ex_理想_气泡_1_ctrlsignal_2 [2]),
    .MEM_RegWrite(ex_mem_1_ctrlsignal_2[2]), .EX_WriteReg_num(EX_W_num), .MEM_WriteReg_num(MEM_W_num),
    .DataHazzard(DataHazzard));
  Comparator #(.width(32), .mode("twosComplement")) comparator_2 (
    .a(ID_IR), .b({32{1'b0}}), .eq(comparator_2_eq));  // open: gt, lt
  Multiplexer #(.select(1), .width(15), .disabled("Z"), .enable("false")) multiplexer_6 (
    .in0({ID_ecall, \单周期硬布线控制器_1_jal }), .in1({15{1'b0}}), .out(multiplexer_6_out), .sel(comparator_2_eq));
  Pull_Resistor #(.pull(1)) pull_resistor_1 (.node(CLK));
  or or_3 (or_3_out, RST, DataHazzard, branch);
  \ID_EX_理想_气泡  \id_ex_理想_气泡_1  (
    .CLK(CLK), .CLR(or_3_out), .en(en), .PC(ID_PC), .imm(multiplexer_5_out), .IR(ID_IR),
    .ctrlSignal(multiplexer_6_out), .A(regifile_1_r1), .W_num(ID_IR[11:7]), .B(regifile_1_r2),
    .Badd({ID_IR[31], ID_IR[7], ID_IR[30:25], ID_IR[11:8]}),
    .J({ID_IR[31], ID_IR[19:12], ID_IR[20], ID_IR[30:21]}), .PC_2(EX_PC), .imm_2(\id_ex_理想_气泡_1_imm_2 ),
    .IR_2(EX_IR), .ctrlSignal_2({EX_ecall, \id_ex_理想_气泡_1_ctrlsignal_2 , EX_jalr, EX_jal}),
    .A_2(\id_ex_理想_气泡_1_a_2 ), .W_num_2(EX_W_num), .B_2(R2data), .Badd_2(\id_ex_理想_气泡_1_badd_2 ),
    .J_2(\id_ex_理想_气泡_1_j_2 ));
  Counter #(.width(16), .max('hffff), .ongoal("stay"), .trigger("rising"), .behavior("new")) counter_2 (
    .count(en), .Q(\总周期数 ), .clk(CLK));  // open: load, D, carry, clr, preset, down
  Multiplexer #(.select(1), .width(32), .disabled("Z"), .enable("false")) multiplexer_7 (
    .in0(R2data), .in1(\id_ex_理想_气泡_1_imm_2 ), .out(multiplexer_7_out), .sel(\id_ex_理想_气泡_1_ctrlsignal_2 [13]));
  Shifter #(.width(12), .shift("ll")) shifter_1 (.in(\id_ex_理想_气泡_1_badd_2 ), .\dist (4'b0001), .out(shifter_1_out));
  assign bit_extender_3_out = {{20{shifter_1_out[11]}}, shifter_1_out};  // Bit_Extender bit_extender_3
  Shifter #(.width(20), .shift("ll")) shifter_2 (.in(\id_ex_理想_气泡_1_j_2 ), .\dist (5'b00001), .out(shifter_2_out));
  assign bit_extender_4_out = {{12{shifter_2_out[19]}}, shifter_2_out};  // Bit_Extender bit_extender_4
  Counter #(.width(16), .max('hffff), .ongoal("stay"), .trigger("rising"), .behavior("new")) counter_3 (
    .count(en), .Q(\无条件分支数 ), .clk(multiplexer_8_out));  // open: load, D, carry, clr, preset, down
  Multiplexer #(.select(1), .width(1), .disabled("Z"), .enable("false")) multiplexer_8 (
    .in0(and_3_out), .in1(1'b0), .out(multiplexer_8_out), .sel(CLK));
  and and_3 (and_3_out, or_4_out, CLK);
  or or_4 (or_4_out, EX_jal, EX_jalr);
  and and_4 (and_4_out, \id_ex_理想_气泡_1_ctrlsignal_2 [11], ~EX);  // AND_Gate
  and and_5 (and_5_out, \id_ex_理想_气泡_1_ctrlsignal_2 [10], EX);
  ALU alu_1 (
    .X(\id_ex_理想_气泡_1_a_2 ), .Y(multiplexer_7_out), .AluOP(\id_ex_理想_气泡_1_ctrlsignal_2 [9:6]), .Equal(EX),
    .Result(EX_ALU_res), .out_6(alu_1_out_6));  // open: Result_2, out_4
  and and_6 (and_6_out, \id_ex_理想_气泡_1_ctrlsignal_2 [12], alu_1_out_6);
  Adder #(.width(32)) adder_2 (.a(bit_extender_3_out), .b(EX_PC), .out(adder_2_out));  // open: cin, cout
  Adder #(.width(32)) adder_3 (.a(bit_extender_4_out), .b(EX_PC), .out(adder_3_out));  // open: cin, cout
  or or_5 (branch, EX_B, EX_jal, EX_jalr);
  or or_6 (EX_B, and_6_out, and_4_out, and_5_out);
  Multiplexer #(.select(1), .width(32), .disabled("Z"), .enable("false")) multiplexer_9 (
    .in0(adder_2_out), .in1(adder_3_out), .out(multiplexer_9_out), .sel(EX_jal));
  Counter #(.width(16), .max('hffff), .ongoal("stay"), .trigger("rising"), .behavior("new")) counter_4 (
    .count(en), .Q(\条件分支成功数 ), .clk(multiplexer_10_out));  // open: load, D, carry, clr, preset, down
  Multiplexer #(.select(1), .width(1), .disabled("Z"), .enable("false")) multiplexer_10 (
    .in0(and_7_out), .in1(1'b0), .out(multiplexer_10_out), .sel(CLK));
  and and_7 (and_7_out, EX_B, CLK);
  and and_8 (and_8_out, or_7_out, CLK);
  or or_7 (or_7_out, DataHazzard, branch);
  EX_MEM ex_mem_1 (
    .PC_2(M_PC), .ctrlSignal_2({ex_mem_1_ctrlsignal_2[7:5], MemWrite, ex_mem_1_ctrlsignal_2[3:0]}),
    .IR_2(MEM_IR), .B_2(MDin), .ALU_2(ex_mem_1_alu_2), .PC(EX_PC),
    .ctrlSignal({EX, EX_ecall, \id_ex_理想_气泡_1_ctrlsignal_2 [5:2], EX_jalr, EX_jal}), .IR(EX_IR), .B(R2data),
    .ALU(EX_ALU_res), .W_num_2(MEM_W_num), .W_num(EX_W_num), .CLK(CLK), .CLR(RST), .en(en));
  Counter #(.width(16), .max('hffff), .ongoal("stay"), .trigger("rising"), .behavior("new")) counter_5 (
    .count(en), .Q(\插入气泡数 ), .clk(multiplexer_11_out));  // open: load, D, carry, clr, preset, down
  Multiplexer #(.select(1), .width(1), .disabled("Z"), .enable("false")) multiplexer_11 (
    .in0(and_8_out), .in1(1'b0), .out(multiplexer_11_out), .sel(CLK));
  RAM #(.addrWidth(10), .dataWidth(32), .bus("separate"), .Select("high")) ram_1 (
    .addr(ex_mem_1_alu_2[11:2]), .din(MDin), .data(ram_1_data), .str(MemWrite), .clk(CLK));  // open: sel, ld, clr
  MEM_WB mem_wb_1 (
    .PC(M_PC), .ctrlSignal({ex_mem_1_ctrlsignal_2[7:5], ex_mem_1_ctrlsignal_2[3:0]}), .IR(MEM_IR),
    .ALU(ex_mem_1_alu_2), .MD(ram_1_data), .PC_2(WB_PC),
    .ctrlSignal_2({WB, WB_ecall, mem_wb_1_ctrlsignal_2[4:3], RegWrite, mem_wb_1_ctrlsignal_2[1:0]}),
    .IR_2(WB_IR), .ALU_2(mem_wb_1_alu_2), .MD_2(mem_wb_1_md_2), .W_num(MEM_W_num), .W_num_2(WD_W_num),
    .en(en), .CLR(RST), .CLK(CLK));
  Multiplexer #(.select(1), .width(32), .disabled("Z"), .enable("false")) multiplexer_12 (
    .in0(mem_wb_1_alu_2), .in1(mem_wb_1_md_2), .out(multiplexer_12_out), .sel(mem_wb_1_ctrlsignal_2[3]));
  Multiplexer #(.select(2), .width(8), .disabled("Z"), .enable("false")) multiplexer_13 (
    .in0(multiplexer_12_out[7:0]), .in1(multiplexer_12_out[15:8]), .in2(multiplexer_12_out[23:16]),
    .in3(multiplexer_12_out[31:24]), .out(multiplexer_13_out), .sel(mem_wb_1_alu_2[1:0]));
  Multiplexer #(.select(1), .width(32), .disabled("Z"), .enable("false")) multiplexer_14 (
    .in0(multiplexer_12_out), .in1(bit_extender_5_out), .out(multiplexer_14_out),
    .sel(mem_wb_1_ctrlsignal_2[4]));
  assign bit_extender_5_out = {{24{multiplexer_13_out[7]}}, multiplexer_13_out};  // Bit_Extender bit_extender_5
  and and_9 (and_9_out, ~WB, WB_ecall);  // AND_Gate
  Register #(.width(32), .trigger("rising"), .Select("low")) register_1 (
    .D(R2data), .en(EX_ecall), .Q(LedData), .clk(CLK));  // open: clr
  not not_1 (en, halt);
  and and_10 (halt, ~Go, and_9_out);  // AND_Gate
  Adder #(.width(32)) adder_4 (.a(32'h4), .b(WB_PC), .out(adder_4_out));  // open: cin, cout
  or or_8 (or_8_out, mem_wb_1_ctrlsignal_2[1], mem_wb_1_ctrlsignal_2[0]);
  Multiplexer #(.select(1), .width(32), .disabled("Z"), .enable("false")) multiplexer_15 (
    .in0(multiplexer_14_out), .in1(adder_4_out), .out(RDin), .sel(or_8_out));

  // Other names for the same wires on the sheet: ID_W_num[4:0] = ID_IR[11:7]; WB_RegWrite = RegWrite;
  //   MEM_PC[31:0] = M_PC

  // Notes on the sheet:
  //   中断源
  //   时空图监测，可删除
  //   中断等待指示
  //   数码管输出
  //   ID:jal 1;jalr 1;RegWrite 1;MemToReg 1;MemWrite 1;lb 1;ALUOP 4;Beq 1;Bne 1;Blt 1;AluSrc 1;ecall 1;
  //   MEM: ... = 1;
  //   指令存储器
  //   contents of rom_1 (hex, n*v repeats v):
  //   100493 100006f 100493 200913 300993 100006f 100493 200913 300993 100006f 100493 200913 300993
  //   100006f 100493 200913 300993 29c000ef 100413 100493 1f49493 900533 2200893 73 24d493 48463 fedff06f
  //   900533 2200893 73 100493 249493 900533 2200893 73 48463 fedff06f 100493 1f49493 900533 2200893 73
  //   4034d493 900533 2200893 73 4044d493 900533 2200893 73 4044d493 900533 2200893 73 4044d493 900533
  //   2200893 73 4044d493 900533 2200893 73 4044d493 900533 2200893 73 4044d493 900533 2200893 73 4044d493
  //   900533 2200893 73 100413 1f41993 41f9d993 433 c00913 300b13 140413 f47413 800293 100313 499993
  //   89e9b3 1300533 2200893 73 406282b3 fe0294e3 140413 f00f93 1f47433 1c41413 800293 100313 49d993
  //   89e9b3 1300533 2200893 73 406282b3 fe0294e3 1c45413 406b0b33 b0463 f95ff06f 2b3 fff2c293 829293
  //   ff2e293 500533 2200893 73 fff00413 493 84a023 140413 448493 84a023 140413 448493 84a023 140413
  //   448493 84a023 140413 448493 84a023 140413 448493 84a023 140413 448493 84a023 140413 448493 84a023
  //   140413 448493 84a023 140413 448493 84a023 140413 448493 84a023 140413 448493 84a023 140413 448493
  //   84a023 140413 448493 84a023 140413 448493 84a023 140413 448493 84a023 140413 448493 140413 433
  //   3c00493 42983 4aa03 149a2b3 28663 134a023 1442023 ffc48493 fe9412e3 800533 2200893 73 440413 3c00493
  //   fc9416e3 a00893 73 413 140413 800533 2200893 73 240413 800533 2200893 73 340413 800533 2200893 73
  //   440413 800533 2200893 73 540413 800533 2200893 73 640413 800533 2200893 73 740413 800533 2200893 73
  //   840413 800533 2200893 2200893 73 8067
  //   I jalr
  //   sw
  //   控制位
  //   B
  //   jal
  //   流水调试日志用
  //   暂停节拍，不能为0
  //   戳工具置1进入计数暂停模式，ctrl+k时钟自动运行到对应节拍暂停
  //   ctrl+k关闭时钟连续运行，将控制位置零，进入单步调试模式调试
  //   可计数暂停的时钟源
  //   为方便自动评测，需要输出流水线各段保存的PC值，注意是PC不是PC+4，另外ID段寄存器写入信息，Mem段内存写入信息也要输出
  //   数据存储器
endmodule

module \重定向流水线  (
  output RegWrite,
  output MemWrite,
  output [31:0] IF_PC,
  output [31:0] ID_PC,
  output [31:0] EX_PC,
  output [31:0] M_PC,
  output [31:0] WB_PC,
  output [31:0] RDin,
  output [31:0] MDin,
  output [31:0] LedData
);

  wire alu_1_out_6, and_1_out, and_2_out, and_3_out, and_4_out, and_5_out, and_6_out, and_7_out, and_8_out,
       and_9_out, and_10_out, branch, CLK, clock_1_out, comparator_1_eq, comparator_1_lt, comparator_2_eq,
       d_ff_1_q, en, EX, EX_B, EX_ecall, EX_jal, EX_jalr, Go, halt, ID_ecall, IR1, IR2, IR3, LoadUse,
       MEM_RegWrite, multiplexer_10_out, multiplexer_12_out, multiplexer_13_out, multiplexer_14_out,
       nand_1_out, or_2_out, or_3_out, or_4_out, or_7_out, or_8_out, RST, W1, W2, W3, WB, WB_ecall,
       \单周期硬布线控制器_1_s_type ;
  wire [0:0] or_1_out;
  wire [4:0] EX_W_num, MEM_W_num, mem_wb_1_ctrlsignal_2, multiplexer_2_out, multiplexer_3_out, WD_W_num;
  wire [4:1] pckSignal;
  wire [7:0] ex_mem_1_ctrlsignal_2, multiplexer_16_out;
  wire [11:0] \id_ex_重定向_1_badd_2 , shifter_1_out;
  wire [12:0] CNT_num;
  wire [13:0] \单周期硬布线控制器_1_jal ;
  wire [15:0] \LoadUse次数 , \总周期数 , \插入气泡数 , \无条件分支数 , \条件分支成功数 ;
  wire [18:0] multiplexer_6_out;
  wire [18:2] \id_ex_重定向_1_ctrlsignal_2 ;
  wire [19:0] \id_ex_重定向_1_j_2 , shifter_2_out;
  wire [31:0] A1, A2, adder_1_out, adder_2_out, adder_3_out, adder_4_out, B1, B2, bit_extender_1_out,
       bit_extender_2_out, bit_extender_3_out, bit_extender_4_out, bit_extender_5_out, EX_ALU_res, EX_IR,
       \id_ex_重定向_1_imm_2 , ID_IR, IF_IR, MEM_alu_res, MEM_IR, mem_wb_1_alu_2, mem_wb_1_md_2,
       multiplexer_1_out, multiplexer_4_out, multiplexer_5_out, multiplexer_7_out, multiplexer_11_out,
       multiplexer_15_out, multiplexer_17_out, ram_1_data, regifile_1_r1, regifile_1_r2, WB_IR;

  Button \u_总复位  (.out(RST));
  Button _1 (.out(IR1));
  Button _2 (.out(IR2));
  Button _3 (.out(IR3));
  // Probe on \总周期数 
  // Probe on \总周期数 
  Button \u_继续运行  (.out(Go));
  LED #(.active("true")) led_1 (.in(W1));
  LED #(.active("true")) led_2 (.in(W2));
  LED #(.active("true")) led_3 (.in(W3));
  Hex_Digit_Display hex_digit_display_1 (.value(LedData[31:28]));  // open: dp
  // Probe on IF_PC[19:0]
  // RiscV_Probe riscv_probe_1: pin names not known; wires that end beside it: IF_IR
  or or_1 (or_1_out[0], EX_jal, EX_B);
  Hex_Digit_Display hex_digit_display_2 (.value(LedData[23:20]));  // open: dp
  Hex_Digit_Display hex_digit_display_3 (.value(LedData[27:24]));  // open: dp
  // Probe on ID_PC[19:0]
  // RiscV_Probe riscv_probe_2: pin names not known; wires that end beside it: ID_IR
  and and_1 (and_1_out, ~LoadUse, en);  // AND_Gate
  Multiplexer #(.select(2), .width(32), .disabled("Z"), .enable("false")) multiplexer_1 (
    .in0(adder_1_out), .in1(multiplexer_11_out), .in2(EX_ALU_res), .out(multiplexer_1_out),
    .sel({EX_jalr, or_1_out[0]}));  // open: in3
  Hex_Digit_Display hex_digit_display_4 (.value(LedData[19:16]));  // open: dp
  Hex_Digit_Display hex_digit_display_5 (.value(LedData[15:12]));  // open: dp
  Register #(.width(32), .trigger("rising"), .Select("low")) PC (
    .D(multiplexer_1_out), .en(and_1_out), .Q(IF_PC), .clk(CLK), .clr(RST));
  Hex_Digit_Display hex_digit_display_6 (.value(LedData[11:8]));  // open: dp
  Hex_Digit_Display hex_digit_display_7 (.value(LedData[7:4]));  // open: dp
  // Probe on EX_PC[19:0]
  // RiscV_Probe riscv_probe_3: pin names not known; wires that end beside it: EX_IR
  Adder #(.width(32)) adder_1 (.a(IF_PC), .b(32'h4), .out(adder_1_out));  // open: cin, cout
  Hex_Digit_Display hex_digit_display_8 (.value(LedData[3:0]));  // open: dp
  // Probe on \总周期数 
  // Probe on M_PC[19:0]
  // RiscV_Probe riscv_probe_4: pin names not known; wires that end beside it: MEM_IR
  or or_2 (or_2_out, RST, branch);
  ROM #(.addrWidth(10), .dataWidth(32), .Select("high")) rom_1 (.addr(IF_PC[11:2]), .data(IF_IR));
  IF_ID if_id_1 (.PC_2(ID_PC), .IR_2(ID_IR), .PC(IF_PC), .IR(IF_IR), .CLK(CLK), .CLR(or_2_out), .en(and_2_out));
  and and_2 (and_2_out, ~LoadUse, en);  // AND_Gate
  // Probe on \总周期数 
  // Probe on \无条件分支数 
  // Probe on \条件分支成功数 
  // Probe on \插入气泡数 
  // Probe on \LoadUse次数 
  // Probe on IF_PC[11:0]
  // Probe on WB_PC[19:0]
  // RiscV_Probe riscv_probe_5: pin names not known; wires that end beside it: WB_IR
  // Probe on ID_PC[11:0]
  // Probe on EX_PC[11:0]
  \单周期硬布线控制器  \u_单周期硬布线控制器_1  (
    .Funct({ID_IR[30], ID_IR[25], ID_IR[14:12]}), .OP(ID_IR[6:2]), .ALU_OP(\单周期硬布线控制器_1_jal [9:6]),
    .MemToReg(\单周期硬布线控制器_1_jal [3]), .MemWrite(\单周期硬布线控制器_1_jal [4]), .ALU_SRC(\单周期硬布线控制器_1_jal [13]),
    .RegWrite(\单周期硬布线控制器_1_jal [2]), .ecall(ID_ecall), .S_type(\单周期硬布线控制器_1_s_type ),
    .Jalr(\单周期硬布线控制器_1_jal [1]), .Beq(\单周期硬布线控制器_1_jal [10]), .JAL(\单周期硬布线控制器_1_jal [0]),
    .Bne(\单周期硬布线控制器_1_jal [11]), .in_3(ID_IR[21]), .lb(\单周期硬布线控制器_1_jal [5]), .blt(\单周期硬布线控制器_1_jal [12]));  // open: uret, CSRRSI, CSRRCI
  Multiplexer #(.select(1), .width(5), .disabled("Z"), .enable("false")) multiplexer_2 (
    .in0(ID_IR[19:15]), .in1(5'b10001), .out(multiplexer_2_out), .sel(ID_ecall));
  Multiplexer #(.select(1), .width(5), .disabled("Z"), .enable("false")) multiplexer_3 (
    .in0(ID_IR[24:20]), .in1(5'b01010), .out(multiplexer_3_out), .sel(ID_ecall));
  assign bit_extender_1_out = {{20{ID_IR[31]}}, ID_IR[31:20]};  // Bit_Extender bit_extender_1
  assign bit_extender_2_out = {{20{ID_IR[31]}}, {ID_IR[31:25], ID_IR[11:7]}};  // Bit_Extender bit_extender_2
  // Probe on M_PC[11:0]
  D_Flip_Flop #(.trigger("high"), .Pre_Clr_Positions("LEGACY"), .NegatePresetClear("false"), .enable("true"), .NewFFLayout("false")) d_ff_1 (.Q(d_ff_1_q));  // open: clk, D, Qn, preset, en, reset
  // Probe on 13'h19b
  Multiplexer #(.select(1), .width(32), .disabled("Z"), .enable("false")) multiplexer_4 (
    .in0(bit_extender_1_out), .in1(bit_extender_2_out), .out(multiplexer_4_out), .sel(\单周期硬布线控制器_1_s_type ));
  // Probe on WB_PC[11:0]
  Comparator #(.width(13), .mode("twosComplement")) comparator_1 (
    .a(CNT_num), .b(13'h19b), .eq(comparator_1_eq), .lt(comparator_1_lt));  // open: gt
  Clock #(.highDuration(1), .lowDuration(1)) clock_1 (.out(clock_1_out));
  Multiplexer #(.select(1), .width(32), .disabled("Z"), .enable("false")) multiplexer_5 (
    .in0(multiplexer_4_out), .in1(32'h22), .out(multiplexer_5_out), .sel(ID_ecall));
  nand nand_1 (nand_1_out, d_ff_1_q, comparator_1_eq);
  Counter #(.width(13), .max('h1fff), .ongoal("stay"), .trigger("rising"), .behavior("old")) counter_1 (
    .count(comparator_1_lt), .Q(CNT_num), .clk(clock_1_out));  // open: load, D, carry, clr, preset
  Regifile regifile_1 (
    .Din(RDin), .Clk(CLK), .R1(regifile_1_r1), .R2(regifile_1_r2), .WE(RegWrite), .W_num(WD_W_num),
    .R1_num(multiplexer_2_out), .R2_num(multiplexer_3_out));
  assign CLK = nand_1_out ? clock_1_out : 1'bz;  // Controlled_Buffer controlled_buffer_1
  \重定向相关处理逻辑  \u_重定向相关处理逻辑_1  (
    .op_code(ID_IR[6:2]), .Funct({ID_IR[30], ID_IR[25], ID_IR[14:12]}), .r1(multiplexer_2_out),
    .r2(multiplexer_3_out), .EX_MemRead(\id_ex_重定向_1_ctrlsignal_2 [3]), .EX_WriteReg_num(EX_W_num),
    .EX_RegWrite(\id_ex_重定向_1_ctrlsignal_2 [2]), .MEM_RegWrite(MEM_RegWrite), .MEM_WriteReg_num(MEM_W_num),
    .LoadUse(LoadUse), .r1Forward(pckSignal[2:1]), .r2Forward(pckSignal[4:3]));
  Comparator #(.width(32), .mode("twosComplement")) comparator_2 (
    .a(ID_IR), .b({32{1'b0}}), .eq(comparator_2_eq));  // open: gt, lt
  Multiplexer #(.select(1), .width(19), .disabled("Z"), .enable("false")) multiplexer_6 (
    .in0({pckSignal, ID_ecall, \单周期硬布线控制器_1_jal }), .in1({19{1'b0}}), .out(multiplexer_6_out),
    .sel(comparator_2_eq));
  Pull_Resistor #(.pull(1)) pull_resistor_1 (.node(CLK));
  or or_3 (or_3_out, RST, LoadUse, branch);
  \ID_EX_重定向  \id_ex_重定向_1  (
    .PC_2(EX_PC), .imm_2(\id_ex_重定向_1_imm_2 ), .IR_2(EX_IR),
    .ctrlSignal_2({\id_ex_重定向_1_ctrlsignal_2 [18:15], EX_ecall, \id_ex_重定向_1_ctrlsignal_2 [13:2], EX_jalr, EX_jal}),
    .A_2(A1), .B_2(B1), .PC(ID_PC), .imm(multiplexer_5_out), .IR(ID_IR), .ctrlSignal(multiplexer_6_out),
    .A(regifile_1_r1), .B(regifile_1_r2), .W_num_2(EX_W_num), .W_num(ID_IR[11:7]),
    .Badd_2(\id_ex_重定向_1_badd_2 ), .Badd({ID_IR[31], ID_IR[7], ID_IR[30:25], ID_IR[11:8]}),
    .J_2(\id_ex_重定向_1_j_2 ), .J({ID_IR[31], ID_IR[19:12], ID_IR[20], ID_IR[30:21]}), .CLK(CLK),
    .CLR(or_3_out), .en(en));
  Counter #(.width(16), .max('hffff), .ongoal("stay"), .trigger("rising"), .behavior("new")) counter_2 (
    .count(en), .Q(\总周期数 ), .clk(CLK));  // open: load, D, carry, clr, preset, down
  Multiplexer #(.select(1), .width(32), .disabled("Z"), .enable("false")) multiplexer_7 (
    .in0(B2), .in1(\id_ex_重定向_1_imm_2 ), .out(multiplexer_7_out), .sel(\id_ex_重定向_1_ctrlsignal_2 [13]));
  Multiplexer #(.select(2), .width(32), .disabled("Z"), .enable("false")) multiplexer_8 (
    .in0(A1), .in1(RDin), .in2(MEM_alu_res), .out(A2), .sel(\id_ex_重定向_1_ctrlsignal_2 [16:15]));  // open: in3
  Multiplexer #(.select(2), .width(32), .disabled("Z"), .enable("false")) multiplexer_9 (
    .in0(B1), .in1(RDin), .in2(MEM_alu_res), .out(B2), .sel(\id_ex_重定向_1_ctrlsignal_2 [18:17]));  // open: in3
  Shifter #(.width(12), .shift("ll")) shifter_1 (.in(\id_ex_重定向_1_badd_2 ), .\dist (4'b0001), .out(shifter_1_out));
  assign bit_extender_3_out = {{20{shifter_1_out[11]}}, shifter_1_out};  // Bit_Extender bit_extender_3
  assign bit_extender_4_out = {{12{shifter_2_out[19]}}, shifter_2_out};  // Bit_Extender bit_extender_4
  Shifter #(.width(20), .shift("ll")) shifter_2 (.in(\id_ex_重定向_1_j_2 ), .\dist (5'b00001), .out(shifter_2_out));
  Counter #(.width(16), .max('hffff), .ongoal("stay"), .trigger("rising"), .behavior("new")) counter_3 (
    .count(en), .Q(\无条件分支数 ), .clk(multiplexer_10_out));  // open: load, D, carry, clr, preset, down
  Multiplexer #(.select(1), .width(1), .disabled("Z"), .enable("false")) multiplexer_10 (
    .in0(and_3_out), .in1(1'b0), .out(multiplexer_10_out), .sel(CLK));
  and and_3 (and_3_out, or_4_out, CLK);
  or or_4 (or_4_out, EX_jal, EX_jalr);
  and and_4 (and_4_out, \id_ex_重定向_1_ctrlsignal_2 [11], ~EX);  // AND_Gate
  and and_5 (and_5_out, \id_ex_重定向_1_ctrlsignal_2 [10], EX);
  ALU alu_1 (
    .X(A2), .Y(multiplexer_7_out), .AluOP(\id_ex_重定向_1_ctrlsignal_2 [9:6]), .Equal(EX), .Result(EX_ALU_res),
    .out_6(alu_1_out_6));  // open: Result_2, out_4
  and and_6 (and_6_out, \id_ex_重定向_1_ctrlsignal_2 [12], alu_1_out_6);
  Adder #(.width(32)) adder_2 (.a(bit_extender_3_out), .b(EX_PC), .out(adder_2_out));  // open: cin, cout
  Adder #(.width(32)) adder_3 (.a(bit_extender_4_out), .b(EX_PC), .out(adder_3_out));  // open: cin, cout
  or or_5 (branch, EX_B, EX_jal, EX_jalr);
  or or_6 (EX_B, and_6_out, and_4_out, and_5_out);
  Multiplexer #(.select(1), .width(32), .disabled("Z"), .enable("false")) multiplexer_11 (
    .in0(adder_2_out), .in1(adder_3_out), .out(multiplexer_11_out), .sel(EX_jal));
  Counter #(.width(16), .max('hffff), .ongoal("stay"), .trigger("rising"), .behavior("new")) counter_4 (
    .count(en), .Q(\条件分支成功数 ), .clk(multiplexer_12_out));  // open: load, D, carry, clr, preset, down
  Multiplexer #(.select(1), .width(1), .disabled("Z"), .enable("false")) multiplexer_12 (
    .in0(and_7_out), .in1(1'b0), .out(multiplexer_12_out), .sel(CLK));
  and and_7 (and_7_out, EX_B, CLK);
  and and_8 (and_8_out, or_7_out, CLK);
  or or_7 (or_7_out, LoadUse, branch);
  EX_MEM ex_mem_1 (
    .PC_2(M_PC),
    .ctrlSignal_2({ex_mem_1_ctrlsignal_2[7:5], MemWrite, ex_mem_1_ctrlsignal_2[3], MEM_RegWrite, ex_mem_1_ctrlsignal_2[1:0]}),
    .IR_2(MEM_IR), .B_2(MDin), .ALU_2(MEM_alu_res), .PC(EX_PC),
    .ctrlSignal({EX, EX_ecall, \id_ex_重定向_1_ctrlsignal_2 [5:2], EX_jalr, EX_jal}), .IR(EX_IR), .B(B2),
    .ALU(EX_ALU_res), .W_num_2(MEM_W_num), .W_num(EX_W_num), .CLK(CLK), .CLR(RST), .en(en));
  Counter #(.width(16), .max('hffff), .ongoal("stay"), .trigger("rising"), .behavior("new")) counter_5 (
    .count(en), .Q(\插入气泡数 ), .clk(multiplexer_13_out));  // open: load, D, carry, clr, preset, down
  Multiplexer #(.select(1), .width(1), .disabled("Z"), .enable("false")) multiplexer_13 (
    .in0(and_8_out), .in1(1'b0), .out(multiplexer_13_out), .sel(CLK));
  Multiplexer #(.select(1), .width(1), .disabled("Z"), .enable("false")) multiplexer_14 (
    .in0(and_9_out), .in1(1'b0), .out(multiplexer_14_out), .sel(CLK));
  and and_9 (and_9_out, LoadUse, CLK);
  Counter #(.width(16), .max('hffff), .ongoal("stay"), .trigger("rising"), .behavior("new")) counter_6 (
    .count(en), .Q(\LoadUse次数 ), .clk(multiplexer_14_out));  // open: load, D, carry, clr, preset, down
  RAM #(.addrWidth(10), .dataWidth(32), .bus("separate"), .Select("high")) ram_1 (
    .addr(MEM_alu_res[11:2]), .din(MDin), .data(ram_1_data), .str(MemWrite), .clk(CLK));  // open: sel, ld, clr
  MEM_WB mem_wb_1 (
    .PC(M_PC),
    .ctrlSignal({ex_mem_1_ctrlsignal_2[7:5], ex_mem_1_ctrlsignal_2[3], MEM_RegWrite, ex_mem_1_ctrlsignal_2[1:0]}),
    .IR(MEM_IR), .ALU(MEM_alu_res), .MD(ram_1_data), .PC_2(WB_PC),
    .ctrlSignal_2({WB, WB_ecall, mem_wb_1_ctrlsignal_2[4:3], RegWrite, mem_wb_1_ctrlsignal_2[1:0]}),
    .IR_2(WB_IR), .ALU_2(mem_wb_1_alu_2), .MD_2(mem_wb_1_md_2), .W_num(MEM_W_num), .W_num_2(WD_W_num),
    .en(en), .CLR(RST), .CLK(CLK));
  Multiplexer #(.select(1), .width(32), .disabled("Z"), .enable("false")) multiplexer_15 (
    .in0(mem_wb_1_alu_2), .in1(mem_wb_1_md_2), .out(multiplexer_15_out), .sel(mem_wb_1_ctrlsignal_2[3]));
  Multiplexer #(.select(2), .width(8), .disabled("Z"), .enable("false")) multiplexer_16 (
    .in0(multiplexer_15_out[7:0]), .in1(multiplexer_15_out[15:8]), .in2(multiplexer_15_out[23:16]),
    .in3(multiplexer_15_out[31:24]), .out(multiplexer_16_out), .sel(mem_wb_1_alu_2[1:0]));
  Multiplexer #(.select(1), .width(32), .disabled("Z"), .enable("false")) multiplexer_17 (
    .in0(multiplexer_15_out), .in1(bit_extender_5_out), .out(multiplexer_17_out),
    .sel(mem_wb_1_ctrlsignal_2[4]));
  assign bit_extender_5_out = {{24{multiplexer_16_out[7]}}, multiplexer_16_out};  // Bit_Extender bit_extender_5
  and and_10 (and_10_out, ~WB, WB_ecall);  // AND_Gate
  Register #(.width(32), .trigger("rising"), .Select("low")) register_1 (
    .D(B2), .en(EX_ecall), .Q(LedData), .clk(CLK));  // open: clr
  not not_1 (en, halt);
  and and_11 (halt, ~Go, and_10_out);  // AND_Gate
  Adder #(.width(32)) adder_4 (.a(32'h4), .b(WB_PC), .out(adder_4_out));  // open: cin, cout
  or or_8 (or_8_out, mem_wb_1_ctrlsignal_2[1], mem_wb_1_ctrlsignal_2[0]);
  Multiplexer #(.select(1), .width(32), .disabled("Z"), .enable("false")) multiplexer_18 (
    .in0(multiplexer_17_out), .in1(adder_4_out), .out(RDin), .sel(or_8_out));

  // Other names for the same wires on the sheet: ID_W_num[4:0] = ID_IR[11:7]; pckSignal[0] = ID_ecall;
  //   WB_RegWrite = RegWrite; MEM_PC[31:0] = M_PC; R2data[31:0] = B2

  // Notes on the sheet:
  //   中断源
  //   时空图监测，可删除
  //   中断等待指示
  //   数码管输出
  //   ID:jal 1;jalr 1;RegWrite 1;MemToReg 1;MemWrite 1;lb 1;ALUOP 4;Beq 1;Bne 1;Blt 1;AluSrc 1;ecall 1;r1Forward 1;r2Forward 1;
  //   MEM: ... = 1;
  //   指令存储器
  //   contents of rom_1 (hex, n*v repeats v):
  //   100493 100006f 100493 200913 300993 100006f 100493 200913 300993 100006f 100493 200913 300993
  //   100006f 100493 200913 300993 29c000ef 100413 100493 1f49493 900533 2200893 73 24d493 48463 fedff06f
  //   900533 2200893 73 100493 249493 900533 2200893 73 48463 fedff06f 100493 1f49493 900533 2200893 73
  //   4034d493 900533 2200893 73 4044d493 900533 2200893 73 4044d493 900533 2200893 73 4044d493 900533
  //   2200893 73 4044d493 900533 2200893 73 4044d493 900533 2200893 73 4044d493 900533 2200893 73 4044d493
  //   900533 2200893 73 100413 1f41993 41f9d993 433 c00913 300b13 140413 f47413 800293 100313 499993
  //   89e9b3 1300533 2200893 73 406282b3 fe0294e3 140413 f00f93 1f47433 1c41413 800293 100313 49d993
  //   89e9b3 1300533 2200893 73 406282b3 fe0294e3 1c45413 406b0b33 b0463 f95ff06f 2b3 fff2c293 829293
  //   ff2e293 500533 2200893 73 fff00413 493 84a023 140413 448493 84a023 140413 448493 84a023 140413
  //   448493 84a023 140413 448493 84a023 140413 448493 84a023 140413 448493 84a023 140413 448493 84a023
  //   140413 448493 84a023 140413 448493 84a023 140413 448493 84a023 140413 448493 84a023 140413 448493
  //   84a023 140413 448493 84a023 140413 448493 84a023 140413 448493 84a023 140413 448493 140413 433
  //   3c00493 42983 4aa03 149a2b3 28663 134a023 1442023 ffc48493 fe9412e3 800533 2200893 73 440413 3c00493
  //   fc9416e3 a00893 73 413 140413 800533 2200893 73 240413 800533 2200893 73 340413 800533 2200893 73
  //   440413 800533 2200893 73 540413 800533 2200893 73 640413 800533 2200893 73 740413 800533 2200893 73
  //   840413 800533 2200893 2200893 73 8067 5*0 8248493 849493 8148493 891913 490913 891913 490913 932023
  //   12484b3 430313 fffe0e13 fe0e18e3 2000e13 313 30483 900533 2200893 73 130313 fffe0e13 fe0e14e3 a00893
  //   73 ff100493 900533 2200893 73 148493 fe04c8e3 a00893 73 413 140413 800533 2200893 73 240413 800533
  //   2200893 73 340413 800533 2200893 73 440413 800533 2200893 73 540413 800533 2200893 73 640413 800533
  //   2200893 73 740413 800533 2200893 73 840413 800533 2200893 2200893 73 8067
  //   I jalr
  //   sw
  //   控制位
  //   B
  //   jal
  //   流水调试日志用
  //   暂停节拍，不能为0
  //   戳工具置1进入计数暂停模式，ctrl+k时钟自动运行到对应节拍暂停
  //   ctrl+k关闭时钟连续运行，将控制位置零，进入单步调试模式调试
  //   可计数暂停的时钟源
  //   为方便自动评测，需要输出流水线各段保存的PC值，注意是PC不是PC+4，另外ID段寄存器写入信息，Mem段内存写入信息也要输出
  //   数据存储器
endmodule
module \动态预测  (
  output RegWrite,
  output MemWrite,
  output [31:0] IF_PC,
  output [31:0] ID_PC,
  output [31:0] EX_PC,
  output [31:0] M_PC,
  output [31:0] WB_PC,
  output [31:0] RDin,
  output [31:0] MDin,
  output [31:0] LedData
);

  wire alu_1_out_6, and_1_out, and_2_out, and_3_out, and_4_out, and_5_out, and_6_out, and_7_out, and_8_out,
       and_9_out, and_10_out, and_11_out, and_12_out, and_13_out, and_14_out, branch, CLK, clock_1_out,
       comparator_1_eq, comparator_1_lt, comparator_2_eq, comparator_3_eq, d_ff_1_q, en, EX, EX_B, EX_B_IR,
       EX_ecall, EX_jal, EX_jalr, EX_pre, Go, halt, ID_ecall, ID_pre, IR1, IR2, IR3, LoadUse, MEM_RegWrite,
       multiplexer_13_out, multiplexer_15_out, multiplexer_16_out, multiplexer_17_out, multiplexer_18_out,
       multiplexer_19_out, nand_1_out, or_2_out, or_3_out, or_4_out, or_5_out, or_9_out, or_10_out,
       or_11_out, or_12_out, pre, preErr, RST, W1, W2, W3, WB, WB_ecall, \单周期硬布线控制器_1_s_type ;
  wire [0:0] or_1_out;
  wire [1:0] \id_ex_预测_1_ctrlsignal_2_2 ;
  wire [4:0] EX_W_num, MEM_W_num, mem_wb_1_ctrlsignal_2, multiplexer_5_out, multiplexer_6_out, WD_W_num;
  wire [4:1] pckSignal;
  wire [7:0] ex_mem_1_ctrlsignal_2, multiplexer_21_out;
  wire [11:0] \id_ex_预测_1_badd_2 , shifter_1_out;
  wire [12:0] CNT_num;
  wire [13:0] \单周期硬布线控制器_1_jal ;
  wire [15:0] \LoadUse次数 , \总周期数 , \插入气泡数 , \无条件分支数 , \条件分支成功数 , \预测失败次数 , \预测成功次数 ;
  wire [18:0] multiplexer_9_out;
  wire [18:2] \id_ex_预测_1_ctrlsignal_2 ;
  wire [19:0] \id_ex_预测_1_j_2 , shifter_2_out;
  wire [31:0] A1, A2, adder_1_out, adder_2_out, adder_3_out, adder_4_out, adder_5_out, B1, B2,
       bit_extender_1_out, bit_extender_2_out, bit_extender_3_out, bit_extender_4_out, bit_extender_5_out,
       btb_1_jumpaddr, EX_ALU_res, EX_IR, \id_ex_预测_1_imm_2 , ID_IR, IF_IR, MEM_alu_res, MEM_IR,
       mem_wb_1_alu_2, mem_wb_1_md_2, multiplexer_1_out, multiplexer_2_out, multiplexer_4_out,
       multiplexer_7_out, multiplexer_8_out, multiplexer_10_out, multiplexer_14_out, multiplexer_20_out,
       multiplexer_22_out, preAddr, ram_1_data, regifile_1_r1, regifile_1_r2, WB_IR;

  Button \u_总复位  (.out(RST));
  Button _1 (.out(IR1));
  Button _2 (.out(IR2));
  Button _3 (.out(IR3));
  // Probe on \总周期数 
  // Probe on \总周期数 
  Button \u_继续运行  (.out(Go));
  LED #(.active("true")) led_1 (.in(W1));
  LED #(.active("true")) led_2 (.in(W2));
  LED #(.active("true")) led_3 (.in(W3));
  Adder #(.width(32)) adder_1 (.a(EX_PC), .b(32'h4), .out(adder_1_out));  // open: cin, cout
  Hex_Digit_Display hex_digit_display_1 (.value(LedData[31:28]));  // open: dp
  // Probe on IF_PC[19:0]
  // RiscV_Probe riscv_probe_1: pin names not known; wires that end beside it: IF_IR
  Multiplexer #(.select(1), .width(32), .disabled("Z"), .enable("false")) multiplexer_1 (
    .in0(preAddr), .in1(multiplexer_2_out), .out(multiplexer_1_out), .sel(preErr));
  or or_1 (or_1_out[0], EX_jal, EX_B);
  Hex_Digit_Display hex_digit_display_2 (.value(LedData[27:24]));  // open: dp
  Hex_Digit_Display hex_digit_display_3 (.value(LedData[23:20]));  // open: dp
  // Probe on ID_PC[19:0]
  // RiscV_Probe riscv_probe_2: pin names not known; wires that end beside it: ID_IR
  and and_1 (and_1_out, ~LoadUse, en);  // AND_Gate
  Multiplexer #(.select(2), .width(32), .disabled("Z"), .enable("false")) multiplexer_2 (
    .in0(adder_1_out), .in1(multiplexer_14_out), .in2(EX_ALU_res), .out(multiplexer_2_out),
    .sel({EX_jalr, or_1_out[0]}));  // open: in3
  Hex_Digit_Display hex_digit_display_4 (.value(LedData[19:16]));  // open: dp
  Hex_Digit_Display hex_digit_display_5 (.value(LedData[15:12]));  // open: dp
  Register #(.width(32), .trigger("rising"), .Select("low")) PC (
    .D(multiplexer_1_out), .en(and_1_out), .Q(IF_PC), .clk(CLK), .clr(RST));
  Multiplexer #(.select(1), .width(32), .disabled("Z"), .enable("false")) multiplexer_3 (
    .in0(adder_2_out), .in1(btb_1_jumpaddr), .out(preAddr), .sel(pre));
  or or_2 (or_2_out, EX_B_IR, EX_jal, EX_jalr);
  Multiplexer #(.select(1), .width(32), .disabled("Z"), .enable("false")) multiplexer_4 (
    .in0(multiplexer_14_out), .in1(EX_ALU_res), .out(multiplexer_4_out), .sel(EX_jalr));
  Hex_Digit_Display hex_digit_display_6 (.value(LedData[7:4]));  // open: dp
  Hex_Digit_Display hex_digit_display_7 (.value(LedData[11:8]));  // open: dp
  // Probe on EX_PC[19:0]
  // RiscV_Probe riscv_probe_3: pin names not known; wires that end beside it: EX_IR
  Adder #(.width(32)) adder_2 (.a(IF_PC), .b(32'h4), .out(adder_2_out));  // open: cin, cout
  BTB btb_1 (
    .CLK(CLK), .PC(IF_PC), .EX_branch(or_2_out), .EX_branchTaken(branch), .EX_PC(EX_PC),
    .EX_branchAddr(multiplexer_4_out), .predictJump(pre), .jumpAddr(btb_1_jumpaddr));
  Hex_Digit_Display hex_digit_display_8 (.value(LedData[3:0]));  // open: dp
  // Probe on \总周期数 
  // Probe on M_PC[19:0]
  // RiscV_Probe riscv_probe_4: pin names not known; wires that end beside it: MEM_IR
  or or_3 (or_3_out, RST, preErr);
  ROM #(.addrWidth(10), .dataWidth(32), .Select("high")) rom_1 (.addr(IF_PC[11:2]), .data(IF_IR));
  and and_2 (and_2_out, ~LoadUse, en);  // AND_Gate
  \IF_ID_预测  \if_id_预测_1  (
    .CLK(CLK), .CLR(or_3_out), .en(and_2_out), .PC(IF_PC), .IR(IF_IR), .pre(pre), .PC_2(ID_PC), .IR_2(ID_IR),
    .pre_2(ID_pre));
  // Probe on \总周期数 
  // Probe on \无条件分支数 
  // Probe on \条件分支成功数 
  // Probe on \插入气泡数 
  // Probe on \LoadUse次数 
  // Probe on IF_PC[11:0]
  // Probe on WB_PC[19:0]
  // RiscV_Probe riscv_probe_5: pin names not known; wires that end beside it: WB_IR
  // Probe on EX_PC[11:0]
  // Probe on ID_PC[11:0]
  \单周期硬布线控制器  \u_单周期硬布线控制器_1  (
    .Funct({ID_IR[30], ID_IR[25], ID_IR[14:12]}), .OP(ID_IR[6:2]), .ALU_OP(\单周期硬布线控制器_1_jal [9:6]),
    .MemToReg(\单周期硬布线控制器_1_jal [3]), .MemWrite(\单周期硬布线控制器_1_jal [4]), .ALU_SRC(\单周期硬布线控制器_1_jal [13]),
    .RegWrite(\单周期硬布线控制器_1_jal [2]), .ecall(ID_ecall), .S_type(\单周期硬布线控制器_1_s_type ),
    .Jalr(\单周期硬布线控制器_1_jal [1]), .Beq(\单周期硬布线控制器_1_jal [10]), .JAL(\单周期硬布线控制器_1_jal [0]),
    .Bne(\单周期硬布线控制器_1_jal [11]), .in_3(ID_IR[21]), .lb(\单周期硬布线控制器_1_jal [5]), .blt(\单周期硬布线控制器_1_jal [12]));  // open: uret, CSRRSI, CSRRCI
  Multiplexer #(.select(1), .width(5), .disabled("Z"), .enable("false")) multiplexer_5 (
    .in0(ID_IR[19:15]), .in1(5'b10001), .out(multiplexer_5_out), .sel(ID_ecall));
  Multiplexer #(.select(1), .width(5), .disabled("Z"), .enable("false")) multiplexer_6 (
    .in0(ID_IR[24:20]), .in1(5'b01010), .out(multiplexer_6_out), .sel(ID_ecall));
  assign bit_extender_1_out = {{20{ID_IR[31]}}, ID_IR[31:20]};  // Bit_Extender bit_extender_1
  assign bit_extender_2_out = {{20{ID_IR[31]}}, {ID_IR[31:25], ID_IR[11:7]}};  // Bit_Extender bit_extender_2
  // Probe on M_PC[11:0]
  D_Flip_Flop #(.trigger("high"), .Pre_Clr_Positions("LEGACY"), .NegatePresetClear("false"), .enable("true"), .NewFFLayout("false")) d_ff_1 (.Q(d_ff_1_q));  // open: clk, D, Qn, preset, en, reset
  // Probe on 13'h59
  Multiplexer #(.select(1), .width(32), .disabled("Z"), .enable("false")) multiplexer_7 (
    .in0(bit_extender_1_out), .in1(bit_extender_2_out), .out(multiplexer_7_out), .sel(\单周期硬布线控制器_1_s_type ));
  // Probe on WB_PC[11:0]
  Comparator #(.width(13), .mode("twosComplement")) comparator_1 (
    .a(CNT_num), .b(13'h59), .eq(comparator_1_eq), .lt(comparator_1_lt));  // open: gt
  Clock #(.highDuration(1), .lowDuration(1)) clock_1 (.out(clock_1_out));
  Multiplexer #(.select(1), .width(32), .disabled("Z"), .enable("false")) multiplexer_8 (
    .in0(multiplexer_7_out), .in1(32'h22), .out(multiplexer_8_out), .sel(ID_ecall));
  nand nand_1 (nand_1_out, d_ff_1_q, comparator_1_eq);
  Counter #(.width(13), .max('h1fff), .ongoal("stay"), .trigger("rising"), .behavior("old")) counter_1 (
    .count(comparator_1_lt), .Q(CNT_num), .clk(clock_1_out));  // open: load, D, carry, clr, preset
  Regifile regifile_1 (
    .Din(RDin), .Clk(CLK), .R1(regifile_1_r1), .R2(regifile_1_r2), .WE(RegWrite), .W_num(WD_W_num),
    .R1_num(multiplexer_5_out), .R2_num(multiplexer_6_out));
  assign CLK = nand_1_out ? clock_1_out : 1'bz;  // Controlled_Buffer controlled_buffer_1
  \重定向相关处理逻辑  \u_重定向相关处理逻辑_1  (
    .op_code(ID_IR[6:2]), .Funct({ID_IR[30], ID_IR[25], ID_IR[14:12]}), .r1(multiplexer_5_out),
    .r2(multiplexer_6_out), .EX_MemRead(\id_ex_预测_1_ctrlsignal_2 [3]), .EX_WriteReg_num(EX_W_num),
    .EX_RegWrite(\id_ex_预测_1_ctrlsignal_2 [2]), .MEM_RegWrite(MEM_RegWrite), .MEM_WriteReg_num(MEM_W_num),
    .LoadUse(LoadUse), .r1Forward(pckSignal[2:1]), .r2Forward(pckSignal[4:3]));
  Comparator #(.width(32), .mode("twosComplement")) comparator_2 (
    .a(ID_IR), .b({32{1'b0}}), .eq(comparator_2_eq));  // open: gt, lt
  Multiplexer #(.select(1), .width(19), .disabled("Z"), .enable("false")) multiplexer_9 (
    .in0({pckSignal, ID_ecall, \单周期硬布线控制器_1_jal }), .in1({19{1'b0}}), .out(multiplexer_9_out),
    .sel(comparator_2_eq));
  Pull_Resistor #(.pull(1)) pull_resistor_1 (.node(CLK));
  or or_4 (or_4_out, RST, LoadUse, preErr);
  \ID_EX_预测  \id_ex_预测_1  (
    .CLK(CLK), .CLR(or_4_out), .en(en), .PC(ID_PC), .imm(multiplexer_8_out), .IR(ID_IR),
    .ctrlSignal(multiplexer_9_out), .A(regifile_1_r1), .W_num(ID_IR[11:7]), .B(regifile_1_r2),
    .Badd({ID_IR[31], ID_IR[7], ID_IR[30:25], ID_IR[11:8]}), .pre(ID_pre),
    .J({ID_IR[31], ID_IR[19:12], ID_IR[20], ID_IR[30:21]}), .PC_2(EX_PC), .imm_2(\id_ex_预测_1_imm_2 ),
    .IR_2(EX_IR),
    .ctrlSignal_2({\id_ex_预测_1_ctrlsignal_2 [18:17], \id_ex_预测_1_ctrlsignal_2_2 , EX_ecall, \id_ex_预测_1_ctrlsignal_2 [13:2], EX_jalr, EX_jal}),
    .A_2(A1), .W_num_2(EX_W_num), .B_2(B1), .Badd_2(\id_ex_预测_1_badd_2 ), .pre_2(EX_pre),
    .J_2(\id_ex_预测_1_j_2 ));
  Counter #(.width(16), .max('hffff), .ongoal("stay"), .trigger("rising"), .behavior("new")) counter_2 (
    .count(en), .Q(\总周期数 ), .clk(CLK));  // open: load, D, carry, clr, preset, down
  Multiplexer #(.select(1), .width(32), .disabled("Z"), .enable("false")) multiplexer_10 (
    .in0(B2), .in1(\id_ex_预测_1_imm_2 ), .out(multiplexer_10_out), .sel(\id_ex_预测_1_ctrlsignal_2 [13]));
  Multiplexer #(.select(2), .width(32), .disabled("Z"), .enable("false")) multiplexer_11 (
    .in0(A1), .in1(RDin), .in2(MEM_alu_res), .out(A2), .sel(\id_ex_预测_1_ctrlsignal_2_2 ));  // open: in3
  Multiplexer #(.select(2), .width(32), .disabled("Z"), .enable("false")) multiplexer_12 (
    .in0(B1), .in1(RDin), .in2(MEM_alu_res), .out(B2), .sel(\id_ex_预测_1_ctrlsignal_2 [18:17]));  // open: in3
  Shifter #(.width(12), .shift("ll")) shifter_1 (.in(\id_ex_预测_1_badd_2 ), .\dist (4'b0001), .out(shifter_1_out));
  assign bit_extender_3_out = {{20{shifter_1_out[11]}}, shifter_1_out};  // Bit_Extender bit_extender_3
  Shifter #(.width(20), .shift("ll")) shifter_2 (.in(\id_ex_预测_1_j_2 ), .\dist (5'b00001), .out(shifter_2_out));
  assign bit_extender_4_out = {{12{shifter_2_out[19]}}, shifter_2_out};  // Bit_Extender bit_extender_4
  Counter #(.width(16), .max('hffff), .ongoal("stay"), .trigger("rising"), .behavior("new")) counter_3 (
    .count(en), .Q(\无条件分支数 ), .clk(multiplexer_13_out));  // open: load, D, carry, clr, preset, down
  Multiplexer #(.select(1), .width(1), .disabled("Z"), .enable("false")) multiplexer_13 (
    .in0(and_3_out), .in1(1'b0), .out(multiplexer_13_out), .sel(CLK));
  and and_3 (and_3_out, or_5_out, CLK);
  or or_5 (or_5_out, EX_jal, EX_jalr);
  or or_6 (EX_B_IR, \id_ex_预测_1_ctrlsignal_2 [10], \id_ex_预测_1_ctrlsignal_2 [11], \id_ex_预测_1_ctrlsignal_2 [12]);
  and and_4 (and_4_out, \id_ex_预测_1_ctrlsignal_2 [11], ~EX);  // AND_Gate
  and and_5 (and_5_out, \id_ex_预测_1_ctrlsignal_2 [10], EX);
  ALU alu_1 (
    .X(A2), .Y(multiplexer_10_out), .AluOP(\id_ex_预测_1_ctrlsignal_2 [9:6]), .Equal(EX), .Result(EX_ALU_res),
    .out_6(alu_1_out_6));  // open: Result_2, out_4
  and and_6 (and_6_out, \id_ex_预测_1_ctrlsignal_2 [12], alu_1_out_6);
  Adder #(.width(32)) adder_3 (.a(bit_extender_3_out), .b(EX_PC), .out(adder_3_out));  // open: cin, cout
  Adder #(.width(32)) adder_4 (.a(bit_extender_4_out), .b(EX_PC), .out(adder_4_out));  // open: cin, cout
  or or_7 (branch, EX_B, EX_jal, EX_jalr);
  Comparator #(.width(1), .mode("twosComplement")) comparator_3 (
    .a(branch), .b(EX_pre), .eq(comparator_3_eq));  // open: gt, lt
  or or_8 (EX_B, and_6_out, and_4_out, and_5_out);
  Multiplexer #(.select(1), .width(32), .disabled("Z"), .enable("false")) multiplexer_14 (
    .in0(adder_3_out), .in1(adder_4_out), .out(multiplexer_14_out), .sel(EX_jal));
  not not_1 (preErr, comparator_3_eq);
  Counter #(.width(16), .max('hffff), .ongoal("stay"), .trigger("rising"), .behavior("new")) counter_4 (
    .count(en), .Q(\条件分支成功数 ), .clk(multiplexer_15_out));  // open: load, D, carry, clr, preset, down
  Multiplexer #(.select(1), .width(1), .disabled("Z"), .enable("false")) multiplexer_15 (
    .in0(and_7_out), .in1(1'b0), .out(multiplexer_15_out), .sel(CLK));
  and and_7 (and_7_out, EX_B, CLK);
  and and_8 (and_8_out, or_9_out, CLK);
  or or_9 (or_9_out, preErr, LoadUse);
  EX_MEM ex_mem_1 (
    .PC_2(M_PC),
    .ctrlSignal_2({ex_mem_1_ctrlsignal_2[7:5], MemWrite, ex_mem_1_ctrlsignal_2[3], MEM_RegWrite, ex_mem_1_ctrlsignal_2[1:0]}),
    .IR_2(MEM_IR), .B_2(MDin), .ALU_2(MEM_alu_res), .PC(EX_PC),
    .ctrlSignal({EX, EX_ecall, \id_ex_预测_1_ctrlsignal_2 [5:2], EX_jalr, EX_jal}), .IR(EX_IR), .B(B2),
    .ALU(EX_ALU_res), .W_num_2(MEM_W_num), .W_num(EX_W_num), .CLK(CLK), .CLR(RST), .en(en));
  Counter #(.width(16), .max('hffff), .ongoal("stay"), .trigger("rising"), .behavior("new")) counter_5 (
    .count(en), .Q(\插入气泡数 ), .clk(multiplexer_16_out));  // open: load, D, carry, clr, preset, down
  Multiplexer #(.select(1), .width(1), .disabled("Z"), .enable("false")) multiplexer_16 (
    .in0(and_8_out), .in1(1'b0), .out(multiplexer_16_out), .sel(CLK));
  Multiplexer #(.select(1), .width(1), .disabled("Z"), .enable("false")) multiplexer_17 (
    .in0(and_9_out), .in1(1'b0), .out(multiplexer_17_out), .sel(CLK));
  and and_9 (and_9_out, LoadUse, CLK);
  Counter #(.width(16), .max('hffff), .ongoal("stay"), .trigger("rising"), .behavior("new")) counter_6 (
    .count(en), .Q(\LoadUse次数 ), .clk(multiplexer_17_out));  // open: load, D, carry, clr, preset, down
  // Probe on \预测失败次数 
  // Probe on \预测成功次数 
  and and_10 (and_10_out, or_10_out, preErr);
  or or_10 (or_10_out, EX_B_IR, EX_jal, EX_jalr);
  RAM #(.addrWidth(10), .dataWidth(32), .bus("separate"), .Select("high")) ram_1 (
    .addr(MEM_alu_res[11:2]), .din(MDin), .data(ram_1_data), .str(MemWrite), .clk(CLK));  // open: sel, ld, clr
  Counter #(.width(16), .max('hffff), .ongoal("stay"), .trigger("rising"), .behavior("new")) counter_7 (
    .count(en), .Q(\预测失败次数 ), .clk(multiplexer_18_out));  // open: load, D, carry, clr, preset, down
  Multiplexer #(.select(1), .width(1), .disabled("Z"), .enable("false")) multiplexer_18 (
    .in0(and_11_out), .in1(1'b0), .out(multiplexer_18_out), .sel(CLK));
  and and_11 (and_11_out, and_10_out, CLK);
  MEM_WB mem_wb_1 (
    .PC(M_PC),
    .ctrlSignal({ex_mem_1_ctrlsignal_2[7:5], ex_mem_1_ctrlsignal_2[3], MEM_RegWrite, ex_mem_1_ctrlsignal_2[1:0]}),
    .IR(MEM_IR), .ALU(MEM_alu_res), .MD(ram_1_data), .PC_2(WB_PC),
    .ctrlSignal_2({WB, WB_ecall, mem_wb_1_ctrlsignal_2[4:3], RegWrite, mem_wb_1_ctrlsignal_2[1:0]}),
    .IR_2(WB_IR), .ALU_2(mem_wb_1_alu_2), .MD_2(mem_wb_1_md_2), .W_num(MEM_W_num), .W_num_2(WD_W_num),
    .en(en), .CLR(RST), .CLK(CLK));
  or or_11 (or_11_out, EX_B_IR, EX_jal, EX_jalr);
  Counter #(.width(16), .max('hffff), .ongoal("stay"), .trigger("rising"), .behavior("new")) counter_8 (
    .count(en), .Q(\预测成功次数 ), .clk(multiplexer_19_out));  // open: load, D, carry, clr, preset, down
  Multiplexer #(.select(1), .width(1), .disabled("Z"), .enable("false")) multiplexer_19 (
    .in0(and_12_out), .in1(1'b0), .out(multiplexer_19_out), .sel(CLK));
  and and_12 (and_12_out, and_13_out, CLK);
  and and_13 (and_13_out, or_11_out, ~preErr);  // AND_Gate
  Multiplexer #(.select(1), .width(32), .disabled("Z"), .enable("false")) multiplexer_20 (
    .in0(mem_wb_1_alu_2), .in1(mem_wb_1_md_2), .out(multiplexer_20_out), .sel(mem_wb_1_ctrlsignal_2[3]));
  Multiplexer #(.select(2), .width(8), .disabled("Z"), .enable("false")) multiplexer_21 (
    .in0(multiplexer_20_out[7:0]), .in1(multiplexer_20_out[15:8]), .in2(multiplexer_20_out[23:16]),
    .in3(multiplexer_20_out[31:24]), .out(multiplexer_21_out), .sel(mem_wb_1_alu_2[1:0]));
  Multiplexer #(.select(1), .width(32), .disabled("Z"), .enable("false")) multiplexer_22 (
    .in0(multiplexer_20_out), .in1(bit_extender_5_out), .out(multiplexer_22_out),
    .sel(mem_wb_1_ctrlsignal_2[4]));
  assign bit_extender_5_out = {{24{multiplexer_21_out[7]}}, multiplexer_21_out};  // Bit_Extender bit_extender_5
  and and_14 (and_14_out, ~WB, WB_ecall);  // AND_Gate
  Register #(.width(32), .trigger("rising"), .Select("low")) register_1 (
    .D(B2), .en(EX_ecall), .Q(LedData), .clk(CLK));  // open: clr
  not not_2 (en, halt);
  and and_15 (halt, ~Go, and_14_out);  // AND_Gate
  Adder #(.width(32)) adder_5 (.a(32'h4), .b(WB_PC), .out(adder_5_out));  // open: cin, cout
  or or_12 (or_12_out, mem_wb_1_ctrlsignal_2[1], mem_wb_1_ctrlsignal_2[0]);
  Multiplexer #(.select(1), .width(32), .disabled("Z"), .enable("false")) multiplexer_23 (
    .in0(multiplexer_22_out), .in1(adder_5_out), .out(RDin), .sel(or_12_out));

  // Other names for the same wires on the sheet: pckSignal[0] = ID_ecall; ID_W_num[4:0] = ID_IR[11:7];
  //   WB_RegWrite = RegWrite; MEM_PC[31:0] = M_PC; R2data[31:0] = B2

  // Notes on the sheet:
  //   中断源
  //   时空图监测，可删除
  //   中断等待指示
  //   数码管输出
  //   ID:jal 1;jalr 1;RegWrite 1;MemToReg 1;MemWrite 1;lb 1;ALUOP 4;Beq 1;Bne 1;Blt 1;AluSrc 1;ecall 1;r1Forward 1;r2Forward 1;
  //   MEM: ... = 1;
  //   指令存储器
  //   contents of rom_1 (hex, n*v repeats v):
  //   100493 100006f 100493 200913 300993 100006f 100493 200913 300993 100006f 100493 200913 300993
  //   100006f 100493 200913 300993 3b8000ef 100413 100493 1f49493 900533 2200893 73 24d493 48463 fedff06f
  //   900533 2200893 73 100493 249493 900533 2200893 73 48463 fedff06f 100493 1f49493 900533 2200893 73
  //   4034d493 900533 2200893 73 4044d493 900533 2200893 73 4044d493 900533 2200893 73 4044d493 900533
  //   2200893 73 4044d493 900533 2200893 73 4044d493 900533 2200893 73 4044d493 900533 2200893 73 4044d493
  //   900533 2200893 73 100413 1f41993 41f9d993 433 c00913 300b13 140413 f47413 800293 100313 499993
  //   89e9b3 1300533 2200893 73 406282b3 fe0294e3 140413 f00f93 1f47433 1c41413 800293 100313 49d993
  //   89e9b3 1300533 2200893 73 406282b3 fe0294e3 1c45413 406b0b33 b0463 f95ff06f 2b3 fff2c293 829293
  //   ff2e293 500533 2200893 73 fff00413 493 84a023 140413 448493 84a023 140413 448493 84a023 140413
  //   448493 84a023 140413 448493 84a023 140413 448493 84a023 140413 448493 84a023 140413 448493 84a023
  //   140413 448493 84a023 140413 448493 84a023 140413 448493 84a023 140413 448493 84a023 140413 448493
  //   84a023 140413 448493 84a023 140413 448493 84a023 140413 448493 84a023 140413 448493 140413 433
  //   3c00493 42983 4aa03 149a2b3 28663 134a023 1442023 ffc48493 fe9412e3 800533 2200893 73 440413 3c00493
  //   fc9416e3 3200893 73 100293 300313 800493 849493 7648493 900533 2200893 73 800e13 5494b3 6494b3
  //   900533 2200893 73 fffe0e13 fe0e14e3 a00893 73 fff00293 313 1900413 841413 9700493 940533 2200893 73
  //   5484b3 494b313 fe0306e3 a00893 73 313 1000e13 8400493 849493 8348493 400913 891913 490913 849493
  //   8248493 849493 8148493 891913 490913 891913 490913 932023 12484b3 430313 fffe0e13 fe0e18e3 2000e13
  //   313 30483 900533 2200893 73 130313 fffe0e13 fe0e14e3 a00893 73 ff100493 900533 2200893 73 148493
  //   fe04c8e3 a00893 73 413 140413 800533 2200893 73 240413 800533 2200893 73 340413 800533 2200893 73
  //   440413 800533 2200893 73 540413 800533 2200893 73 640413 800533 2200893 73 740413 800533 2200893 73
  //   840413 800533 2200893 2200893 73 8067
  //   I jalr
  //   sw
  //   控制位
  //   B
  //   jal
  //   流水调试日志用
  //   暂停节拍，不能为0
  //   戳工具置1进入计数暂停模式，ctrl+k时钟自动运行到对应节拍暂停
  //   ctrl+k关闭时钟连续运行，将控制位置零，进入单步调试模式调试
  //   可计数暂停的时钟源
  //   为方便自动评测，需要输出流水线各段保存的PC值，注意是PC不是PC+4，另外ID段寄存器写入信息，Mem段内存写入信息也要输出
  //   数据存储器
endmodule

module BTB (
  input  CLK,
  input  [31:0] PC,
  input  EX_branch,
  input  EX_branchTaken,
  input  [31:0] EX_PC,
  input  [31:0] EX_branchAddr,
  output predictJump,
  output [31:0] jumpAddr
);

  wire and_9_out, and_10_out, and_11_out, and_12_out, and_13_out, and_14_out, and_15_out, and_16_out,
       and_17_out, comparator_1_eq, comparator_2_eq, comparator_3_eq, comparator_4_eq, comparator_5_eq,
       comparator_6_eq, comparator_7_eq, comparator_8_eq, comparator_9_eq, comparator_10_eq,
       comparator_11_eq, comparator_12_eq, comparator_13_eq, comparator_14_eq, comparator_15_eq,
       comparator_16_eq, controlled_buffer_9_out, en0, en1, en2, en3, en4, en5, en6, en7, find0, find1,
       find2, find3, find4, find5, find6, find7, l0, l1, l2, l3, l4, l5, l6, l7, miss, not_1_out, not_2_out,
       not_3_out, not_4_out, not_5_out, not_6_out, not_7_out, not_8_out, not_found, or_1_out, or_2_out,
       or_3_out, or_4_out, or_5_out, or_6_out, or_7_out, or_8_out, or_9_out, or_10_out, or_11_out, or_12_out,
       or_13_out, or_14_out, or_15_out, or_16_out, predictHistory_2_z, predictHistory_3_z,
       predictHistory_4_z, predictHistory_5_z, predictHistory_6_z, predictHistory_7_z, predictHistory_8_z,
       predictHistory_z, priority_encoder_1_en_out, register_1_q, register_2_q, register_3_q, register_4_q,
       register_5_q, register_6_q, register_7_q, register_8_q, valid0, valid1, valid2, valid3, valid4,
       valid5, valid6, valid7;
  wire [2:0] multiplexer_2_out, priority_encoder_1_out, \归并比较_1_max_num , \归并比较_2_max_num , \归并比较_3_max_num ,
       \归并比较_4_max_num , \归并比较_5_max_num , \归并比较_6_max_num , \归并比较_7_max_num ;
  wire [15:0] count0, count1, count2, count3, count4, count5, count6, count7, \归并比较_1_max , \归并比较_2_max ,
       \归并比较_3_max , \归并比较_4_max , \归并比较_5_max , \归并比较_6_max ;
  wire [31:0] branchAddr_2_q, branchAddr_3_q, branchAddr_4_q, branchAddr_5_q, branchAddr_6_q, branchAddr_7_q,
       branchAddr_8_q, branchAddr_q, tag0, tag1, tag2, tag3, tag4, tag5, tag6, tag7;

  Register #(.width(1), .trigger("rising"), .Select("low")) valid (
    .D(1'b1), .en(en0), .Q(valid0), .clk(CLK));  // open: clr
  Register #(.width(1), .trigger("rising"), .Select("low")) valid_2 (
    .D(1'b1), .en(en1), .Q(valid1), .clk(CLK));  // open: clr
  Register #(.width(1), .trigger("rising"), .Select("low")) valid_3 (
    .D(1'b1), .en(en2), .Q(valid2), .clk(CLK));  // open: clr
  Register #(.width(1), .trigger("rising"), .Select("low")) valid_4 (
    .D(1'b1), .en(en3), .Q(valid3), .clk(CLK));  // open: clr
  Register #(.width(1), .trigger("rising"), .Select("low")) valid_5 (
    .D(1'b1), .en(en4), .Q(valid4), .clk(CLK));  // open: clr
  Register #(.width(1), .trigger("rising"), .Select("low")) valid_6 (
    .D(1'b1), .en(en5), .Q(valid5), .clk(CLK));  // open: clr
  Register #(.width(1), .trigger("rising"), .Select("low")) valid_7 (
    .D(1'b1), .en(en6), .Q(valid6), .clk(CLK));  // open: clr
  Register #(.width(1), .trigger("rising"), .Select("low")) valid_8 (
    .D(1'b1), .en(en7), .Q(valid7), .clk(CLK));  // open: clr
  Register #(.width(32), .trigger("rising"), .Select("low")) tag (
    .D(EX_PC), .en(en0), .Q(tag0), .clk(CLK));  // open: clr
  or or_1 (or_1_out, en0, find0);
  Register #(.width(32), .trigger("rising"), .Select("low")) tag_2 (
    .D(EX_PC), .en(en1), .Q(tag1), .clk(CLK));  // open: clr
  or or_2 (or_2_out, en1, find1);
  Register #(.width(32), .trigger("rising"), .Select("low")) tag_3 (
    .D(EX_PC), .en(en2), .Q(tag2), .clk(CLK));  // open: clr
  or or_3 (or_3_out, en2, find2);
  Register #(.width(32), .trigger("rising"), .Select("low")) tag_4 (
    .D(EX_PC), .en(en3), .Q(tag3), .clk(CLK));  // open: clr
  or or_4 (or_4_out, en3, find3);
  Register #(.width(32), .trigger("rising"), .Select("low")) tag_5 (
    .D(EX_PC), .en(en4), .Q(tag4), .clk(CLK));  // open: clr
  or or_5 (or_5_out, en4, find4);
  Register #(.width(32), .trigger("rising"), .Select("low")) tag_6 (
    .D(EX_PC), .en(en5), .Q(tag5), .clk(CLK));  // open: clr
  or or_6 (or_6_out, en5, find5);
  Register #(.width(32), .trigger("rising"), .Select("low")) tag_7 (
    .D(EX_PC), .en(en6), .Q(tag6), .clk(CLK));  // open: clr
  or or_7 (or_7_out, en6, find6);
  Register #(.width(32), .trigger("rising"), .Select("low")) tag_8 (
    .D(EX_PC), .en(en7), .Q(tag7), .clk(CLK));  // open: clr
  or or_8 (or_8_out, en7, find7);
  Counter #(.width(16), .max('hffff), .ongoal("wrap"), .trigger("rising"), .behavior("new")) \u_淘汰计数  (
    .D({16{1'b0}}), .Q(count0), .clk(CLK), .clr(register_1_q));  // open: load, count, carry, preset, down
  Register #(.width(1), .trigger("rising"), .Select("low")) register_1 (
    .D(or_1_out), .Q(register_1_q), .clk(CLK));  // open: en, clr
  Counter #(.width(16), .max('hffff), .ongoal("wrap"), .trigger("rising"), .behavior("new")) \u_淘汰计数_2  (
    .D({16{1'b0}}), .Q(count1), .clk(CLK), .clr(register_2_q));  // open: load, count, carry, preset, down
  Register #(.width(1), .trigger("rising"), .Select("low")) register_2 (
    .D(or_2_out), .Q(register_2_q), .clk(CLK));  // open: en, clr
  Counter #(.width(16), .max('hffff), .ongoal("wrap"), .trigger("rising"), .behavior("new")) \u_淘汰计数_3  (
    .D({16{1'b0}}), .Q(count2), .clk(CLK), .clr(register_3_q));  // open: load, count, carry, preset, down
  Register #(.width(1), .trigger("rising"), .Select("low")) register_3 (
    .D(or_3_out), .Q(register_3_q), .clk(CLK));  // open: en, clr
  Counter #(.width(16), .max('hffff), .ongoal("wrap"), .trigger("rising"), .behavior("new")) \u_淘汰计数_4  (
    .D({16{1'b0}}), .Q(count3), .clk(CLK), .clr(register_4_q));  // open: load, count, carry, preset, down
  Register #(.width(1), .trigger("rising"), .Select("low")) register_4 (
    .D(or_4_out), .Q(register_4_q), .clk(CLK));  // open: en, clr
  Counter #(.width(16), .max('hffff), .ongoal("wrap"), .trigger("rising"), .behavior("new")) \u_淘汰计数_5  (
    .D({16{1'b0}}), .Q(count4), .clk(CLK), .clr(register_5_q));  // open: load, count, carry, preset, down
  Register #(.width(1), .trigger("rising"), .Select("low")) register_5 (
    .D(or_5_out), .Q(register_5_q), .clk(CLK));  // open: en, clr
  Counter #(.width(16), .max('hffff), .ongoal("wrap"), .trigger("rising"), .behavior("new")) \u_淘汰计数_6  (
    .D({16{1'b0}}), .Q(count5), .clk(CLK), .clr(register_6_q));  // open: load, count, carry, preset, down
  Register #(.width(1), .trigger("rising"), .Select("low")) register_6 (
    .D(or_6_out), .Q(register_6_q), .clk(CLK));  // open: en, clr
  Counter #(.width(16), .max('hffff), .ongoal("wrap"), .trigger("rising"), .behavior("new")) \u_淘汰计数_7  (
    .D({16{1'b0}}), .Q(count6), .clk(CLK), .clr(register_7_q));  // open: load, count, carry, preset, down
  Register #(.width(1), .trigger("rising"), .Select("low")) register_7 (
    .D(or_7_out), .Q(register_7_q), .clk(CLK));  // open: en, clr
  Counter #(.width(16), .max('hffff), .ongoal("wrap"), .trigger("rising"), .behavior("new")) \u_淘汰计数_8  (
    .D({16{1'b0}}), .Q(count7), .clk(CLK), .clr(register_8_q));  // open: load, count, carry, preset, down
  Register #(.width(1), .trigger("rising"), .Select("low")) register_8 (
    .D(or_8_out), .Q(register_8_q), .clk(CLK));  // open: en, clr
  Register #(.width(32), .trigger("rising"), .Select("low")) branchAddr (
    .D(EX_branchAddr), .en(en0), .Q(branchAddr_q), .clk(CLK));  // open: clr
  Register #(.width(32), .trigger("rising"), .Select("low")) branchAddr_2 (
    .D(EX_branchAddr), .en(en1), .Q(branchAddr_2_q), .clk(CLK));  // open: clr
  Register #(.width(32), .trigger("rising"), .Select("low")) branchAddr_3 (
    .D(EX_branchAddr), .en(en2), .Q(branchAddr_3_q), .clk(CLK));  // open: clr
  Register #(.width(32), .trigger("rising"), .Select("low")) branchAddr_4 (
    .D(EX_branchAddr), .en(en3), .Q(branchAddr_4_q), .clk(CLK));  // open: clr
  Register #(.width(32), .trigger("rising"), .Select("low")) branchAddr_5 (
    .D(EX_branchAddr), .en(en4), .Q(branchAddr_5_q), .clk(CLK));  // open: clr
  Register #(.width(32), .trigger("rising"), .Select("low")) branchAddr_6 (
    .D(EX_branchAddr), .en(en5), .Q(branchAddr_6_q), .clk(CLK));  // open: clr
  Register #(.width(32), .trigger("rising"), .Select("low")) branchAddr_7 (
    .D(EX_branchAddr), .en(en6), .Q(branchAddr_7_q), .clk(CLK));  // open: clr
  Register #(.width(32), .trigger("rising"), .Select("low")) branchAddr_8 (
    .D(EX_branchAddr), .en(en7), .Q(branchAddr_8_q), .clk(CLK));  // open: clr
  assign jumpAddr = l0 ? branchAddr_q : 32'bz;  // Controlled_Buffer controlled_buffer_1
  assign jumpAddr = l1 ? branchAddr_2_q : 32'bz;  // Controlled_Buffer controlled_buffer_2
  assign jumpAddr = l2 ? branchAddr_3_q : 32'bz;  // Controlled_Buffer controlled_buffer_3
  assign jumpAddr = l3 ? branchAddr_4_q : 32'bz;  // Controlled_Buffer controlled_buffer_4
  assign jumpAddr = l4 ? branchAddr_5_q : 32'bz;  // Controlled_Buffer controlled_buffer_5
  assign jumpAddr = l5 ? branchAddr_6_q : 32'bz;  // Controlled_Buffer controlled_buffer_6
  assign jumpAddr = l6 ? branchAddr_7_q : 32'bz;  // Controlled_Buffer controlled_buffer_7
  assign jumpAddr = l7 ? branchAddr_8_q : 32'bz;  // Controlled_Buffer controlled_buffer_8
  or or_9 (or_9_out, en4, find4);
  or or_10 (or_10_out, en7, find7);
  or or_11 (or_11_out, en0, find0);
  \预测状态转换  predictHistory (.CLK(CLK), .x(EX_branchTaken), .z(predictHistory_z), .en(or_11_out));
  or or_12 (or_12_out, en1, find1);
  \预测状态转换  predictHistory_2 (.CLK(CLK), .x(EX_branchTaken), .z(predictHistory_2_z), .en(or_12_out));
  or or_13 (or_13_out, en2, find2);
  \预测状态转换  predictHistory_3 (.CLK(CLK), .x(EX_branchTaken), .z(predictHistory_3_z), .en(or_13_out));
  or or_14 (or_14_out, en3, find3);
  \预测状态转换  predictHistory_4 (.CLK(CLK), .x(EX_branchTaken), .z(predictHistory_4_z), .en(or_14_out));
  \预测状态转换  predictHistory_5 (.CLK(CLK), .x(EX_branchTaken), .z(predictHistory_5_z), .en(or_9_out));
  or or_15 (or_15_out, en5, find5);
  \预测状态转换  predictHistory_6 (.CLK(CLK), .x(EX_branchTaken), .z(predictHistory_6_z), .en(or_15_out));
  or or_16 (or_16_out, en6, find6);
  \预测状态转换  predictHistory_7 (.CLK(CLK), .x(EX_branchTaken), .z(predictHistory_7_z), .en(or_16_out));
  \预测状态转换  predictHistory_8 (.CLK(CLK), .x(EX_branchTaken), .z(predictHistory_8_z), .en(or_10_out));
  assign controlled_buffer_9_out = l0 ? predictHistory_z : 1'bz;  // Controlled_Buffer controlled_buffer_9
  assign controlled_buffer_9_out = l1 ? predictHistory_2_z : 1'bz;  // Controlled_Buffer controlled_buffer_10
  assign controlled_buffer_9_out = l2 ? predictHistory_3_z : 1'bz;  // Controlled_Buffer controlled_buffer_11
  assign controlled_buffer_9_out = l3 ? predictHistory_4_z : 1'bz;  // Controlled_Buffer controlled_buffer_12
  assign controlled_buffer_9_out = l4 ? predictHistory_5_z : 1'bz;  // Controlled_Buffer controlled_buffer_13
  assign controlled_buffer_9_out = l5 ? predictHistory_6_z : 1'bz;  // Controlled_Buffer controlled_buffer_14
  assign controlled_buffer_9_out = l6 ? predictHistory_7_z : 1'bz;  // Controlled_Buffer controlled_buffer_15
  assign controlled_buffer_9_out = l7 ? predictHistory_8_z : 1'bz;  // Controlled_Buffer controlled_buffer_16
  Multiplexer #(.select(1), .width(1), .disabled("Z"), .enable("false")) multiplexer_1 (
    .in0(controlled_buffer_9_out), .in1(1'b0), .out(predictJump), .sel(miss));
  Comparator #(.width(32), .mode("unsigned")) comparator_1 (.a(tag0), .b(PC), .eq(comparator_1_eq));  // open: gt, lt
  Comparator #(.width(32), .mode("unsigned")) comparator_2 (.a(tag1), .b(PC), .eq(comparator_2_eq));  // open: gt, lt
  Comparator #(.width(32), .mode("unsigned")) comparator_3 (.a(tag2), .b(PC), .eq(comparator_3_eq));  // open: gt, lt
  Comparator #(.width(32), .mode("unsigned")) comparator_4 (.a(tag3), .b(PC), .eq(comparator_4_eq));  // open: gt, lt
  Comparator #(.width(32), .mode("unsigned")) comparator_5 (.a(tag4), .b(PC), .eq(comparator_5_eq));  // open: gt, lt
  Comparator #(.width(32), .mode("unsigned")) comparator_6 (.a(tag5), .b(PC), .eq(comparator_6_eq));  // open: gt, lt
  Comparator #(.width(32), .mode("unsigned")) comparator_7 (.a(tag6), .b(PC), .eq(comparator_7_eq));  // open: gt, lt
  Comparator #(.width(32), .mode("unsigned")) comparator_8 (.a(tag7), .b(PC), .eq(comparator_8_eq));  // open: gt, lt
  and and_1 (l0, comparator_1_eq, valid0);
  and and_2 (l1, comparator_2_eq, valid1);
  and and_3 (l2, comparator_3_eq, valid2);
  and and_4 (l3, comparator_4_eq, valid3);
  and and_5 (l4, comparator_5_eq, valid4);
  and and_6 (l5, comparator_6_eq, valid5);
  and and_7 (l6, comparator_7_eq, valid6);
  and and_8 (l7, comparator_8_eq, valid7);
  not not_1 (not_1_out, valid0);
  not not_2 (not_2_out, valid1);
  not not_3 (not_3_out, valid2);
  not not_4 (not_4_out, valid3);
  not not_5 (not_5_out, valid4);
  not not_6 (not_6_out, valid5);
  not not_7 (not_7_out, valid6);
  not not_8 (not_8_out, valid7);
  \归并比较  \u_归并比较_1  (
    .x(count0), .y(count1), .x_num(3'b000), .y_num(3'b001), .max(\归并比较_1_max ), .max_num(\归并比较_1_max_num ));
  \归并比较  \u_归并比较_2  (
    .x(count2), .y(count3), .x_num(3'b010), .y_num(3'b011), .max(\归并比较_2_max ), .max_num(\归并比较_2_max_num ));
  \归并比较  \u_归并比较_3  (
    .x(count4), .y(count5), .x_num(3'b100), .y_num(3'b101), .max(\归并比较_3_max ), .max_num(\归并比较_3_max_num ));
  \归并比较  \u_归并比较_4  (
    .x(count6), .y(count7), .x_num(3'b110), .y_num(3'b111), .max(\归并比较_4_max ), .max_num(\归并比较_4_max_num ));
  \归并比较  \u_归并比较_5  (
    .x(\归并比较_1_max ), .y(\归并比较_2_max ), .x_num(\归并比较_1_max_num ), .y_num(\归并比较_2_max_num ),
    .max(\归并比较_5_max ), .max_num(\归并比较_5_max_num ));
  \归并比较  \u_归并比较_6  (
    .x(\归并比较_3_max ), .y(\归并比较_4_max ), .x_num(\归并比较_3_max_num ), .y_num(\归并比较_4_max_num ),
    .max(\归并比较_6_max ), .max_num(\归并比较_6_max_num ));
  Priority_Encoder #(.select(3), .disabled("Z")) priority_encoder_1 (
    .in0(not_1_out), .in1(not_2_out), .in2(not_3_out), .in3(not_4_out), .in4(not_5_out), .in5(not_6_out),
    .in6(not_7_out), .in7(not_8_out), .out(priority_encoder_1_out), .en_out(priority_encoder_1_en_out));  // open: gs, en_in
  \归并比较  \u_归并比较_7  (
    .x(\归并比较_5_max ), .y(\归并比较_6_max ), .x_num(\归并比较_5_max_num ), .y_num(\归并比较_6_max_num ),
    .max_num(\归并比较_7_max_num ));  // open: max
  Multiplexer #(.select(1), .width(3), .disabled("Z"), .enable("false")) multiplexer_2 (
    .in0(priority_encoder_1_out), .in1(\归并比较_7_max_num ), .out(multiplexer_2_out),
    .sel(priority_encoder_1_en_out));
  Demultiplexer #(.select(3), .width(1), .tristate("false"), .disabled("Z"), .enable("false")) demultiplexer_1 (
    .out0(en0), .out1(en1), .out2(en2), .out3(en3), .out4(en4), .out5(en5), .out6(en6), .out7(en7),
    .in(and_9_out), .sel(multiplexer_2_out));
  and and_9 (and_9_out, EX_branch, not_found);
  Comparator #(.width(32), .mode("unsigned")) comparator_9 (.a(tag0), .b(EX_PC), .eq(comparator_9_eq));  // open: gt, lt
  Comparator #(.width(32), .mode("unsigned")) comparator_10 (
    .a(tag1), .b(EX_PC), .eq(comparator_10_eq));  // open: gt, lt
  Comparator #(.width(32), .mode("unsigned")) comparator_11 (
    .a(tag2), .b(EX_PC), .eq(comparator_11_eq));  // open: gt, lt
  Comparator #(.width(32), .mode("unsigned")) comparator_12 (
    .a(tag3), .b(EX_PC), .eq(comparator_12_eq));  // open: gt, lt
  Comparator #(.width(32), .mode("unsigned")) comparator_13 (
    .a(tag4), .b(EX_PC), .eq(comparator_13_eq));  // open: gt, lt
  Comparator #(.width(32), .mode("unsigned")) comparator_14 (
    .a(tag5), .b(EX_PC), .eq(comparator_14_eq));  // open: gt, lt
  Comparator #(.width(32), .mode("unsigned")) comparator_15 (
    .a(tag6), .b(EX_PC), .eq(comparator_15_eq));  // open: gt, lt
  Comparator #(.width(32), .mode("unsigned")) comparator_16 (
    .a(tag7), .b(EX_PC), .eq(comparator_16_eq));  // open: gt, lt
  and and_10 (and_10_out, comparator_9_eq, valid0);
  and and_11 (and_11_out, comparator_10_eq, valid1);
  and and_12 (and_12_out, comparator_11_eq, valid2);
  and and_13 (and_13_out, comparator_12_eq, valid3);
  and and_14 (and_14_out, comparator_13_eq, valid4);
  and and_15 (and_15_out, comparator_14_eq, valid5);
  and and_16 (and_16_out, comparator_15_eq, valid6);
  and and_17 (and_17_out, comparator_16_eq, valid7);
  and and_18 (find0, EX_branch, and_10_out);
  and and_19 (find1, EX_branch, and_11_out);
  and and_20 (find2, EX_branch, and_12_out);
  and and_21 (find3, EX_branch, and_13_out);
  and and_22 (find4, EX_branch, and_14_out);
  and and_23 (find5, EX_branch, and_15_out);
  and and_24 (find6, EX_branch, and_16_out);
  and and_25 (find7, EX_branch, and_17_out);
  nor nor_1 (not_found, find0, find1, find2, find3, find4, find5, find6, find7);
  nor nor_2 (miss, l0, l1, l2, l3, l4, l5, l6, l7);
endmodule

module \中断按键参考电路  (
  input  \同步清零信号 ,
  output \与中断屏蔽位与 
);

  wire \_1号中断_out , and_1_out, clock_1_out, d_ff_1_q, or_1_out, or_2_out;

  Clock #(.highDuration(1), .lowDuration(1)) clock_1 (.out(clock_1_out));
  Button \_1号中断  (.out(\_1号中断_out ));
  or or_1 (or_1_out, \与中断屏蔽位与 , d_ff_1_q);
  LED #(.active("true")) \_1号中断等待指示灯  (.in(or_1_out));
  D_Flip_Flop #(.trigger("rising"), .Pre_Clr_Positions("LEGACY"), .NegatePresetClear("false"), .enable("true"), .NewFFLayout("false")) d_ff_1 (
    .clk(\_1号中断_out ), .D(1'b1), .Q(d_ff_1_q), .reset(\与中断屏蔽位与 ));  // open: Qn, preset, en
  or or_2 (or_2_out, d_ff_1_q, \与中断屏蔽位与 );
  and and_1 (and_1_out, or_2_out, ~\同步清零信号 );  // AND_Gate
  D_Flip_Flop #(.trigger("rising"), .Pre_Clr_Positions("LEGACY"), .NegatePresetClear("false"), .enable("true"), .NewFFLayout("false")) IR1 (
    .clk(clock_1_out), .D(and_1_out), .Q(\与中断屏蔽位与 ));  // open: Qn, preset, en, reset

  // Notes on the sheet:
  //   中断信号采样参考电路
  //   Reset 
endmodule

module \单周期_单级中断  (
  input  IR1,
  input  IR2,
  input  IR3,
  output RegWrite,
  output MemWrite,
  output [31:0] PC,
  output [31:0] IR,
  output [31:0] RDin,
  output [31:0] MDin,
  output [31:0] LedData
);

  wire alu_1_out_6, and_1_out, and_2_out, and_4_out, and_5_out, and_6_out, and_7_out, and_9_out, and_10_out,
       and_14_out, B, blt, CLK, clock_1_out, CLR1, CLR2, CLR3, comparator_1_eq, comparator_2_eq,
       comparator_3_eq, comparator_4_eq, comparator_5_eq, comparator_5_lt, d_ff_1_q, d_ff_2_q, d_ff_3_q,
       d_ff_4_q, decoder_1_out1, decoder_1_out2, decoder_1_out3, ecall, en, Go, halt, \int , IR1_q, IR1_t,
       IR2_q, IR2_t, IR3_q, IR3_t, IRA, IRB, IRC, jal, jalr, lb, nand_1_out, not_1_out, not_3_out, or_4_out,
       or_6_out, or_7_out, or_8_out, or_12_out, priority_encoder_2_gs, register_1_q, RST, S_type, tunnel,
       uret, W1, W2, W3, \单周期硬布线控制器_1_alu_src , \单周期硬布线控制器_1_beq , \单周期硬布线控制器_1_bne , \单周期硬布线控制器_1_memtoreg ;
  wire [0:0] or_1_out;
  wire [1:0] intID, priority_encoder_1_out, register_2_q;
  wire [3:0] \单周期硬布线控制器_1_alu_op ;
  wire [4:0] multiplexer_3_out, multiplexer_4_out;
  wire [7:0] multiplexer_13_out;
  wire [11:0] shifter_1_out;
  wire [12:0] CNT_num;
  wire [15:0] \总周期数 ;
  wire [19:0] shifter_2_out;
  wire [31:0] adder_1_out, adder_2_out, adder_3_out, adder_4_out, alu_res, beforeIntPC, bit_extender_1_out,
       bit_extender_2_out, bit_extender_3_out, bit_extender_4_out, bit_extender_5_out, intPC,
       multiplexer_1_out, multiplexer_6_out, multiplexer_7_out, multiplexer_8_out, multiplexer_10_out,
       multiplexer_11_out, multiplexer_12_out, ram_1_data, regifile_1_r1, uretPC;

  Button \u_继续运行  (.out(Go));
  Button _1 ();  // open: out
  Button _2 ();  // open: out
  Button _3 ();  // open: out
  LED #(.active("true")) led_1 (.in(W1));
  LED #(.active("true")) led_2 (.in(W2));
  LED #(.active("true")) led_3 (.in(W3));
  Counter #(.width(16), .max('hffff), .ongoal("stay"), .trigger("rising"), .behavior("new")) counter_1 (
    .count(en), .Q(\总周期数 ), .clk(CLK));  // open: load, D, carry, clr, preset, down
  and and_1 (and_1_out, ~uret, ~\int );  // AND_Gate
  Hex_Digit_Display hex_digit_display_1 (.value(LedData[31:28]));  // open: dp
  Comparator #(.width(16), .mode("twosComplement")) comparator_1 (
    .a(16'h23b), .b(\总周期数 ), .eq(comparator_1_eq));  // open: gt, lt
  Comparator #(.width(16), .mode("twosComplement")) comparator_2 (
    .a(\总周期数 ), .b(16'h1), .eq(comparator_2_eq));  // open: gt, lt
  Comparator #(.width(16), .mode("twosComplement")) comparator_3 (
    .a(\总周期数 ), .b(16'h4), .eq(comparator_3_eq));  // open: gt, lt
  Comparator #(.width(16), .mode("twosComplement")) comparator_4 (
    .a(\总周期数 ), .b(16'h7), .eq(comparator_4_eq));  // open: gt, lt
  Priority_Encoder #(.select(2), .disabled("Z")) priority_encoder_1 (
    .in0(and_1_out), .in1(uret), .in2(\int ), .out(priority_encoder_1_out));  // open: in3, gs, en_out, en_in
  or or_1 (or_1_out[0], jal, B);
  or or_2 (W2, IR2_q, d_ff_2_q);
  or or_3 (W3, IR3_q, d_ff_3_q);
  Hex_Digit_Display hex_digit_display_2 (.value(LedData[27:24]));  // open: dp
  Hex_Digit_Display hex_digit_display_3 (.value(LedData[23:20]));  // open: dp
  or or_4 (or_4_out, comparator_1_eq, comparator_2_eq);
  assign IRA = or_4_out ? ~CLK : 1'bz;  // Controlled_Inverter controlled_inverter_1
  assign IRB = comparator_3_eq ? ~CLK : 1'bz;  // Controlled_Inverter controlled_inverter_2
  assign IRC = comparator_4_eq ? ~CLK : 1'bz;  // Controlled_Inverter controlled_inverter_3
  Multiplexer #(.select(2), .width(32), .disabled("Z"), .enable("false")) multiplexer_1 (
    .in0(beforeIntPC), .in1(uretPC), .in2(intPC), .out(multiplexer_1_out), .sel(priority_encoder_1_out));  // open: in3
  Multiplexer #(.select(2), .width(32), .disabled("Z"), .enable("false")) multiplexer_2 (
    .in0(adder_1_out), .in1(multiplexer_10_out), .in2(alu_res), .out(beforeIntPC), .sel({jalr, or_1_out[0]}));  // open: in3
  D_Flip_Flop #(.trigger("rising"), .Pre_Clr_Positions("LEGACY"), .NegatePresetClear("false"), .enable("true"), .NewFFLayout("false")) d_ff_1 (
    .clk(IR1_t), .D(1'b1), .Q(d_ff_1_q), .reset(IR1_q));  // open: Qn, preset, en
  or or_5 (W1, IR1_q, d_ff_1_q);
  D_Flip_Flop #(.trigger("rising"), .Pre_Clr_Positions("LEGACY"), .NegatePresetClear("false"), .enable("true"), .NewFFLayout("false")) d_ff_2 (
    .clk(IR2_t), .D(1'b1), .Q(d_ff_2_q), .reset(IR2_q));  // open: Qn, preset, en
  D_Flip_Flop #(.trigger("rising"), .Pre_Clr_Positions("LEGACY"), .NegatePresetClear("false"), .enable("true"), .NewFFLayout("false")) d_ff_3 (
    .clk(IR3_t), .D(1'b1), .Q(d_ff_3_q), .reset(IR3_q));  // open: Qn, preset, en
  Hex_Digit_Display hex_digit_display_4 (.value(LedData[15:12]));  // open: dp
  Hex_Digit_Display hex_digit_display_5 (.value(LedData[19:16]));  // open: dp
  Pull_Resistor #(.pull(0)) pull_resistor_1 (.node(IRA));
  Pull_Resistor #(.pull(0)) pull_resistor_2 (.node(IRB));
  Pull_Resistor #(.pull(0)) pull_resistor_3 (.node(IRC));
  and and_2 (and_2_out, ~tunnel, ecall);  // AND_Gate
  not not_1 (not_1_out, halt);
  or or_6 (or_6_out, d_ff_1_q, IR1_q);
  or or_7 (or_7_out, d_ff_2_q, IR2_q);
  or or_8 (or_8_out, d_ff_3_q, IR3_q);
  Hex_Digit_Display hex_digit_display_6 (.value(LedData[7:4]));  // open: dp
  Hex_Digit_Display hex_digit_display_7 (.value(LedData[11:8]));  // open: dp
  // Probe on \总周期数 
  not not_2 (en, halt);
  and and_3 (halt, ~Go, and_2_out);  // AND_Gate
  Register #(.width(32), .trigger("rising"), .Select("low")) u_PC (
    .D(multiplexer_1_out), .en(not_1_out), .Q(PC), .clk(CLK), .clr(RST));
  and and_4 (and_4_out, or_6_out, ~CLR1);  // AND_Gate
  and and_5 (and_5_out, or_7_out, ~CLR2);  // AND_Gate
  and and_6 (and_6_out, or_8_out, ~CLR3);  // AND_Gate
  Hex_Digit_Display hex_digit_display_8 (.value(LedData[3:0]));  // open: dp
  Button button_1 (.out(RST));
  Adder #(.width(32)) adder_1 (.a(PC), .b(32'h4), .out(adder_1_out));  // open: cin, cout
  D_Flip_Flop #(.trigger("rising"), .Pre_Clr_Positions("LEGACY"), .NegatePresetClear("false"), .enable("true"), .NewFFLayout("false")) u_IR1 (
    .clk(CLK), .D(and_4_out), .Q(IR1_q));  // open: Qn, preset, en, reset
  D_Flip_Flop #(.trigger("rising"), .Pre_Clr_Positions("LEGACY"), .NegatePresetClear("false"), .enable("true"), .NewFFLayout("false")) u_IR2 (
    .clk(CLK), .D(and_5_out), .Q(IR2_q));  // open: Qn, preset, en, reset
  D_Flip_Flop #(.trigger("rising"), .Pre_Clr_Positions("LEGACY"), .NegatePresetClear("false"), .enable("true"), .NewFFLayout("false")) u_IR3 (
    .clk(CLK), .D(and_6_out), .Q(IR3_q));  // open: Qn, preset, en, reset
  // RiscV_Probe riscv_probe_1: pin names not known; wires that end beside it: IR
  or or_9 (IR1_t, IR1, IRA);
  ROM #(.addrWidth(10), .dataWidth(32), .Select("high")) rom_1 (.addr(PC[11:2]), .data(IR));
  or or_10 (IR2_t, IR2, IRB);
  Priority_Encoder #(.select(2), .disabled("Z")) priority_encoder_2 (
    .in1(IR1_q), .in2(IR2_q), .in3(IR3_q), .out(intID), .gs(priority_encoder_2_gs));  // open: in0, en_out, en_in
  \单周期硬布线控制器  \u_单周期硬布线控制器_1  (
    .Funct({IR[30], IR[25], IR[14:12]}), .OP(IR[6:2]), .ALU_OP(\单周期硬布线控制器_1_alu_op ),
    .MemToReg(\单周期硬布线控制器_1_memtoreg ), .MemWrite(MemWrite), .ALU_SRC(\单周期硬布线控制器_1_alu_src ),
    .RegWrite(RegWrite), .ecall(ecall), .S_type(S_type), .Jalr(jalr), .Beq(\单周期硬布线控制器_1_beq ), .JAL(jal),
    .Bne(\单周期硬布线控制器_1_bne ), .in_3(IR[21]), .uret(uret), .lb(lb), .blt(blt));  // open: CSRRSI, CSRRCI
  Multiplexer #(.select(1), .width(5), .disabled("Z"), .enable("false")) multiplexer_3 (
    .in0(IR[19:15]), .in1(5'b10001), .out(multiplexer_3_out), .sel(ecall));
  Multiplexer #(.select(1), .width(5), .disabled("Z"), .enable("false")) multiplexer_4 (
    .in0(IR[24:20]), .in1(5'b01010), .out(multiplexer_4_out), .sel(ecall));
  or or_11 (IR3_t, IR3, IRC);
  assign bit_extender_1_out = {{20{IR[31]}}, IR[31:20]};  // Bit_Extender bit_extender_1
  assign bit_extender_2_out = {{20{IR[31]}}, {IR[31:25], IR[11:7]}};  // Bit_Extender bit_extender_2
  Shifter #(.width(12), .shift("ll")) shifter_1 (
    .in({IR[31], IR[7], IR[30:25], IR[11:8]}), .\dist (4'b0001), .out(shifter_1_out));
  Shifter #(.width(20), .shift("ll")) shifter_2 (
    .in({IR[31], IR[19:12], IR[20], IR[30:21]}), .\dist (5'b00001), .out(shifter_2_out));
  Multiplexer #(.select(2), .width(32), .disabled("Z"), .enable("false")) multiplexer_5 (
    .in1(32'h30ac), .in2(32'h3150), .in3(32'h31f4), .out(intPC), .sel(intID));  // open: in0
  Regifile regifile_1 (
    .Din(RDin), .Clk(CLK), .R1(regifile_1_r1), .R2(MDin), .WE(RegWrite), .W_num(IR[11:7]),
    .R1_num(multiplexer_3_out), .R2_num(multiplexer_4_out));
  Multiplexer #(.select(1), .width(32), .disabled("Z"), .enable("false")) multiplexer_6 (
    .in0(bit_extender_1_out), .in1(bit_extender_2_out), .out(multiplexer_6_out), .sel(S_type));
  assign bit_extender_3_out = {{20{shifter_1_out[11]}}, shifter_1_out};  // Bit_Extender bit_extender_3
  assign bit_extender_4_out = {{12{shifter_2_out[19]}}, shifter_2_out};  // Bit_Extender bit_extender_4
  Multiplexer #(.select(1), .width(32), .disabled("Z"), .enable("false")) multiplexer_7 (
    .in0(multiplexer_6_out), .in1(32'h22), .out(multiplexer_7_out), .sel(ecall));
  Adder #(.width(32)) adder_2 (.a(PC), .b(bit_extender_4_out), .out(adder_2_out));  // open: cin, cout
  and and_7 (and_7_out, priority_encoder_2_gs, ~uret);  // AND_Gate
  Multiplexer #(.select(1), .width(32), .disabled("Z"), .enable("false")) multiplexer_8 (
    .in0(MDin), .in1(multiplexer_7_out), .out(multiplexer_8_out), .sel(\单周期硬布线控制器_1_alu_src ));
  Adder #(.width(32)) adder_3 (.a(PC), .b(bit_extender_3_out), .out(adder_3_out));  // open: cin, cout
  Register #(.width(1), .trigger("rising"), .Select("low")) register_1 (
    .D(and_7_out), .Q(register_1_q), .clk(CLK), .clr(RST));  // open: en
  Register #(.width(32), .trigger("rising"), .Select("low")) mEPC (
    .D(beforeIntPC), .en(\int ), .Q(uretPC), .clk(CLK), .clr(RST));
  Register #(.width(2), .trigger("rising"), .Select("low")) register_2 (
    .D(intID), .en(\int ), .Q(register_2_q), .clk(CLK), .clr(RST));
  ALU alu_1 (
    .X(regifile_1_r1), .Y(multiplexer_8_out), .AluOP(\单周期硬布线控制器_1_alu_op ), .Equal(tunnel), .Result(alu_res),
    .out_6(alu_1_out_6));  // open: Result_2, out_4
  Multiplexer #(.select(1), .width(32), .disabled("Z"), .enable("false")) multiplexer_9 (
    .in0(multiplexer_11_out), .in1(adder_4_out), .out(RDin), .sel(or_12_out));
  or or_12 (or_12_out, jalr, jal);
  Multiplexer #(.select(1), .width(32), .disabled("Z"), .enable("false")) multiplexer_10 (
    .in0(adder_3_out), .in1(adder_2_out), .out(multiplexer_10_out), .sel(jal));
  and and_8 (\int , priority_encoder_2_gs, not_3_out);
  not not_3 (not_3_out, register_1_q);
  Decoder #(.select(2), .tristate("false"), .disabled("Z"), .enable("false")) decoder_1 (
    .out1(decoder_1_out1), .out2(decoder_1_out2), .out3(decoder_1_out3), .sel(register_2_q));  // open: out0
  Adder #(.width(32)) adder_4 (.a(32'h4), .b(PC), .out(adder_4_out));  // open: cin, cout
  and and_9 (and_9_out, \单周期硬布线控制器_1_beq , tunnel);
  and and_10 (and_10_out, \单周期硬布线控制器_1_bne , ~tunnel);  // AND_Gate
  and and_11 (CLR1, decoder_1_out1, uret);
  and and_12 (CLR2, decoder_1_out2, uret);
  and and_13 (CLR3, decoder_1_out3, uret);
  D_Flip_Flop #(.trigger("high"), .Pre_Clr_Positions("LEGACY"), .NegatePresetClear("false"), .enable("true"), .NewFFLayout("false")) d_ff_4 (.Q(d_ff_4_q));  // open: clk, D, Qn, preset, en, reset
  // Probe on 13'hc
  and and_14 (and_14_out, blt, alu_1_out_6);
  Multiplexer #(.select(1), .width(32), .disabled("Z"), .enable("false")) multiplexer_11 (
    .in0(multiplexer_12_out), .in1(bit_extender_5_out), .out(multiplexer_11_out), .sel(lb));
  Register #(.width(32), .trigger("rising"), .Select("low")) register_3 (
    .D(MDin), .en(ecall), .Q(LedData), .clk(CLK));  // open: clr
  Comparator #(.width(13), .mode("twosComplement")) comparator_5 (
    .a(CNT_num), .b(13'hc), .eq(comparator_5_eq), .lt(comparator_5_lt));  // open: gt
  Clock #(.highDuration(1), .lowDuration(1)) clock_1 (.out(clock_1_out));
  or or_13 (B, and_9_out, and_10_out, and_14_out);
  RAM #(.addrWidth(10), .dataWidth(32), .bus("separate"), .Select("high")) ram_1 (
    .addr(alu_res[11:2]), .din(MDin), .data(ram_1_data), .str(MemWrite), .clk(CLK));  // open: sel, ld, clr
  Counter #(.width(13), .max('h1fff), .ongoal("stay"), .trigger("rising"), .behavior("old")) counter_2 (
    .count(comparator_5_lt), .Q(CNT_num), .clk(clock_1_out));  // open: load, D, carry, clr, preset
  Multiplexer #(.select(1), .width(32), .disabled("Z"), .enable("false")) multiplexer_12 (
    .in0(alu_res), .in1(ram_1_data), .out(multiplexer_12_out), .sel(\单周期硬布线控制器_1_memtoreg ));
  assign bit_extender_5_out = {{24{multiplexer_13_out[7]}}, multiplexer_13_out};  // Bit_Extender bit_extender_5
  nand nand_1 (nand_1_out, d_ff_4_q, comparator_5_eq);
  Multiplexer #(.select(2), .width(8), .disabled("Z"), .enable("false")) multiplexer_13 (
    .in0(multiplexer_12_out[7:0]), .in1(multiplexer_12_out[15:8]), .in2(multiplexer_12_out[23:16]),
    .in3(multiplexer_12_out[31:24]), .out(multiplexer_13_out), .sel(alu_res[1:0]));
  assign CLK = nand_1_out ? clock_1_out : 1'bz;  // Controlled_Buffer controlled_buffer_1
  Pull_Resistor #(.pull(1)) pull_resistor_4 (.node(CLK));

  // Other names for the same wires on the sheet: R2data[31:0] = MDin

  // Notes on the sheet:
  //   中断源
  //   中断等待指示
  //   总复位信号应将除ROM以外所有存储组件全部清零
  //   单级中断测试信号模拟器
  //   数码管输出
  //   数码管输出应该用寄存器锁存，否则显示数据只能一闪而过
  //   指令探针
  //   指令存储器
  //   指令字
  //   contents of rom_1 (hex, n*v repeats v):
  //   7d000113 100413 1f41993 41f9d993 433 c00913 800b13 140413 f47413 800293 100313 499993 89e9b3 1300533
  //   2200893 73 406282b3 fe0294e3 140413 f00f93 1f47433 1c41413 800293 100313 49d993 89e9b3 1300533
  //   2200893 73 406282b3 fe0294e3 1c45413 406b0b33 b0463 f95ff06f 2b3 fff2c293 1029293 fff2e293 500533
  //   2200893 73 f5dff06f 1112023 410113 a12023 410113 812023 410113 1312023 410113 1412023 410113 1512023
  //   410113 1612023 410113 100b13 300a13 100a93 1600433 441413 14469b3 1300533 2200893 73 fe0416e3
  //   415a0a33 fe0a10e3 ffc10113 12b03 ffc10113 12a83 ffc10113 12a03 ffc10113 12983 ffc10113 12403
  //   ffc10113 12503 ffc10113 12883 200073 1112023 410113 a12023 410113 812023 410113 1312023 410113
  //   1412023 410113 1512023 410113 1612023 410113 200b13 300a13 100a93 1600433 441413 14469b3 1300533
  //   2200893 73 fe0416e3 415a0a33 fe0a10e3 ffc10113 12b03 ffc10113 12a83 ffc10113 12a03 ffc10113 12983
  //   ffc10113 12403 ffc10113 12503 ffc10113 12883 200073 1112023 410113 a12023 410113 812023 410113
  //   1312023 410113 1412023 410113 1512023 410113 1612023 410113 300b13 300a13 100a93 1600433 441413
  //   14469b3 1300533 2200893 73 fe0416e3 415a0a33 fe0a10e3 ffc10113 12b03 ffc10113 12a83 ffc10113 12a03
  //   ffc10113 12983 ffc10113 12403 ffc10113 12503 ffc10113 12883 200073
  //   JAL
  //   JALR
  //   URET
  //   I jalr
  //   sw
  //   B
  //   Beq
  //   Bne
  //   MemToReg
  //   MemWrite
  //   AluOP
  //   AluSrcB
  //   RegWrite
  //   jal
  //   为方便自动评测，需要输出PC，IR，寄存器堆写如数据RDin
  //   RAM写使能MemWrite、RAM写入数据MDin等信号
  //   控制位
  //   暂停节拍，不能为0
  //   数据存储器
  //   戳工具置1进入计数暂停模式，ctrl+k时钟自动运行到对应节拍暂停
  //   ctrl+k关闭时钟连续运行，将控制位置零，进入单步调试模式调试
  //   可计数暂停的时钟源
endmodule

module \单周期_多级中断  (
  input  IR1,
  input  IR2,
  input  IR3,
  output RegWrite,
  output MemWrite,
  output [31:0] PC,
  output [31:0] IR,
  output [31:0] RDin,
  output [31:0] MDin,
  output [31:0] LedData
);

  wire alu_1_out_6, and_1_out, and_2_out, and_4_out, and_5_out, and_6_out, and_8_out, and_9_out, and_10_out,
       and_11_out, B, blt, CLK, clock_1_out, CLR1, CLR2, CLR3, comparator_1_eq, comparator_2_eq,
       comparator_3_eq, comparator_4_eq, comparator_5_eq, comparator_6_eq, comparator_7_eq, comparator_7_lt,
       CSRRCI, CSRRSI, d_ff_1_q, d_ff_2_q, d_ff_3_q, d_ff_4_q, decoder_1_out1, decoder_1_out2,
       decoder_1_out3, decoder_2_out1, decoder_2_out2, decoder_2_out3, decoder_3_out0, decoder_3_out1,
       decoder_3_out2, ecall, en, Go, halt, hasInt, IE, IE_q, \int , intReach, IR1_q, IR1_t, IR2_q, IR2_t,
       IR3_q, IR3_t, IRA, IRB, IRC, jal, jalr, lb, nand_1_out, not_1_out, or_4_out, or_5_out, or_7_out,
       or_8_out, or_9_out, or_13_out, or_15_out, register_1_q, register_2_q, register_3_q, RST, S_type,
       tunnel, uret, W1, W2, W3, \单周期硬布线控制器_1_alu_src , \单周期硬布线控制器_1_beq , \单周期硬布线控制器_1_bne ,
       \单周期硬布线控制器_1_memtoreg ;
  wire [0:0] or_1_out;
  wire [1:0] intID, multiplexer_5_out, newIntID, priority_encoder_1_out, stack;
  wire [3:0] \单周期硬布线控制器_1_alu_op ;
  wire [4:0] multiplexer_3_out, multiplexer_4_out;
  wire [7:0] multiplexer_14_out, multiplexer_14_out_2, multiplexer_14_out_3, multiplexer_14_out_4,
       multiplexer_15_out;
  wire [11:0] shifter_1_out;
  wire [12:0] CNT_num;
  wire [15:0] \总周期数 ;
  wire [19:0] shifter_2_out;
  wire [31:0] adder_1_out, adder_2_out, adder_3_out, adder_4_out, alu_res, beforeIntPC, bit_extender_1_out,
       bit_extender_2_out, bit_extender_3_out, bit_extender_4_out, bit_extender_5_out, intPC, mEPC1_q,
       mEPC2_q, mEPC3_q, multiplexer_1_out, multiplexer_8_out, multiplexer_9_out, multiplexer_10_out,
       multiplexer_12_out, multiplexer_13_out, ram_1_data, regifile_1_r1, uretPC;

  Button \u_继续运行  (.out(Go));
  Button _1 (.out(IRA));
  Button _2 (.out(IRB));
  Button _3 (.out(IRC));
  LED #(.active("true")) led_1 (.in(W1));
  LED #(.active("true")) led_2 (.in(W2));
  LED #(.active("true")) led_3 (.in(W3));
  and and_1 (and_1_out, ~uret, ~\int );  // AND_Gate
  Hex_Digit_Display hex_digit_display_1 (.value(LedData[31:28]));  // open: dp
  Comparator #(.width(16), .mode("twosComplement")) comparator_1 (
    .a(\总周期数 ), .b(16'h7), .eq(comparator_1_eq));  // open: gt, lt
  Comparator #(.width(16), .mode("twosComplement")) comparator_2 (
    .a(\总周期数 ), .b(16'h241), .eq(comparator_2_eq));  // open: gt, lt
  Priority_Encoder #(.select(2), .disabled("Z")) priority_encoder_1 (
    .in0(and_1_out), .in1(uret), .in2(\int ), .out(priority_encoder_1_out));  // open: in3, gs, en_out, en_in
  or or_1 (or_1_out[0], jal, B);
  or or_2 (W2, IR2_q, d_ff_2_q);
  or or_3 (W3, IR3_q, d_ff_3_q);
  Hex_Digit_Display hex_digit_display_2 (.value(LedData[27:24]));  // open: dp
  Hex_Digit_Display hex_digit_display_3 (.value(LedData[23:20]));  // open: dp
  Comparator #(.width(16), .mode("twosComplement")) comparator_3 (
    .a(16'h258), .b(\总周期数 ), .eq(comparator_3_eq));  // open: gt, lt
  or or_4 (or_4_out, comparator_3_eq, comparator_4_eq);
  Comparator #(.width(16), .mode("twosComplement")) comparator_4 (
    .a(\总周期数 ), .b(16'h1), .eq(comparator_4_eq));  // open: gt, lt
  Comparator #(.width(16), .mode("twosComplement")) comparator_5 (
    .a(\总周期数 ), .b(16'h4), .eq(comparator_5_eq));  // open: gt, lt
  or or_5 (or_5_out, comparator_1_eq, comparator_2_eq);
  Multiplexer #(.select(2), .width(32), .disabled("Z"), .enable("false")) multiplexer_1 (
    .in0(beforeIntPC), .in1(uretPC), .in2(intPC), .out(multiplexer_1_out), .sel(priority_encoder_1_out));  // open: in3
  Multiplexer #(.select(2), .width(32), .disabled("Z"), .enable("false")) multiplexer_2 (
    .in0(adder_1_out), .in1(multiplexer_12_out), .in2(alu_res), .out(beforeIntPC), .sel({jalr, or_1_out[0]}));  // open: in3
  D_Flip_Flop #(.trigger("rising"), .Pre_Clr_Positions("LEGACY"), .NegatePresetClear("false"), .enable("true"), .NewFFLayout("false")) d_ff_1 (
    .clk(IR1_t), .D(1'b1), .Q(d_ff_1_q), .reset(IR1_q));  // open: Qn, preset, en
  or or_6 (W1, IR1_q, d_ff_1_q);
  D_Flip_Flop #(.trigger("rising"), .Pre_Clr_Positions("LEGACY"), .NegatePresetClear("false"), .enable("true"), .NewFFLayout("false")) d_ff_2 (
    .clk(IR2_t), .D(1'b1), .Q(d_ff_2_q), .reset(IR2_q));  // open: Qn, preset, en
  D_Flip_Flop #(.trigger("rising"), .Pre_Clr_Positions("LEGACY"), .NegatePresetClear("false"), .enable("true"), .NewFFLayout("false")) d_ff_3 (
    .clk(IR3_t), .D(1'b1), .Q(d_ff_3_q), .reset(IR3_q));  // open: Qn, preset, en
  Hex_Digit_Display hex_digit_display_4 (.value(LedData[19:16]));  // open: dp
  Hex_Digit_Display hex_digit_display_5 (.value(LedData[15:12]));  // open: dp
  Pull_Resistor #(.pull(0)) pull_resistor_1 (.node(IRA));
  assign IRA = or_4_out ? ~CLK : 1'bz;  // Controlled_Inverter controlled_inverter_1
  Pull_Resistor #(.pull(0)) pull_resistor_2 (.node(IRB));
  assign IRB = comparator_5_eq ? ~CLK : 1'bz;  // Controlled_Inverter controlled_inverter_2
  Pull_Resistor #(.pull(0)) pull_resistor_3 (.node(IRC));
  assign IRC = or_5_out ? ~CLK : 1'bz;  // Controlled_Inverter controlled_inverter_3
  and and_2 (and_2_out, ~tunnel, ecall);  // AND_Gate
  not not_1 (not_1_out, halt);
  or or_7 (or_7_out, d_ff_1_q, IR1_q);
  or or_8 (or_8_out, d_ff_2_q, IR2_q);
  or or_9 (or_9_out, d_ff_3_q, IR3_q);
  Hex_Digit_Display hex_digit_display_6 (.value(LedData[7:4]));  // open: dp
  Hex_Digit_Display hex_digit_display_7 (.value(LedData[11:8]));  // open: dp
  // Probe on \总周期数 
  not not_2 (en, halt);
  and and_3 (halt, ~Go, and_2_out);  // AND_Gate
  Register #(.width(32), .trigger("rising"), .Select("low")) u_PC (
    .D(multiplexer_1_out), .en(not_1_out), .Q(PC), .clk(CLK), .clr(RST));
  and and_4 (and_4_out, or_7_out, ~CLR1);  // AND_Gate
  and and_5 (and_5_out, or_8_out, ~CLR2);  // AND_Gate
  and and_6 (and_6_out, or_9_out, ~CLR3);  // AND_Gate
  Hex_Digit_Display hex_digit_display_8 (.value(LedData[3:0]));  // open: dp
  Button button_1 (.out(RST));
  Adder #(.width(32)) adder_1 (.a(PC), .b(32'h4), .out(adder_1_out));  // open: cin, cout
  D_Flip_Flop #(.trigger("rising"), .Pre_Clr_Positions("LEGACY"), .NegatePresetClear("false"), .enable("true"), .NewFFLayout("false")) u_IR1 (
    .clk(CLK), .D(and_4_out), .Q(IR1_q));  // open: Qn, preset, en, reset
  D_Flip_Flop #(.trigger("rising"), .Pre_Clr_Positions("LEGACY"), .NegatePresetClear("false"), .enable("true"), .NewFFLayout("false")) u_IR2 (
    .clk(CLK), .D(and_5_out), .Q(IR2_q));  // open: Qn, preset, en, reset
  D_Flip_Flop #(.trigger("rising"), .Pre_Clr_Positions("LEGACY"), .NegatePresetClear("false"), .enable("true"), .NewFFLayout("false")) u_IR3 (
    .clk(CLK), .D(and_6_out), .Q(IR3_q));  // open: Qn, preset, en, reset
  // RiscV_Probe riscv_probe_1: pin names not known; wires that end beside it: IR
  or or_10 (IR1_t, IR1, IRA);
  ROM #(.addrWidth(10), .dataWidth(32), .Select("high")) rom_1 (.addr(PC[11:2]), .data(IR));
  Decoder #(.select(2), .tristate("false"), .disabled("Z"), .enable("false")) decoder_1 (
    .out1(decoder_1_out1), .out2(decoder_1_out2), .out3(decoder_1_out3), .sel(newIntID));  // open: out0
  or or_11 (IR2_t, IR2, IRB);
  Priority_Encoder #(.select(2), .disabled("Z")) priority_encoder_2 (
    .in0(1'b1), .in1(IR1_q), .in2(IR2_q), .in3(IR3_q), .out(newIntID));  // open: gs, en_out, en_in
  \单周期硬布线控制器  \u_单周期硬布线控制器_1  (
    .Funct({IR[30], IR[25], IR[14:12]}), .OP(IR[6:2]), .ALU_OP(\单周期硬布线控制器_1_alu_op ),
    .MemToReg(\单周期硬布线控制器_1_memtoreg ), .MemWrite(MemWrite), .ALU_SRC(\单周期硬布线控制器_1_alu_src ),
    .RegWrite(RegWrite), .ecall(ecall), .S_type(S_type), .Jalr(jalr), .Beq(\单周期硬布线控制器_1_beq ), .JAL(jal),
    .Bne(\单周期硬布线控制器_1_bne ), .in_3(IR[21]), .uret(uret), .lb(lb), .blt(blt), .CSRRSI(CSRRSI), .CSRRCI(CSRRCI));
  Multiplexer #(.select(1), .width(5), .disabled("Z"), .enable("false")) multiplexer_3 (
    .in0(IR[19:15]), .in1(5'b10001), .out(multiplexer_3_out), .sel(ecall));
  Multiplexer #(.select(1), .width(5), .disabled("Z"), .enable("false")) multiplexer_4 (
    .in0(IR[24:20]), .in1(5'b01010), .out(multiplexer_4_out), .sel(ecall));
  Multiplexer #(.select(1), .width(2), .disabled("Z"), .enable("false")) multiplexer_5 (
    .in0(multiplexer_5_out), .in1(newIntID), .out(multiplexer_5_out), .sel(IE));
  Register #(.width(1), .trigger("rising"), .Select("low")) register_1 (
    .D(1'b1), .en(decoder_1_out1), .Q(register_1_q), .clk(intReach), .clr(CLR1));
  Register #(.width(1), .trigger("rising"), .Select("low")) register_2 (
    .D(1'b1), .en(decoder_1_out2), .Q(register_2_q), .clk(intReach), .clr(CLR2));
  Register #(.width(1), .trigger("rising"), .Select("low")) register_3 (
    .D(1'b1), .en(decoder_1_out3), .Q(register_3_q), .clk(intReach), .clr(CLR3));
  or or_12 (IR3_t, IR3, IRC);
  assign bit_extender_1_out = {{20{IR[31]}}, IR[31:20]};  // Bit_Extender bit_extender_1
  assign bit_extender_2_out = {{20{IR[31]}}, {IR[31:25], IR[11:7]}};  // Bit_Extender bit_extender_2
  Shifter #(.width(12), .shift("ll")) shifter_1 (
    .in({IR[31], IR[7], IR[30:25], IR[11:8]}), .\dist (4'b0001), .out(shifter_1_out));
  Shifter #(.width(20), .shift("ll")) shifter_2 (
    .in({IR[31], IR[19:12], IR[20], IR[30:21]}), .\dist (5'b00001), .out(shifter_2_out));
  Multiplexer #(.select(2), .width(32), .disabled("Z"), .enable("false")) multiplexer_6 (
    .in1(32'h30ac), .in2(32'h3158), .in3(32'h3204), .out(intPC), .sel(newIntID));  // open: in0
  Register #(.width(2), .trigger("rising"), .Select("low")) register_4 (
    .D(multiplexer_5_out), .Q(intID), .clk(CLK));  // open: en, clr
  Multiplexer #(.select(2), .width(1), .disabled("Z"), .enable("false")) multiplexer_7 (
    .in0(1'b1), .in1(register_1_q), .in2(register_2_q), .in3(register_3_q), .out(hasInt), .sel(newIntID));
  Regifile regifile_1 (
    .Din(RDin), .Clk(CLK), .R1(regifile_1_r1), .R2(MDin), .WE(RegWrite), .W_num(IR[11:7]),
    .R1_num(multiplexer_3_out), .R2_num(multiplexer_4_out));
  Multiplexer #(.select(1), .width(32), .disabled("Z"), .enable("false")) multiplexer_8 (
    .in0(bit_extender_1_out), .in1(bit_extender_2_out), .out(multiplexer_8_out), .sel(S_type));
  assign bit_extender_3_out = {{20{shifter_1_out[11]}}, shifter_1_out};  // Bit_Extender bit_extender_3
  assign bit_extender_4_out = {{12{shifter_2_out[19]}}, shifter_2_out};  // Bit_Extender bit_extender_4
  Comparator #(.width(2), .mode("unsigned")) comparator_6 (
    .a(multiplexer_5_out), .b(intID), .eq(comparator_6_eq));  // open: gt, lt
  Multiplexer #(.select(1), .width(32), .disabled("Z"), .enable("false")) multiplexer_9 (
    .in0(multiplexer_8_out), .in1(32'h22), .out(multiplexer_9_out), .sel(ecall));
  Adder #(.width(32)) adder_2 (.a(PC), .b(bit_extender_4_out), .out(adder_2_out));  // open: cin, cout
  Multiplexer #(.select(1), .width(32), .disabled("Z"), .enable("false")) multiplexer_10 (
    .in0(MDin), .in1(multiplexer_9_out), .out(multiplexer_10_out), .sel(\单周期硬布线控制器_1_alu_src ));
  Adder #(.width(32)) adder_3 (.a(PC), .b(bit_extender_3_out), .out(adder_3_out));  // open: cin, cout
  and and_7 (\int , ~comparator_6_eq, ~hasInt);  // AND_Gate
  ALU alu_1 (
    .X(regifile_1_r1), .Y(multiplexer_10_out), .AluOP(\单周期硬布线控制器_1_alu_op ), .Equal(tunnel),
    .Result(alu_res), .out_6(alu_1_out_6));  // open: Result_2, out_4
  Multiplexer #(.select(1), .width(32), .disabled("Z"), .enable("false")) multiplexer_11 (
    .in0(multiplexer_13_out), .in1(adder_4_out), .out(RDin), .sel(or_13_out));
  or or_13 (or_13_out, jalr, jal);
  Multiplexer #(.select(1), .width(32), .disabled("Z"), .enable("false")) multiplexer_12 (
    .in0(adder_3_out), .in1(adder_2_out), .out(multiplexer_12_out), .sel(jal));
  Register #(.width(1), .trigger("rising"), .Select("low")) register_5 (
    .D(\int ), .Q(intReach), .clk(CLK));  // open: en, clr
  Adder #(.width(32)) adder_4 (.a(32'h4), .b(PC), .out(adder_4_out));  // open: cin, cout
  and and_8 (and_8_out, ~uret, ~CSRRSI);  // AND_Gate
  and and_9 (and_9_out, \单周期硬布线控制器_1_beq , tunnel);
  and and_10 (and_10_out, \单周期硬布线控制器_1_bne , ~tunnel);  // AND_Gate
  not not_3 (IE, IE_q);
  Register #(.width(1), .trigger("rising"), .Select("low")) u_IE (
    .D(1'b0), .Q(IE_q), .clk(and_8_out), .clr(RST), .preset(CSRRCI));  // open: en, cs
  D_Flip_Flop #(.trigger("high"), .Pre_Clr_Positions("LEGACY"), .NegatePresetClear("false"), .enable("true"), .NewFFLayout("false")) d_ff_4 (.Q(d_ff_4_q));  // open: clk, D, Qn, preset, en, reset
  // Probe on 13'hcd
  and and_11 (and_11_out, blt, alu_1_out_6);
  Multiplexer #(.select(1), .width(32), .disabled("Z"), .enable("false")) multiplexer_13 (
    .in0({multiplexer_14_out_4, multiplexer_14_out_3, multiplexer_14_out_2, multiplexer_14_out}),
    .in1(bit_extender_5_out), .out(multiplexer_13_out), .sel(lb));
  Register #(.width(32), .trigger("rising"), .Select("low")) register_6 (
    .D(MDin), .en(ecall), .Q(LedData), .clk(CLK));  // open: clr
  Decoder #(.select(2), .tristate("false"), .disabled("Z"), .enable("false")) decoder_2 (
    .out1(decoder_2_out1), .out2(decoder_2_out2), .out3(decoder_2_out3), .sel(intID));  // open: out0
  Comparator #(.width(13), .mode("twosComplement")) comparator_7 (
    .a(CNT_num), .b(13'hcd), .eq(comparator_7_eq), .lt(comparator_7_lt));  // open: gt
  Clock #(.highDuration(1), .lowDuration(1)) clock_1 (.out(clock_1_out));
  Counter #(.width(16), .max('hffff), .ongoal("stay"), .trigger("rising"), .behavior("new")) counter_1 (
    .count(en), .Q(\总周期数 ), .clk(CLK));  // open: load, D, carry, clr, preset, down
  or or_14 (B, and_9_out, and_10_out, and_11_out);
  RAM #(.addrWidth(10), .dataWidth(32), .bus("separate"), .Select("high")) ram_1 (
    .addr(alu_res[11:2]), .din(MDin), .data(ram_1_data), .str(MemWrite), .clk(CLK));  // open: sel, ld, clr
  Counter #(.width(13), .max('h1fff), .ongoal("stay"), .trigger("rising"), .behavior("old")) counter_2 (
    .count(comparator_7_lt), .Q(CNT_num), .clk(clock_1_out));  // open: load, D, carry, clr, preset
  Multiplexer #(.select(1), .width(32), .disabled("Z"), .enable("false")) multiplexer_14 (
    .in0(alu_res), .in1(ram_1_data),
    .out({multiplexer_14_out_4, multiplexer_14_out_3, multiplexer_14_out_2, multiplexer_14_out}),
    .sel(\单周期硬布线控制器_1_memtoreg ));
  assign bit_extender_5_out = {{24{multiplexer_15_out[7]}}, multiplexer_15_out};  // Bit_Extender bit_extender_5
  or or_15 (or_15_out, \int , uret);
  and and_12 (CLR1, decoder_2_out1, uret);
  and and_13 (CLR2, decoder_2_out2, uret);
  and and_14 (CLR3, decoder_2_out3, uret);
  nand nand_1 (nand_1_out, d_ff_4_q, comparator_7_eq);
  Multiplexer #(.select(2), .width(8), .disabled("Z"), .enable("false")) multiplexer_15 (
    .in0(multiplexer_14_out), .in1(multiplexer_14_out_2), .in2(multiplexer_14_out_3),
    .in3(multiplexer_14_out_4), .out(multiplexer_15_out), .sel(alu_res[1:0]));
  Counter #(.width(2), .max('h3), .ongoal("wrap"), .trigger("rising"), .behavior("new")) counter_3 (
    .count(or_15_out), .Q(stack), .clk(CLK), .down(uret));  // open: load, D, carry, clr, preset
  Decoder #(.select(2), .tristate("false"), .disabled("Z"), .enable("false")) decoder_3 (
    .out0(decoder_3_out0), .out1(decoder_3_out1), .out2(decoder_3_out2), .sel(stack));  // open: out3
  assign CLK = nand_1_out ? clock_1_out : 1'bz;  // Controlled_Buffer controlled_buffer_1
  Pull_Resistor #(.pull(1)) pull_resistor_4 (.node(CLK));
  Register #(.width(32), .trigger("rising"), .Select("low")) mEPC1 (
    .D(beforeIntPC), .en(decoder_3_out0), .Q(mEPC1_q), .clk(CLK), .clr(RST));
  Register #(.width(32), .trigger("rising"), .Select("low")) mEPC2 (
    .D(beforeIntPC), .en(decoder_3_out1), .Q(mEPC2_q), .clk(CLK), .clr(RST));
  Register #(.width(32), .trigger("rising"), .Select("low")) mEPC3 (
    .D(beforeIntPC), .en(decoder_3_out2), .Q(mEPC3_q), .clk(CLK), .clr(RST));
  Multiplexer #(.select(2), .width(32), .disabled("Z"), .enable("false")) multiplexer_16 (
    .in1(mEPC1_q), .in2(mEPC2_q), .in3(mEPC3_q), .out(uretPC), .sel(stack));  // open: in0

  // Other names for the same wires on the sheet: R2data[31:0] = MDin

  // Notes on the sheet:
  //   中断源
  //   中断等待指示
  //   总复位信号应将除ROM以外所有存储组件全部清零
  //   多级中断测试信号模拟器
  //   数码管输出
  //   数码管输出应该用寄存器锁存，否则显示数据只能一闪而过
  //   指令探针
  //   指令存储器
  //   指令字
  //   contents of rom_1 (hex, n*v repeats v):
  //   7d000113 100413 1f41993 41f9d993 433 c00913 800b13 140413 f47413 800293 100313 499993 89e9b3 1300533
  //   2200893 73 406282b3 fe0294e3 140413 f00f93 1f47433 1c41413 800293 100313 49d993 89e9b3 1300533
  //   2200893 73 406282b3 fe0294e3 1c45413 406b0b33 b0463 f95ff06f 2b3 fff2c293 1029293 fff2e293 500533
  //   2200893 73 f5dff06f 1112023 410113 a12023 410113 812023 410113 1312023 410113 1412023 410113 1512023
  //   410113 1612023 410113 40e073 100b13 300a13 100a93 1600433 441413 14469b3 1300533 2200893 73 fe0416e3
  //   415a0a33 fe0a10e3 40f073 ffc10113 12b03 ffc10113 12a83 ffc10113 12a03 ffc10113 12983 ffc10113 12403
  //   ffc10113 12503 ffc10113 12883 200073 1112023 410113 a12023 410113 812023 410113 1312023 410113
  //   1412023 410113 1512023 410113 1612023 410113 40e073 200b13 300a13 100a93 1600433 441413 14469b3
  //   1300533 2200893 73 fe0416e3 415a0a33 fe0a10e3 40f073 ffc10113 12b03 ffc10113 12a83 ffc10113 12a03
  //   ffc10113 12983 ffc10113 12403 ffc10113 12503 ffc10113 12883 200073 1112023 410113 a12023 410113
  //   812023 410113 1312023 410113 1412023 410113 1512023 410113 1612023 410113 40e073 300b13 300a13
  //   100a93 1600433 441413 14469b3 1300533 2200893 73 fe0416e3 415a0a33 fe0a10e3 40f073 ffc10113 12b03
  //   ffc10113 12a83 ffc10113 12a03 ffc10113 12983 ffc10113 12403 ffc10113 12503 ffc10113 12883 200073
  //   JAL
  //   JALR
  //   URET
  //   I jalr
  //   sw
  //   B
  //   Beq
  //   Bne
  //   MemToReg
  //   MemWrite
  //   AluOP
  //   AluSrcB
  //   RegWrite
  //   jal
  //   为方便自动评测，需要输出PC，IR，寄存器堆写如数据RDin
  //   RAM写使能MemWrite、RAM写入数据MDin等信号
  //   控制位
  //   暂停节拍，不能为0
  //   数据存储器
  //   戳工具置1进入计数暂停模式，ctrl+k时钟自动运行到对应节拍暂停
  //   ctrl+k关闭时钟连续运行，将控制位置零，进入单步调试模式调试
  //   可计数暂停的时钟源
endmodule

module \流水中断  (
  input  IR1,
  input  IR2,
  input  IR3,
  output RegWrite,
  output MemWrite,
  output [31:0] PC,
  output [31:0] IR,
  output [31:0] RDin,
  output [31:0] MDin,
  output [31:0] LedData
);

  wire alu_1_out_6, and_1_out, and_2_out, and_3_out, and_4_out, and_5_out, and_6_out, and_7_out, and_12_out,
       and_13_out, and_14_out, and_15_out, branch, CLK, clock_1_out, CLR1, CLR2, CLR3, comparator_1_eq,
       comparator_2_eq, comparator_2_lt, d_ff_1_q, d_ff_2_q, d_ff_3_q, d_ff_4_q, decoder_1_out1,
       decoder_1_out2, decoder_1_out3, en, EX, EX_B, EX_ecall, EX_jal, EX_jalr, EX_uret, Go, halt, ID_ecall,
       ID_uret, IE_q, \int , IR1_q, IR1_t, IR2_q, IR2_t, IR3_q, IR3_t, IRA, IRB, IRC, LoadUse, MEM_RegWrite,
       nand_1_out, not_1_out, or_5_out, or_6_out, or_7_out, or_8_out, or_12_out, or_15_out, or_16_out,
       priority_encoder_2_gs, RST, W1, W2, W3, WB, WB_ecall, \单周期硬布线控制器_1_s_type ;
  wire [0:0] or_1_out;
  wire [1:0] IE_2_q, intID, priority_encoder_1_out;
  wire [3:0] \单周期硬布线控制器_1_alu_op ;
  wire [4:0] EX_W_num, MEM_W_num, mem_wb_1_ctrlsignal_2, multiplexer_3_out, multiplexer_4_out, WD_W_num;
  wire [4:1] \id_ex_重定向_中断_1_ctrlsignal_2_2 , pckSignal;
  wire [7:0] ex_mem_1_ctrlsignal_2, multiplexer_14_out;
  wire [11:0] \id_ex_重定向_中断_1_badd_2 , shifter_1_out;
  wire [12:0] CNT_num;
  wire [13:0] \单周期硬布线控制器_1_jal ;
  wire [13:2] \id_ex_重定向_中断_1_ctrlsignal_2 ;
  wire [15:0] \总周期数 ;
  wire [19:0] \id_ex_重定向_中断_1_j_2 , multiplexer_8_out, shifter_2_out;
  wire [31:0] A1, A2, adder_1_out, adder_2_out, adder_3_out, adder_4_out, B1, B2, bit_extender_1_out,
       bit_extender_2_out, bit_extender_3_out, bit_extender_4_out, bit_extender_5_out, EX_ALU_res, EX_IR,
       EX_PC, \id_ex_重定向_中断_1_imm_2 , ID_IR, ID_PC, IF_IR, IF_PC, intPC, MEM_alu_res, MEM_IR, MEM_PC,
       mem_wb_1_alu_2, mem_wb_1_md_2, multiplexer_1_out, multiplexer_2_out, multiplexer_5_out,
       multiplexer_7_out, multiplexer_9_out, multiplexer_12_out, multiplexer_13_out, multiplexer_15_out,
       ram_1_data, regifile_1_r1, regifile_1_r2, uretPC, WB_IR, WB_PC;

  Button \u_继续运行  (.out(Go));
  Button _1 (.out(IRA));
  Button _2 (.out(IRB));
  Button _3 (.out(IRC));
  // Probe on \总周期数 
  // Probe on \总周期数 
  LED #(.active("true")) led_1 (.in(W1));
  LED #(.active("true")) led_2 (.in(W2));
  LED #(.active("true")) led_3 (.in(W3));
  Button button_1 (.out(RST));
  and and_1 (and_1_out, ~EX_uret, ~\int );  // AND_Gate
  Hex_Digit_Display hex_digit_display_1 (.value(LedData[31:28]));  // open: dp
  // Probe on IF_PC[19:0]
  // RiscV_Probe riscv_probe_1: pin names not known; wires that end beside it: IF_IR
  Priority_Encoder #(.select(2), .disabled("Z")) priority_encoder_1 (
    .in0(and_1_out), .in1(EX_uret), .in2(\int ), .out(priority_encoder_1_out));  // open: in3, gs, en_out, en_in
  or or_1 (or_1_out[0], EX_jal, EX_B);
  Hex_Digit_Display hex_digit_display_2 (.value(LedData[27:24]));  // open: dp
  Hex_Digit_Display hex_digit_display_3 (.value(LedData[23:20]));  // open: dp
  // Probe on ID_PC[19:0]
  // RiscV_Probe riscv_probe_2: pin names not known; wires that end beside it: ID_IR
  and and_2 (and_2_out, ~LoadUse, en);  // AND_Gate
  Multiplexer #(.select(2), .width(32), .disabled("Z"), .enable("false")) multiplexer_1 (
    .in0(multiplexer_2_out), .in1(uretPC), .in2(intPC), .out(multiplexer_1_out), .sel(priority_encoder_1_out));  // open: in3
  Multiplexer #(.select(2), .width(32), .disabled("Z"), .enable("false")) multiplexer_2 (
    .in0(adder_1_out), .in1(multiplexer_12_out), .in2(EX_ALU_res), .out(multiplexer_2_out),
    .sel({EX_jalr, or_1_out[0]}));  // open: in3
  or or_2 (W1, IR1_q, d_ff_1_q);
  or or_3 (W2, IR2_q, d_ff_2_q);
  or or_4 (W3, IR3_q, d_ff_3_q);
  Hex_Digit_Display hex_digit_display_4 (.value(LedData[19:16]));  // open: dp
  Hex_Digit_Display hex_digit_display_5 (.value(LedData[15:12]));  // open: dp
  Register #(.width(32), .trigger("rising"), .Select("low")) u_PC (
    .D(multiplexer_1_out), .en(and_2_out), .Q(IF_PC), .clk(CLK), .clr(RST));
  D_Flip_Flop #(.trigger("rising"), .Pre_Clr_Positions("LEGACY"), .NegatePresetClear("false"), .enable("true"), .NewFFLayout("false")) d_ff_1 (
    .clk(IR1_t), .D(1'b1), .Q(d_ff_1_q), .reset(IR1_q));  // open: Qn, preset, en
  D_Flip_Flop #(.trigger("rising"), .Pre_Clr_Positions("LEGACY"), .NegatePresetClear("false"), .enable("true"), .NewFFLayout("false")) d_ff_2 (
    .clk(IR2_t), .D(1'b1), .Q(d_ff_2_q), .reset(IR2_q));  // open: Qn, preset, en
  D_Flip_Flop #(.trigger("rising"), .Pre_Clr_Positions("LEGACY"), .NegatePresetClear("false"), .enable("true"), .NewFFLayout("false")) d_ff_3 (
    .clk(IR3_t), .D(1'b1), .Q(d_ff_3_q), .reset(IR3_q));  // open: Qn, preset, en
  Hex_Digit_Display hex_digit_display_6 (.value(LedData[7:4]));  // open: dp
  Hex_Digit_Display hex_digit_display_7 (.value(LedData[11:8]));  // open: dp
  // Probe on \总周期数 
  // Probe on EX_PC[19:0]
  // RiscV_Probe riscv_probe_3: pin names not known; wires that end beside it: EX_IR
  Adder #(.width(32)) adder_1 (.a(IF_PC), .b(32'h4), .out(adder_1_out));  // open: cin, cout
  or or_5 (or_5_out, d_ff_1_q, IR1_q);
  or or_6 (or_6_out, d_ff_2_q, IR2_q);
  or or_7 (or_7_out, d_ff_3_q, IR3_q);
  Hex_Digit_Display hex_digit_display_8 (.value(LedData[3:0]));  // open: dp
  and and_3 (and_3_out, or_5_out, ~CLR1);  // AND_Gate
  and and_4 (and_4_out, or_6_out, ~CLR2);  // AND_Gate
  and and_5 (and_5_out, or_7_out, ~CLR3);  // AND_Gate
  // Probe on MEM_PC[19:0]
  // RiscV_Probe riscv_probe_4: pin names not known; wires that end beside it: MEM_IR
  or or_8 (or_8_out, RST, \int , branch, EX_uret);
  ROM #(.addrWidth(10), .dataWidth(32), .Select("high")) rom_1 (.addr(IF_PC[11:2]), .data(IF_IR));
  IF_ID if_id_1 (.PC_2(ID_PC), .IR_2(ID_IR), .PC(IF_PC), .IR(IF_IR), .CLK(CLK), .CLR(or_8_out), .en(and_6_out));
  and and_6 (and_6_out, ~LoadUse, en);  // AND_Gate
  D_Flip_Flop #(.trigger("rising"), .Pre_Clr_Positions("LEGACY"), .NegatePresetClear("false"), .enable("true"), .NewFFLayout("false")) u_IR1 (
    .clk(CLK), .D(and_3_out), .Q(IR1_q));  // open: Qn, preset, en, reset
  D_Flip_Flop #(.trigger("rising"), .Pre_Clr_Positions("LEGACY"), .NegatePresetClear("false"), .enable("true"), .NewFFLayout("false")) u_IR2 (
    .clk(CLK), .D(and_4_out), .Q(IR2_q));  // open: Qn, preset, en, reset
  D_Flip_Flop #(.trigger("rising"), .Pre_Clr_Positions("LEGACY"), .NegatePresetClear("false"), .enable("true"), .NewFFLayout("false")) u_IR3 (
    .clk(CLK), .D(and_5_out), .Q(IR3_q));  // open: Qn, preset, en, reset
  or or_9 (IR1_t, IR1, IRA);
  or or_10 (IR2_t, IR2, IRB);
  // Probe on WB_PC[19:0]
  // RiscV_Probe riscv_probe_5: pin names not known; wires that end beside it: WB_IR
  \单周期硬布线控制器  \u_单周期硬布线控制器_1  (
    .Funct({ID_IR[30], ID_IR[25], ID_IR[14:12]}), .OP(ID_IR[6:2]), .ALU_OP(\单周期硬布线控制器_1_alu_op ),
    .MemToReg(\单周期硬布线控制器_1_jal [3]), .MemWrite(\单周期硬布线控制器_1_jal [4]), .ALU_SRC(\单周期硬布线控制器_1_jal [13]),
    .RegWrite(\单周期硬布线控制器_1_jal [2]), .ecall(ID_ecall), .S_type(\单周期硬布线控制器_1_s_type ),
    .Jalr(\单周期硬布线控制器_1_jal [1]), .Beq(\单周期硬布线控制器_1_jal [10]), .JAL(\单周期硬布线控制器_1_jal [0]),
    .Bne(\单周期硬布线控制器_1_jal [11]), .in_3(ID_IR[21]), .uret(ID_uret), .lb(\单周期硬布线控制器_1_jal [5]),
    .blt(\单周期硬布线控制器_1_jal [12]));  // open: CSRRSI, CSRRCI
  Multiplexer #(.select(1), .width(5), .disabled("Z"), .enable("false")) multiplexer_3 (
    .in0(ID_IR[19:15]), .in1(5'b10001), .out(multiplexer_3_out), .sel(ID_ecall));
  Multiplexer #(.select(1), .width(5), .disabled("Z"), .enable("false")) multiplexer_4 (
    .in0(ID_IR[24:20]), .in1(5'b01010), .out(multiplexer_4_out), .sel(ID_ecall));
  assign bit_extender_1_out = {{20{ID_IR[31]}}, ID_IR[31:20]};  // Bit_Extender bit_extender_1
  assign bit_extender_2_out = {{20{ID_IR[31]}}, {ID_IR[31:25], ID_IR[11:7]}};  // Bit_Extender bit_extender_2
  Priority_Encoder #(.select(2), .disabled("Z")) priority_encoder_2 (
    .in1(IR1_q), .in2(IR2_q), .in3(IR3_q), .out(intID), .gs(priority_encoder_2_gs));  // open: in0, en_out, en_in
  or or_11 (IR3_t, IR3, IRC);
  Multiplexer #(.select(1), .width(32), .disabled("Z"), .enable("false")) multiplexer_5 (
    .in0(bit_extender_1_out), .in1(bit_extender_2_out), .out(multiplexer_5_out), .sel(\单周期硬布线控制器_1_s_type ));
  Multiplexer #(.select(2), .width(32), .disabled("Z"), .enable("false")) multiplexer_6 (
    .in1(32'h30ac), .in2(32'h3150), .in3(32'h31f4), .out(intPC), .sel(intID));  // open: in0
  Multiplexer #(.select(1), .width(32), .disabled("Z"), .enable("false")) multiplexer_7 (
    .in0(multiplexer_5_out), .in1(32'h22), .out(multiplexer_7_out), .sel(ID_ecall));
  Regifile regifile_1 (
    .Din(RDin), .Clk(CLK), .R1(regifile_1_r1), .R2(regifile_1_r2), .WE(RegWrite), .W_num(WD_W_num),
    .R1_num(multiplexer_3_out), .R2_num(multiplexer_4_out));
  \重定向相关处理逻辑  \u_重定向相关处理逻辑_1  (
    .op_code(ID_IR[6:2]), .Funct({ID_IR[30], ID_IR[25], ID_IR[14:12]}), .r1(multiplexer_3_out),
    .r2(multiplexer_4_out), .EX_MemRead(\id_ex_重定向_中断_1_ctrlsignal_2 [3]), .EX_WriteReg_num(EX_W_num),
    .EX_RegWrite(\id_ex_重定向_中断_1_ctrlsignal_2 [2]), .MEM_RegWrite(MEM_RegWrite),
    .MEM_WriteReg_num(MEM_W_num), .LoadUse(LoadUse), .r1Forward(pckSignal[2:1]), .r2Forward(pckSignal[4:3]));
  Comparator #(.width(32), .mode("twosComplement")) comparator_1 (
    .a(ID_IR), .b({32{1'b0}}), .eq(comparator_1_eq));  // open: gt, lt
  Multiplexer #(.select(1), .width(20), .disabled("Z"), .enable("false")) multiplexer_8 (
    .in0({ID_uret, pckSignal, ID_ecall, \单周期硬布线控制器_1_jal [13:10], \单周期硬布线控制器_1_alu_op , \单周期硬布线控制器_1_jal [5:0]}),
    .in1({20{1'b0}}), .out(multiplexer_8_out), .sel(comparator_1_eq));
  and and_7 (and_7_out, priority_encoder_2_gs, ~EX_uret);  // AND_Gate
  or or_12 (or_12_out, RST, LoadUse, EX_uret, branch, \int );
  \ID_EX_重定向_中断  \id_ex_重定向_中断_1  (
    .CLK(CLK), .CLR(or_12_out), .en(en), .PC(ID_PC), .imm(multiplexer_7_out), .IR(ID_IR),
    .ctrlSignal(multiplexer_8_out), .A(regifile_1_r1), .W_num(ID_IR[11:7]), .B(regifile_1_r2),
    .Badd({ID_IR[31], ID_IR[7], ID_IR[30:25], ID_IR[11:8]}),
    .J({ID_IR[31], ID_IR[19:12], ID_IR[20], ID_IR[30:21]}), .PC_2(EX_PC), .imm_2(\id_ex_重定向_中断_1_imm_2 ),
    .IR_2(EX_IR),
    .ctrlSignal_2({EX_uret, \id_ex_重定向_中断_1_ctrlsignal_2_2 , EX_ecall, \id_ex_重定向_中断_1_ctrlsignal_2 , EX_jalr, EX_jal}),
    .A_2(A1), .W_num_2(EX_W_num), .B_2(B1), .Badd_2(\id_ex_重定向_中断_1_badd_2 ), .J_2(\id_ex_重定向_中断_1_j_2 ));
  Register #(.width(1), .trigger("rising"), .Select("low")) IE (
    .D(and_7_out), .Q(IE_q), .clk(CLK), .clr(RST));  // open: en
  not not_1 (not_1_out, IE_q);
  Register #(.width(32), .trigger("rising"), .Select("low")) mEPC (
    .D(EX_PC), .en(\int ), .Q(uretPC), .clk(CLK), .clr(RST));
  Register #(.width(2), .trigger("rising"), .Select("low")) IE_2 (
    .D(intID), .en(\int ), .Q(IE_2_q), .clk(CLK), .clr(RST));
  Decoder #(.select(2), .tristate("false"), .disabled("Z"), .enable("false")) decoder_1 (
    .out1(decoder_1_out1), .out2(decoder_1_out2), .out3(decoder_1_out3), .sel(IE_2_q));  // open: out0
  and and_8 (\int , priority_encoder_2_gs, not_1_out);
  Multiplexer #(.select(1), .width(32), .disabled("Z"), .enable("false")) multiplexer_9 (
    .in0(B2), .in1(\id_ex_重定向_中断_1_imm_2 ), .out(multiplexer_9_out), .sel(\id_ex_重定向_中断_1_ctrlsignal_2 [13]));
  and and_9 (CLR1, decoder_1_out1, EX_uret);
  and and_10 (CLR2, decoder_1_out2, EX_uret);
  and and_11 (CLR3, decoder_1_out3, EX_uret);
  D_Flip_Flop #(.trigger("high"), .Pre_Clr_Positions("LEGACY"), .NegatePresetClear("false"), .enable("true"), .NewFFLayout("false")) d_ff_4 (.Q(d_ff_4_q));  // open: clk, D, Qn, preset, en, reset
  // Probe on 13'h15
  Multiplexer #(.select(2), .width(32), .disabled("Z"), .enable("false")) multiplexer_10 (
    .in0(A1), .in1(RDin), .in2(MEM_alu_res), .out(A2), .sel(\id_ex_重定向_中断_1_ctrlsignal_2_2 [2:1]));  // open: in3
  Multiplexer #(.select(2), .width(32), .disabled("Z"), .enable("false")) multiplexer_11 (
    .in0(B1), .in1(RDin), .in2(MEM_alu_res), .out(B2), .sel(\id_ex_重定向_中断_1_ctrlsignal_2_2 [4:3]));  // open: in3
  Shifter #(.width(12), .shift("ll")) shifter_1 (.in(\id_ex_重定向_中断_1_badd_2 ), .\dist (4'b0001), .out(shifter_1_out));
  assign bit_extender_3_out = {{20{shifter_1_out[11]}}, shifter_1_out};  // Bit_Extender bit_extender_3
  Shifter #(.width(20), .shift("ll")) shifter_2 (.in(\id_ex_重定向_中断_1_j_2 ), .\dist (5'b00001), .out(shifter_2_out));
  assign bit_extender_4_out = {{12{shifter_2_out[19]}}, shifter_2_out};  // Bit_Extender bit_extender_4
  Comparator #(.width(13), .mode("twosComplement")) comparator_2 (
    .a(CNT_num), .b(13'h15), .eq(comparator_2_eq), .lt(comparator_2_lt));  // open: gt
  Clock #(.highDuration(1), .lowDuration(1)) clock_1 (.out(clock_1_out));
  Counter #(.width(16), .max('hffff), .ongoal("stay"), .trigger("rising"), .behavior("new")) counter_1 (
    .count(en), .Q(\总周期数 ), .clk(CLK));  // open: load, D, carry, clr, preset, down
  and and_12 (and_12_out, \id_ex_重定向_中断_1_ctrlsignal_2 [11], ~EX);  // AND_Gate
  and and_13 (and_13_out, \id_ex_重定向_中断_1_ctrlsignal_2 [10], EX);
  ALU alu_1 (
    .X(A2), .Y(multiplexer_9_out), .AluOP(\id_ex_重定向_中断_1_ctrlsignal_2 [9:6]), .Equal(EX),
    .Result(EX_ALU_res), .out_6(alu_1_out_6));  // open: Result_2, out_4
  Counter #(.width(13), .max('h1fff), .ongoal("stay"), .trigger("rising"), .behavior("old")) counter_2 (
    .count(comparator_2_lt), .Q(CNT_num), .clk(clock_1_out));  // open: load, D, carry, clr, preset
  and and_14 (and_14_out, \id_ex_重定向_中断_1_ctrlsignal_2 [12], alu_1_out_6);
  Adder #(.width(32)) adder_2 (.a(bit_extender_3_out), .b(EX_PC), .out(adder_2_out));  // open: cin, cout
  Adder #(.width(32)) adder_3 (.a(bit_extender_4_out), .b(EX_PC), .out(adder_3_out));  // open: cin, cout
  or or_13 (branch, EX_B, EX_jal, EX_jalr);
  nand nand_1 (nand_1_out, d_ff_4_q, comparator_2_eq);
  or or_14 (EX_B, and_14_out, and_12_out, and_13_out);
  Multiplexer #(.select(1), .width(32), .disabled("Z"), .enable("false")) multiplexer_12 (
    .in0(adder_2_out), .in1(adder_3_out), .out(multiplexer_12_out), .sel(EX_jal));
  assign CLK = nand_1_out ? clock_1_out : 1'bz;  // Controlled_Buffer controlled_buffer_1
  Pull_Resistor #(.pull(1)) pull_resistor_1 (.node(CLK));
  or or_15 (or_15_out, RST, \int );
  EX_MEM ex_mem_1 (
    .PC_2(MEM_PC),
    .ctrlSignal_2({ex_mem_1_ctrlsignal_2[7:5], MemWrite, ex_mem_1_ctrlsignal_2[3], MEM_RegWrite, ex_mem_1_ctrlsignal_2[1:0]}),
    .IR_2(MEM_IR), .B_2(MDin), .ALU_2(MEM_alu_res), .PC(EX_PC),
    .ctrlSignal({EX, EX_ecall, \id_ex_重定向_中断_1_ctrlsignal_2 [5:2], EX_jalr, EX_jal}), .IR(EX_IR), .B(B2),
    .ALU(EX_ALU_res), .W_num_2(MEM_W_num), .W_num(EX_W_num), .CLK(CLK), .CLR(or_15_out), .en(en));
  RAM #(.addrWidth(10), .dataWidth(32), .bus("separate"), .Select("high")) ram_1 (
    .addr(MEM_alu_res[11:2]), .din(MDin), .data(ram_1_data), .str(MemWrite), .clk(CLK));  // open: sel, ld, clr
  MEM_WB mem_wb_1 (
    .PC(MEM_PC),
    .ctrlSignal({ex_mem_1_ctrlsignal_2[7:5], ex_mem_1_ctrlsignal_2[3], MEM_RegWrite, ex_mem_1_ctrlsignal_2[1:0]}),
    .IR(MEM_IR), .ALU(MEM_alu_res), .MD(ram_1_data), .PC_2(WB_PC),
    .ctrlSignal_2({WB, WB_ecall, mem_wb_1_ctrlsignal_2[4:3], RegWrite, mem_wb_1_ctrlsignal_2[1:0]}),
    .IR_2(WB_IR), .ALU_2(mem_wb_1_alu_2), .MD_2(mem_wb_1_md_2), .W_num(MEM_W_num), .W_num_2(WD_W_num),
    .en(en), .CLR(RST), .CLK(CLK));
  Multiplexer #(.select(1), .width(32), .disabled("Z"), .enable("false")) multiplexer_13 (
    .in0(mem_wb_1_alu_2), .in1(mem_wb_1_md_2), .out(multiplexer_13_out), .sel(mem_wb_1_ctrlsignal_2[3]));
  Multiplexer #(.select(2), .width(8), .disabled("Z"), .enable("false")) multiplexer_14 (
    .in0(multiplexer_13_out[7:0]), .in1(multiplexer_13_out[15:8]), .in2(multiplexer_13_out[23:16]),
    .in3(multiplexer_13_out[31:24]), .out(multiplexer_14_out), .sel(mem_wb_1_alu_2[1:0]));
  Multiplexer #(.select(1), .width(32), .disabled("Z"), .enable("false")) multiplexer_15 (
    .in0(multiplexer_13_out), .in1(bit_extender_5_out), .out(multiplexer_15_out),
    .sel(mem_wb_1_ctrlsignal_2[4]));
  assign bit_extender_5_out = {{24{multiplexer_14_out[7]}}, multiplexer_14_out};  // Bit_Extender bit_extender_5
  and and_15 (and_15_out, ~WB, WB_ecall);  // AND_Gate
  Register #(.width(32), .trigger("rising"), .Select("low")) register_1 (
    .D(B2), .en(EX_ecall), .Q(LedData), .clk(CLK));  // open: clr
  not not_2 (en, halt);
  and and_16 (halt, ~Go, and_15_out);  // AND_Gate
  Adder #(.width(32)) adder_4 (.a(32'h4), .b(WB_PC), .out(adder_4_out));  // open: cin, cout
  or or_16 (or_16_out, mem_wb_1_ctrlsignal_2[1], mem_wb_1_ctrlsignal_2[0]);
  Multiplexer #(.select(1), .width(32), .disabled("Z"), .enable("false")) multiplexer_16 (
    .in0(multiplexer_15_out), .in1(adder_4_out), .out(RDin), .sel(or_16_out));

  // Other names for the same wires on the sheet: ID_W_num[4:0] = ID_IR[11:7]; pckSignal[0] = ID_ecall;
  //   WB_RegWrite = RegWrite; R2data[31:0] = B2

  // Notes on the sheet:
  //   中断源
  //   时空图监测，可删除
  //   中断等待指示
  //   总复位信号应将除ROM以外所有存储组件全部清零
  //   数码管输出
  //   ID:jal 1;jalr 1;RegWrite 1;MemToReg 1;MemWrite 1;lb 1;ALUOP 4;Beq 1;Bne 1;Blt 1;AluSrc 1;ecall 1;r1Forward 2;r2Forward 2;uret 1;
  //   数码管输出应该用寄存器锁存，否则显示数据只能一闪而过
  //   MEM: ... = 1;
  //   指令存储器
  //   contents of rom_1 (hex, n*v repeats v):
  //   7d000113 100413 1f41993 41f9d993 433 c00913 800b13 140413 f47413 800293 100313 499993 89e9b3 1300533
  //   2200893 73 406282b3 fe0294e3 140413 f00f93 1f47433 1c41413 800293 100313 49d993 89e9b3 1300533
  //   2200893 73 406282b3 fe0294e3 1c45413 406b0b33 b0463 f95ff06f 2b3 fff2c293 1029293 fff2e293 500533
  //   2200893 73 f5dff06f 1112023 410113 a12023 410113 812023 410113 1312023 410113 1412023 410113 1512023
  //   410113 1612023 410113 100b13 300a13 100a93 1600433 441413 14469b3 1300533 2200893 73 fe0416e3
  //   415a0a33 fe0a10e3 ffc10113 12b03 ffc10113 12a83 ffc10113 12a03 ffc10113 12983 ffc10113 12403
  //   ffc10113 12503 ffc10113 12883 200073 1112023 410113 a12023 410113 812023 410113 1312023 410113
  //   1412023 410113 1512023 410113 1612023 410113 200b13 300a13 100a93 1600433 441413 14469b3 1300533
  //   2200893 73 fe0416e3 415a0a33 fe0a10e3 ffc10113 12b03 ffc10113 12a83 ffc10113 12a03 ffc10113 12983
  //   ffc10113 12403 ffc10113 12503 ffc10113 12883 200073 1112023 410113 a12023 410113 812023 410113
  //   1312023 410113 1412023 410113 1512023 410113 1612023 410113 300b13 300a13 100a93 1600433 441413
  //   14469b3 1300533 2200893 73 fe0416e3 415a0a33 fe0a10e3 ffc10113 12b03 ffc10113 12a83 ffc10113 12a03
  //   ffc10113 12983 ffc10113 12403 ffc10113 12503 ffc10113 12883 200073
  //   I jalr
  //   sw
  //   B
  //   jal
  //   为方便自动评测，需要输出PC，IR，寄存器堆写如数据RDin
  //   RAM写使能MemWrite、RAM写入数据MDin等信号
  //   控制位
  //   暂停节拍，不能为0
  //   戳工具置1进入计数暂停模式，ctrl+k时钟自动运行到对应节拍暂停
  //   ctrl+k关闭时钟连续运行，将控制位置零，进入单步调试模式调试
  //   可计数暂停的时钟源
  //   数据存储器
endmodule

module \封装正确性测试  (
);

  wire IR1, IR2, IR3, MemW, RegW;
  wire [31:0] EX_PC, ID_PC, IF_PC, IR, LED, MDin, MDinr, MEM_PC, PC, RDin, RDinr, WB_PC;

  \单周期RISC_V  \u_单周期risc_v_1  (
    .IR1(IR1), .IR2(IR2), .IR3(IR3), .RegWrite(RegW), .MemWrite(MemW), .PC(PC), .IR(IR), .RDin(RDin),
    .MDin(MDin), .LedData(LED));
  \气泡流水线  \u_气泡流水线_1  (
    .RegWrite(RegW), .MemWrite(MemW), .IF_PC(IF_PC), .ID_PC(ID_PC), .EX_PC(EX_PC), .M_PC(MEM_PC),
    .WB_PC(WB_PC), .RDin(RDinr), .MDin(MDinr), .LedData(LED));
  \单周期_单级中断  \u_单周期_单级中断_1  (
    .IR1(IR1), .IR2(IR2), .IR3(IR3), .RegWrite(RegW), .MemWrite(MemW), .PC(PC), .IR(IR), .RDin(RDin),
    .MDin(MDin), .LedData(LED));
  \理想流水线  \u_理想流水线_1  (
    .RegWrite(RegW), .MemWrite(MemW), .IF_PC(IF_PC), .ID_PC(ID_PC), .EX_PC(EX_PC), .M_PC(MEM_PC),
    .WB_PC(WB_PC), .RDin(RDinr), .MDin(MDinr), .LedData(LED));
  \重定向流水线  \u_重定向流水线_1  (
    .RegWrite(RegW), .MemWrite(MemW), .IF_PC(IF_PC), .ID_PC(ID_PC), .EX_PC(EX_PC), .M_PC(MEM_PC),
    .WB_PC(WB_PC), .RDin(RDinr), .MDin(MDinr), .LedData(LED));
  \单周期_多级中断  \u_单周期_多级中断_1  (
    .IR1(IR1), .IR2(IR2), .IR3(IR3), .RegWrite(RegW), .MemWrite(MemW), .PC(PC), .IR(IR), .RDin(RDin),
    .MDin(MDin), .LedData(LED));

  // Notes on the sheet:
  //   单周期封装测试
  //   气泡流水封装测试
  //   单周期+单级中断封装测试
  //   请检查上面封装有无位宽不匹配，引脚标签是否和连接的标签相对应，否则无法在educoder平台上正确测试
  //   理想流水封装测试
  //   重定向流水封装测试
  //   单周期+多级中断封装测试
endmodule

module IF_ID (
  input  CLK,
  input  CLR,
  input  en,
  input  [31:0] PC,
  input  [31:0] IR,
  output [31:0] PC_2,
  output [31:0] IR_2
);

  wire [31:0] multiplexer_1_out, multiplexer_2_out;

  Multiplexer #(.select(1), .width(32), .disabled("Z"), .enable("false")) multiplexer_1 (
    .in0(PC), .in1({32{1'b0}}), .out(multiplexer_1_out), .sel(CLR));
  Multiplexer #(.select(1), .width(32), .disabled("Z"), .enable("false")) multiplexer_2 (
    .in0(IR), .in1({32{1'b0}}), .out(multiplexer_2_out), .sel(CLR));
  Register #(.width(32), .trigger("rising"), .Select("low")) register_1 (
    .D(multiplexer_1_out), .en(en), .Q(PC_2), .clk(CLK));  // open: clr
  Register #(.width(32), .trigger("rising"), .Select("low")) register_2 (
    .D(multiplexer_2_out), .en(en), .Q(IR_2), .clk(CLK));  // open: clr
endmodule

module \IF_ID_预测  (
  input  CLK,
  input  CLR,
  input  en,
  input  [31:0] PC,
  input  [31:0] IR,
  input  pre,
  output [31:0] PC_2,
  output [31:0] IR_2,
  output pre_2
);

  wire multiplexer_1_out;
  wire [31:0] multiplexer_2_out, multiplexer_3_out;

  Multiplexer #(.select(1), .width(1), .disabled("Z"), .enable("false")) multiplexer_1 (
    .in0(pre), .in1(1'b0), .out(multiplexer_1_out), .sel(CLR));
  Multiplexer #(.select(1), .width(32), .disabled("Z"), .enable("false")) multiplexer_2 (
    .in0(PC), .in1({32{1'b0}}), .out(multiplexer_2_out), .sel(CLR));
  Multiplexer #(.select(1), .width(32), .disabled("Z"), .enable("false")) multiplexer_3 (
    .in0(IR), .in1({32{1'b0}}), .out(multiplexer_3_out), .sel(CLR));
  Register #(.width(32), .trigger("rising"), .Select("low")) register_1 (
    .D(multiplexer_2_out), .en(en), .Q(PC_2), .clk(CLK));  // open: clr
  Register #(.width(32), .trigger("rising"), .Select("low")) register_2 (
    .D(multiplexer_3_out), .en(en), .Q(IR_2), .clk(CLK));  // open: clr
  Register #(.width(1), .trigger("rising"), .Select("low")) register_3 (
    .D(multiplexer_1_out), .en(en), .Q(pre_2), .clk(CLK));  // open: clr
endmodule

module \ID_EX_理想_气泡  (
  input  CLK,
  input  CLR,
  input  en,
  input  [31:0] PC,
  input  [31:0] imm,
  input  [31:0] IR,
  input  [14:0] ctrlSignal,
  input  [31:0] A,
  input  [4:0] W_num,
  input  [31:0] B,
  input  [11:0] Badd,
  input  [19:0] J,
  output [31:0] PC_2,
  output [31:0] imm_2,
  output [31:0] IR_2,
  output [14:0] ctrlSignal_2,
  output [31:0] A_2,
  output [4:0] W_num_2,
  output [31:0] B_2,
  output [11:0] Badd_2,
  output [19:0] J_2
);

  wire [4:0] multiplexer_7_out;
  wire [11:0] multiplexer_8_out;
  wire [14:0] multiplexer_6_out;
  wire [19:0] multiplexer_9_out;
  wire [31:0] multiplexer_1_out, multiplexer_2_out, multiplexer_3_out, multiplexer_4_out, multiplexer_5_out;

  Multiplexer #(.select(1), .width(32), .disabled("Z"), .enable("false")) multiplexer_1 (
    .in0(PC), .in1({32{1'b0}}), .out(multiplexer_1_out), .sel(CLR));
  Multiplexer #(.select(1), .width(32), .disabled("Z"), .enable("false")) multiplexer_2 (
    .in0(IR), .in1({32{1'b0}}), .out(multiplexer_2_out), .sel(CLR));
  Multiplexer #(.select(1), .width(32), .disabled("Z"), .enable("false")) multiplexer_3 (
    .in0(A), .in1({32{1'b0}}), .out(multiplexer_3_out), .sel(CLR));
  Multiplexer #(.select(1), .width(32), .disabled("Z"), .enable("false")) multiplexer_4 (
    .in0(B), .in1({32{1'b0}}), .out(multiplexer_4_out), .sel(CLR));
  Register #(.width(32), .trigger("rising"), .Select("low")) register_1 (
    .D(multiplexer_1_out), .en(en), .Q(PC_2), .clk(CLK));  // open: clr
  Register #(.width(32), .trigger("rising"), .Select("low")) register_2 (
    .D(multiplexer_2_out), .en(en), .Q(IR_2), .clk(CLK));  // open: clr
  Register #(.width(32), .trigger("rising"), .Select("low")) register_3 (
    .D(multiplexer_3_out), .en(en), .Q(A_2), .clk(CLK));  // open: clr
  Register #(.width(32), .trigger("rising"), .Select("low")) register_4 (
    .D(multiplexer_4_out), .en(en), .Q(B_2), .clk(CLK));  // open: clr
  Multiplexer #(.select(1), .width(32), .disabled("Z"), .enable("false")) multiplexer_5 (
    .in0(imm), .in1({32{1'b0}}), .out(multiplexer_5_out), .sel(CLR));
  Multiplexer #(.select(1), .width(15), .disabled("Z"), .enable("false")) multiplexer_6 (
    .in0(ctrlSignal), .in1({15{1'b0}}), .out(multiplexer_6_out), .sel(CLR));
  Multiplexer #(.select(1), .width(5), .disabled("Z"), .enable("false")) multiplexer_7 (
    .in0(W_num), .in1({5{1'b0}}), .out(multiplexer_7_out), .sel(CLR));
  Multiplexer #(.select(1), .width(12), .disabled("Z"), .enable("false")) multiplexer_8 (
    .in0(Badd), .in1({12{1'b0}}), .out(multiplexer_8_out), .sel(CLR));
  Multiplexer #(.select(1), .width(20), .disabled("Z"), .enable("false")) multiplexer_9 (
    .in0(J), .in1({20{1'b0}}), .out(multiplexer_9_out), .sel(CLR));
  Register #(.width(32), .trigger("rising"), .Select("low")) register_5 (
    .D(multiplexer_5_out), .en(en), .Q(imm_2), .clk(CLK));  // open: clr
  Register #(.width(15), .trigger("rising"), .Select("low")) register_6 (
    .D(multiplexer_6_out), .en(en), .Q(ctrlSignal_2), .clk(CLK));  // open: clr
  Register #(.width(5), .trigger("rising"), .Select("low")) register_7 (
    .D(multiplexer_7_out), .en(en), .Q(W_num_2), .clk(CLK));  // open: clr
  Register #(.width(12), .trigger("rising"), .Select("low")) register_8 (
    .D(multiplexer_8_out), .en(en), .Q(Badd_2), .clk(CLK));  // open: clr
  Register #(.width(20), .trigger("rising"), .Select("low")) register_9 (
    .D(multiplexer_9_out), .en(en), .Q(J_2), .clk(CLK));  // open: clr
endmodule
module \ID_EX_重定向  (
  input  CLK,
  input  CLR,
  input  en,
  input  [31:0] PC,
  input  [31:0] imm,
  input  [31:0] IR,
  input  [18:0] ctrlSignal,
  input  [31:0] A,
  input  [4:0] W_num,
  input  [31:0] B,
  input  [11:0] Badd,
  input  [19:0] J,
  output [31:0] PC_2,
  output [31:0] imm_2,
  output [31:0] IR_2,
  output [18:0] ctrlSignal_2,
  output [31:0] A_2,
  output [4:0] W_num_2,
  output [31:0] B_2,
  output [11:0] Badd_2,
  output [19:0] J_2
);

  wire [4:0] multiplexer_7_out;
  wire [11:0] multiplexer_8_out;
  wire [18:0] multiplexer_6_out;
  wire [19:0] multiplexer_9_out;
  wire [31:0] multiplexer_1_out, multiplexer_2_out, multiplexer_3_out, multiplexer_4_out, multiplexer_5_out;

  Multiplexer #(.select(1), .width(32), .disabled("Z"), .enable("false")) multiplexer_1 (
    .in0(PC), .in1({32{1'b0}}), .out(multiplexer_1_out), .sel(CLR));
  Multiplexer #(.select(1), .width(32), .disabled("Z"), .enable("false")) multiplexer_2 (
    .in0(IR), .in1({32{1'b0}}), .out(multiplexer_2_out), .sel(CLR));
  Multiplexer #(.select(1), .width(32), .disabled("Z"), .enable("false")) multiplexer_3 (
    .in0(A), .in1({32{1'b0}}), .out(multiplexer_3_out), .sel(CLR));
  Multiplexer #(.select(1), .width(32), .disabled("Z"), .enable("false")) multiplexer_4 (
    .in0(B), .in1({32{1'b0}}), .out(multiplexer_4_out), .sel(CLR));
  Register #(.width(32), .trigger("rising"), .Select("low")) register_1 (
    .D(multiplexer_1_out), .en(en), .Q(PC_2), .clk(CLK));  // open: clr
  Register #(.width(32), .trigger("rising"), .Select("low")) register_2 (
    .D(multiplexer_2_out), .en(en), .Q(IR_2), .clk(CLK));  // open: clr
  Register #(.width(32), .trigger("rising"), .Select("low")) register_3 (
    .D(multiplexer_3_out), .en(en), .Q(A_2), .clk(CLK));  // open: clr
  Register #(.width(32), .trigger("rising"), .Select("low")) register_4 (
    .D(multiplexer_4_out), .en(en), .Q(B_2), .clk(CLK));  // open: clr
  Multiplexer #(.select(1), .width(32), .disabled("Z"), .enable("false")) multiplexer_5 (
    .in0(imm), .in1({32{1'b0}}), .out(multiplexer_5_out), .sel(CLR));
  Multiplexer #(.select(1), .width(19), .disabled("Z"), .enable("false")) multiplexer_6 (
    .in0(ctrlSignal), .in1({19{1'b0}}), .out(multiplexer_6_out), .sel(CLR));
  Multiplexer #(.select(1), .width(5), .disabled("Z"), .enable("false")) multiplexer_7 (
    .in0(W_num), .in1({5{1'b0}}), .out(multiplexer_7_out), .sel(CLR));
  Multiplexer #(.select(1), .width(12), .disabled("Z"), .enable("false")) multiplexer_8 (
    .in0(Badd), .in1({12{1'b0}}), .out(multiplexer_8_out), .sel(CLR));
  Multiplexer #(.select(1), .width(20), .disabled("Z"), .enable("false")) multiplexer_9 (
    .in0(J), .in1({20{1'b0}}), .out(multiplexer_9_out), .sel(CLR));
  Register #(.width(32), .trigger("rising"), .Select("low")) register_5 (
    .D(multiplexer_5_out), .en(en), .Q(imm_2), .clk(CLK));  // open: clr
  Register #(.width(19), .trigger("rising"), .Select("low")) register_6 (
    .D(multiplexer_6_out), .en(en), .Q(ctrlSignal_2), .clk(CLK));  // open: clr
  Register #(.width(5), .trigger("rising"), .Select("low")) register_7 (
    .D(multiplexer_7_out), .en(en), .Q(W_num_2), .clk(CLK));  // open: clr
  Register #(.width(12), .trigger("rising"), .Select("low")) register_8 (
    .D(multiplexer_8_out), .en(en), .Q(Badd_2), .clk(CLK));  // open: clr
  Register #(.width(20), .trigger("rising"), .Select("low")) register_9 (
    .D(multiplexer_9_out), .en(en), .Q(J_2), .clk(CLK));  // open: clr
endmodule

module \ID_EX_预测  (
  input  CLK,
  input  CLR,
  input  en,
  input  [31:0] PC,
  input  [31:0] imm,
  input  [31:0] IR,
  input  [18:0] ctrlSignal,
  input  [31:0] A,
  input  [4:0] W_num,
  input  [31:0] B,
  input  [11:0] Badd,
  input  pre,
  input  [19:0] J,
  output [31:0] PC_2,
  output [31:0] imm_2,
  output [31:0] IR_2,
  output [18:0] ctrlSignal_2,
  output [31:0] A_2,
  output [4:0] W_num_2,
  output [31:0] B_2,
  output [11:0] Badd_2,
  output pre_2,
  output [19:0] J_2
);

  wire multiplexer_5_out;
  wire [4:0] multiplexer_8_out;
  wire [11:0] multiplexer_9_out;
  wire [18:0] multiplexer_7_out;
  wire [19:0] multiplexer_10_out;
  wire [31:0] multiplexer_1_out, multiplexer_2_out, multiplexer_3_out, multiplexer_4_out, multiplexer_6_out;

  Multiplexer #(.select(1), .width(32), .disabled("Z"), .enable("false")) multiplexer_1 (
    .in0(PC), .in1({32{1'b0}}), .out(multiplexer_1_out), .sel(CLR));
  Multiplexer #(.select(1), .width(32), .disabled("Z"), .enable("false")) multiplexer_2 (
    .in0(IR), .in1({32{1'b0}}), .out(multiplexer_2_out), .sel(CLR));
  Multiplexer #(.select(1), .width(32), .disabled("Z"), .enable("false")) multiplexer_3 (
    .in0(A), .in1({32{1'b0}}), .out(multiplexer_3_out), .sel(CLR));
  Multiplexer #(.select(1), .width(32), .disabled("Z"), .enable("false")) multiplexer_4 (
    .in0(B), .in1({32{1'b0}}), .out(multiplexer_4_out), .sel(CLR));
  Multiplexer #(.select(1), .width(1), .disabled("Z"), .enable("false")) multiplexer_5 (
    .in0(pre), .in1(1'b0), .out(multiplexer_5_out), .sel(CLR));
  Register #(.width(32), .trigger("rising"), .Select("low")) register_1 (
    .D(multiplexer_1_out), .en(en), .Q(PC_2), .clk(CLK));  // open: clr
  Register #(.width(32), .trigger("rising"), .Select("low")) register_2 (
    .D(multiplexer_2_out), .en(en), .Q(IR_2), .clk(CLK));  // open: clr
  Register #(.width(32), .trigger("rising"), .Select("low")) register_3 (
    .D(multiplexer_3_out), .en(en), .Q(A_2), .clk(CLK));  // open: clr
  Register #(.width(32), .trigger("rising"), .Select("low")) register_4 (
    .D(multiplexer_4_out), .en(en), .Q(B_2), .clk(CLK));  // open: clr
  Register #(.width(1), .trigger("rising"), .Select("low")) register_5 (
    .D(multiplexer_5_out), .en(en), .Q(pre_2), .clk(CLK));  // open: clr
  Multiplexer #(.select(1), .width(32), .disabled("Z"), .enable("false")) multiplexer_6 (
    .in0(imm), .in1({32{1'b0}}), .out(multiplexer_6_out), .sel(CLR));
  Multiplexer #(.select(1), .width(19), .disabled("Z"), .enable("false")) multiplexer_7 (
    .in0(ctrlSignal), .in1({19{1'b0}}), .out(multiplexer_7_out), .sel(CLR));
  Multiplexer #(.select(1), .width(5), .disabled("Z"), .enable("false")) multiplexer_8 (
    .in0(W_num), .in1({5{1'b0}}), .out(multiplexer_8_out), .sel(CLR));
  Multiplexer #(.select(1), .width(12), .disabled("Z"), .enable("false")) multiplexer_9 (
    .in0(Badd), .in1({12{1'b0}}), .out(multiplexer_9_out), .sel(CLR));
  Multiplexer #(.select(1), .width(20), .disabled("Z"), .enable("false")) multiplexer_10 (
    .in0(J), .in1({20{1'b0}}), .out(multiplexer_10_out), .sel(CLR));
  Register #(.width(32), .trigger("rising"), .Select("low")) register_6 (
    .D(multiplexer_6_out), .en(en), .Q(imm_2), .clk(CLK));  // open: clr
  Register #(.width(19), .trigger("rising"), .Select("low")) register_7 (
    .D(multiplexer_7_out), .en(en), .Q(ctrlSignal_2), .clk(CLK));  // open: clr
  Register #(.width(5), .trigger("rising"), .Select("low")) register_8 (
    .D(multiplexer_8_out), .en(en), .Q(W_num_2), .clk(CLK));  // open: clr
  Register #(.width(12), .trigger("rising"), .Select("low")) register_9 (
    .D(multiplexer_9_out), .en(en), .Q(Badd_2), .clk(CLK));  // open: clr
  Register #(.width(20), .trigger("rising"), .Select("low")) register_10 (
    .D(multiplexer_10_out), .en(en), .Q(J_2), .clk(CLK));  // open: clr
endmodule

module \ID_EX_重定向_中断  (
  input  CLK,
  input  CLR,
  input  en,
  input  [31:0] PC,
  input  [31:0] imm,
  input  [31:0] IR,
  input  [19:0] ctrlSignal,
  input  [31:0] A,
  input  [4:0] W_num,
  input  [31:0] B,
  input  [11:0] Badd,
  input  [19:0] J,
  output [31:0] PC_2,
  output [31:0] imm_2,
  output [31:0] IR_2,
  output [19:0] ctrlSignal_2,
  output [31:0] A_2,
  output [4:0] W_num_2,
  output [31:0] B_2,
  output [11:0] Badd_2,
  output [19:0] J_2
);

  wire [4:0] multiplexer_7_out;
  wire [11:0] multiplexer_8_out;
  wire [19:0] multiplexer_6_out, multiplexer_9_out;
  wire [31:0] multiplexer_1_out, multiplexer_2_out, multiplexer_3_out, multiplexer_4_out, multiplexer_5_out;

  Multiplexer #(.select(1), .width(32), .disabled("Z"), .enable("false")) multiplexer_1 (
    .in0(PC), .in1({32{1'b0}}), .out(multiplexer_1_out), .sel(CLR));
  Multiplexer #(.select(1), .width(32), .disabled("Z"), .enable("false")) multiplexer_2 (
    .in0(IR), .in1({32{1'b0}}), .out(multiplexer_2_out), .sel(CLR));
  Multiplexer #(.select(1), .width(32), .disabled("Z"), .enable("false")) multiplexer_3 (
    .in0(A), .in1({32{1'b0}}), .out(multiplexer_3_out), .sel(CLR));
  Multiplexer #(.select(1), .width(32), .disabled("Z"), .enable("false")) multiplexer_4 (
    .in0(B), .in1({32{1'b0}}), .out(multiplexer_4_out), .sel(CLR));
  Register #(.width(32), .trigger("rising"), .Select("low")) register_1 (
    .D(multiplexer_1_out), .en(en), .Q(PC_2), .clk(CLK));  // open: clr
  Register #(.width(32), .trigger("rising"), .Select("low")) register_2 (
    .D(multiplexer_2_out), .en(en), .Q(IR_2), .clk(CLK));  // open: clr
  Register #(.width(32), .trigger("rising"), .Select("low")) register_3 (
    .D(multiplexer_3_out), .en(en), .Q(A_2), .clk(CLK));  // open: clr
  Register #(.width(32), .trigger("rising"), .Select("low")) register_4 (
    .D(multiplexer_4_out), .en(en), .Q(B_2), .clk(CLK));  // open: clr
  Multiplexer #(.select(1), .width(32), .disabled("Z"), .enable("false")) multiplexer_5 (
    .in0(imm), .in1({32{1'b0}}), .out(multiplexer_5_out), .sel(CLR));
  Multiplexer #(.select(1), .width(20), .disabled("Z"), .enable("false")) multiplexer_6 (
    .in0(ctrlSignal), .in1({20{1'b0}}), .out(multiplexer_6_out), .sel(CLR));
  Multiplexer #(.select(1), .width(5), .disabled("Z"), .enable("false")) multiplexer_7 (
    .in0(W_num), .in1({5{1'b0}}), .out(multiplexer_7_out), .sel(CLR));
  Multiplexer #(.select(1), .width(12), .disabled("Z"), .enable("false")) multiplexer_8 (
    .in0(Badd), .in1({12{1'b0}}), .out(multiplexer_8_out), .sel(CLR));
  Multiplexer #(.select(1), .width(20), .disabled("Z"), .enable("false")) multiplexer_9 (
    .in0(J), .in1({20{1'b0}}), .out(multiplexer_9_out), .sel(CLR));
  Register #(.width(32), .trigger("rising"), .Select("low")) register_5 (
    .D(multiplexer_5_out), .en(en), .Q(imm_2), .clk(CLK));  // open: clr
  Register #(.width(20), .trigger("rising"), .Select("low")) register_6 (
    .D(multiplexer_6_out), .en(en), .Q(ctrlSignal_2), .clk(CLK));  // open: clr
  Register #(.width(5), .trigger("rising"), .Select("low")) register_7 (
    .D(multiplexer_7_out), .en(en), .Q(W_num_2), .clk(CLK));  // open: clr
  Register #(.width(12), .trigger("rising"), .Select("low")) register_8 (
    .D(multiplexer_8_out), .en(en), .Q(Badd_2), .clk(CLK));  // open: clr
  Register #(.width(20), .trigger("rising"), .Select("low")) register_9 (
    .D(multiplexer_9_out), .en(en), .Q(J_2), .clk(CLK));  // open: clr
endmodule

module EX_MEM (
  input  CLK,
  input  CLR,
  input  en,
  input  [31:0] PC,
  input  [7:0] ctrlSignal,
  input  [31:0] IR,
  input  [4:0] W_num,
  input  [31:0] B,
  input  [31:0] ALU,
  output [31:0] PC_2,
  output [7:0] ctrlSignal_2,
  output [31:0] IR_2,
  output [4:0] W_num_2,
  output [31:0] B_2,
  output [31:0] ALU_2
);

  wire [4:0] multiplexer_6_out;
  wire [7:0] multiplexer_5_out;
  wire [31:0] multiplexer_1_out, multiplexer_2_out, multiplexer_3_out, multiplexer_4_out;

  Multiplexer #(.select(1), .width(32), .disabled("Z"), .enable("false")) multiplexer_1 (
    .in0(PC), .in1({32{1'b0}}), .out(multiplexer_1_out), .sel(CLR));
  Multiplexer #(.select(1), .width(32), .disabled("Z"), .enable("false")) multiplexer_2 (
    .in0(IR), .in1({32{1'b0}}), .out(multiplexer_2_out), .sel(CLR));
  Multiplexer #(.select(1), .width(32), .disabled("Z"), .enable("false")) multiplexer_3 (
    .in0(B), .in1({32{1'b0}}), .out(multiplexer_3_out), .sel(CLR));
  Multiplexer #(.select(1), .width(32), .disabled("Z"), .enable("false")) multiplexer_4 (
    .in0(ALU), .in1({32{1'b0}}), .out(multiplexer_4_out), .sel(CLR));
  Register #(.width(32), .trigger("rising"), .Select("low")) register_1 (
    .D(multiplexer_1_out), .en(en), .Q(PC_2), .clk(CLK));  // open: clr
  Register #(.width(32), .trigger("rising"), .Select("low")) register_2 (
    .D(multiplexer_2_out), .en(en), .Q(IR_2), .clk(CLK));  // open: clr
  Register #(.width(32), .trigger("rising"), .Select("low")) register_3 (
    .D(multiplexer_3_out), .en(en), .Q(B_2), .clk(CLK));  // open: clr
  Register #(.width(32), .trigger("rising"), .Select("low")) register_4 (
    .D(multiplexer_4_out), .en(en), .Q(ALU_2), .clk(CLK));  // open: clr
  Multiplexer #(.select(1), .width(8), .disabled("Z"), .enable("false")) multiplexer_5 (
    .in0(ctrlSignal), .in1({8{1'b0}}), .out(multiplexer_5_out), .sel(CLR));
  Multiplexer #(.select(1), .width(5), .disabled("Z"), .enable("false")) multiplexer_6 (
    .in0(W_num), .in1({5{1'b0}}), .out(multiplexer_6_out), .sel(CLR));
  Register #(.width(8), .trigger("rising"), .Select("low")) register_5 (
    .D(multiplexer_5_out), .en(en), .Q(ctrlSignal_2), .clk(CLK));  // open: clr
  Register #(.width(5), .trigger("rising"), .Select("low")) register_6 (
    .D(multiplexer_6_out), .en(en), .Q(W_num_2), .clk(CLK));  // open: clr
endmodule

module MEM_WB (
  input  CLK,
  input  CLR,
  input  en,
  input  [31:0] PC,
  input  [6:0] ctrlSignal,
  input  [4:0] W_num,
  input  [31:0] IR,
  input  [31:0] ALU,
  input  [31:0] MD,
  output [31:0] PC_2,
  output [6:0] ctrlSignal_2,
  output [4:0] W_num_2,
  output [31:0] IR_2,
  output [31:0] ALU_2,
  output [31:0] MD_2
);

  Register #(.width(32), .trigger("rising"), .Select("low")) register_1 (
    .D(PC), .en(en), .Q(PC_2), .clk(CLK), .clr(CLR));
  Register #(.width(32), .trigger("rising"), .Select("low")) register_2 (
    .D(IR), .en(en), .Q(IR_2), .clk(CLK), .clr(CLR));
  Register #(.width(32), .trigger("rising"), .Select("low")) register_3 (
    .D(ALU), .en(en), .Q(ALU_2), .clk(CLK), .clr(CLR));
  Register #(.width(32), .trigger("rising"), .Select("low")) register_4 (
    .D(MD), .en(en), .Q(MD_2), .clk(CLK), .clr(CLR));
  Register #(.width(7), .trigger("rising"), .Select("low")) register_5 (
    .D(ctrlSignal), .en(en), .Q(ctrlSignal_2), .clk(CLK), .clr(CLR));
  Register #(.width(5), .trigger("rising"), .Select("low")) register_6 (
    .D(W_num), .en(en), .Q(W_num_2), .clk(CLK), .clr(CLR));
endmodule

module \源寄存器使用情况  (
  input  OP2,
  input  OP3,
  input  OP4,
  input  OP5,
  input  OP6,
  input  F12,
  input  F13,
  input  F14,
  input  F25,
  input  F30,
  output r1_used,
  output r2_used
);

  wire and_1_out, and_2_out, and_3_out, and_4_out, and_5_out, and_6_out, and_7_out, and_8_out, and_9_out,
       and_10_out, and_11_out, and_12_out, and_13_out, and_14_out, and_15_out, and_16_out, and_17_out,
       and_18_out, and_19_out, and_20_out, and_21_out, and_22_out, and_23_out, and_24_out, and_25_out,
       and_26_out, and_27_out, and_28_out, and_29_out, and_30_out, and_31_out, and_32_out, and_33_out,
       and_34_out, and_35_out, and_36_out, not_1_out, not_2_out, not_3_out, not_4_out, not_5_out, not_6_out,
       not_7_out, not_8_out, not_9_out, not_10_out, not_11_out, not_12_out, not_13_out, not_14_out,
       not_15_out, not_16_out, not_17_out, not_18_out, not_19_out, not_20_out, not_21_out, not_22_out,
       not_23_out, not_24_out, not_25_out, not_26_out, not_27_out, not_28_out, not_29_out, not_30_out,
       not_31_out, not_32_out, not_33_out, not_34_out, not_35_out, not_36_out, not_37_out, not_38_out,
       not_39_out, not_40_out, not_41_out, not_42_out, not_43_out, not_44_out, not_45_out, not_46_out,
       not_47_out, not_48_out, not_49_out, not_50_out, not_51_out, not_52_out, not_53_out, not_54_out,
       not_55_out, not_56_out, not_57_out, not_58_out, not_59_out, not_60_out, not_61_out, not_62_out,
       not_63_out, not_64_out, not_65_out, not_66_out, not_67_out, not_68_out, not_69_out, not_70_out,
       not_71_out, not_72_out, not_73_out, not_74_out, not_75_out, not_76_out, not_77_out, not_78_out,
       not_79_out, not_80_out, not_81_out, not_82_out, not_83_out, not_84_out, not_85_out, not_86_out,
       not_87_out, not_88_out, not_89_out, not_90_out, not_91_out, not_92_out, not_93_out, not_94_out,
       not_95_out, not_96_out, not_97_out, not_98_out, not_99_out, not_100_out, not_101_out, not_102_out,
       not_103_out, not_104_out, not_105_out, not_106_out, not_107_out, not_108_out, not_109_out,
       not_110_out, not_111_out, not_112_out, not_113_out, not_114_out, not_115_out, not_116_out,
       not_117_out, not_118_out, not_119_out, not_120_out, not_121_out, not_122_out, not_123_out,
       not_124_out, not_125_out, not_126_out, not_127_out, not_128_out, not_129_out, not_130_out,
       not_131_out, not_132_out, not_133_out, not_134_out, not_135_out, not_136_out, not_137_out,
       not_138_out, not_139_out, not_140_out, not_141_out, not_142_out, not_143_out, not_144_out,
       not_145_out, not_146_out, not_147_out, not_148_out, not_149_out, not_150_out, not_151_out,
       not_152_out, not_153_out, not_154_out, not_155_out, not_156_out, not_157_out, not_158_out,
       not_159_out, not_160_out, not_161_out, not_162_out, not_163_out, not_164_out, not_165_out,
       not_166_out, not_167_out, not_168_out, not_169_out, not_170_out, not_171_out, not_172_out,
       not_173_out, not_174_out, not_175_out, not_176_out, not_177_out, not_178_out, not_179_out,
       not_180_out, not_181_out, not_182_out, not_183_out, not_184_out, not_185_out, not_186_out,
       not_187_out, not_188_out, not_189_out, not_190_out, not_191_out, not_192_out, not_193_out,
       not_194_out, not_195_out, not_196_out, not_197_out, not_198_out, not_199_out, not_200_out,
       not_201_out, not_202_out, not_203_out, not_204_out, not_205_out, not_206_out, not_207_out,
       not_208_out, not_209_out, not_210_out, not_211_out, not_212_out, not_213_out, not_214_out,
       not_215_out, not_216_out, not_217_out, not_218_out, not_219_out, not_220_out;

  not not_1 (not_1_out, F30);
  not not_2 (not_2_out, F25);
  not not_3 (not_3_out, F14);
  not not_4 (not_4_out, F13);
  not not_5 (not_5_out, F12);
  not not_6 (not_6_out, OP6);
  not not_7 (not_7_out, OP3);
  not not_8 (not_8_out, OP2);
  not not_9 (not_9_out, F25);
  not not_10 (not_10_out, F14);
  not not_11 (not_11_out, F13);
  not not_12 (not_12_out, F12);
  not not_13 (not_13_out, OP6);
  not not_14 (not_14_out, OP3);
  not not_15 (not_15_out, OP2);
  not not_16 (not_16_out, F30);
  not not_17 (not_17_out, F25);
  not not_18 (not_18_out, OP6);
  not not_19 (not_19_out, OP3);
  not not_20 (not_20_out, OP2);
  not not_21 (not_21_out, F30);
  not not_22 (not_22_out, F25);
  not not_23 (not_23_out, F12);
  not not_24 (not_24_out, OP6);
  not not_25 (not_25_out, OP3);
  not not_26 (not_26_out, OP2);
  not not_27 (not_27_out, F30);
  not not_28 (not_28_out, F25);
  not not_29 (not_29_out, F14);
  not not_30 (not_30_out, F12);
  not not_31 (not_31_out, OP6);
  not not_32 (not_32_out, OP3);
  not not_33 (not_33_out, OP2);
  not not_34 (not_34_out, F30);
  not not_35 (not_35_out, F25);
  not not_36 (not_36_out, F14);
  not not_37 (not_37_out, OP6);
  not not_38 (not_38_out, OP3);
  not not_39 (not_39_out, OP2);
  not not_40 (not_40_out, F14);
  not not_41 (not_41_out, F13);
  not not_42 (not_42_out, F12);
  not not_43 (not_43_out, OP6);
  not not_44 (not_44_out, OP5);
  not not_45 (not_45_out, OP3);
  not not_46 (not_46_out, OP2);
  not not_47 (not_47_out, OP6);
  not not_48 (not_48_out, OP5);
  not not_49 (not_49_out, OP3);
  not not_50 (not_50_out, OP2);
  not not_51 (not_51_out, F12);
  not not_52 (not_52_out, OP6);
  not not_53 (not_53_out, OP5);
  not not_54 (not_54_out, OP3);
  not not_55 (not_55_out, OP2);
  not not_56 (not_56_out, F13);
  not not_57 (not_57_out, F12);
  not not_58 (not_58_out, OP6);
  not not_59 (not_59_out, OP5);
  not not_60 (not_60_out, OP3);
  not not_61 (not_61_out, OP2);
  not not_62 (not_62_out, F14);
  not not_63 (not_63_out, F12);
  not not_64 (not_64_out, OP6);
  not not_65 (not_65_out, OP5);
  not not_66 (not_66_out, OP3);
  not not_67 (not_67_out, OP2);
  not not_68 (not_68_out, F30);
  not not_69 (not_69_out, F25);
  not not_70 (not_70_out, F14);
  not not_71 (not_71_out, F13);
  not not_72 (not_72_out, OP6);
  not not_73 (not_73_out, OP5);
  not not_74 (not_74_out, OP3);
  not not_75 (not_75_out, OP2);
  not not_76 (not_76_out, F30);
  not not_77 (not_77_out, F25);
  not not_78 (not_78_out, F13);
  not not_79 (not_79_out, OP6);
  not not_80 (not_80_out, OP5);
  not not_81 (not_81_out, OP3);
  not not_82 (not_82_out, OP2);
  not not_83 (not_83_out, F25);
  not not_84 (not_84_out, F13);
  not not_85 (not_85_out, OP6);
  not not_86 (not_86_out, OP5);
  not not_87 (not_87_out, OP3);
  not not_88 (not_88_out, OP2);
  not not_89 (not_89_out, F14);
  not not_90 (not_90_out, F12);
  not not_91 (not_91_out, OP6);
  not not_92 (not_92_out, OP5);
  not not_93 (not_93_out, OP4);
  not not_94 (not_94_out, OP3);
  not not_95 (not_95_out, OP2);
  not not_96 (not_96_out, F14);
  not not_97 (not_97_out, F12);
  not not_98 (not_98_out, OP6);
  not not_99 (not_99_out, OP4);
  not not_100 (not_100_out, OP3);
  not not_101 (not_101_out, OP2);
  not not_102 (not_102_out, F14);
  not not_103 (not_103_out, F13);
  not not_104 (not_104_out, F12);
  not not_105 (not_105_out, OP3);
  not not_106 (not_106_out, OP2);
  not not_107 (not_107_out, F14);
  not not_108 (not_108_out, F13);
  not not_109 (not_109_out, F12);
  not not_110 (not_110_out, OP4);
  not not_111 (not_111_out, OP3);
  not not_112 (not_112_out, OP2);
  not not_113 (not_113_out, F14);
  not not_114 (not_114_out, F13);
  not not_115 (not_115_out, OP4);
  not not_116 (not_116_out, OP3);
  not not_117 (not_117_out, OP2);
  not not_118 (not_118_out, F14);
  not not_119 (not_119_out, F13);
  not not_120 (not_120_out, F12);
  not not_121 (not_121_out, OP4);
  not not_122 (not_122_out, OP3);
  not not_123 (not_123_out, F30);
  not not_124 (not_124_out, F25);
  not not_125 (not_125_out, F14);
  not not_126 (not_126_out, F13);
  not not_127 (not_127_out, OP6);
  not not_128 (not_128_out, OP3);
  not not_129 (not_129_out, OP2);
  not not_130 (not_130_out, F14);
  not not_131 (not_131_out, OP6);
  not not_132 (not_132_out, OP5);
  not not_133 (not_133_out, OP3);
  not not_134 (not_134_out, OP2);
  not not_135 (not_135_out, F14);
  not not_136 (not_136_out, F13);
  not not_137 (not_137_out, F12);
  not not_138 (not_138_out, OP6);
  not not_139 (not_139_out, OP5);
  not not_140 (not_140_out, OP4);
  not not_141 (not_141_out, OP3);
  not not_142 (not_142_out, OP2);
  not not_143 (not_143_out, F13);
  not not_144 (not_144_out, F12);
  not not_145 (not_145_out, OP4);
  not not_146 (not_146_out, OP3);
  not not_147 (not_147_out, OP2);
  not not_148 (not_148_out, F30);
  not not_149 (not_149_out, F25);
  not not_150 (not_150_out, F14);
  not not_151 (not_151_out, F13);
  not not_152 (not_152_out, F12);
  not not_153 (not_153_out, OP6);
  not not_154 (not_154_out, OP3);
  not not_155 (not_155_out, OP2);
  not not_156 (not_156_out, F25);
  not not_157 (not_157_out, F14);
  not not_158 (not_158_out, F13);
  not not_159 (not_159_out, F12);
  not not_160 (not_160_out, OP6);
  not not_161 (not_161_out, OP3);
  not not_162 (not_162_out, OP2);
  not not_163 (not_163_out, F30);
  not not_164 (not_164_out, F25);
  not not_165 (not_165_out, OP6);
  not not_166 (not_166_out, OP3);
  not not_167 (not_167_out, OP2);
  not not_168 (not_168_out, F30);
  not not_169 (not_169_out, F25);
  not not_170 (not_170_out, F12);
  not not_171 (not_171_out, OP6);
  not not_172 (not_172_out, OP3);
  not not_173 (not_173_out, OP2);
  not not_174 (not_174_out, F30);
  not not_175 (not_175_out, F25);
  not not_176 (not_176_out, F14);
  not not_177 (not_177_out, F12);
  not not_178 (not_178_out, OP6);
  not not_179 (not_179_out, OP3);
  not not_180 (not_180_out, OP2);
  not not_181 (not_181_out, F30);
  not not_182 (not_182_out, F25);
  not not_183 (not_183_out, F14);
  not not_184 (not_184_out, OP6);
  not not_185 (not_185_out, OP3);
  not not_186 (not_186_out, OP2);
  not not_187 (not_187_out, F14);
  not not_188 (not_188_out, F12);
  not not_189 (not_189_out, OP6);
  not not_190 (not_190_out, OP4);
  not not_191 (not_191_out, OP3);
  not not_192 (not_192_out, OP2);
  not not_193 (not_193_out, F14);
  not not_194 (not_194_out, F13);
  not not_195 (not_195_out, F12);
  not not_196 (not_196_out, OP3);
  not not_197 (not_197_out, OP2);
  not not_198 (not_198_out, F14);
  not not_199 (not_199_out, F13);
  not not_200 (not_200_out, F12);
  not not_201 (not_201_out, OP4);
  not not_202 (not_202_out, OP3);
  not not_203 (not_203_out, OP2);
  not not_204 (not_204_out, F14);
  not not_205 (not_205_out, F13);
  not not_206 (not_206_out, OP4);
  not not_207 (not_207_out, OP3);
  not not_208 (not_208_out, OP2);
  not not_209 (not_209_out, F30);
  not not_210 (not_210_out, F25);
  not not_211 (not_211_out, F14);
  not not_212 (not_212_out, F13);
  not not_213 (not_213_out, OP6);
  not not_214 (not_214_out, OP3);
  not not_215 (not_215_out, OP2);
  not not_216 (not_216_out, F13);
  not not_217 (not_217_out, F12);
  not not_218 (not_218_out, OP4);
  not not_219 (not_219_out, OP3);
  not not_220 (not_220_out, OP2);
  and and_1 (and_1_out, not_1_out, not_2_out, not_3_out, not_4_out, not_5_out, not_6_out, OP5, OP4, not_7_out, not_8_out);
  and and_2 (and_2_out, F30, not_9_out, not_10_out, not_11_out, not_12_out, not_13_out, OP5, OP4, not_14_out, not_15_out);
  and and_3 (and_3_out, not_16_out, not_17_out, F14, F13, F12, not_18_out, OP5, OP4, not_19_out, not_20_out);
  and and_4 (and_4_out, not_21_out, not_22_out, F14, F13, not_23_out, not_24_out, OP5, OP4, not_25_out, not_26_out);
  and and_5 (and_5_out, not_27_out, not_28_out, not_29_out, F13, not_30_out, not_31_out, OP5, OP4, not_32_out, not_33_out);
  and and_6 (and_6_out, not_34_out, not_35_out, not_36_out, F13, F12, not_37_out, OP5, OP4, not_38_out, not_39_out);
  and and_7 (and_7_out, not_40_out, not_41_out, not_42_out, not_43_out, not_44_out, OP4, not_45_out, not_46_out);
  and and_8 (and_8_out, F14, F13, F12, not_47_out, not_48_out, OP4, not_49_out, not_50_out);
  and and_9 (and_9_out, F14, F13, not_51_out, not_52_out, not_53_out, OP4, not_54_out, not_55_out);
  and and_10 (and_10_out, F14, not_56_out, not_57_out, not_58_out, not_59_out, OP4, not_60_out, not_61_out);
  and and_11 (and_11_out, not_62_out, F13, not_63_out, not_64_out, not_65_out, OP4, not_66_out, not_67_out);
  and and_12 (and_12_out, not_68_out, not_69_out, not_70_out, not_71_out, F12, not_72_out, not_73_out, OP4, not_74_out, not_75_out);
  and and_13 (and_13_out, not_76_out, not_77_out, F14, not_78_out, F12, not_79_out, not_80_out, OP4, not_81_out, not_82_out);
  and and_14 (and_14_out, F30, not_83_out, F14, not_84_out, F12, not_85_out, not_86_out, OP4, not_87_out, not_88_out);
  and and_15 (and_15_out, not_89_out, F13, not_90_out, not_91_out, not_92_out, not_93_out, not_94_out, not_95_out);
  and and_16 (and_16_out, not_96_out, F13, not_97_out, not_98_out, OP5, not_99_out, not_100_out, not_101_out);
  and and_17 (and_17_out, not_102_out, not_103_out, not_104_out, OP6, OP5, OP4, not_105_out, not_106_out);
  and and_18 (and_18_out, not_107_out, not_108_out, not_109_out, OP6, OP5, not_110_out, not_111_out, not_112_out);
  and and_19 (and_19_out, not_113_out, not_114_out, F12, OP6, OP5, not_115_out, not_116_out, not_117_out);
  and and_20 (and_20_out, not_118_out, not_119_out, not_120_out, OP6, OP5, not_121_out, not_122_out, OP2);
  and and_21 (and_21_out, not_123_out, not_124_out, not_125_out, not_126_out, F12, not_127_out, OP5, OP4, not_128_out, not_129_out);
  and and_22 (and_22_out, not_130_out, F13, F12, not_131_out, not_132_out, OP4, not_133_out, not_134_out);
  and and_23 (and_23_out, not_135_out, not_136_out, not_137_out, not_138_out, not_139_out, not_140_out, not_141_out, not_142_out);
  and and_24 (and_24_out, F14, not_143_out, not_144_out, OP6, OP5, not_145_out, not_146_out, not_147_out);
  and and_25 (and_25_out, not_148_out, not_149_out, not_150_out, not_151_out, not_152_out, not_153_out, OP5, OP4, not_154_out, not_155_out);
  and and_26 (and_26_out, F30, not_156_out, not_157_out, not_158_out, not_159_out, not_160_out, OP5, OP4, not_161_out, not_162_out);
  and and_27 (and_27_out, not_163_out, not_164_out, F14, F13, F12, not_165_out, OP5, OP4, not_166_out, not_167_out);
  and and_28 (and_28_out, not_168_out, not_169_out, F14, F13, not_170_out, not_171_out, OP5, OP4, not_172_out, not_173_out);
  and and_29 (and_29_out, not_174_out, not_175_out, not_176_out, F13, not_177_out, not_178_out, OP5, OP4, not_179_out, not_180_out);
  and and_30 (and_30_out, not_181_out, not_182_out, not_183_out, F13, F12, not_184_out, OP5, OP4, not_185_out, not_186_out);
  and and_31 (and_31_out, not_187_out, F13, not_188_out, not_189_out, OP5, not_190_out, not_191_out, not_192_out);
  and and_32 (and_32_out, not_193_out, not_194_out, not_195_out, OP6, OP5, OP4, not_196_out, not_197_out);
  and and_33 (and_33_out, not_198_out, not_199_out, not_200_out, OP6, OP5, not_201_out, not_202_out, not_203_out);
  and and_34 (and_34_out, not_204_out, not_205_out, F12, OP6, OP5, not_206_out, not_207_out, not_208_out);
  and and_35 (and_35_out, not_209_out, not_210_out, not_211_out, not_212_out, F12, not_213_out, OP5, OP4, not_214_out, not_215_out);
  and and_36 (and_36_out, F14, not_216_out, not_217_out, OP6, OP5, not_218_out, not_219_out, not_220_out);
  or or_1 (r2_used, and_25_out, and_26_out, and_27_out, and_28_out, and_29_out, and_30_out, and_31_out, and_32_out, and_33_out, and_34_out, and_35_out, and_36_out);
  or or_2 (r1_used, and_1_out, and_2_out, and_3_out, and_4_out, and_5_out, and_6_out, and_7_out, and_8_out, and_9_out, and_10_out, and_11_out, and_12_out, and_13_out, and_14_out, and_15_out, and_16_out, and_17_out, and_18_out, and_19_out, and_20_out, and_21_out, and_22_out, and_23_out, and_24_out);
endmodule

module \数据相关检测逻辑  (
  input  [4:0] op_code,
  input  [4:0] Funct,
  input  [4:0] R1_num,
  input  [4:0] R2_num,
  input  EX_RegWrite,
  input  MEM_RegWrite,
  input  [4:0] EX_WriteReg_num,
  input  [4:0] MEM_WriteReg_num,
  output DataHazzard
);

  wire and_1_out, and_2_out, and_3_out, and_4_out, comparator_1_eq, comparator_2_eq, comparator_3_eq,
       comparator_4_eq, comparator_5_eq, comparator_6_eq, \源寄存器使用情况_1_r1_used , \源寄存器使用情况_1_r2_used ;

  \源寄存器使用情况  \u_源寄存器使用情况_1  (
    .OP2(op_code[0]), .OP3(op_code[1]), .OP4(op_code[2]), .OP5(op_code[3]), .OP6(op_code[4]), .F12(Funct[0]),
    .F13(Funct[1]), .F14(Funct[2]), .F25(Funct[3]), .F30(Funct[4]), .r1_used(\源寄存器使用情况_1_r1_used ),
    .r2_used(\源寄存器使用情况_1_r2_used ));
  Comparator #(.width(5), .mode("twosComplement")) comparator_1 (
    .a(R1_num), .b({5{1'b0}}), .eq(comparator_1_eq));  // open: gt, lt
  Comparator #(.width(5), .mode("twosComplement")) comparator_2 (
    .a(R1_num), .b(EX_WriteReg_num), .eq(comparator_2_eq));  // open: gt, lt
  Comparator #(.width(5), .mode("twosComplement")) comparator_3 (
    .a(R2_num), .b({5{1'b0}}), .eq(comparator_3_eq));  // open: gt, lt
  Comparator #(.width(5), .mode("twosComplement")) comparator_4 (
    .a(R2_num), .b(EX_WriteReg_num), .eq(comparator_4_eq));  // open: gt, lt
  Comparator #(.width(5), .mode("twosComplement")) comparator_5 (
    .a(R1_num), .b(MEM_WriteReg_num), .eq(comparator_5_eq));  // open: gt, lt
  Comparator #(.width(5), .mode("twosComplement")) comparator_6 (
    .a(R2_num), .b(MEM_WriteReg_num), .eq(comparator_6_eq));  // open: gt, lt
  and and_1 (and_1_out, \源寄存器使用情况_1_r1_used , ~comparator_1_eq, EX_RegWrite, comparator_2_eq);  // AND_Gate
  and and_2 (and_2_out, \源寄存器使用情况_1_r2_used , ~comparator_3_eq, EX_RegWrite, comparator_4_eq);  // AND_Gate
  and and_3 (and_3_out, \源寄存器使用情况_1_r1_used , ~comparator_1_eq, MEM_RegWrite, comparator_5_eq);  // AND_Gate
  and and_4 (and_4_out, \源寄存器使用情况_1_r2_used , ~comparator_3_eq, MEM_RegWrite, comparator_6_eq);  // AND_Gate
  or or_1 (DataHazzard, and_1_out, and_2_out, and_3_out, and_4_out);
endmodule

module \重定向相关处理逻辑  (
  input  [4:0] op_code,
  input  [4:0] Funct,
  input  EX_RegWrite,
  input  [4:0] r1,
  input  [4:0] r2,
  input  MEM_RegWrite,
  input  EX_MemRead,
  input  [4:0] MEM_WriteReg_num,
  input  [4:0] EX_WriteReg_num,
  output [1:0] r1Forward,
  output LoadUse,
  output [1:0] r2Forward
);

  wire and_1_out, and_2_out, comparator_1_eq, comparator_2_eq, comparator_3_eq, comparator_4_eq,
       comparator_5_eq, comparator_6_eq, comparator_7_eq, comparator_8_eq, comparator_9_eq, comparator_10_eq,
       r1_used, r2_used;
  wire [1:0] and_4_out, and_6_out;

  \源寄存器使用情况  \u_源寄存器使用情况_1  (
    .OP2(op_code[0]), .OP3(op_code[1]), .OP4(op_code[2]), .OP5(op_code[3]), .OP6(op_code[4]), .F12(Funct[0]),
    .F13(Funct[1]), .F14(Funct[2]), .F25(Funct[3]), .F30(Funct[4]), .r1_used(r1_used), .r2_used(r2_used));
  Comparator #(.width(5), .mode("twosComplement")) comparator_1 (
    .a(r1), .b({5{1'b0}}), .eq(comparator_1_eq));  // open: gt, lt
  Comparator #(.width(5), .mode("twosComplement")) comparator_2 (
    .a(r2), .b({5{1'b0}}), .eq(comparator_2_eq));  // open: gt, lt
  Comparator #(.width(5), .mode("twosComplement")) comparator_3 (
    .a(r1), .b(EX_WriteReg_num), .eq(comparator_3_eq));  // open: gt, lt
  Comparator #(.width(5), .mode("twosComplement")) comparator_4 (
    .a(r2), .b(EX_WriteReg_num), .eq(comparator_4_eq));  // open: gt, lt
  Comparator #(.width(5), .mode("twosComplement")) comparator_5 (
    .a(r2), .b({5{1'b0}}), .eq(comparator_5_eq));  // open: gt, lt
  and and_1 (and_1_out, r1_used, ~comparator_1_eq, EX_MemRead, comparator_3_eq);  // AND_Gate
  and and_2 (and_2_out, r2_used, ~comparator_2_eq, EX_MemRead, comparator_4_eq);  // AND_Gate
  Comparator #(.width(5), .mode("twosComplement")) comparator_6 (
    .a(r2), .b(EX_WriteReg_num), .eq(comparator_6_eq));  // open: gt, lt
  Comparator #(.width(5), .mode("twosComplement")) comparator_7 (
    .a(r2), .b(MEM_WriteReg_num), .eq(comparator_7_eq));  // open: gt, lt
  or or_1 (LoadUse, and_1_out, and_2_out);
  and and_3 (and_4_out[1], r2_used, ~comparator_5_eq, EX_RegWrite, comparator_6_eq);  // AND_Gate
  and and_4 (and_4_out[0], r2_used, ~comparator_5_eq, MEM_RegWrite, comparator_7_eq);  // AND_Gate
  Multiplexer #(.select(2), .width(2), .disabled("Z"), .enable("false")) multiplexer_1 (
    .in0(2'b00), .in1(2'b01), .in2(2'b10), .in3(2'b10), .out(r2Forward), .sel(and_4_out));
  Comparator #(.width(5), .mode("twosComplement")) comparator_8 (
    .a(r1), .b({5{1'b0}}), .eq(comparator_8_eq));  // open: gt, lt
  Comparator #(.width(5), .mode("twosComplement")) comparator_9 (
    .a(r1), .b(EX_WriteReg_num), .eq(comparator_9_eq));  // open: gt, lt
  Comparator #(.width(5), .mode("twosComplement")) comparator_10 (
    .a(r1), .b(MEM_WriteReg_num), .eq(comparator_10_eq));  // open: gt, lt
  and and_5 (and_6_out[1], r1_used, ~comparator_8_eq, EX_RegWrite, comparator_9_eq);  // AND_Gate
  and and_6 (and_6_out[0], r1_used, ~comparator_8_eq, MEM_RegWrite, comparator_10_eq);  // AND_Gate
  Multiplexer #(.select(2), .width(2), .disabled("Z"), .enable("false")) multiplexer_2 (
    .in0(2'b00), .in1(2'b01), .in2(2'b10), .in3(2'b10), .out(r1Forward), .sel(and_6_out));
endmodule

module \预测状态转换  (
  input  CLK,
  input  x,
  input  en,
  output z
);

  wire _1_q, and_1_out, and_2_out, comparator_1_eq, xor_1_out;
  wire [31:0] counter_1_q;

  Counter #(.width(32), .max('hffffffff), .ongoal("wrap"), .trigger("rising"), .behavior("new")) counter_1 (
    .Q(counter_1_q), .clk(CLK));  // open: load, D, count, carry, clr, preset, down
  Comparator #(.width(32), .mode("unsigned")) comparator_1 (
    .a(counter_1_q), .b({32{1'b0}}), .eq(comparator_1_eq));  // open: gt, lt
  and and_1 (and_1_out, x, _1_q);
  and and_2 (and_2_out, ~x, _1_q);  // AND_Gate
  xor xor_1 (xor_1_out, z, x);
  J_K_Flip_Flop #(.trigger("falling"), .Pre_Clr_Positions("ABOVE_BELOW"), .NegatePresetClear("false"), .enable("true"), .NewFFLayout("true")) _2 (
    .J(and_1_out), .clk(CLK), .K(and_2_out), .Q(z), .preset(comparator_1_eq), .en(en));  // open: Qn, reset
  J_K_Flip_Flop #(.trigger("falling"), .Pre_Clr_Positions("ABOVE_BELOW"), .NegatePresetClear("false"), .enable("true"), .NewFFLayout("true")) _1 (
    .J(xor_1_out), .clk(CLK), .K(_1_q), .Q(_1_q), .preset(comparator_1_eq), .en(en));  // open: Qn, reset
endmodule

module \归并比较  (
  input  [15:0] x,
  input  [15:0] y,
  input  [2:0] x_num,
  input  [2:0] y_num,
  output [15:0] max,
  output [2:0] max_num
);

  wire comparator_1_eq, comparator_1_gt, or_1_out;

  Multiplexer #(.select(1), .width(16), .disabled("Z"), .enable("false")) multiplexer_1 (
    .in0(x), .in1(y), .out(max), .sel(or_1_out));
  Comparator #(.width(16), .mode("twosComplement")) comparator_1 (
    .a(y), .b(x), .gt(comparator_1_gt), .eq(comparator_1_eq));  // open: lt
  or or_1 (or_1_out, comparator_1_gt, comparator_1_eq);
  Multiplexer #(.select(1), .width(3), .disabled("Z"), .enable("false")) multiplexer_2 (
    .in0(x_num), .in1(y_num), .out(max_num), .sel(or_1_out));
endmodule
