// Logisim project cpu-riscv.circ as structural Verilog: 23 circuits, main circuit ◇单周期RISC-V
module \单周期_单级中断  (
  input  IR1,
  input  IR2,
  input  IR3,
  output RegWrite,
  output MemWrite,
  output [31:0] PC,
  output [31:0] IR,
  output [31:0] RDin,
  output [31:0] MDin,
  output [31:0] LedData
);

  wire _1_out, _2_out, _3_out, Alu, AluEQ, AluSrcB, and_1_out, and_2_out, and_3_out, and_4_out, and_6_out,
       and_7_out, and_8_out, Beq, BGE, bltu, Bne, CLK, comparator_1_eq, comparator_2_eq, comparator_3_eq,
       comparator_4_eq, ecall, ENINT, Go, halt, INTR, IR1_t, IR2_t, IR3_t, IRA, IRB, IRC, IRD, IRE, IRF, IRG,
       IRH, IRI, IRJ, IRK, IRL, IRM, JAL, JALR, lb, LUI, MemToReg, not_1_out, not_2_out, or_1_out, or_3_out,
       RST, S, U_type, URET, W1, W2, W3, \中断请求 ;
  wire [1:0] priority_encoder_1_out;
  wire [1:1] or_6_out;
  wire [3:0] AluOP, \中断输入_1_int_n ;
  wire [4:0] multiplexer_4_out, multiplexer_5_out;
  wire [7:0] multiplexer_15_out;
  wire [15:0] \总周期数 ;
  wire [31:0] adder_2_out, adder_3_out, bit_extender_1_out, bit_extender_2_out, bit_extender_3_out,
       bit_extender_4_out, bit_extender_5_out, Calcuresult, Dout, INT_PC, LBDout, mEPC_q, multiplexer_1_out,
       multiplexer_2_out, multiplexer_6_out, multiplexer_7_out, multiplexer_9_out, multiplexer_10_out,
       multiplexer_12_out, multiplexer_13_out, NEWPC, PC_4, r2data, regifile_1_r1, shifter_1_out,
       shifter_2_out, shifter_3_out, shifter_4_out, \输出逻辑_1_d0 , \输出逻辑_1_d1 , \输出逻辑_1_d2 , \输出逻辑_1_d3 ,
       \输出逻辑_1_d4 , \输出逻辑_1_d5 , \输出逻辑_1_d6 , \输出逻辑_1_d7 , \输出逻辑_1_d8 , \输出逻辑_1_d9 , \输出逻辑_1_d10 ,
       \输出逻辑_1_d11 , \输出逻辑_1_d12 , \输出逻辑_1_d13 , \输出逻辑_1_d14 , \输出逻辑_1_d15 , \输出逻辑_1_d16 , \输出逻辑_1_d17 ,
       \输出逻辑_1_d18 , \输出逻辑_1_d19 , \输出逻辑_1_d20 , \输出逻辑_1_d21 , \输出逻辑_1_d22 , \输出逻辑_1_d23 , \输出逻辑_1_d24 ,
       \输出逻辑_1_d25 , \输出逻辑_1_d26 , \输出逻辑_1_d27 , \输出逻辑_1_d28 , \输出逻辑_1_d29 , \输出逻辑_1_d30 , \输出逻辑_1_d31 ;

  Clock #(.highDuration(1), .lowDuration(1)) clock_1 (.out(CLK));
  Button _1 (.out(_1_out));
  Button _2 (.out(_2_out));
  Button _3 (.out(_3_out));
  Button \u_继续运行  (.out(Go));
  LED #(.active("true")) led_1 (.in(W1));
  LED #(.active("true")) led_2 (.in(W2));
  LED #(.active("true")) led_3 (.in(W3));
  Hex_Digit_Display hex_digit_display_1 (.value(LedData[31:28]));  // open: dp
  Hex_Digit_Display hex_digit_display_2 (.value(LedData[27:24]));  // open: dp
  Hex_Digit_Display hex_digit_display_3 (.value(LedData[23:20]));  // open: dp
  Hex_Digit_Display hex_digit_display_4 (.value(LedData[19:16]));  // open: dp
  Hex_Digit_Display hex_digit_display_5 (.value(LedData[15:12]));  // open: dp
  Hex_Digit_Display hex_digit_display_6 (.value(LedData[11:8]));  // open: dp
  Hex_Digit_Display hex_digit_display_7 (.value(LedData[7:4]));  // open: dp
  // Probe on \总周期数 
  Hex_Digit_Display hex_digit_display_8 (.value(LedData[3:0]));  // open: dp
  Multiplexer #(.select(2), .width(32), .disabled("Z"), .enable("false")) multiplexer_1 (
    .in0(PC_4), .in1(Calcuresult), .in2(adder_3_out), .in3(adder_2_out), .out(multiplexer_1_out),
    .sel(priority_encoder_1_out));
  not not_1 (not_1_out, halt);
  Priority_Encoder #(.select(2), .disabled("Z")) priority_encoder_1 (
    .in0(1'b1), .in1(JALR), .in2(JAL), .in3(or_1_out), .out(priority_encoder_1_out));  // open: gs, en_out, en_in
  or or_1 (or_1_out, or_3_out, and_4_out, and_1_out);
  and and_1 (and_1_out, Alu, bltu);
  Multiplexer #(.select(1), .width(32), .disabled("Z"), .enable("false")) multiplexer_2 (
    .in0(NEWPC), .in1(INT_PC), .out(multiplexer_2_out), .sel(\中断请求 ));
  not not_2 (not_2_out, halt);
  Counter #(.width(16), .max('hffff), .ongoal("wrap"), .trigger("rising"), .behavior("new")) counter_1 (
    .count(not_1_out), .Q(\总周期数 ), .clk(CLK));  // open: load, D, carry, clr, preset, down
  or or_2 (IR1_t, IR1, IRA);
  or or_3 (or_3_out, and_2_out, and_3_out);
  and and_2 (and_2_out, Beq, AluEQ);
  and and_3 (and_3_out, ~AluEQ, Bne);  // AND_Gate
  Register #(.width(32), .trigger("rising"), .Select("low")) u_PC (
    .D(multiplexer_2_out), .en(not_2_out), .Q(PC), .clk(CLK), .clr(RST));
  Adder #(.width(32)) adder_1 (.a(PC), .b(32'h4), .out(PC_4));  // open: cin, cout
  or or_4 (IR2_t, IR2, IRB);
  and and_4 (and_4_out, ~Alu, BGE);  // AND_Gate
  Register #(.width(32), .trigger("rising"), .Select("low")) mEPC (
    .D(multiplexer_1_out), .en(\中断请求 ), .Q(mEPC_q), .clk(CLK));  // open: clr
  // RiscV_Probe riscv_probe_1: pin names not known; wires that end beside it: IR
  ROM #(.addrWidth(12), .dataWidth(32), .Select("high")) rom_1 (.addr(PC[13:2]), .data(IR));
  Multiplexer #(.select(1), .width(32), .disabled("Z"), .enable("false")) multiplexer_3 (
    .in0(multiplexer_1_out), .in1(mEPC_q), .out(NEWPC), .sel(URET));
  or or_5 (IR3_t, IR3, IRC);
  \单周期硬布线控制器  \u_单周期硬布线控制器_1  (
    .Funct({IR[30], IR[25], IR[14:12]}), .OP(IR[6:2]), .ALU_OP(AluOP), .MemToReg(MemToReg),
    .MemWrite(MemWrite), .ALU_SRC(AluSrcB), .RegWrite(RegWrite), .ecall(ecall), .S_type(S), .Jalr(JALR),
    .Beq(Beq), .JAL(JAL), .Bne(Bne), .in_3(IR[21]), .uret(URET), .LUI(LUI), .lb(lb), .bltu(bltu), .BGE(BGE),
    .U_type(U_type));  // open: re2_used, rs1_used, CSRRSI, CSRRCI
  Multiplexer #(.select(1), .width(5), .disabled("Z"), .enable("false")) multiplexer_4 (
    .in0(IR[19:15]), .in1(5'b10001), .out(multiplexer_4_out), .sel(ecall));
  Multiplexer #(.select(1), .width(5), .disabled("Z"), .enable("false")) multiplexer_5 (
    .in0(IR[24:20]), .in1(5'b01010), .out(multiplexer_5_out), .sel(ecall));
  assign bit_extender_1_out = {{20{IR[31]}}, IR[31:20]};  // Bit_Extender bit_extender_1
  assign bit_extender_2_out = {{20{IR[31]}}, {IR[31:25], IR[11:7]}};  // Bit_Extender bit_extender_2
  assign bit_extender_3_out = {{20{IR[31]}}, {IR[31], IR[7], IR[30:25], IR[11:8]}};  // Bit_Extender bit_extender_3
  assign bit_extender_4_out = {{12{IR[31]}}, {IR[31], IR[19:12], IR[20], IR[30:21]}};  // Bit_Extender bit_extender_4
  assign bit_extender_5_out = {{12{IR[31]}}, IR[31:12]};  // Bit_Extender bit_extender_5
  \中断输入  \u_中断输入_1  (
    .IRA(IRA), .IRB(IRB), .IRC(IRC), .CLK(CLK), .CLR(URET), .IRD(IRD), .IRE(IRE), .IRF(IRF), .IRG(IRG),
    .IRH(IRH), .IRI(IRI), .IRJ(IRJ), .IRK(IRK), .INTR(INTR), .INT_N(\中断输入_1_int_n ), .IRL(IRL), .IRM(IRM));  // open: IRAW, IRBW, IRCW, IRDW, IREW, IRFW, IRGW, IRHW, IRIW, IRJW, IRKW, IRLW, IRMW
  and and_5 (\中断请求 , ENINT, INTR);
  Shifter #(.width(32), .shift("ll")) shifter_1 (.in(bit_extender_3_out), .\dist (5'b00001), .out(shifter_1_out));
  Shifter #(.width(32), .shift("ll")) shifter_2 (.in(bit_extender_4_out), .\dist (5'b00001), .out(shifter_2_out));
  Multiplexer #(.select(1), .width(32), .disabled("Z"), .enable("false")) multiplexer_6 (
    .in0(RDin), .in1({IR[31:12], {12{1'b0}}}), .out(multiplexer_6_out), .sel(LUI));
  Shifter #(.width(32), .shift("ll")) shifter_3 (.in(bit_extender_5_out), .\dist (5'b01100), .out(shifter_3_out));
  and and_6 (and_6_out, ~URET, INTR);  // AND_Gate
  Regifile regifile_1 (
    .Din(multiplexer_6_out), .Clk(CLK), .R1(regifile_1_r1), .R2(MDin), .WE(RegWrite), .W_num(IR[11:7]),
    .R1_num(multiplexer_4_out), .R2_num(multiplexer_5_out));
  Multiplexer #(.select(1), .width(32), .disabled("Z"), .enable("false")) multiplexer_7 (
    .in0(MDin), .in1(multiplexer_9_out), .out(multiplexer_7_out), .sel(AluSrcB));
  Multiplexer #(.select(1), .width(32), .disabled("Z"), .enable("false")) multiplexer_8 (
    .in0(bit_extender_1_out), .in1(bit_extender_2_out), .out(r2data), .sel(S));
  Adder #(.width(32)) adder_2 (.a(shifter_1_out), .b(PC), .out(adder_2_out));  // open: cin, cout
  Adder #(.width(32)) adder_3 (.a(PC), .b(shifter_2_out), .out(adder_3_out));  // open: cin, cout
  Multiplexer #(.select(1), .width(32), .disabled("Z"), .enable("false")) multiplexer_9 (
    .in0(r2data), .in1(shifter_3_out), .out(multiplexer_9_out), .sel(U_type));
  D_Flip_Flop #(.trigger("rising"), .Pre_Clr_Positions("LEGACY"), .NegatePresetClear("false"), .enable("true"), .NewFFLayout("false")) d_ff_1 (
    .clk(CLK), .D(and_6_out), .Qn(ENINT));  // open: Q, preset, en, reset
  Multiplexer #(.select(1), .width(32), .disabled("Z"), .enable("false")) multiplexer_10 (
    .in0(regifile_1_r1), .in1(PC), .out(multiplexer_10_out), .sel(U_type));
  Multiplexer #(.select(4), .width(32), .disabled("Z"), .enable("false")) multiplexer_11 (
    .in1(32'h1b84), .in2(32'h1ba4), .in3(32'h1bc4), .in4(32'h1be4), .in5(32'h1c04), .in6(32'h1c24),
    .in7(32'h1c44), .in8(32'h1c64), .in9(32'h1c84), .in10(32'hc1e6c), .in11(32'h1e78), .in12(32'h1fcc),
    .in13(32'h1fd4), .out(INT_PC), .sel(\中断输入_1_int_n ));  // open: in0, in14, in15
  ALU alu_1 (
    .X(multiplexer_10_out), .Y(multiplexer_7_out), .AluOP(AluOP), .Equal(AluEQ), .Result(Calcuresult),
    .out_6(Alu));  // open: Result_2, out_4
  Shifter #(.width(32), .shift("ll")) shifter_4 (.in(MDin), .\dist (5'b10000), .out(shifter_4_out));
  Comparator #(.width(32), .mode("twosComplement")) comparator_1 (
    .a(regifile_1_r1), .b(32'h22), .eq(comparator_1_eq));  // open: gt, lt
  Multiplexer #(.select(1), .width(32), .disabled("Z"), .enable("false")) multiplexer_12 (
    .in0(MDin), .in1(shifter_4_out), .out(multiplexer_12_out), .sel(Calcuresult[1]));
  and and_7 (and_7_out, ~comparator_1_eq, ecall);  // AND_Gate
  Register #(.width(32), .trigger("rising"), .Select("low")) register_1 (
    .D(MDin), .en(and_8_out), .Q(LedData), .clk(CLK));  // open: clr
  and and_8 (and_8_out, comparator_1_eq, ecall);
  D_Flip_Flop #(.trigger("falling"), .Pre_Clr_Positions("ABOVE_BELOW"), .NegatePresetClear("false"), .enable("true"), .NewFFLayout("true")) d_ff_2 (
    .clk(CLK), .D(1'b1), .Q(halt), .en(and_7_out), .reset(Go));  // open: Qn, preset
  RAM #(.addrWidth(24), .dataWidth(32), .bus("separate"), .Select("high")) ram_1 (
    .addr(Calcuresult[25:2]), .din(multiplexer_12_out), .data(Dout), .str(MemWrite), .sel(1'b1), .clk(CLK),
    .ld(1'b1));  // open: clr
  Multiplexer #(.select(1), .width(32), .disabled("Z"), .enable("false")) multiplexer_13 (
    .in0(Dout), .in1(LBDout), .out(multiplexer_13_out), .sel(lb));
  \输出逻辑  \u_输出逻辑_1  (
    .out(and_8_out), .\reg (LedData), .CLK(CLK), .D0(\输出逻辑_1_d0 ), .D16(\输出逻辑_1_d16 ), .D1(\输出逻辑_1_d1 ),
    .D17(\输出逻辑_1_d17 ), .D2(\输出逻辑_1_d2 ), .D18(\输出逻辑_1_d18 ), .D3(\输出逻辑_1_d3 ), .D19(\输出逻辑_1_d19 ),
    .D4(\输出逻辑_1_d4 ), .D20(\输出逻辑_1_d20 ), .D21(\输出逻辑_1_d21 ), .D5(\输出逻辑_1_d5 ), .D6(\输出逻辑_1_d6 ),
    .D22(\输出逻辑_1_d22 ), .D7(\输出逻辑_1_d7 ), .D23(\输出逻辑_1_d23 ), .D8(\输出逻辑_1_d8 ), .D24(\输出逻辑_1_d24 ),
    .D9(\输出逻辑_1_d9 ), .D25(\输出逻辑_1_d25 ), .D10(\输出逻辑_1_d10 ), .D26(\输出逻辑_1_d26 ), .D11(\输出逻辑_1_d11 ),
    .D27(\输出逻辑_1_d27 ), .D12(\输出逻辑_1_d12 ), .D28(\输出逻辑_1_d28 ), .D13(\输出逻辑_1_d13 ), .D29(\输出逻辑_1_d29 ),
    .D14(\输出逻辑_1_d14 ), .D30(\输出逻辑_1_d30 ), .D15(\输出逻辑_1_d15 ), .D31(\输出逻辑_1_d31 ));  // open: en, rst
  or or_6 (or_6_out[1], JAL, JALR);
  Multiplexer #(.select(2), .width(32), .disabled("Z"), .enable("false")) multiplexer_14 (
    .in0(Calcuresult), .in1(multiplexer_13_out), .in2(PC_4), .in3(PC_4), .out(RDin),
    .sel({or_6_out[1], MemToReg}));
  // AND_Gate and_9 has open pins: in0=comparator_2_eq, in1=comparator_3_eq, in2=comparator_4_eq, out=open
  Comparator #(.width(32), .mode("twosComplement")) comparator_2 (
    .a(LedData), .b(32'h4), .eq(comparator_2_eq));  // open: gt, lt
  Comparator #(.width(32), .mode("twosComplement")) comparator_3 (
    .a(LedData), .b(32'h3), .eq(comparator_3_eq));  // open: gt, lt
  Comparator #(.width(32), .mode("twosComplement")) comparator_4 (
    .a(LedData), .b(32'h5), .eq(comparator_4_eq));  // open: gt, lt
  // RGBLed #(.multibit("false")) rgbled_1: pin names not known; wires that end beside it: comparator_2_eq, comparator_3_eq, comparator_4_eq
  Multiplexer #(.select(2), .width(8), .disabled("Z"), .enable("false")) multiplexer_15 (
    .in0(Dout[7:0]), .in1(Dout[15:8]), .in2(Dout[23:16]), .in3(Dout[31:24]), .out(multiplexer_15_out),
    .sel(Calcuresult[1:0]));
  DotMatrix #(.inputtype("row"), .matrixcols(32), .matrixrows(32), .persist(0), .dotshape("square")) dotmatrix_1 (
    .row0(\输出逻辑_1_d0 ), .row1(\输出逻辑_1_d1 ), .row2(\输出逻辑_1_d2 ), .row3(\输出逻辑_1_d3 ), .row4(\输出逻辑_1_d4 ),
    .row5(\输出逻辑_1_d5 ), .row6(\输出逻辑_1_d6 ), .row7(\输出逻辑_1_d7 ), .row8(\输出逻辑_1_d8 ), .row9(\输出逻辑_1_d9 ),
    .row10(\输出逻辑_1_d10 ), .row11(\输出逻辑_1_d11 ), .row12(\输出逻辑_1_d12 ), .row13(\输出逻辑_1_d13 ),
    .row14(\输出逻辑_1_d14 ), .row15(\输出逻辑_1_d15 ), .row16(\输出逻辑_1_d16 ), .row17(\输出逻辑_1_d17 ),
    .row18(\输出逻辑_1_d18 ), .row19(\输出逻辑_1_d19 ), .row20(\输出逻辑_1_d20 ), .row21(\输出逻辑_1_d21 ),
    .row22(\输出逻辑_1_d22 ), .row23(\输出逻辑_1_d23 ), .row24(\输出逻辑_1_d24 ), .row25(\输出逻辑_1_d25 ),
    .row26(\输出逻辑_1_d26 ), .row27(\输出逻辑_1_d27 ), .row28(\输出逻辑_1_d28 ), .row29(\输出逻辑_1_d29 ),
    .row30(\输出逻辑_1_d30 ), .row31(\输出逻辑_1_d31 ));
  assign LBDout = {{24{multiplexer_15_out[7]}}, multiplexer_15_out};  // Bit_Extender bit_extender_6
  Button \u_重开  (.out(IRL));
  Button button_1 (.out(IRA));
  Button button_2 (.out(IRD));
  Button PVP (.out(IRJ));
  Button button_3 (.out(IRG));
  Button button_4 (.out(IRC));
  Button button_5 (.out(IRB));
  Button button_6 (.out(IRE));
  Button button_7 (.out(IRF));
  Button button_8 (.out(IRI));
  Button button_9 (.out(IRH));
  Button PVE (.out(IRK));
  Button \u_结束  (.out(IRM));

  // Notes on the sheet:
  //   中断源
  //   中断等待指示
  //   总复位信号应将除ROM以外所有存储组件全部清零
  //   数码管输出
  //   数码管输出应该用寄存器锁存，否则显示数据只能一闪而过
  //   指令探针
  //   指令存储器
  //   指令字
  //   contents of rom_1 (hex, n*v repeats v):
  //   7dd0106f fe010113 812e23 2010413 fe042623 5c0006f fe042423 3c0006f 12400693 fec42703 70793 179793
  //   e787b3 fe842703 e787b3 279793 f687b3 100713 e7a023 fe842783 178793 fef42423 fe842703 200793 fce7d0e3
  //   fec42783 178793 fef42623 fec42703 200793 fae7d0e3 fe042223 5c0006f fe042023 3c0006f 10000693
  //   fe442703 70793 179793 e787b3 fe042703 e787b3 279793 f687b3 713 e7a023 fe042783 178793 fef42023
  //   fe042703 200793 fce7d0e3 fe442783 178793 fef42223 fe442703 200793 fae7d0e3 1607a623 1607a823
  //   1607aa23 13 1c12403 2010113 8067 f5010113 a812623 b010413 fe042623 fe042423 580006f fe042223 380006f
  //   14800693 fe842703 70793 179793 e787b3 fe442703 e787b3 279793 f687b3 7a023 fe442783 178793 fef42223
  //   fe442703 200793 fce7d2e3 fe842783 178793 fef42423 fe842703 200793 fae7d2e3 fe042023 4800006f
  //   fc042e23 440006f 12400693 fe042703 70793 179793 e787b3 fdc42703 e787b3 279793 f687b3 7a783 fec42703
  //   f707b3 fef42623 fdc42783 178793 fcf42e23 fdc42703 200793 fae7dce3 fec42783 ffd78793 800713 40f76663
  //   279713 797 1478793 f707b3 7a783 78067 fc042c23 940006f 12400693 fe042703 70793 179793 e787b3
  //   fd842703 e787b3 279793 f687b3 7a703 100793 4f71c63 14800693 fe042703 70793 179793 e787b3 fd842703
  //   e787b3 279793 f687b3 7a783 178693 14800613 fe042703 70793 179793 e787b3 fd842703 e787b3 279793
  //   f607b3 d7a023 fd842783 178793 fcf42c23 fd842703 200793 f6e7d4e3 34c0006f fc042a23 940006f 12400693
  //   fe042703 70793 179793 e787b3 fd442703 e787b3 279793 f687b3 7a703 100793 4f71c63 14800693 fe042703
  //   70793 179793 e787b3 fd442703 e787b3 279793 f687b3 7a783 a78693 14800613 fe042703 70793 179793 e787b3
  //   fd442703 e787b3 279793 f607b3 d7a023 fd442783 178793 fcf42a23 fd442703 200793 f6e7d4e3 2a40006f
  //   fc042823 940006f 12400693 fe042703 70793 179793 e787b3 fd042703 e787b3 279793 f687b3 7a703 100793
  //   4f71c63 14800693 fe042703 70793 179793 e787b3 fd042703 e787b3 279793 f687b3 7a783 3278693 14800613
  //   fe042703 70793 179793 e787b3 fd042703 e787b3 279793 f607b3 d7a023 fd042783 178793 fcf42823 fd042703
  //   200793 f6e7d4e3 1fc0006f fc042623 940006f 12400693 fe042703 70793 179793 e787b3 fcc42703 e787b3
  //   279793 f687b3 7a703 100793 4f71c63 14800693 fe042703 70793 179793 e787b3 fcc42703 e787b3 279793
  //   f687b3 7a783 c878693 14800613 fe042703 70793 179793 e787b3 fcc42703 e787b3 279793 f607b3 d7a023
  //   fcc42783 178793 fcf42623 fcc42703 200793 f6e7d4e3 1540006f fc042423 940006f 12400693 fe042703 70793
  //   179793 e787b3 fc842703 e787b3 279793 f687b3 7a703 100793 4f71c63 14800693 fe042703 70793 179793
  //   e787b3 fc842703 e787b3 279793 f687b3 7a783 1f478693 14800613 fe042703 70793 179793 e787b3 fc842703
  //   e787b3 279793 f607b3 d7a023 fc842783 178793 fcf42423 fc842703 200793 f6e7d4e3 ac0006f fc042223
  //   940006f 12400693 fe042703 70793 179793 e787b3 fc442703 e787b3 279793 f687b3 7a703 100793 4f71c63
  //   14800693 fe042703 70793 179793 e787b3 fc442703 e787b3 279793 f687b3 7a783 3e878693 14800613 fe042703
  //   70793 179793 e787b3 fc442703 e787b3 279793 f607b3 d7a023 fc442783 178793 fcf42223 fc442703 200793
  //   f6e7d4e3 13 fe042623 fe042783 178793 fef42023 fe042703 200793 b6e7dee3 fc042023 4800006f fa042e23
  //   440006f 12400693 fbc42703 70793 179793 e787b3 fc042703 e787b3 279793 f687b3 7a783 fec42703 f707b3
  //   fef42623 fbc42783 178793 faf42e23 fbc42703 200793 fae7dce3 fec42783 ffd78793 800713 40f76663 279713
  //   797 1478793 f707b3 7a783 78067 fa042c23 940006f 12400693 fb842703 70793 179793 e787b3 fc042703
  //   e787b3 279793 f687b3 7a703 100793 4f71c63 14800693 fb842703 70793 179793 e787b3 fc042703 e787b3
  //   279793 f687b3 7a783 178693 14800613 fb842703 70793 179793 e787b3 fc042703 e787b3 279793 f607b3
  //   d7a023 fb842783 178793 faf42c23 fb842703 200793 f6e7d4e3 34c0006f fa042a23 940006f 12400693 fb442703
  //   70793 179793 e787b3 fc042703 e787b3 279793 f687b3 7a703 100793 4f71c63 14800693 fb442703 70793
  //   179793 e787b3 fc042703 e787b3 279793 f687b3 7a783 a78693 14800613 fb442703 70793 179793 e787b3
  //   fc042703 e787b3 279793 f607b3 d7a023 fb442783 178793 faf42a23 fb442703 200793 f6e7d4e3 2a40006f
  //   fa042823 940006f 12400693 fb042703 70793 179793 e787b3 fc042703 e787b3 279793 f687b3 7a703 100793
  //   4f71c63 1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
  //   JAL
  //   JALR
  //   URET
  //   LUI
  //   Beq
  //   Bne
  //   AluOP
  //   AluSrcB
  //   RegWrite
  //   MemToReg
  //   MemWrite
  //   LUI
  //   为方便自动评测，需要输出PC，IR，寄存器堆写如数据RDin
  //   RAM写使能MemWrite、RAM写入数据MDin等信号
  //   数据存储器
  //   用这个时钟源需要去掉电路中的其他时钟源
  //   红色圆形胜
  //   蓝色叉叉胜
  //   绿色平局
endmodule

module \单周期RISC_V  (
  input  IR1,
  input  IR2,
  input  IR3,
  output RegWrite,
  output MemWrite,
  output [31:0] PC,
  output [31:0] IR,
  output [31:0] RDin,
  output [31:0] MDin,
  output [31:0] LedData
);

  wire Alu, AluEQ, AluSrcB, and_1_out, and_2_out, and_3_out, and_4_out, and_5_out, and_6_out, Beq, BGE, bltu,
       Bne, CLK, clock_1_out, comparator_1_eq, comparator_2_eq, comparator_2_lt, d_ff_2_q, ecall, Go, halt,
       IR1_t, IR2_t, IR3_t, IRA, IRB, IRC, JAL, JALR, lb, LUI, MemToReg, nand_1_out, not_1_out, not_2_out,
       or_1_out, or_2_out, RST, S, U_type, URET, W1, W2, W3;
  wire [1:0] priority_encoder_1_out;
  wire [1:1] or_6_out;
  wire [3:0] AluOP;
  wire [4:0] multiplexer_2_out, multiplexer_3_out;
  wire [7:0] multiplexer_10_out;
  wire [12:0] CNT_num;
  wire [15:0] \总周期数 ;
  wire [31:0] adder_2_out, adder_3_out, bit_extender_1_out, bit_extender_2_out, bit_extender_3_out,
       bit_extender_4_out, bit_extender_5_out, Calcuresult, Dout, LBDout, multiplexer_1_out,
       multiplexer_4_out, multiplexer_5_out, multiplexer_7_out, multiplexer_8_out, PC_4, r2data,
       regifile_1_r1, shifter_1_out, shifter_2_out, shifter_3_out, shifter_4_out;

  Button \u_继续运行  (.out(Go));
  Button _1 (.out(IRA));
  Button _2 (.out(IRB));
  Button _3 (.out(IRC));
  LED #(.active("true")) led_1 (.in(W1));
  LED #(.active("true")) led_2 (.in(W2));
  LED #(.active("true")) led_3 (.in(W3));
  Priority_Encoder #(.select(2), .disabled("Z")) priority_encoder_1 (
    .in0(1'b1), .in1(JALR), .in2(JAL), .in3(or_2_out), .out(priority_encoder_1_out));  // open: gs, en_out, en_in
  not not_1 (not_1_out, halt);
  Hex_Digit_Display hex_digit_display_1 (.value(LedData[31:28]));  // open: dp
  or or_1 (or_1_out, and_3_out, and_4_out);
  or or_2 (or_2_out, or_1_out, and_2_out, and_1_out);
  and and_1 (and_1_out, Alu, bltu);
  and and_2 (and_2_out, ~Alu, BGE);  // AND_Gate
  Multiplexer #(.select(2), .width(32), .disabled("Z"), .enable("false")) multiplexer_1 (
    .in0(PC_4), .in1(Calcuresult), .in2(adder_3_out), .in3(adder_2_out), .out(multiplexer_1_out),
    .sel(priority_encoder_1_out));
  Register #(.width(32), .trigger("rising"), .Select("low")) u_PC (
    .D(multiplexer_1_out), .en(not_2_out), .Q(PC), .clk(CLK), .clr(RST));
  not not_2 (not_2_out, halt);
  Counter #(.width(16), .max('hffff), .ongoal("wrap"), .trigger("rising"), .behavior("new")) counter_1 (
    .count(not_1_out), .Q(\总周期数 ), .clk(CLK));  // open: load, D, carry, clr, preset, down
  Hex_Digit_Display hex_digit_display_2 (.value(LedData[23:20]));  // open: dp
  Hex_Digit_Display hex_digit_display_3 (.value(LedData[27:24]));  // open: dp
  and and_3 (and_3_out, Beq, AluEQ);
  and and_4 (and_4_out, ~AluEQ, Bne);  // AND_Gate
  Adder #(.width(32)) adder_1 (.a(PC), .b(32'h4), .out(PC_4));  // open: cin, cout
  Hex_Digit_Display hex_digit_display_4 (.value(LedData[15:12]));  // open: dp
  Hex_Digit_Display hex_digit_display_5 (.value(LedData[19:16]));  // open: dp
  // RiscV_Probe riscv_probe_1: pin names not known; wires that end beside it: IR
  Hex_Digit_Display hex_digit_display_6 (.value(LedData[11:8]));  // open: dp
  Hex_Digit_Display hex_digit_display_7 (.value(LedData[7:4]));  // open: dp
  // Probe on \总周期数 
  ROM #(.addrWidth(10), .dataWidth(32), .Select("high")) rom_1 (.addr(PC[11:2]), .data(IR));
  Hex_Digit_Display hex_digit_display_8 (.value(LedData[3:0]));  // open: dp
  \单周期硬布线控制器  \u_单周期硬布线控制器_1  (
    .Funct({IR[30], IR[25], IR[14:12]}), .OP(IR[6:2]), .ALU_OP(AluOP), .MemToReg(MemToReg),
    .MemWrite(MemWrite), .ALU_SRC(AluSrcB), .RegWrite(RegWrite), .ecall(ecall), .S_type(S), .Jalr(JALR),
    .Beq(Beq), .JAL(JAL), .Bne(Bne), .in_3(IR[21]), .uret(URET), .LUI(LUI), .lb(lb), .bltu(bltu), .BGE(BGE),
    .U_type(U_type));  // open: re2_used, rs1_used, CSRRSI, CSRRCI
  Multiplexer #(.select(1), .width(5), .disabled("Z"), .enable("false")) multiplexer_2 (
    .in0(IR[19:15]), .in1(5'b10001), .out(multiplexer_2_out), .sel(ecall));
  Multiplexer #(.select(1), .width(5), .disabled("Z"), .enable("false")) multiplexer_3 (
    .in0(IR[24:20]), .in1(5'b01010), .out(multiplexer_3_out), .sel(ecall));
  assign bit_extender_1_out = {{12{IR[31]}}, IR[31:12]};  // Bit_Extender bit_extender_1
  or or_3 (IR1_t, IR1, IRA);
  assign bit_extender_2_out = {{20{IR[31]}}, IR[31:20]};  // Bit_Extender bit_extender_2
  assign bit_extender_3_out = {{20{IR[31]}}, {IR[31:25], IR[11:7]}};  // Bit_Extender bit_extender_3
  assign bit_extender_4_out = {{20{IR[31]}}, {IR[31], IR[7], IR[30:25], IR[11:8]}};  // Bit_Extender bit_extender_4
  assign bit_extender_5_out = {{12{IR[31]}}, {IR[31], IR[19:12], IR[20], IR[30:21]}};  // Bit_Extender bit_extender_5
  Shifter #(.width(32), .shift("ll")) shifter_1 (.in(bit_extender_1_out), .\dist (5'b01100), .out(shifter_1_out));
  or or_4 (IR2_t, IR2, IRB);
  Regifile regifile_1 (
    .Din(multiplexer_4_out), .Clk(CLK), .R1(regifile_1_r1), .R2(MDin), .WE(RegWrite), .W_num(IR[11:7]),
    .R1_num(multiplexer_2_out), .R2_num(multiplexer_3_out));
  Shifter #(.width(32), .shift("ll")) shifter_2 (.in(bit_extender_4_out), .\dist (5'b00001), .out(shifter_2_out));
  Shifter #(.width(32), .shift("ll")) shifter_3 (.in(bit_extender_5_out), .\dist (5'b00001), .out(shifter_3_out));
  Multiplexer #(.select(1), .width(32), .disabled("Z"), .enable("false")) multiplexer_4 (
    .in0(RDin), .in1({IR[31:12], {12{1'b0}}}), .out(multiplexer_4_out), .sel(LUI));
  Multiplexer #(.select(1), .width(32), .disabled("Z"), .enable("false")) multiplexer_5 (
    .in0(MDin), .in1(r2data), .out(multiplexer_5_out), .sel(AluSrcB));
  Multiplexer #(.select(1), .width(32), .disabled("Z"), .enable("false")) multiplexer_6 (
    .in0(bit_extender_2_out), .in1(bit_extender_3_out), .out(r2data), .sel(S));
  Adder #(.width(32)) adder_2 (.a(shifter_2_out), .b(PC), .out(adder_2_out));  // open: cin, cout
  Adder #(.width(32)) adder_3 (.a(PC), .b(shifter_3_out), .out(adder_3_out));  // open: cin, cout
  or or_5 (IR3_t, IR3, IRC);
  ALU alu_1 (
    .X(regifile_1_r1), .Y(multiplexer_5_out), .AluOP(AluOP), .Equal(AluEQ), .Result(Calcuresult), .out_6(Alu));  // open: Result_2, out_4
  Shifter #(.width(32), .shift("ll")) shifter_4 (.in(MDin), .\dist (5'b10000), .out(shifter_4_out));
  Comparator #(.width(32), .mode("twosComplement")) comparator_1 (
    .a(regifile_1_r1), .b(32'h22), .eq(comparator_1_eq));  // open: gt, lt
  Multiplexer #(.select(1), .width(32), .disabled("Z"), .enable("false")) multiplexer_7 (
    .in0(MDin), .in1(shifter_4_out), .out(multiplexer_7_out), .sel(Calcuresult[1]));
  and and_5 (and_5_out, ~comparator_1_eq, ecall);  // AND_Gate
  D_Flip_Flop #(.trigger("falling"), .Pre_Clr_Positions("ABOVE_BELOW"), .NegatePresetClear("false"), .enable("true"), .NewFFLayout("true")) d_ff_1 (
    .clk(CLK), .D(1'b1), .Q(halt), .en(and_5_out), .reset(Go));  // open: Qn, preset
  Register #(.width(32), .trigger("rising"), .Select("low")) register_1 (
    .D(MDin), .en(and_6_out), .Q(LedData), .clk(CLK));  // open: clr
  and and_6 (and_6_out, comparator_1_eq, ecall);
  RAM #(.addrWidth(24), .dataWidth(32), .bus("separate"), .Select("high")) ram_1 (
    .addr(Calcuresult[25:2]), .din(multiplexer_7_out), .data(Dout), .str(MemWrite), .sel(1'b1), .clk(CLK),
    .ld(1'b1));  // open: clr
  Multiplexer #(.select(1), .width(32), .disabled("Z"), .enable("false")) multiplexer_8 (
    .in0(Dout), .in1(LBDout), .out(multiplexer_8_out), .sel(lb));
  D_Flip_Flop #(.trigger("high"), .Pre_Clr_Positions("LEGACY"), .NegatePresetClear("false"), .enable("true"), .NewFFLayout("false")) d_ff_2 (.Q(d_ff_2_q));  // open: clk, D, Qn, preset, en, reset
  // Probe on 13'hc
  or or_6 (or_6_out[1], JAL, JALR);
  Multiplexer #(.select(2), .width(32), .disabled("Z"), .enable("false")) multiplexer_9 (
    .in0(Calcuresult), .in1(multiplexer_8_out), .in2(PC_4), .in3(PC_4), .out(RDin),
    .sel({or_6_out[1], MemToReg}));
  Comparator #(.width(13), .mode("twosComplement")) comparator_2 (
    .a(CNT_num), .b(13'hc), .eq(comparator_2_eq), .lt(comparator_2_lt));  // open: gt
  Clock #(.highDuration(1), .lowDuration(1)) clock_1 (.out(clock_1_out));
  Counter #(.width(13), .max('h1fff), .ongoal("stay"), .trigger("rising"), .behavior("old")) counter_2 (
    .count(comparator_2_lt), .Q(CNT_num), .clk(clock_1_out));  // open: load, D, carry, clr, preset
  nand nand_1 (nand_1_out, d_ff_2_q, comparator_2_eq);
  Multiplexer #(.select(2), .width(8), .disabled("Z"), .enable("false")) multiplexer_10 (
    .in0(Dout[7:0]), .in1(Dout[15:8]), .in2(Dout[23:16]), .in3(Dout[31:24]), .out(multiplexer_10_out),
    .sel(Calcuresult[1:0]));
  assign CLK = nand_1_out ? clock_1_out : 1'bz;  // Controlled_Buffer controlled_buffer_1
  Pull_Resistor #(.pull(1)) pull_resistor_1 (.node(CLK));
  assign LBDout = {{24{multiplexer_10_out[7]}}, multiplexer_10_out};  // Bit_Extender bit_extender_6

  // Notes on the sheet:
  //   中断源
  //   中断等待指示
  //   数码管输出应该用寄存器锁存，否则显示数据只能一闪而过
  //   数码管输出
  //   指令探针
  //   指令存储器
  //   指令字
  //   contents of rom_1 (hex, n*v repeats v):
  //   84a023
  //   JAL
  //   JALR
  //   URET
  //   LUI
  //   Beq
  //   Bne
  //   MemToReg
  //   MemWrite
  //   AluOP
  //   AluSrcB
  //   RegWrite
  //   LUI
  //   数据存储器
  //   为方便自动评测，需要输出PC，IR，寄存器堆写如数据RDin
  //   RAM写使能MemWrite、RAM写入数据MDin等信号
  //   控制位
  //   暂停节拍，不能为0
  //   戳工具置1进入计数暂停模式，ctrl+k时钟自动运行到对应节拍暂停
  //   ctrl+k关闭时钟连续运行，将控制位置零，进入单步调试模式调试
  //   用这个时钟源需要去掉电路中的其他时钟源
  //   可计数暂停的时钟源
endmodule

// 单周期硬布线控制器
module \单周期硬布线控制器  (
  input  [4:0] OP,
  input  [4:0] Funct,
  input  in_3,
  output [3:0] ALU_OP,
  output uret,
  output U_type,
  output MemToReg,
  output ecall,
  output MemWrite,
  output ALU_SRC,
  output RegWrite,
  output S_type,
  output Beq,
  output Bne,
  output Jalr,
  output JAL,
  output CSRRSI,
  output LUI,
  output lb,
  output bltu,
  output CSRRCI,
  output re2_used,
  output rs1_used,
  output BGE
);

  wire \控制信号自动生成_1_ecall ;

  \运算控制器自动生成  \u_运算控制器自动生成_1  (
    .OP2(OP[0]), .OP3(OP[1]), .OP4(OP[2]), .OP5(OP[3]), .OP6(OP[4]), .F12(Funct[0]), .F13(Funct[1]),
    .F14(Funct[2]), .F25(Funct[3]), .F30(Funct[4]), .S0(ALU_OP[0]), .S1(ALU_OP[1]), .S2(ALU_OP[2]),
    .S3(ALU_OP[3]));
  \控制信号自动生成  \u_控制信号自动生成_1  (
    .OP2(OP[0]), .OP3(OP[1]), .OP4(OP[2]), .OP5(OP[3]), .OP6(OP[4]), .F12(Funct[0]), .F13(Funct[1]),
    .F14(Funct[2]), .F25(Funct[3]), .F30(Funct[4]), .rs2used(re2_used), .rs1used(rs1_used),
    .MemToReg(MemToReg), .MemWrite(MemWrite), .ALU_SRC(ALU_SRC), .RegWrite(RegWrite),
    .ecall(\控制信号自动生成_1_ecall ), .S_Type(S_type), .BEQ(Beq), .BNE(Bne), .JALR(Jalr), .JAL(JAL), .LUI(LUI),
    .LB(lb), .BLTU(bltu), .CSRRSI(CSRRSI), .CSRRCI(CSRRCI), .BGE(BGE), .U_type(U_type));
  and and_1 (uret, in_3, \控制信号自动生成_1_ecall );
  and and_2 (ecall, ~in_3, \控制信号自动生成_1_ecall );  // AND_Gate

  // Other names for the same wires on the sheet: IR21 = in_3; OP_CODE[4:0] = OP

  // Notes on the sheet:
  //   运算器控制器，根据指令生成运算器功能选择信号
  //   控制信号生成，产生数据通路需要的其他控制信号
endmodule

// 运算器控制器
module \运算控制器自动生成  (
  input  OP2,
  input  OP3,
  input  OP4,
  input  OP5,
  input  OP6,
  input  F12,
  input  F13,
  input  F14,
  input  F25,
  input  F30,
  output S0,
  output S1,
  output S2,
  output S3
);

  wire and_1_out, and_2_out, and_3_out, and_4_out, and_5_out, and_6_out, and_7_out, and_8_out, and_9_out,
       and_10_out, and_11_out, and_12_out, and_13_out, and_14_out, and_15_out, and_16_out, and_17_out,
       and_18_out, and_19_out, and_20_out, and_21_out, and_22_out, and_23_out, and_24_out, and_25_out,
       and_26_out, and_27_out, and_28_out, and_29_out, and_30_out, and_31_out, and_32_out, and_33_out,
       and_34_out, and_35_out, and_36_out, and_37_out, and_38_out, and_39_out, and_40_out, and_41_out,
       and_42_out, and_43_out, and_44_out, and_45_out, and_46_out, and_47_out, not_1_out, not_2_out,
       not_3_out, not_4_out, not_5_out, not_6_out, not_7_out, not_8_out, not_9_out, not_10_out, not_11_out,
       not_12_out, not_13_out, not_14_out, not_15_out, not_16_out, not_17_out, not_18_out, not_19_out,
       not_20_out, not_21_out, not_22_out, not_23_out, not_24_out, not_25_out, not_26_out, not_27_out,
       not_28_out, not_29_out, not_30_out, not_31_out, not_32_out, not_33_out, not_34_out, not_35_out,
       not_36_out, not_37_out, not_38_out, not_39_out, not_40_out, not_41_out, not_42_out, not_43_out,
       not_44_out, not_45_out, not_46_out, not_47_out, not_48_out, not_49_out, not_50_out, not_51_out,
       not_52_out, not_53_out, not_54_out, not_55_out, not_56_out, not_57_out, not_58_out, not_59_out,
       not_60_out, not_61_out, not_62_out, not_63_out, not_64_out, not_65_out, not_66_out, not_67_out,
       not_68_out, not_69_out, not_70_out, not_71_out, not_72_out, not_73_out, not_74_out, not_75_out,
       not_76_out, not_77_out, not_78_out, not_79_out, not_80_out, not_81_out, not_82_out, not_83_out,
       not_84_out, not_85_out, not_86_out, not_87_out, not_88_out, not_89_out, not_90_out, not_91_out,
       not_92_out, not_93_out, not_94_out, not_95_out, not_96_out, not_97_out, not_98_out, not_99_out,
       not_100_out, not_101_out, not_102_out, not_103_out, not_104_out, not_105_out, not_106_out,
       not_107_out, not_108_out, not_109_out, not_110_out, not_111_out, not_112_out, not_113_out,
       not_114_out, not_115_out, not_116_out, not_117_out, not_118_out, not_119_out, not_120_out,
       not_121_out, not_122_out, not_123_out, not_124_out, not_125_out, not_126_out, not_127_out,
       not_128_out, not_129_out, not_130_out, not_131_out, not_132_out, not_133_out, not_134_out,
       not_135_out, not_136_out, not_137_out, not_138_out, not_139_out, not_140_out, not_141_out,
       not_142_out, not_143_out, not_144_out, not_145_out, not_146_out, not_147_out, not_148_out,
       not_149_out, not_150_out, not_151_out, not_152_out, not_153_out, not_154_out, not_155_out,
       not_156_out, not_157_out, not_158_out, not_159_out, not_160_out, not_161_out, not_162_out,
       not_163_out, not_164_out, not_165_out, not_166_out, not_167_out, not_168_out, not_169_out,
       not_170_out, not_171_out, not_172_out, not_173_out, not_174_out, not_175_out, not_176_out,
       not_177_out, not_178_out, not_179_out, not_180_out, not_181_out, not_182_out, not_183_out,
       not_184_out, not_185_out, not_186_out, not_187_out, not_188_out, not_189_out, not_190_out,
       not_191_out, not_192_out, not_193_out, not_194_out, not_195_out, not_196_out, not_197_out,
       not_198_out, not_199_out, not_200_out, not_201_out, not_202_out, not_203_out, not_204_out,
       not_205_out, not_206_out, not_207_out, not_208_out, not_209_out, not_210_out, not_211_out,
       not_212_out, not_213_out, not_214_out, not_215_out, not_216_out, not_217_out, not_218_out,
       not_219_out, not_220_out, not_221_out, not_222_out, not_223_out, not_224_out, not_225_out,
       not_226_out, not_227_out, not_228_out, not_229_out, not_230_out, not_231_out, not_232_out,
       not_233_out, not_234_out, not_235_out, not_236_out, not_237_out, not_238_out, not_239_out,
       not_240_out, not_241_out, not_242_out, not_243_out, not_244_out, not_245_out, not_246_out,
       not_247_out, not_248_out, not_249_out, not_250_out, not_251_out, not_252_out, not_253_out,
       not_254_out, not_255_out, not_256_out, not_257_out, not_258_out, not_259_out, not_260_out,
       not_261_out, not_262_out, not_263_out, not_264_out, not_265_out, not_266_out, not_267_out, not_268_out;

  not not_1 (not_1_out, F30);
  not not_2 (not_2_out, F25);
  not not_3 (not_3_out, F14);
  not not_4 (not_4_out, F13);
  not not_5 (not_5_out, F12);
  not not_6 (not_6_out, OP6);
  not not_7 (not_7_out, OP3);
  not not_8 (not_8_out, OP2);
  not not_9 (not_9_out, F30);
  not not_10 (not_10_out, F25);
  not not_11 (not_11_out, OP6);
  not not_12 (not_12_out, OP3);
  not not_13 (not_13_out, OP2);
  not not_14 (not_14_out, F30);
  not not_15 (not_15_out, F25);
  not not_16 (not_16_out, F14);
  not not_17 (not_17_out, F12);
  not not_18 (not_18_out, OP6);
  not not_19 (not_19_out, OP3);
  not not_20 (not_20_out, OP2);
  not not_21 (not_21_out, F14);
  not not_22 (not_22_out, F13);
  not not_23 (not_23_out, F12);
  not not_24 (not_24_out, OP6);
  not not_25 (not_25_out, OP5);
  not not_26 (not_26_out, OP3);
  not not_27 (not_27_out, OP2);
  not not_28 (not_28_out, OP6);
  not not_29 (not_29_out, OP5);
  not not_30 (not_30_out, OP3);
  not not_31 (not_31_out, OP2);
  not not_32 (not_32_out, F13);
  not not_33 (not_33_out, F12);
  not not_34 (not_34_out, OP6);
  not not_35 (not_35_out, OP5);
  not not_36 (not_36_out, OP3);
  not not_37 (not_37_out, OP2);
  not not_38 (not_38_out, F14);
  not not_39 (not_39_out, F12);
  not not_40 (not_40_out, OP6);
  not not_41 (not_41_out, OP5);
  not not_42 (not_42_out, OP3);
  not not_43 (not_43_out, OP2);
  not not_44 (not_44_out, F25);
  not not_45 (not_45_out, F13);
  not not_46 (not_46_out, OP6);
  not not_47 (not_47_out, OP5);
  not not_48 (not_48_out, OP3);
  not not_49 (not_49_out, OP2);
  not not_50 (not_50_out, F14);
  not not_51 (not_51_out, F12);
  not not_52 (not_52_out, OP6);
  not not_53 (not_53_out, OP5);
  not not_54 (not_54_out, OP4);
  not not_55 (not_55_out, OP3);
  not not_56 (not_56_out, OP2);
  not not_57 (not_57_out, F14);
  not not_58 (not_58_out, F12);
  not not_59 (not_59_out, OP6);
  not not_60 (not_60_out, OP4);
  not not_61 (not_61_out, OP3);
  not not_62 (not_62_out, OP2);
  not not_63 (not_63_out, F14);
  not not_64 (not_64_out, F13);
  not not_65 (not_65_out, F12);
  not not_66 (not_66_out, OP4);
  not not_67 (not_67_out, OP3);
  not not_68 (not_68_out, F25);
  not not_69 (not_69_out, F13);
  not not_70 (not_70_out, OP6);
  not not_71 (not_71_out, OP3);
  not not_72 (not_72_out, OP2);
  not not_73 (not_73_out, F14);
  not not_74 (not_74_out, F13);
  not not_75 (not_75_out, F12);
  not not_76 (not_76_out, OP6);
  not not_77 (not_77_out, OP5);
  not not_78 (not_78_out, OP4);
  not not_79 (not_79_out, OP3);
  not not_80 (not_80_out, OP2);
  not not_81 (not_81_out, F13);
  not not_82 (not_82_out, OP4);
  not not_83 (not_83_out, OP3);
  not not_84 (not_84_out, OP2);
  not not_85 (not_85_out, OP6);
  not not_86 (not_86_out, OP5);
  not not_87 (not_87_out, OP3);
  not not_88 (not_88_out, F25);
  not not_89 (not_89_out, F14);
  not not_90 (not_90_out, F13);
  not not_91 (not_91_out, F12);
  not not_92 (not_92_out, OP6);
  not not_93 (not_93_out, OP3);
  not not_94 (not_94_out, OP2);
  not not_95 (not_95_out, F30);
  not not_96 (not_96_out, F25);
  not not_97 (not_97_out, OP6);
  not not_98 (not_98_out, OP3);
  not not_99 (not_99_out, OP2);
  not not_100 (not_100_out, F30);
  not not_101 (not_101_out, F25);
  not not_102 (not_102_out, F14);
  not not_103 (not_103_out, F12);
  not not_104 (not_104_out, OP6);
  not not_105 (not_105_out, OP3);
  not not_106 (not_106_out, OP2);
  not not_107 (not_107_out, OP6);
  not not_108 (not_108_out, OP5);
  not not_109 (not_109_out, OP3);
  not not_110 (not_110_out, OP2);
  not not_111 (not_111_out, F14);
  not not_112 (not_112_out, F12);
  not not_113 (not_113_out, OP6);
  not not_114 (not_114_out, OP5);
  not not_115 (not_115_out, OP3);
  not not_116 (not_116_out, OP2);
  not not_117 (not_117_out, F30);
  not not_118 (not_118_out, F25);
  not not_119 (not_119_out, F13);
  not not_120 (not_120_out, OP6);
  not not_121 (not_121_out, OP5);
  not not_122 (not_122_out, OP3);
  not not_123 (not_123_out, OP2);
  not not_124 (not_124_out, F14);
  not not_125 (not_125_out, F13);
  not not_126 (not_126_out, F12);
  not not_127 (not_127_out, OP4);
  not not_128 (not_128_out, OP3);
  not not_129 (not_129_out, OP2);
  not not_130 (not_130_out, F14);
  not not_131 (not_131_out, F13);
  not not_132 (not_132_out, OP4);
  not not_133 (not_133_out, OP3);
  not not_134 (not_134_out, OP2);
  not not_135 (not_135_out, F13);
  not not_136 (not_136_out, OP4);
  not not_137 (not_137_out, OP3);
  not not_138 (not_138_out, OP2);
  not not_139 (not_139_out, F30);
  not not_140 (not_140_out, F25);
  not not_141 (not_141_out, F14);
  not not_142 (not_142_out, F13);
  not not_143 (not_143_out, F12);
  not not_144 (not_144_out, OP6);
  not not_145 (not_145_out, OP3);
  not not_146 (not_146_out, OP2);
  not not_147 (not_147_out, F25);
  not not_148 (not_148_out, F14);
  not not_149 (not_149_out, F13);
  not not_150 (not_150_out, F12);
  not not_151 (not_151_out, OP6);
  not not_152 (not_152_out, OP3);
  not not_153 (not_153_out, OP2);
  not not_154 (not_154_out, F30);
  not not_155 (not_155_out, F25);
  not not_156 (not_156_out, OP6);
  not not_157 (not_157_out, OP3);
  not not_158 (not_158_out, OP2);
  not not_159 (not_159_out, F30);
  not not_160 (not_160_out, F25);
  not not_161 (not_161_out, F14);
  not not_162 (not_162_out, OP6);
  not not_163 (not_163_out, OP3);
  not not_164 (not_164_out, OP2);
  not not_165 (not_165_out, F14);
  not not_166 (not_166_out, F13);
  not not_167 (not_167_out, F12);
  not not_168 (not_168_out, OP6);
  not not_169 (not_169_out, OP5);
  not not_170 (not_170_out, OP3);
  not not_171 (not_171_out, OP2);
  not not_172 (not_172_out, OP6);
  not not_173 (not_173_out, OP5);
  not not_174 (not_174_out, OP3);
  not not_175 (not_175_out, OP2);
  not not_176 (not_176_out, F14);
  not not_177 (not_177_out, F12);
  not not_178 (not_178_out, OP6);
  not not_179 (not_179_out, OP5);
  not not_180 (not_180_out, OP4);
  not not_181 (not_181_out, OP3);
  not not_182 (not_182_out, OP2);
  not not_183 (not_183_out, F14);
  not not_184 (not_184_out, F12);
  not not_185 (not_185_out, OP6);
  not not_186 (not_186_out, OP4);
  not not_187 (not_187_out, OP3);
  not not_188 (not_188_out, OP2);
  not not_189 (not_189_out, F14);
  not not_190 (not_190_out, F13);
  not not_191 (not_191_out, F12);
  not not_192 (not_192_out, OP4);
  not not_193 (not_193_out, OP3);
  not not_194 (not_194_out, OP2);
  not not_195 (not_195_out, F14);
  not not_196 (not_196_out, F13);
  not not_197 (not_197_out, OP4);
  not not_198 (not_198_out, OP3);
  not not_199 (not_199_out, OP2);
  not not_200 (not_200_out, F14);
  not not_201 (not_201_out, F13);
  not not_202 (not_202_out, F12);
  not not_203 (not_203_out, OP4);
  not not_204 (not_204_out, OP3);
  not not_205 (not_205_out, F14);
  not not_206 (not_206_out, F13);
  not not_207 (not_207_out, F12);
  not not_208 (not_208_out, OP6);
  not not_209 (not_209_out, OP5);
  not not_210 (not_210_out, OP4);
  not not_211 (not_211_out, OP3);
  not not_212 (not_212_out, OP2);
  not not_213 (not_213_out, F12);
  not not_214 (not_214_out, OP4);
  not not_215 (not_215_out, OP3);
  not not_216 (not_216_out, OP2);
  not not_217 (not_217_out, F30);
  not not_218 (not_218_out, F13);
  not not_219 (not_219_out, OP6);
  not not_220 (not_220_out, OP3);
  not not_221 (not_221_out, OP2);
  not not_222 (not_222_out, OP6);
  not not_223 (not_223_out, OP5);
  not not_224 (not_224_out, OP3);
  not not_225 (not_225_out, F30);
  not not_226 (not_226_out, F25);
  not not_227 (not_227_out, F12);
  not not_228 (not_228_out, OP6);
  not not_229 (not_229_out, OP3);
  not not_230 (not_230_out, OP2);
  not not_231 (not_231_out, F30);
  not not_232 (not_232_out, F25);
  not not_233 (not_233_out, F14);
  not not_234 (not_234_out, F12);
  not not_235 (not_235_out, OP6);
  not not_236 (not_236_out, OP3);
  not not_237 (not_237_out, OP2);
  not not_238 (not_238_out, F30);
  not not_239 (not_239_out, F25);
  not not_240 (not_240_out, F14);
  not not_241 (not_241_out, OP6);
  not not_242 (not_242_out, OP3);
  not not_243 (not_243_out, OP2);
  not not_244 (not_244_out, F12);
  not not_245 (not_245_out, OP6);
  not not_246 (not_246_out, OP5);
  not not_247 (not_247_out, OP3);
  not not_248 (not_248_out, OP2);
  not not_249 (not_249_out, F13);
  not not_250 (not_250_out, F12);
  not not_251 (not_251_out, OP6);
  not not_252 (not_252_out, OP5);
  not not_253 (not_253_out, OP3);
  not not_254 (not_254_out, OP2);
  not not_255 (not_255_out, F14);
  not not_256 (not_256_out, F12);
  not not_257 (not_257_out, OP6);
  not not_258 (not_258_out, OP5);
  not not_259 (not_259_out, OP3);
  not not_260 (not_260_out, OP2);
  not not_261 (not_261_out, F12);
  not not_262 (not_262_out, OP4);
  not not_263 (not_263_out, OP3);
  not not_264 (not_264_out, OP2);
  not not_265 (not_265_out, F13);
  not not_266 (not_266_out, OP4);
  not not_267 (not_267_out, OP3);
  not not_268 (not_268_out, OP2);
  and and_1 (and_1_out, not_1_out, not_2_out, not_3_out, not_4_out, not_5_out, not_6_out, OP5, OP4, not_7_out, not_8_out);
  and and_2 (and_2_out, not_9_out, not_10_out, F14, F13, F12, not_11_out, OP5, OP4, not_12_out, not_13_out);
  and and_3 (and_3_out, not_14_out, not_15_out, not_16_out, F13, not_17_out, not_18_out, OP5, OP4, not_19_out, not_20_out);
  and and_4 (and_4_out, not_21_out, not_22_out, not_23_out, not_24_out, not_25_out, OP4, not_26_out, not_27_out);
  and and_5 (and_5_out, F14, F13, F12, not_28_out, not_29_out, OP4, not_30_out, not_31_out);
  and and_6 (and_6_out, F14, not_32_out, not_33_out, not_34_out, not_35_out, OP4, not_36_out, not_37_out);
  and and_7 (and_7_out, not_38_out, F13, not_39_out, not_40_out, not_41_out, OP4, not_42_out, not_43_out);
  and and_8 (and_8_out, F30, not_44_out, F14, not_45_out, F12, not_46_out, not_47_out, OP4, not_48_out, not_49_out);
  and and_9 (and_9_out, not_50_out, F13, not_51_out, not_52_out, not_53_out, not_54_out, not_55_out, not_56_out);
  and and_10 (and_10_out, not_57_out, F13, not_58_out, not_59_out, OP5, not_60_out, not_61_out, not_62_out);
  and and_11 (and_11_out, not_63_out, not_64_out, not_65_out, OP6, OP5, not_66_out, not_67_out, OP2);
  and and_12 (and_12_out, F30, not_68_out, F14, not_69_out, F12, not_70_out, OP5, OP4, not_71_out, not_72_out);
  and and_13 (and_13_out, not_73_out, not_74_out, not_75_out, not_76_out, not_77_out, not_78_out, not_79_out, not_80_out);
  and and_14 (and_14_out, F14, not_81_out, F12, OP6, OP5, not_82_out, not_83_out, not_84_out);
  and and_15 (and_15_out, not_85_out, not_86_out, OP4, not_87_out, OP2);
  and and_16 (and_16_out, F30, not_88_out, not_89_out, not_90_out, not_91_out, not_92_out, OP5, OP4, not_93_out, not_94_out);
  and and_17 (and_17_out, not_95_out, not_96_out, F14, F13, F12, not_97_out, OP5, OP4, not_98_out, not_99_out);
  and and_18 (and_18_out, not_100_out, not_101_out, not_102_out, F13, not_103_out, not_104_out, OP5, OP4, not_105_out, not_106_out);
  and and_19 (and_19_out, F14, F13, F12, not_107_out, not_108_out, OP4, not_109_out, not_110_out);
  and and_20 (and_20_out, not_111_out, F13, not_112_out, not_113_out, not_114_out, OP4, not_115_out, not_116_out);
  and and_21 (and_21_out, not_117_out, not_118_out, F14, not_119_out, F12, not_120_out, not_121_out, OP4, not_122_out, not_123_out);
  and and_22 (and_22_out, not_124_out, not_125_out, not_126_out, OP6, OP5, not_127_out, not_128_out, not_129_out);
  and and_23 (and_23_out, not_130_out, not_131_out, F12, OP6, OP5, not_132_out, not_133_out, not_134_out);
  and and_24 (and_24_out, F14, not_135_out, F12, OP6, OP5, not_136_out, not_137_out, not_138_out);
  and and_25 (and_25_out, not_139_out, not_140_out, not_141_out, not_142_out, not_143_out, not_144_out, OP5, OP4, not_145_out, not_146_out);
  and and_26 (and_26_out, F30, not_147_out, not_148_out, not_149_out, not_150_out, not_151_out, OP5, OP4, not_152_out, not_153_out);
  and and_27 (and_27_out, not_154_out, not_155_out, F14, F13, F12, not_156_out, OP5, OP4, not_157_out, not_158_out);
  and and_28 (and_28_out, not_159_out, not_160_out, not_161_out, F13, F12, not_162_out, OP5, OP4, not_163_out, not_164_out);
  and and_29 (and_29_out, not_165_out, not_166_out, not_167_out, not_168_out, not_169_out, OP4, not_170_out, not_171_out);
  and and_30 (and_30_out, F14, F13, F12, not_172_out, not_173_out, OP4, not_174_out, not_175_out);
  and and_31 (and_31_out, not_176_out, F13, not_177_out, not_178_out, not_179_out, not_180_out, not_181_out, not_182_out);
  and and_32 (and_32_out, not_183_out, F13, not_184_out, not_185_out, OP5, not_186_out, not_187_out, not_188_out);
  and and_33 (and_33_out, not_189_out, not_190_out, not_191_out, OP6, OP5, not_192_out, not_193_out, not_194_out);
  and and_34 (and_34_out, not_195_out, not_196_out, F12, OP6, OP5, not_197_out, not_198_out, not_199_out);
  and and_35 (and_35_out, not_200_out, not_201_out, not_202_out, OP6, OP5, not_203_out, not_204_out, OP2);
  and and_36 (and_36_out, not_205_out, not_206_out, not_207_out, not_208_out, not_209_out, not_210_out, not_211_out, not_212_out);
  and and_37 (and_37_out, F14, F13, not_213_out, OP6, OP5, not_214_out, not_215_out, not_216_out);
  and and_38 (and_38_out, not_217_out, F25, F14, not_218_out, F12, not_219_out, OP5, OP4, not_220_out, not_221_out);
  and and_39 (and_39_out, not_222_out, not_223_out, OP4, not_224_out, OP2);
  and and_40 (and_40_out, not_225_out, not_226_out, F14, F13, not_227_out, not_228_out, OP5, OP4, not_229_out, not_230_out);
  and and_41 (and_41_out, not_231_out, not_232_out, not_233_out, F13, not_234_out, not_235_out, OP5, OP4, not_236_out, not_237_out);
  and and_42 (and_42_out, not_238_out, not_239_out, not_240_out, F13, F12, not_241_out, OP5, OP4, not_242_out, not_243_out);
  and and_43 (and_43_out, F14, F13, not_244_out, not_245_out, not_246_out, OP4, not_247_out, not_248_out);
  and and_44 (and_44_out, F14, not_249_out, not_250_out, not_251_out, not_252_out, OP4, not_253_out, not_254_out);
  and and_45 (and_45_out, not_255_out, F13, not_256_out, not_257_out, not_258_out, OP4, not_259_out, not_260_out);
  and and_46 (and_46_out, F14, F13, not_261_out, OP6, OP5, not_262_out, not_263_out, not_264_out);
  and and_47 (and_47_out, F14, not_265_out, F12, OP6, OP5, not_266_out, not_267_out, not_268_out);
  or or_1 (S0, and_1_out, and_2_out, and_3_out, and_4_out, and_5_out, and_6_out, and_7_out, and_8_out, and_9_out, and_10_out, and_11_out, and_12_out, and_13_out, and_14_out, and_15_out);
  or or_2 (S1, and_16_out, and_17_out, and_18_out, and_19_out, and_20_out, and_21_out, and_22_out, and_23_out, and_24_out);
  or or_3 (S2, and_25_out, and_26_out, and_27_out, and_28_out, and_29_out, and_30_out, and_31_out, and_32_out, and_33_out, and_34_out, and_35_out, and_36_out, and_37_out, and_38_out, and_39_out);
  or or_4 (S3, and_40_out, and_41_out, and_42_out, and_43_out, and_44_out, and_45_out, and_46_out, and_47_out);
endmodule

// 控制信号生成
module \控制信号自动生成  (
  input  OP2,
  input  OP3,
  input  OP4,
  input  OP5,
  input  OP6,
  input  F12,
  input  F13,
  input  F14,
  input  F25,
  input  F30,
  output rs2used,
  output rs1used,
  output MemToReg,
  output MemWrite,
  output ALU_SRC,
  output RegWrite,
  output ecall,
  output S_Type,
  output BEQ,
  output BNE,
  output JALR,
  output JAL,
  output LUI,
  output LB,
  output BLTU,
  output CSRRSI,
  output CSRRCI,
  output BGE,
  output U_type
);

  wire and_1_out, and_2_out, and_3_out, and_4_out, and_5_out, and_6_out, and_7_out, and_8_out, and_9_out,
       and_10_out, and_11_out, and_12_out, and_13_out, and_14_out, and_15_out, and_16_out, and_17_out,
       and_18_out, and_19_out, and_20_out, and_21_out, and_22_out, and_23_out, and_24_out, and_25_out,
       and_26_out, and_27_out, and_28_out, and_29_out, and_30_out, and_31_out, and_32_out, and_33_out,
       and_34_out, and_35_out, and_36_out, and_37_out, and_38_out, and_39_out, and_41_out, and_42_out,
       and_43_out, and_44_out, and_45_out, and_46_out, and_47_out, and_48_out, and_49_out, and_50_out,
       and_51_out, and_52_out, and_53_out, and_54_out, and_55_out, and_56_out, and_57_out, and_58_out,
       and_59_out, and_60_out, and_61_out, and_62_out, and_63_out, and_64_out, and_65_out, and_66_out,
       and_67_out, and_68_out, and_69_out, and_70_out, and_71_out, and_72_out, and_73_out, and_74_out,
       and_75_out, not_1_out, not_2_out, not_3_out, not_4_out, not_5_out, not_6_out, not_7_out, not_8_out,
       not_9_out, not_10_out, not_11_out, not_12_out, not_13_out, not_14_out, not_15_out, not_16_out,
       not_17_out, not_18_out, not_19_out, not_20_out, not_21_out, not_22_out, not_23_out, not_24_out,
       not_25_out, not_26_out, not_27_out, not_28_out, not_29_out, not_30_out, not_31_out, not_32_out,
       not_33_out, not_34_out, not_35_out, not_36_out, not_37_out, not_38_out, not_39_out, not_40_out,
       not_41_out, not_42_out, not_43_out, not_44_out, not_45_out, not_46_out, not_47_out, not_48_out,
       not_49_out, not_50_out, not_51_out, not_52_out, not_53_out, not_54_out, not_55_out, not_56_out,
       not_57_out, not_58_out, not_59_out, not_60_out, not_61_out, not_62_out, not_63_out, not_64_out,
       not_65_out, not_66_out, not_67_out, not_68_out, not_69_out, not_70_out, not_71_out, not_72_out,
       not_73_out, not_74_out, not_75_out, not_76_out, not_77_out, not_78_out, not_79_out, not_80_out,
       not_81_out, not_82_out, not_83_out, not_84_out, not_85_out, not_86_out, not_87_out, not_88_out,
       not_89_out, not_90_out, not_91_out, not_92_out, not_93_out, not_94_out, not_95_out, not_96_out,
       not_97_out, not_98_out, not_99_out, not_100_out, not_101_out, not_102_out, not_103_out, not_104_out,
       not_105_out, not_106_out, not_107_out, not_108_out, not_109_out, not_110_out, not_111_out,
       not_112_out, not_113_out, not_114_out, not_115_out, not_116_out, not_117_out, not_118_out,
       not_119_out, not_120_out, not_121_out, not_122_out, not_123_out, not_124_out, not_125_out,
       not_126_out, not_127_out, not_128_out, not_129_out, not_130_out, not_131_out, not_132_out,
       not_133_out, not_134_out, not_135_out, not_136_out, not_137_out, not_138_out, not_139_out,
       not_140_out, not_141_out, not_142_out, not_143_out, not_144_out, not_145_out, not_146_out,
       not_147_out, not_148_out, not_149_out, not_150_out, not_151_out, not_152_out, not_153_out,
       not_154_out, not_155_out, not_156_out, not_157_out, not_158_out, not_159_out, not_160_out,
       not_161_out, not_162_out, not_163_out, not_164_out, not_165_out, not_166_out, not_167_out,
       not_168_out, not_169_out, not_170_out, not_171_out, not_172_out, not_173_out, not_174_out,
       not_175_out, not_176_out, not_177_out, not_178_out, not_179_out, not_180_out, not_181_out,
       not_182_out, not_183_out, not_184_out, not_185_out, not_186_out, not_187_out, not_188_out,
       not_189_out, not_190_out, not_191_out, not_192_out, not_193_out, not_194_out, not_195_out,
       not_196_out, not_197_out, not_198_out, not_199_out, not_200_out, not_201_out, not_202_out,
       not_203_out, not_204_out, not_205_out, not_206_out, not_207_out, not_208_out, not_209_out,
       not_210_out, not_211_out, not_212_out, not_213_out, not_214_out, not_215_out, not_216_out,
       not_217_out, not_218_out, not_219_out, not_220_out, not_221_out, not_222_out, not_223_out,
       not_224_out, not_225_out, not_226_out, not_227_out, not_228_out, not_229_out, not_230_out,
       not_231_out, not_232_out, not_233_out, not_234_out, not_235_out, not_236_out, not_237_out,
       not_238_out, not_239_out, not_240_out, not_241_out, not_242_out, not_243_out, not_244_out,
       not_245_out, not_246_out, not_247_out, not_248_out, not_249_out, not_250_out, not_251_out,
       not_252_out, not_253_out, not_254_out, not_255_out, not_256_out, not_257_out, not_258_out,
       not_259_out, not_260_out, not_261_out, not_262_out, not_263_out, not_264_out, not_265_out,
       not_266_out, not_267_out, not_268_out, not_269_out, not_270_out, not_271_out, not_272_out,
       not_273_out, not_274_out, not_275_out, not_276_out, not_277_out, not_278_out, not_279_out,
       not_280_out, not_281_out, not_282_out, not_283_out, not_284_out, not_285_out, not_286_out,
       not_287_out, not_288_out, not_289_out, not_290_out, not_291_out, not_292_out, not_293_out,
       not_294_out, not_295_out, not_296_out, not_297_out, not_298_out, not_299_out, not_300_out,
       not_301_out, not_302_out, not_303_out, not_304_out, not_305_out, not_306_out, not_307_out,
       not_308_out, not_309_out, not_310_out, not_311_out, not_312_out, not_313_out, not_314_out,
       not_315_out, not_316_out, not_317_out, not_318_out, not_319_out, not_320_out, not_321_out,
       not_322_out, not_323_out, not_324_out, not_325_out, not_326_out, not_327_out, not_328_out,
       not_329_out, not_330_out, not_331_out, not_332_out, not_333_out, not_334_out, not_335_out,
       not_336_out, not_337_out, not_338_out, not_339_out, not_340_out, not_341_out, not_342_out,
       not_343_out, not_344_out, not_345_out, not_346_out, not_347_out, not_348_out, not_349_out,
       not_350_out, not_351_out, not_352_out, not_353_out, not_354_out, not_355_out, not_356_out,
       not_357_out, not_358_out, not_359_out, not_360_out, not_361_out, not_362_out, not_363_out,
       not_364_out, not_365_out, not_366_out, not_367_out, not_368_out, not_369_out, not_370_out,
       not_371_out, not_372_out, not_373_out, not_374_out, not_375_out, not_376_out, not_377_out,
       not_378_out, not_379_out, not_380_out, not_381_out, not_382_out, not_383_out, not_384_out,
       not_385_out, not_386_out, not_387_out, not_388_out, not_389_out, not_390_out, not_391_out,
       not_392_out, not_393_out, not_394_out, not_395_out, not_396_out, not_397_out, not_398_out,
       not_399_out, not_400_out, not_401_out, not_402_out, not_403_out, not_404_out, not_405_out,
       not_406_out, not_407_out, not_408_out, not_409_out, not_410_out, not_411_out, not_412_out,
       not_413_out, not_414_out, not_415_out, not_416_out, not_417_out, not_418_out, not_419_out,
       not_420_out, not_421_out, not_422_out, not_423_out, not_424_out, not_425_out, not_426_out,
       not_427_out, not_428_out, not_429_out, not_430_out, not_431_out, not_432_out, not_433_out,
       not_434_out, not_435_out, not_436_out, not_437_out, not_438_out, not_439_out, not_440_out,
       not_441_out, not_442_out, not_443_out, not_444_out, not_445_out, not_446_out, not_447_out,
       not_448_out, not_449_out, not_450_out, not_451_out, not_452_out, not_453_out, not_454_out,
       not_455_out, not_456_out, not_457_out, not_458_out, not_459_out, not_460_out, not_461_out,
       not_462_out, not_463_out, not_464_out, not_465_out, not_466_out, not_467_out, not_468_out,
       not_469_out, not_470_out, not_471_out, not_472_out, not_473_out, not_474_out, not_475_out,
       not_476_out, not_477_out, not_478_out, not_479_out, not_480_out, not_481_out, not_482_out,
       not_483_out, not_484_out, not_485_out, not_486_out, not_487_out, not_488_out, not_489_out,
       not_490_out, not_491_out, not_492_out, not_493_out, not_494_out, not_495_out, not_496_out;

  not not_1 (not_1_out, F30);
  not not_2 (not_2_out, F25);
  not not_3 (not_3_out, F14);
  not not_4 (not_4_out, F13);
  not not_5 (not_5_out, F12);
  not not_6 (not_6_out, OP6);
  not not_7 (not_7_out, OP3);
  not not_8 (not_8_out, OP2);
  not not_9 (not_9_out, F25);
  not not_10 (not_10_out, F14);
  not not_11 (not_11_out, F13);
  not not_12 (not_12_out, F12);
  not not_13 (not_13_out, OP6);
  not not_14 (not_14_out, OP3);
  not not_15 (not_15_out, OP2);
  not not_16 (not_16_out, F30);
  not not_17 (not_17_out, F25);
  not not_18 (not_18_out, OP6);
  not not_19 (not_19_out, OP3);
  not not_20 (not_20_out, OP2);
  not not_21 (not_21_out, F30);
  not not_22 (not_22_out, F25);
  not not_23 (not_23_out, F12);
  not not_24 (not_24_out, OP6);
  not not_25 (not_25_out, OP3);
  not not_26 (not_26_out, OP2);
  not not_27 (not_27_out, F30);
  not not_28 (not_28_out, F25);
  not not_29 (not_29_out, F14);
  not not_30 (not_30_out, F12);
  not not_31 (not_31_out, OP6);
  not not_32 (not_32_out, OP3);
  not not_33 (not_33_out, OP2);
  not not_34 (not_34_out, F30);
  not not_35 (not_35_out, F25);
  not not_36 (not_36_out, F14);
  not not_37 (not_37_out, OP6);
  not not_38 (not_38_out, OP3);
  not not_39 (not_39_out, OP2);
  not not_40 (not_40_out, F14);
  not not_41 (not_41_out, F12);
  not not_42 (not_42_out, OP6);
  not not_43 (not_43_out, OP4);
  not not_44 (not_44_out, OP3);
  not not_45 (not_45_out, OP2);
  not not_46 (not_46_out, F14);
  not not_47 (not_47_out, F13);
  not not_48 (not_48_out, F12);
  not not_49 (not_49_out, OP4);
  not not_50 (not_50_out, OP3);
  not not_51 (not_51_out, OP2);
  not not_52 (not_52_out, F14);
  not not_53 (not_53_out, F13);
  not not_54 (not_54_out, OP4);
  not not_55 (not_55_out, OP3);
  not not_56 (not_56_out, OP2);
  not not_57 (not_57_out, F25);
  not not_58 (not_58_out, F13);
  not not_59 (not_59_out, OP6);
  not not_60 (not_60_out, OP3);
  not not_61 (not_61_out, OP2);
  not not_62 (not_62_out, F12);
  not not_63 (not_63_out, OP4);
  not not_64 (not_64_out, OP3);
  not not_65 (not_65_out, OP2);
  not not_66 (not_66_out, F13);
  not not_67 (not_67_out, OP4);
  not not_68 (not_68_out, OP3);
  not not_69 (not_69_out, OP2);
  not not_70 (not_70_out, F30);
  not not_71 (not_71_out, F13);
  not not_72 (not_72_out, OP6);
  not not_73 (not_73_out, OP3);
  not not_74 (not_74_out, OP2);
  not not_75 (not_75_out, F30);
  not not_76 (not_76_out, F25);
  not not_77 (not_77_out, F14);
  not not_78 (not_78_out, F13);
  not not_79 (not_79_out, F12);
  not not_80 (not_80_out, OP6);
  not not_81 (not_81_out, OP3);
  not not_82 (not_82_out, OP2);
  not not_83 (not_83_out, F25);
  not not_84 (not_84_out, F14);
  not not_85 (not_85_out, F13);
  not not_86 (not_86_out, F12);
  not not_87 (not_87_out, OP6);
  not not_88 (not_88_out, OP3);
  not not_89 (not_89_out, OP2);
  not not_90 (not_90_out, F30);
  not not_91 (not_91_out, F25);
  not not_92 (not_92_out, OP6);
  not not_93 (not_93_out, OP3);
  not not_94 (not_94_out, OP2);
  not not_95 (not_95_out, F30);
  not not_96 (not_96_out, F25);
  not not_97 (not_97_out, F12);
  not not_98 (not_98_out, OP6);
  not not_99 (not_99_out, OP3);
  not not_100 (not_100_out, OP2);
  not not_101 (not_101_out, F30);
  not not_102 (not_102_out, F25);
  not not_103 (not_103_out, F14);
  not not_104 (not_104_out, F12);
  not not_105 (not_105_out, OP6);
  not not_106 (not_106_out, OP3);
  not not_107 (not_107_out, OP2);
  not not_108 (not_108_out, F30);
  not not_109 (not_109_out, F25);
  not not_110 (not_110_out, F14);
  not not_111 (not_111_out, OP6);
  not not_112 (not_112_out, OP3);
  not not_113 (not_113_out, OP2);
  not not_114 (not_114_out, F14);
  not not_115 (not_115_out, F13);
  not not_116 (not_116_out, F12);
  not not_117 (not_117_out, OP6);
  not not_118 (not_118_out, OP5);
  not not_119 (not_119_out, OP3);
  not not_120 (not_120_out, OP2);
  not not_121 (not_121_out, OP6);
  not not_122 (not_122_out, OP5);
  not not_123 (not_123_out, OP3);
  not not_124 (not_124_out, OP2);
  not not_125 (not_125_out, F12);
  not not_126 (not_126_out, OP6);
  not not_127 (not_127_out, OP5);
  not not_128 (not_128_out, OP3);
  not not_129 (not_129_out, OP2);
  not not_130 (not_130_out, F13);
  not not_131 (not_131_out, F12);
  not not_132 (not_132_out, OP6);
  not not_133 (not_133_out, OP5);
  not not_134 (not_134_out, OP3);
  not not_135 (not_135_out, OP2);
  not not_136 (not_136_out, F14);
  not not_137 (not_137_out, F12);
  not not_138 (not_138_out, OP6);
  not not_139 (not_139_out, OP5);
  not not_140 (not_140_out, OP3);
  not not_141 (not_141_out, OP2);
  not not_142 (not_142_out, F30);
  not not_143 (not_143_out, F25);
  not not_144 (not_144_out, F14);
  not not_145 (not_145_out, F13);
  not not_146 (not_146_out, OP6);
  not not_147 (not_147_out, OP5);
  not not_148 (not_148_out, OP3);
  not not_149 (not_149_out, OP2);
  not not_150 (not_150_out, F30);
  not not_151 (not_151_out, F25);
  not not_152 (not_152_out, F13);
  not not_153 (not_153_out, OP6);
  not not_154 (not_154_out, OP5);
  not not_155 (not_155_out, OP3);
  not not_156 (not_156_out, OP2);
  not not_157 (not_157_out, F25);
  not not_158 (not_158_out, F13);
  not not_159 (not_159_out, OP6);
  not not_160 (not_160_out, OP5);
  not not_161 (not_161_out, OP3);
  not not_162 (not_162_out, OP2);
  not not_163 (not_163_out, F14);
  not not_164 (not_164_out, F12);
  not not_165 (not_165_out, OP6);
  not not_166 (not_166_out, OP5);
  not not_167 (not_167_out, OP4);
  not not_168 (not_168_out, OP3);
  not not_169 (not_169_out, OP2);
  not not_170 (not_170_out, F14);
  not not_171 (not_171_out, F12);
  not not_172 (not_172_out, OP6);
  not not_173 (not_173_out, OP4);
  not not_174 (not_174_out, OP3);
  not not_175 (not_175_out, OP2);
  not not_176 (not_176_out, F14);
  not not_177 (not_177_out, F13);
  not not_178 (not_178_out, F12);
  not not_179 (not_179_out, OP4);
  not not_180 (not_180_out, OP3);
  not not_181 (not_181_out, OP2);
  not not_182 (not_182_out, F14);
  not not_183 (not_183_out, F13);
  not not_184 (not_184_out, OP4);
  not not_185 (not_185_out, OP3);
  not not_186 (not_186_out, OP2);
  not not_187 (not_187_out, F14);
  not not_188 (not_188_out, F13);
  not not_189 (not_189_out, F12);
  not not_190 (not_190_out, OP4);
  not not_191 (not_191_out, OP3);
  not not_192 (not_192_out, F25);
  not not_193 (not_193_out, F13);
  not not_194 (not_194_out, OP6);
  not not_195 (not_195_out, OP3);
  not not_196 (not_196_out, OP2);
  not not_197 (not_197_out, F14);
  not not_198 (not_198_out, F13);
  not not_199 (not_199_out, F12);
  not not_200 (not_200_out, OP6);
  not not_201 (not_201_out, OP5);
  not not_202 (not_202_out, OP4);
  not not_203 (not_203_out, OP3);
  not not_204 (not_204_out, OP2);
  not not_205 (not_205_out, F12);
  not not_206 (not_206_out, OP4);
  not not_207 (not_207_out, OP3);
  not not_208 (not_208_out, OP2);
  not not_209 (not_209_out, F13);
  not not_210 (not_210_out, OP4);
  not not_211 (not_211_out, OP3);
  not not_212 (not_212_out, OP2);
  not not_213 (not_213_out, F30);
  not not_214 (not_214_out, F13);
  not not_215 (not_215_out, OP6);
  not not_216 (not_216_out, OP3);
  not not_217 (not_217_out, OP2);
  not not_218 (not_218_out, F14);
  not not_219 (not_219_out, F12);
  not not_220 (not_220_out, OP6);
  not not_221 (not_221_out, OP5);
  not not_222 (not_222_out, OP4);
  not not_223 (not_223_out, OP3);
  not not_224 (not_224_out, OP2);
  not not_225 (not_225_out, F14);
  not not_226 (not_226_out, F13);
  not not_227 (not_227_out, F12);
  not not_228 (not_228_out, OP6);
  not not_229 (not_229_out, OP5);
  not not_230 (not_230_out, OP4);
  not not_231 (not_231_out, OP3);
  not not_232 (not_232_out, OP2);
  not not_233 (not_233_out, F14);
  not not_234 (not_234_out, F12);
  not not_235 (not_235_out, OP6);
  not not_236 (not_236_out, OP4);
  not not_237 (not_237_out, OP3);
  not not_238 (not_238_out, OP2);
  not not_239 (not_239_out, F14);
  not not_240 (not_240_out, F13);
  not not_241 (not_241_out, F12);
  not not_242 (not_242_out, OP6);
  not not_243 (not_243_out, OP5);
  not not_244 (not_244_out, OP3);
  not not_245 (not_245_out, OP2);
  not not_246 (not_246_out, OP6);
  not not_247 (not_247_out, OP5);
  not not_248 (not_248_out, OP3);
  not not_249 (not_249_out, OP2);
  not not_250 (not_250_out, F12);
  not not_251 (not_251_out, OP6);
  not not_252 (not_252_out, OP5);
  not not_253 (not_253_out, OP3);
  not not_254 (not_254_out, OP2);
  not not_255 (not_255_out, F13);
  not not_256 (not_256_out, F12);
  not not_257 (not_257_out, OP6);
  not not_258 (not_258_out, OP5);
  not not_259 (not_259_out, OP3);
  not not_260 (not_260_out, OP2);
  not not_261 (not_261_out, F14);
  not not_262 (not_262_out, F12);
  not not_263 (not_263_out, OP6);
  not not_264 (not_264_out, OP5);
  not not_265 (not_265_out, OP3);
  not not_266 (not_266_out, OP2);
  not not_267 (not_267_out, F30);
  not not_268 (not_268_out, F25);
  not not_269 (not_269_out, F14);
  not not_270 (not_270_out, F13);
  not not_271 (not_271_out, OP6);
  not not_272 (not_272_out, OP5);
  not not_273 (not_273_out, OP3);
  not not_274 (not_274_out, OP2);
  not not_275 (not_275_out, F30);
  not not_276 (not_276_out, F25);
  not not_277 (not_277_out, F13);
  not not_278 (not_278_out, OP6);
  not not_279 (not_279_out, OP5);
  not not_280 (not_280_out, OP3);
  not not_281 (not_281_out, OP2);
  not not_282 (not_282_out, F25);
  not not_283 (not_283_out, F13);
  not not_284 (not_284_out, OP6);
  not not_285 (not_285_out, OP5);
  not not_286 (not_286_out, OP3);
  not not_287 (not_287_out, OP2);
  not not_288 (not_288_out, F14);
  not not_289 (not_289_out, F12);
  not not_290 (not_290_out, OP6);
  not not_291 (not_291_out, OP5);
  not not_292 (not_292_out, OP4);
  not not_293 (not_293_out, OP3);
  not not_294 (not_294_out, OP2);
  not not_295 (not_295_out, F14);
  not not_296 (not_296_out, F12);
  not not_297 (not_297_out, OP6);
  not not_298 (not_298_out, OP4);
  not not_299 (not_299_out, OP3);
  not not_300 (not_300_out, OP2);
  not not_301 (not_301_out, F14);
  not not_302 (not_302_out, F13);
  not not_303 (not_303_out, F12);
  not not_304 (not_304_out, OP4);
  not not_305 (not_305_out, OP3);
  not not_306 (not_306_out, F14);
  not not_307 (not_307_out, F13);
  not not_308 (not_308_out, F12);
  not not_309 (not_309_out, OP6);
  not not_310 (not_310_out, OP5);
  not not_311 (not_311_out, OP4);
  not not_312 (not_312_out, OP3);
  not not_313 (not_313_out, OP2);
  not not_314 (not_314_out, OP6);
  not not_315 (not_315_out, OP5);
  not not_316 (not_316_out, OP3);
  not not_317 (not_317_out, F30);
  not not_318 (not_318_out, F25);
  not not_319 (not_319_out, F14);
  not not_320 (not_320_out, F13);
  not not_321 (not_321_out, F12);
  not not_322 (not_322_out, OP6);
  not not_323 (not_323_out, OP3);
  not not_324 (not_324_out, OP2);
  not not_325 (not_325_out, F25);
  not not_326 (not_326_out, F14);
  not not_327 (not_327_out, F13);
  not not_328 (not_328_out, F12);
  not not_329 (not_329_out, OP6);
  not not_330 (not_330_out, OP3);
  not not_331 (not_331_out, OP2);
  not not_332 (not_332_out, F30);
  not not_333 (not_333_out, F25);
  not not_334 (not_334_out, OP6);
  not not_335 (not_335_out, OP3);
  not not_336 (not_336_out, OP2);
  not not_337 (not_337_out, F30);
  not not_338 (not_338_out, F25);
  not not_339 (not_339_out, F12);
  not not_340 (not_340_out, OP6);
  not not_341 (not_341_out, OP3);
  not not_342 (not_342_out, OP2);
  not not_343 (not_343_out, F30);
  not not_344 (not_344_out, F25);
  not not_345 (not_345_out, F14);
  not not_346 (not_346_out, F12);
  not not_347 (not_347_out, OP6);
  not not_348 (not_348_out, OP3);
  not not_349 (not_349_out, OP2);
  not not_350 (not_350_out, F30);
  not not_351 (not_351_out, F25);
  not not_352 (not_352_out, F14);
  not not_353 (not_353_out, OP6);
  not not_354 (not_354_out, OP3);
  not not_355 (not_355_out, OP2);
  not not_356 (not_356_out, F14);
  not not_357 (not_357_out, F13);
  not not_358 (not_358_out, F12);
  not not_359 (not_359_out, OP6);
  not not_360 (not_360_out, OP5);
  not not_361 (not_361_out, OP3);
  not not_362 (not_362_out, OP2);
  not not_363 (not_363_out, OP6);
  not not_364 (not_364_out, OP5);
  not not_365 (not_365_out, OP3);
  not not_366 (not_366_out, OP2);
  not not_367 (not_367_out, F12);
  not not_368 (not_368_out, OP6);
  not not_369 (not_369_out, OP5);
  not not_370 (not_370_out, OP3);
  not not_371 (not_371_out, OP2);
  not not_372 (not_372_out, F13);
  not not_373 (not_373_out, F12);
  not not_374 (not_374_out, OP6);
  not not_375 (not_375_out, OP5);
  not not_376 (not_376_out, OP3);
  not not_377 (not_377_out, OP2);
  not not_378 (not_378_out, F14);
  not not_379 (not_379_out, F12);
  not not_380 (not_380_out, OP6);
  not not_381 (not_381_out, OP5);
  not not_382 (not_382_out, OP3);
  not not_383 (not_383_out, OP2);
  not not_384 (not_384_out, F30);
  not not_385 (not_385_out, F25);
  not not_386 (not_386_out, F14);
  not not_387 (not_387_out, F13);
  not not_388 (not_388_out, OP6);
  not not_389 (not_389_out, OP5);
  not not_390 (not_390_out, OP3);
  not not_391 (not_391_out, OP2);
  not not_392 (not_392_out, F30);
  not not_393 (not_393_out, F25);
  not not_394 (not_394_out, F13);
  not not_395 (not_395_out, OP6);
  not not_396 (not_396_out, OP5);
  not not_397 (not_397_out, OP3);
  not not_398 (not_398_out, OP2);
  not not_399 (not_399_out, F25);
  not not_400 (not_400_out, F13);
  not not_401 (not_401_out, OP6);
  not not_402 (not_402_out, OP5);
  not not_403 (not_403_out, OP3);
  not not_404 (not_404_out, OP2);
  not not_405 (not_405_out, F14);
  not not_406 (not_406_out, F12);
  not not_407 (not_407_out, OP6);
  not not_408 (not_408_out, OP5);
  not not_409 (not_409_out, OP4);
  not not_410 (not_410_out, OP3);
  not not_411 (not_411_out, OP2);
  not not_412 (not_412_out, OP4);
  not not_413 (not_413_out, F14);
  not not_414 (not_414_out, F13);
  not not_415 (not_415_out, F12);
  not not_416 (not_416_out, OP4);
  not not_417 (not_417_out, OP3);
  not not_418 (not_418_out, F25);
  not not_419 (not_419_out, F13);
  not not_420 (not_420_out, OP6);
  not not_421 (not_421_out, OP3);
  not not_422 (not_422_out, OP2);
  not not_423 (not_423_out, OP6);
  not not_424 (not_424_out, OP3);
  not not_425 (not_425_out, F14);
  not not_426 (not_426_out, F13);
  not not_427 (not_427_out, F12);
  not not_428 (not_428_out, OP6);
  not not_429 (not_429_out, OP5);
  not not_430 (not_430_out, OP4);
  not not_431 (not_431_out, OP3);
  not not_432 (not_432_out, OP2);
  not not_433 (not_433_out, F30);
  not not_434 (not_434_out, F13);
  not not_435 (not_435_out, OP6);
  not not_436 (not_436_out, OP3);
  not not_437 (not_437_out, OP2);
  not not_438 (not_438_out, OP6);
  not not_439 (not_439_out, OP5);
  not not_440 (not_440_out, OP3);
  not not_441 (not_441_out, F30);
  not not_442 (not_442_out, F25);
  not not_443 (not_443_out, F14);
  not not_444 (not_444_out, F13);
  not not_445 (not_445_out, F12);
  not not_446 (not_446_out, OP3);
  not not_447 (not_447_out, OP2);
  not not_448 (not_448_out, F14);
  not not_449 (not_449_out, F12);
  not not_450 (not_450_out, OP6);
  not not_451 (not_451_out, OP4);
  not not_452 (not_452_out, OP3);
  not not_453 (not_453_out, OP2);
  not not_454 (not_454_out, F14);
  not not_455 (not_455_out, F13);
  not not_456 (not_456_out, F12);
  not not_457 (not_457_out, OP4);
  not not_458 (not_458_out, OP3);
  not not_459 (not_459_out, OP2);
  not not_460 (not_460_out, F14);
  not not_461 (not_461_out, F13);
  not not_462 (not_462_out, OP4);
  not not_463 (not_463_out, OP3);
  not not_464 (not_464_out, OP2);
  not not_465 (not_465_out, F14);
  not not_466 (not_466_out, F13);
  not not_467 (not_467_out, F12);
  not not_468 (not_468_out, OP4);
  not not_469 (not_469_out, OP3);
  not not_470 (not_470_out, OP4);
  not not_471 (not_471_out, OP6);
  not not_472 (not_472_out, OP3);
  not not_473 (not_473_out, F14);
  not not_474 (not_474_out, F13);
  not not_475 (not_475_out, F12);
  not not_476 (not_476_out, OP6);
  not not_477 (not_477_out, OP5);
  not not_478 (not_478_out, OP4);
  not not_479 (not_479_out, OP3);
  not not_480 (not_480_out, OP2);
  not not_481 (not_481_out, F12);
  not not_482 (not_482_out, OP4);
  not not_483 (not_483_out, OP3);
  not not_484 (not_484_out, OP2);
  not not_485 (not_485_out, F12);
  not not_486 (not_486_out, OP3);
  not not_487 (not_487_out, OP2);
  not not_488 (not_488_out, OP3);
  not not_489 (not_489_out, OP2);
  not not_490 (not_490_out, F13);
  not not_491 (not_491_out, OP4);
  not not_492 (not_492_out, OP3);
  not not_493 (not_493_out, OP2);
  not not_494 (not_494_out, OP6);
  not not_495 (not_495_out, OP5);
  not not_496 (not_496_out, OP3);
  and and_1 (and_1_out, not_1_out, not_2_out, not_3_out, not_4_out, not_5_out, not_6_out, OP5, OP4, not_7_out, not_8_out);
  and and_2 (and_2_out, F30, not_9_out, not_10_out, not_11_out, not_12_out, not_13_out, OP5, OP4, not_14_out, not_15_out);
  and and_3 (and_3_out, not_16_out, not_17_out, F14, F13, F12, not_18_out, OP5, OP4, not_19_out, not_20_out);
  and and_4 (and_4_out, not_21_out, not_22_out, F14, F13, not_23_out, not_24_out, OP5, OP4, not_25_out, not_26_out);
  and and_5 (and_5_out, not_27_out, not_28_out, not_29_out, F13, not_30_out, not_31_out, OP5, OP4, not_32_out, not_33_out);
  and and_6 (and_6_out, not_34_out, not_35_out, not_36_out, F13, F12, not_37_out, OP5, OP4, not_38_out, not_39_out);
  and and_7 (and_7_out, not_40_out, F13, not_41_out, not_42_out, OP5, not_43_out, not_44_out, not_45_out);
  and and_8 (and_8_out, not_46_out, not_47_out, not_48_out, OP6, OP5, not_49_out, not_50_out, not_51_out);
  and and_9 (and_9_out, not_52_out, not_53_out, F12, OP6, OP5, not_54_out, not_55_out, not_56_out);
  and and_10 (and_10_out, F30, not_57_out, F14, not_58_out, F12, not_59_out, OP5, OP4, not_60_out, not_61_out);
  and and_11 (and_11_out, F14, F13, not_62_out, OP6, OP5, not_63_out, not_64_out, not_65_out);
  and and_12 (and_12_out, F14, not_66_out, F12, OP6, OP5, not_67_out, not_68_out, not_69_out);
  and and_13 (and_13_out, not_70_out, F25, F14, not_71_out, F12, not_72_out, OP5, OP4, not_73_out, not_74_out);
  and and_14 (and_14_out, not_75_out, not_76_out, not_77_out, not_78_out, not_79_out, not_80_out, OP5, OP4, not_81_out, not_82_out);
  and and_15 (and_15_out, F30, not_83_out, not_84_out, not_85_out, not_86_out, not_87_out, OP5, OP4, not_88_out, not_89_out);
  and and_16 (and_16_out, not_90_out, not_91_out, F14, F13, F12, not_92_out, OP5, OP4, not_93_out, not_94_out);
  and and_17 (and_17_out, not_95_out, not_96_out, F14, F13, not_97_out, not_98_out, OP5, OP4, not_99_out, not_100_out);
  and and_18 (and_18_out, not_101_out, not_102_out, not_103_out, F13, not_104_out, not_105_out, OP5, OP4, not_106_out, not_107_out);
  and and_19 (and_19_out, not_108_out, not_109_out, not_110_out, F13, F12, not_111_out, OP5, OP4, not_112_out, not_113_out);
  and and_20 (and_20_out, not_114_out, not_115_out, not_116_out, not_117_out, not_118_out, OP4, not_119_out, not_120_out);
  and and_21 (and_21_out, F14, F13, F12, not_121_out, not_122_out, OP4, not_123_out, not_124_out);
  and and_22 (and_22_out, F14, F13, not_125_out, not_126_out, not_127_out, OP4, not_128_out, not_129_out);
  and and_23 (and_23_out, F14, not_130_out, not_131_out, not_132_out, not_133_out, OP4, not_134_out, not_135_out);
  and and_24 (and_24_out, not_136_out, F13, not_137_out, not_138_out, not_139_out, OP4, not_140_out, not_141_out);
  and and_25 (and_25_out, not_142_out, not_143_out, not_144_out, not_145_out, F12, not_146_out, not_147_out, OP4, not_148_out, not_149_out);
  and and_26 (and_26_out, not_150_out, not_151_out, F14, not_152_out, F12, not_153_out, not_154_out, OP4, not_155_out, not_156_out);
  and and_27 (and_27_out, F30, not_157_out, F14, not_158_out, F12, not_159_out, not_160_out, OP4, not_161_out, not_162_out);
  and and_28 (and_28_out, not_163_out, F13, not_164_out, not_165_out, not_166_out, not_167_out, not_168_out, not_169_out);
  and and_29 (and_29_out, not_170_out, F13, not_171_out, not_172_out, OP5, not_173_out, not_174_out, not_175_out);
  and and_30 (and_30_out, not_176_out, not_177_out, not_178_out, OP6, OP5, not_179_out, not_180_out, not_181_out);
  and and_31 (and_31_out, not_182_out, not_183_out, F12, OP6, OP5, not_184_out, not_185_out, not_186_out);
  and and_32 (and_32_out, not_187_out, not_188_out, not_189_out, OP6, OP5, not_190_out, not_191_out, OP2);
  and and_33 (and_33_out, F30, not_192_out, F14, not_193_out, F12, not_194_out, OP5, OP4, not_195_out, not_196_out);
  and and_34 (and_34_out, not_197_out, not_198_out, not_199_out, not_200_out, not_201_out, not_202_out, not_203_out, not_204_out);
  and and_35 (and_35_out, F14, F13, not_205_out, OP6, OP5, not_206_out, not_207_out, not_208_out);
  and and_36 (and_36_out, F14, not_209_out, F12, OP6, OP5, not_210_out, not_211_out, not_212_out);
  and and_37 (and_37_out, not_213_out, F25, F14, not_214_out, F12, not_215_out, OP5, OP4, not_216_out, not_217_out);
  and and_38 (and_38_out, not_218_out, F13, not_219_out, not_220_out, not_221_out, not_222_out, not_223_out, not_224_out);
  and and_39 (and_39_out, not_225_out, not_226_out, not_227_out, not_228_out, not_229_out, not_230_out, not_231_out, not_232_out);
  and and_40 (MemWrite, not_233_out, F13, not_234_out, not_235_out, OP5, not_236_out, not_237_out, not_238_out);
  and and_41 (and_41_out, not_239_out, not_240_out, not_241_out, not_242_out, not_243_out, OP4, not_244_out, not_245_out);
  and and_42 (and_42_out, F14, F13, F12, not_246_out, not_247_out, OP4, not_248_out, not_249_out);
  and and_43 (and_43_out, F14, F13, not_250_out, not_251_out, not_252_out, OP4, not_253_out, not_254_out);
  and and_44 (and_44_out, F14, not_255_out, not_256_out, not_257_out, not_258_out, OP4, not_259_out, not_260_out);
  and and_45 (and_45_out, not_261_out, F13, not_262_out, not_263_out, not_264_out, OP4, not_265_out, not_266_out);
  and and_46 (and_46_out, not_267_out, not_268_out, not_269_out, not_270_out, F12, not_271_out, not_272_out, OP4, not_273_out, not_274_out);
  and and_47 (and_47_out, not_275_out, not_276_out, F14, not_277_out, F12, not_278_out, not_279_out, OP4, not_280_out, not_281_out);
  and and_48 (and_48_out, F30, not_282_out, F14, not_283_out, F12, not_284_out, not_285_out, OP4, not_286_out, not_287_out);
  and and_49 (and_49_out, not_288_out, F13, not_289_out, not_290_out, not_291_out, not_292_out, not_293_out, not_294_out);
  and and_50 (and_50_out, not_295_out, F13, not_296_out, not_297_out, OP5, not_298_out, not_299_out, not_300_out);
  and and_51 (and_51_out, not_301_out, not_302_out, not_303_out, OP6, OP5, not_304_out, not_305_out, OP2);
  and and_52 (and_52_out, not_306_out, not_307_out, not_308_out, not_309_out, not_310_out, not_311_out, not_312_out, not_313_out);
  and and_53 (and_53_out, not_314_out, not_315_out, OP4, not_316_out, OP2);
  and and_54 (and_54_out, not_317_out, not_318_out, not_319_out, not_320_out, not_321_out, not_322_out, OP5, OP4, not_323_out, not_324_out);
  and and_55 (and_55_out, F30, not_325_out, not_326_out, not_327_out, not_328_out, not_329_out, OP5, OP4, not_330_out, not_331_out);
  and and_56 (and_56_out, not_332_out, not_333_out, F14, F13, F12, not_334_out, OP5, OP4, not_335_out, not_336_out);
  and and_57 (and_57_out, not_337_out, not_338_out, F14, F13, not_339_out, not_340_out, OP5, OP4, not_341_out, not_342_out);
  and and_58 (and_58_out, not_343_out, not_344_out, not_345_out, F13, not_346_out, not_347_out, OP5, OP4, not_348_out, not_349_out);
  and and_59 (and_59_out, not_350_out, not_351_out, not_352_out, F13, F12, not_353_out, OP5, OP4, not_354_out, not_355_out);
  and and_60 (and_60_out, not_356_out, not_357_out, not_358_out, not_359_out, not_360_out, OP4, not_361_out, not_362_out);
  and and_61 (and_61_out, F14, F13, F12, not_363_out, not_364_out, OP4, not_365_out, not_366_out);
  and and_62 (and_62_out, F14, F13, not_367_out, not_368_out, not_369_out, OP4, not_370_out, not_371_out);
  and and_63 (and_63_out, F14, not_372_out, not_373_out, not_374_out, not_375_out, OP4, not_376_out, not_377_out);
  and and_64 (and_64_out, not_378_out, F13, not_379_out, not_380_out, not_381_out, OP4, not_382_out, not_383_out);
  and and_65 (and_65_out, not_384_out, not_385_out, not_386_out, not_387_out, F12, not_388_out, not_389_out, OP4, not_390_out, not_391_out);
  and and_66 (and_66_out, not_392_out, not_393_out, F14, not_394_out, F12, not_395_out, not_396_out, OP4, not_397_out, not_398_out);
  and and_67 (and_67_out, F30, not_399_out, F14, not_400_out, F12, not_401_out, not_402_out, OP4, not_403_out, not_404_out);
  and and_68 (and_68_out, not_405_out, F13, not_406_out, not_407_out, not_408_out, not_409_out, not_410_out, not_411_out);
  and and_69 (and_69_out, OP6, OP5, not_412_out, OP3, OP2);
  and and_70 (and_70_out, not_413_out, not_414_out, not_415_out, OP6, OP5, not_416_out, not_417_out, OP2);
  and and_71 (and_71_out, F30, not_418_out, F14, not_419_out, F12, not_420_out, OP5, OP4, not_421_out, not_422_out);
  and and_72 (and_72_out, not_423_out, OP5, OP4, not_424_out, OP2);
  and and_73 (and_73_out, not_425_out, not_426_out, not_427_out, not_428_out, not_429_out, not_430_out, not_431_out, not_432_out);
  and and_74 (and_74_out, not_433_out, F25, F14, not_434_out, F12, not_435_out, OP5, OP4, not_436_out, not_437_out);
  and and_75 (and_75_out, not_438_out, not_439_out, OP4, not_440_out, OP2);
  and and_76 (ecall, not_441_out, not_442_out, not_443_out, not_444_out, not_445_out, OP6, OP5, OP4, not_446_out, not_447_out);
  and and_77 (S_Type, not_448_out, F13, not_449_out, not_450_out, OP5, not_451_out, not_452_out, not_453_out);
  and and_78 (BEQ, not_454_out, not_455_out, not_456_out, OP6, OP5, not_457_out, not_458_out, not_459_out);
  and and_79 (BNE, not_460_out, not_461_out, F12, OP6, OP5, not_462_out, not_463_out, not_464_out);
  and and_80 (JALR, not_465_out, not_466_out, not_467_out, OP6, OP5, not_468_out, not_469_out, OP2);
  and and_81 (JAL, OP6, OP5, not_470_out, OP3, OP2);
  and and_82 (LUI, not_471_out, OP5, OP4, not_472_out, OP2);
  and and_83 (LB, not_473_out, not_474_out, not_475_out, not_476_out, not_477_out, not_478_out, not_479_out, not_480_out);
  and and_84 (BLTU, F14, F13, not_481_out, OP6, OP5, not_482_out, not_483_out, not_484_out);
  and and_85 (CSRRSI, F14, F13, not_485_out, OP6, OP5, OP4, not_486_out, not_487_out);
  and and_86 (CSRRCI, F14, F13, F12, OP6, OP5, OP4, not_488_out, not_489_out);
  and and_87 (BGE, F14, not_490_out, F12, OP6, OP5, not_491_out, not_492_out, not_493_out);
  and and_88 (U_type, not_494_out, not_495_out, OP4, not_496_out, OP2);
  or or_1 (MemToReg, and_38_out, and_39_out);
  or or_2 (rs2used, and_1_out, and_2_out, and_3_out, and_4_out, and_5_out, and_6_out, and_7_out, and_8_out, and_9_out, and_10_out, and_11_out, and_12_out, and_13_out);
  or or_3 (ALU_SRC, and_41_out, and_42_out, and_43_out, and_44_out, and_45_out, and_46_out, and_47_out, and_48_out, and_49_out, and_50_out, and_51_out, and_52_out, and_53_out);
  or or_4 (rs1used, and_14_out, and_15_out, and_16_out, and_17_out, and_18_out, and_19_out, and_20_out, and_21_out, and_22_out, and_23_out, and_24_out, and_25_out, and_26_out, and_27_out, and_28_out, and_29_out, and_30_out, and_31_out, and_32_out, and_33_out, and_34_out, and_35_out, and_36_out, and_37_out);
  or or_5 (RegWrite, and_54_out, and_55_out, and_56_out, and_57_out, and_58_out, and_59_out, and_60_out, and_61_out, and_62_out, and_63_out, and_64_out, and_65_out, and_66_out, and_67_out, and_68_out, and_69_out, and_70_out, and_71_out, and_72_out, and_73_out, and_74_out, and_75_out);
endmodule

// ALU
module ALU (
  input  [31:0] X,
  input  [31:0] Y,
  input  [3:0] AluOP,
  output out_4,
  output Equal,
  output out_6,
  output [31:0] Result,
  output [31:0] Result_2
);

  wire [0:0] comparator_1_lt, comparator_2_lt;
  wire [31:0] adder_1_out, AND_out, divider_1_out, divider_1_rem, multiplier_1_cout, multiplier_1_out,
       NOR_out, OR_out, shifter_1_out, shifter_2_out, shifter_3_out, subtractor_1_out, XOR_out;

  assign AND_out = X & Y;  // AND_Gate AND, 32 bits wide
  assign OR_out = X | Y;  // OR_Gate OR, 32 bits wide
  Shifter #(.width(32), .shift("ll")) shifter_1 (.in(X), .\dist (Y[4:0]), .out(shifter_1_out));
  Shifter #(.width(32), .shift("ar")) shifter_2 (.in(X), .\dist (Y[4:0]), .out(shifter_2_out));
  Shifter #(.width(32), .shift("lr")) shifter_3 (.in(X), .\dist (Y[4:0]), .out(shifter_3_out));
  Multiplier #(.width(32)) multiplier_1 (.a(X), .b(Y), .out(multiplier_1_out), .cout(multiplier_1_cout));  // open: cin
  Divider #(.width(32)) divider_1 (.a(X), .b(Y), .out(divider_1_out), .rem(divider_1_rem));  // open: upper
  Adder #(.width(32)) adder_1 (.a(X), .b(Y), .out(adder_1_out));  // open: cin, cout
  Subtractor #(.width(32)) subtractor_1 (.a(X), .b(Y), .out(subtractor_1_out));  // open: bin, bout
  assign XOR_out = X ^ Y;  // XOR_Gate XOR, 32 bits wide
  assign NOR_out = ~(X | Y);  // NOR_Gate NOR, 32 bits wide
  Comparator #(.width(32), .mode("twosComplement")) comparator_1 (
    .a(X), .b(Y), .eq(Equal), .lt(comparator_1_lt[0]));  // open: gt
  Comparator #(.width(32), .mode("unsigned")) comparator_2 (.a(X), .b(Y), .lt(comparator_2_lt[0]));  // open: gt, eq
  Multiplexer #(.select(4), .width(32), .disabled("Z"), .enable("false")) multiplexer_1 (
    .in0(shifter_1_out), .in1(shifter_2_out), .in2(shifter_3_out), .in3(multiplier_1_out),
    .in4(divider_1_out), .in5(adder_1_out), .in6(subtractor_1_out), .in7(AND_out), .in8(OR_out),
    .in9(XOR_out), .in10(NOR_out), .in11({{31{1'b0}}, comparator_1_lt[0]}),
    .in12({{31{1'b0}}, comparator_2_lt[0]}), .in13({32{1'b0}}), .in14({32{1'b0}}), .in15({32{1'b0}}),
    .out(Result), .sel(AluOP));
  Multiplexer #(.select(4), .width(32), .disabled("Z"), .enable("false")) multiplexer_2 (
    .in0({32{1'b0}}), .in1({32{1'b0}}), .in2({32{1'b0}}), .in3(multiplier_1_cout), .in4(divider_1_rem),
    .in5({32{1'b0}}), .in6({32{1'b0}}), .in7({32{1'b0}}), .in8({32{1'b0}}), .in9({32{1'b0}}),
    .in10({32{1'b0}}), .in11({32{1'b0}}), .in12({32{1'b0}}), .in13({32{1'b0}}), .in14({32{1'b0}}),
    .in15({32{1'b0}}), .out(Result_2), .sel(AluOP));
  Multiplexer #(.select(4), .width(1), .disabled("Z"), .enable("false")) multiplexer_3 (
    .in0(1'b0), .in1(1'b0), .in2(1'b0), .in3(1'b0), .in4(1'b0), .in5(1'b0), .in6(1'b0), .in7(1'b0),
    .in8(1'b0), .in9(1'b0), .in10(1'b0), .in11(comparator_1_lt[0]), .in12(comparator_2_lt[0]), .in13(1'b0),
    .in14(1'b0), .in15(1'b0), .out(out_6), .sel(AluOP));
  not not_1 (out_4, out_6);

  // Other names for the same wires on the sheet: Result2[31:0] = Result_2; S[3:0] = AluOP; tunnel = out_6;
  //   tunnel_t = out_4

  // Notes on the sheet:
  //   不要改变此引脚区域内容，也不要改变ALU封装形式
  //   输入引脚
  //   输出引脚
endmodule

module Regifile (
  input  [31:0] Din,
  input  Clk,
  input  WE,
  input  [4:0] R1_num,
  input  [4:0] W_num,
  input  [4:0] R2_num,
  output [31:0] R1,
  output [31:0] R2
);

  // RegisterFile registerfile_1: pin names not known; wires that end beside it: Din, Clk, WE, W_num, R1_num, R2_num, R1, R2
endmodule
module \理想流水线  (
  output RegWrite,
  output MemWrite,
  output [31:0] IF_PC,
  output [31:0] ID_PC,
  output [31:0] EX_PC,
  output [31:0] M_PC,
  output [31:0] WB_PC,
  output [31:0] RDin,
  output [31:0] MDin,
  output [31:0] LedData
);

  wire Alu, AluEQ, and_1_out, and_2_out, and_3_out, and_4_out, and_5_out, and_6_out, and_7_out, and_8_out,
       and_9_out, bltu, CLK, clock_1_out, clock_2_out, comparator_1_eq, comparator_2_eq, comparator_2_lt,
       comparator_3_gt, comparator_3_lt, d_ff_1_q, ecall, EX_ecall, EX_halt, exmem_1_out_19, exmem_1_out_20,
       exmem_1_out_21, exmem_1_out_22, exmem_1_out_23, exmem_1_out_26, exmem_1_out_27, Go, halt,
       id_ex_1_out_30, id_ex_1_out_31, id_ex_1_out_33, id_ex_1_out_34, id_ex_1_out_37, id_ex_1_out_38,
       id_ex_1_out_39, id_ex_1_out_40, id_ex_1_out_43, id_ex_1_out_45, id_ex_1_out_48, IR1, IR2, IR3, JAL,
       mem_wb_1_out_19, mem_wb_1_out_20, mem_wb_1_out_21, mem_wb_1_out_22, mem_wb_1_out_23, mem_wb_1_out_27,
       nand_1_out, not_1_out, not_2_out, not_4_out, or_1_out, or_2_out, RST, S, tunnel, undriven, W1, W2, W3,
       \单周期硬布线控制器_1_alu_src , \单周期硬布线控制器_1_beq , \单周期硬布线控制器_1_bne , \单周期硬布线控制器_1_jalr , \单周期硬布线控制器_1_lb ,
       \单周期硬布线控制器_1_lui , \单周期硬布线控制器_1_memtoreg , \单周期硬布线控制器_1_memwrite , \单周期硬布线控制器_1_regwrite ,
       \单周期硬布线控制器_1_uret ;
  wire [1:0] or_4_out, priority_encoder_1_out;
  wire [3:0] id_ex_1_out_47, \单周期硬布线控制器_1_alu_op ;
  wire [4:0] exmem_1_out_24, id_ex_1_out_49, multiplexer_2_out, multiplexer_3_out, WB_rd;
  wire [7:0] multiplexer_9_out;
  wire [12:0] CNT_num;
  wire [15:0] \LoadUse次数 , \总周期数 , \插入气泡数 , \无条件分支数 , \条件分支成功数 ;
  wire [31:0] adder_3_out, bit_extender_1_out, bit_extender_2_out, bit_extender_3_out, bit_extender_4_out,
       Calcuresult, EX_IR, exmem_1_out_28, exmem_1_out_29, exmem_1_out_31, id_ex_1_out_32, id_ex_1_out_36,
       id_ex_1_out_41, id_ex_1_out_46, id_ex_1_out_50, ID_IR, IF_IR, jaddr, LBDout, MEM_IR, mem_wb_1_out_28,
       mem_wb_1_out_31, multiplexer_1_out, multiplexer_4_out, multiplexer_5_out, multiplexer_6_out,
       multiplexer_10_out, PC_4, ram_1_data, regifile_1_r1, regifile_1_r2, shifter_1_out, shifter_2_out,
       WB_Dout, WB_IR;

  Button \u_总复位  (.out(RST));
  Button _1 (.out(IR1));
  Button _2 (.out(IR2));
  Button _3 (.out(IR3));
  // Probe on \总周期数 
  // Probe on \总周期数 
  Button \u_继续运行  (.out(Go));
  LED #(.active("true")) led_1 (.in(W1));
  LED #(.active("true")) led_2 (.in(W2));
  LED #(.active("true")) led_3 (.in(W3));
  not not_1 (not_1_out, halt);
  Hex_Digit_Display hex_digit_display_1 (.value(LedData[31:28]));  // open: dp
  // Probe on IF_PC[19:0]
  // RiscV_Probe riscv_probe_1: pin names not known; wires that end beside it: IF_IR
  Counter #(.width(16), .max('hffff), .ongoal("wrap"), .trigger("rising"), .behavior("new")) counter_1 (
    .count(not_1_out), .Q(\总周期数 ), .clk(CLK), .down(undriven));  // open: load, D, carry, clr, preset
  Hex_Digit_Display hex_digit_display_2 (.value(LedData[27:24]));  // open: dp
  Hex_Digit_Display hex_digit_display_3 (.value(LedData[23:20]));  // open: dp
  // Probe on ID_PC[19:0]
  // RiscV_Probe riscv_probe_2: pin names not known; wires that end beside it: ID_IR
  Multiplexer #(.select(2), .width(32), .disabled("Z"), .enable("false")) multiplexer_1 (
    .in0(PC_4), .in1(jaddr), .in2(Calcuresult), .out(multiplexer_1_out), .sel(priority_encoder_1_out));  // open: in3
  Hex_Digit_Display hex_digit_display_4 (.value(LedData[19:16]));  // open: dp
  Hex_Digit_Display hex_digit_display_5 (.value(LedData[15:12]));  // open: dp
  not not_2 (not_2_out, halt);
  Hex_Digit_Display hex_digit_display_6 (.value(LedData[11:8]));  // open: dp
  Hex_Digit_Display hex_digit_display_7 (.value(LedData[7:4]));  // open: dp
  Clock #(.highDuration(1), .lowDuration(1)) clock_1 (.out(clock_1_out));
  // Probe on EX_PC[19:0]
  // RiscV_Probe riscv_probe_3: pin names not known; wires that end beside it: clock_1_out, EX_IR, CLK
  Register #(.width(32), .trigger("rising"), .Select("low")) PC (
    .D(multiplexer_1_out), .en(not_2_out), .Q(IF_PC), .clk(CLK), .clr(RST));
  Hex_Digit_Display hex_digit_display_8 (.value(LedData[3:0]));  // open: dp
  Adder #(.width(32)) adder_1 (.a(IF_PC), .b(32'h4), .out(PC_4));  // open: cin, cout
  // Probe on \总周期数 
  // Probe on M_PC[19:0]
  // RiscV_Probe riscv_probe_4: pin names not known; wires that end beside it: MEM_IR
  // Probe on \总周期数 
  // Probe on \无条件分支数 
  // Probe on \条件分支成功数 
  // Probe on \插入气泡数 
  // Probe on \LoadUse次数 
  // RiscV_Probe riscv_probe_5: pin names not known; wires that end beside it: IF_IR
  ROM #(.addrWidth(10), .dataWidth(32), .Select("high")) rom_1 (.addr(IF_PC[11:2]), .data(IF_IR));
  // Probe on IF_PC[11:0]
  // Probe on WB_PC[19:0]
  // RiscV_Probe riscv_probe_6: pin names not known; wires that end beside it: WB_IR
  // Probe on EX_PC[11:0]
  // Probe on ID_PC[11:0]
  IF_ID if_id_1 (.PC(IF_PC), .PC_2(ID_PC), .IR(IF_IR), .IR_2(ID_IR), .CLK(CLK), .e(1'b1), .reset(1'b0), .bt(1'b0));
  // Probe on M_PC[11:0]
  D_Flip_Flop #(.trigger("high"), .Pre_Clr_Positions("LEGACY"), .NegatePresetClear("false"), .enable("true"), .NewFFLayout("false")) d_ff_1 (.Q(d_ff_1_q));  // open: clk, D, Qn, preset, en, reset
  // Probe on 13'hc
  Comparator #(.width(32), .mode("twosComplement")) comparator_1 (
    .a({32{1'b0}}), .b(ID_IR), .eq(comparator_1_eq));  // open: gt, lt
  and and_1 (and_1_out, tunnel, \单周期硬布线控制器_1_lb );
  // Probe on WB_PC[11:0]
  Comparator #(.width(13), .mode("twosComplement")) comparator_2 (
    .a(CNT_num), .b(13'hc), .eq(comparator_2_eq), .lt(comparator_2_lt));  // open: gt
  Clock #(.highDuration(1), .lowDuration(1)) clock_2 (.out(clock_2_out));
  not not_3 (tunnel, comparator_1_eq);
  nand nand_1 (nand_1_out, d_ff_1_q, comparator_2_eq);
  Counter #(.width(13), .max('h1fff), .ongoal("stay"), .trigger("rising"), .behavior("old")) counter_2 (
    .count(comparator_2_lt), .Q(CNT_num), .clk(clock_2_out));  // open: load, D, carry, clr, preset
  \单周期硬布线控制器  \u_单周期硬布线控制器_1  (
    .Funct({ID_IR[30], ID_IR[25], ID_IR[14:12]}), .OP(ID_IR[6:2]), .ALU_OP(\单周期硬布线控制器_1_alu_op ),
    .MemToReg(\单周期硬布线控制器_1_memtoreg ), .MemWrite(\单周期硬布线控制器_1_memwrite ), .ALU_SRC(\单周期硬布线控制器_1_alu_src ),
    .RegWrite(\单周期硬布线控制器_1_regwrite ), .ecall(ecall), .S_type(S), .Jalr(\单周期硬布线控制器_1_jalr ),
    .Beq(\单周期硬布线控制器_1_beq ), .JAL(JAL), .Bne(\单周期硬布线控制器_1_bne ), .in_3(ID_IR[21]), .uret(\单周期硬布线控制器_1_uret ),
    .LUI(\单周期硬布线控制器_1_lui ), .lb(\单周期硬布线控制器_1_lb ), .bltu(bltu));  // open: re2_used, rs1_used, CSRRSI, CSRRCI, BGE, U_type
  assign CLK = nand_1_out ? clock_2_out : 1'bz;  // Controlled_Buffer controlled_buffer_1
  Multiplexer #(.select(1), .width(5), .disabled("Z"), .enable("false")) multiplexer_2 (
    .in0(ID_IR[19:15]), .in1(5'b10001), .out(multiplexer_2_out), .sel(ecall));
  Multiplexer #(.select(1), .width(5), .disabled("Z"), .enable("false")) multiplexer_3 (
    .in0(ID_IR[24:20]), .in1(5'b01010), .out(multiplexer_3_out), .sel(ecall));
  assign bit_extender_1_out = {{20{ID_IR[31]}}, ID_IR[31:20]};  // Bit_Extender bit_extender_1
  assign bit_extender_2_out = {{20{ID_IR[31]}}, {ID_IR[31:25], ID_IR[11:7]}};  // Bit_Extender bit_extender_2
  assign bit_extender_3_out = {{20{ID_IR[31]}}, {ID_IR[31], ID_IR[7], ID_IR[30:25], ID_IR[11:8]}};  // Bit_Extender bit_extender_3
  assign bit_extender_4_out = {{12{ID_IR[31]}}, {ID_IR[31], ID_IR[19:12], ID_IR[20], ID_IR[30:21]}};  // Bit_Extender bit_extender_4
  Pull_Resistor #(.pull(1)) pull_resistor_1 (.node(CLK));
  and and_2 (and_2_out, tunnel, \单周期硬布线控制器_1_memtoreg );
  and and_3 (and_3_out, tunnel, \单周期硬布线控制器_1_regwrite );
  Regifile regifile_1 (
    .Din(RDin), .Clk(CLK), .R1(regifile_1_r1), .R2(regifile_1_r2), .WE(RegWrite), .W_num(WB_rd),
    .R1_num(multiplexer_2_out), .R2_num(multiplexer_3_out));
  Multiplexer #(.select(1), .width(32), .disabled("Z"), .enable("false")) multiplexer_4 (
    .in0(bit_extender_1_out), .in1(bit_extender_2_out), .out(multiplexer_4_out), .sel(S));
  Multiplexer #(.select(1), .width(32), .disabled("Z"), .enable("false")) multiplexer_5 (
    .in0(bit_extender_3_out), .in1(bit_extender_4_out), .out(multiplexer_5_out), .sel(JAL));
  Shifter #(.width(32), .shift("ll")) shifter_1 (.in(multiplexer_5_out), .\dist (5'b00001), .out(shifter_1_out));
  and and_4 (and_4_out, tunnel, \单周期硬布线控制器_1_alu_src );
  ID_EX id_ex_1 (
    .in_1(and_1_out), .PC(ID_PC), .PC_2(EX_PC), .IR(ID_IR), .IR_2(EX_IR), .CLK(CLK), .e(1'b1), .reset(1'b0),
    .flush(1'b0), .out_30(id_ex_1_out_30), .in_4(\单周期硬布线控制器_1_lui ), .out_33(id_ex_1_out_33),
    .in_6(\单周期硬布线控制器_1_uret ), .in_9(\单周期硬布线控制器_1_jalr ), .out_38(id_ex_1_out_38), .in_11(JAL),
    .out_40(id_ex_1_out_40), .in_14(\单周期硬布线控制器_1_beq ), .out_43(id_ex_1_out_43), .in_16(\单周期硬布线控制器_1_bne ),
    .out_45(id_ex_1_out_45), .in_19(and_2_out), .out_48(id_ex_1_out_48), .in_2(\单周期硬布线控制器_1_memwrite ),
    .out_31(id_ex_1_out_31), .in_5(and_4_out), .out_34(id_ex_1_out_34), .in_8(and_3_out),
    .out_37(id_ex_1_out_37), .in_10(bltu), .out_39(id_ex_1_out_39), .in_13(S), .in_15(ecall),
    .out_44(EX_ecall), .op(\单周期硬布线控制器_1_alu_op ), .out_47(id_ex_1_out_47), .rd(ID_IR[11:7]),
    .out_49(id_ex_1_out_49), .out_36(id_ex_1_out_36), .in_7(regifile_1_r2), .in_3(regifile_1_r1),
    .out_32(id_ex_1_out_32), .in_12(multiplexer_4_out), .out_41(id_ex_1_out_41), .in_17(shifter_1_out),
    .out_46(id_ex_1_out_46), .in_21({ID_IR[31:12], {12{1'b0}}}), .out_50(id_ex_1_out_50));  // open: out_35, out_42, in_28, out_53, in_29, out_54
  Priority_Encoder #(.select(2), .disabled("Z")) priority_encoder_1 (
    .in0(1'b1), .in1(or_1_out), .in2(id_ex_1_out_38), .out(priority_encoder_1_out));  // open: in3, gs, en_out, en_in
  Multiplexer #(.select(1), .width(32), .disabled("Z"), .enable("false")) multiplexer_6 (
    .in0(id_ex_1_out_36), .in1(id_ex_1_out_41), .out(multiplexer_6_out), .sel(id_ex_1_out_34));
  or or_1 (or_1_out, and_5_out, and_6_out, and_7_out, id_ex_1_out_40);
  Adder #(.width(32)) adder_2 (.a(id_ex_1_out_46), .b(EX_PC), .out(jaddr));  // open: cin, cout
  Comparator #(.width(32), .mode("twosComplement")) comparator_3 (
    .a(id_ex_1_out_32), .b(32'h22), .gt(comparator_3_gt), .lt(comparator_3_lt));  // open: eq
  and and_5 (and_5_out, id_ex_1_out_45, ~AluEQ);  // AND_Gate
  and and_6 (and_6_out, AluEQ, id_ex_1_out_43);
  and and_7 (and_7_out, Alu, id_ex_1_out_39);
  ALU alu_1 (
    .X(id_ex_1_out_32), .Y(multiplexer_6_out), .AluOP(id_ex_1_out_47), .Equal(AluEQ), .Result(Calcuresult),
    .out_6(Alu));  // open: Result_2, out_4
  or or_2 (or_2_out, comparator_3_gt, comparator_3_lt);
  not not_4 (not_4_out, or_2_out);
  and and_8 (and_8_out, EX_ecall, or_2_out);
  and and_9 (and_9_out, not_4_out, EX_ecall);
  D_Flip_Flop #(.trigger("falling"), .Pre_Clr_Positions("ABOVE_BELOW"), .NegatePresetClear("false"), .enable("true"), .NewFFLayout("true")) d_ff_2 (
    .clk(CLK), .D(1'b1), .Q(EX_halt), .en(and_8_out), .reset(Go));  // open: Qn, preset
  Register #(.width(32), .trigger("rising"), .Select("low")) register_1 (
    .D(id_ex_1_out_36), .en(and_9_out), .Q(LedData), .clk(CLK));  // open: clr
  EXMEM exmem_1 (
    .in_1(id_ex_1_out_30), .in_2(id_ex_1_out_33), .in_3(id_ex_1_out_38), .in_4(id_ex_1_out_40),
    .in_5(id_ex_1_out_48), .rd(id_ex_1_out_49), .in_7(id_ex_1_out_31), .in_8(id_ex_1_out_37), .in_9(EX_halt),
    .PC(EX_PC), .IR(EX_IR), .out_19(exmem_1_out_19), .out_20(exmem_1_out_20), .out_21(exmem_1_out_21),
    .out_22(exmem_1_out_22), .out_23(exmem_1_out_23), .out_24(exmem_1_out_24), .out_25(MemWrite),
    .out_26(exmem_1_out_26), .out_27(exmem_1_out_27), .out_28(exmem_1_out_28), .out_29(exmem_1_out_29),
    .PC_2(M_PC), .out_31(exmem_1_out_31), .IR_2(MEM_IR), .in_13(id_ex_1_out_50), .in_10(Calcuresult),
    .in_11(id_ex_1_out_36), .reset(1'b0), .bt(1'b0), .e(1'b1), .CLK(CLK));
  Shifter #(.width(32), .shift("ll")) shifter_2 (.in(exmem_1_out_29), .\dist (5'b10000), .out(shifter_2_out));
  Multiplexer #(.select(1), .width(32), .disabled("Z"), .enable("false")) multiplexer_7 (
    .in0(exmem_1_out_29), .in1(shifter_2_out), .out(MDin), .sel(exmem_1_out_28[1]));
  RAM #(.addrWidth(10), .dataWidth(32), .bus("separate"), .Select("high")) ram_1 (
    .addr(exmem_1_out_28[11:2]), .din(MDin), .data(ram_1_data), .str(MemWrite), .sel(1'b1), .clk(CLK),
    .ld(1'b1));  // open: clr
  MEM_WB mem_wb_1 (
    .in_1(exmem_1_out_19), .in_2(exmem_1_out_20), .in_3(exmem_1_out_21), .in_4(exmem_1_out_22),
    .in_5(exmem_1_out_23), .rd(exmem_1_out_24), .in_7(MemWrite), .in_8(exmem_1_out_26),
    .in_9(exmem_1_out_27), .PC(M_PC), .IR(MEM_IR), .out_19(mem_wb_1_out_19), .out_20(mem_wb_1_out_20),
    .out_21(mem_wb_1_out_21), .out_22(mem_wb_1_out_22), .out_23(mem_wb_1_out_23), .out_24(WB_rd),
    .out_26(RegWrite), .out_27(mem_wb_1_out_27), .out_28(mem_wb_1_out_28), .out_29(WB_Dout), .PC_2(WB_PC),
    .out_31(mem_wb_1_out_31), .IR_2(WB_IR), .in_13(exmem_1_out_31), .in_10(exmem_1_out_28),
    .in_11(ram_1_data), .reset(1'b0), .bt(1'b0), .e(1'b1), .CLK(CLK));  // open: out_25
  or or_3 (or_4_out[1], mem_wb_1_out_20, mem_wb_1_out_21, mem_wb_1_out_22);
  or or_4 (or_4_out[0], mem_wb_1_out_20, mem_wb_1_out_23);
  Adder #(.width(32)) adder_3 (.a(WB_PC), .b(32'h4), .out(adder_3_out));  // open: cin, cout
  Multiplexer #(.select(2), .width(32), .disabled("Z"), .enable("false")) multiplexer_8 (
    .in0(mem_wb_1_out_28), .in1(multiplexer_10_out), .in2(adder_3_out), .in3(mem_wb_1_out_31), .out(RDin),
    .sel(or_4_out));
  D_Flip_Flop #(.trigger("rising"), .Pre_Clr_Positions("ABOVE_BELOW"), .NegatePresetClear("false"), .enable("true"), .NewFFLayout("true")) d_ff_3 (
    .clk(mem_wb_1_out_27), .D(1'b1), .Q(halt), .en(1'b1), .reset(Go));  // open: Qn, preset
  Multiplexer #(.select(2), .width(8), .disabled("Z"), .enable("false")) multiplexer_9 (
    .in0(WB_Dout[7:0]), .in1(WB_Dout[15:8]), .in2(WB_Dout[23:16]), .in3(WB_Dout[31:24]),
    .out(multiplexer_9_out), .sel(mem_wb_1_out_28[1:0]));
  Multiplexer #(.select(1), .width(32), .disabled("Z"), .enable("false")) multiplexer_10 (
    .in0(WB_Dout), .in1(LBDout), .out(multiplexer_10_out), .sel(mem_wb_1_out_19));
  assign LBDout = {{24{multiplexer_9_out[7]}}, multiplexer_9_out};  // Bit_Extender bit_extender_5

  // Other names for the same wires on the sheet: rd[4:0] = ID_IR[11:7]; IR[31:0] = IF_IR; MEM_PC[31:0] = M_PC;
  //   PC[31:0] = IF_PC

  // Notes on the sheet:
  //   中断源
  //   中断等待指示
  //   数码管输出
  //   指令存储器
  //   指令探针
  //   contents of rom_1 (hex, n*v repeats v):
  //   413 493 913 993 46413 14e493 296913 39e993 842023 942223 1242423 1342623 a00893 493 913 993 73
  //   控制位
  //   流水调试日志用
  //   暂停节拍，不能为0
  //   指令字
  //   戳工具置1进入计数暂停模式，ctrl+k时钟自动运行到对应节拍暂停
  //   ctrl+k关闭时钟连续运行，将控制位置零，进入单步调试模式调试
  //   用这个时钟源需要去掉电路中的其他时钟源
  //   JAL
  //   JALR
  //   URET
  //   LUI
  //   lb
  //   Beq
  //   Bne
  //   AluOP
  //   AluSrcB
  //   RegWrite
  //   bltu
  //   S_type
  //   可计数暂停的时钟源
  //   MemToReg
  //   MemWrite
  //   LUI
  //   为方便自动评测，需要输出流水线各段保存的PC值，注意是PC不是PC+4，另外ID段寄存器写入信息，Mem段内存写入信息也要输出
  //   时空图监测，可删除
  //   lb
  //   lb
  //   lui
  //   LUI
  //   URET
  //   URET
  //   JALR
  //   JAL
  //   JAL
  //   Beq
  //   Beq
  //   Bne
  //   Bne
  //   MTR
  //   MTR
  //   MW
  //   MW
  //   AluSrc
  //   AluSrcB
  //   Rw
  //   RW
  //   bltu
  //   s
  //   ecall
  //   r1
  //   r2
  //   r2
  //   imm12
  //   imm12
  //   immj
  //   lui
  //   result
  //   r2
  //   lui
  //   lb
  //   lui
  //   JALR
  //   JAL
  //   MTR
  //   MW
  //   RW
  //   lui
  //   数据存储器
  //   lb
  //   lb
  //   lui
  //   lui
  //   JALR
  //   JALR
  //   JAL
  //   JAL
  //   MTR
  //   MTR
  //   MTR
  //   MW
  //   MW
  //   RW
  //   RW
  //   halt
  //   halt
endmodule

module \气泡流水线  (
  output RegWrite,
  output MemWrite,
  output [31:0] IF_PC,
  output [31:0] ID_PC,
  output [31:0] EX_PC,
  output [31:0] M_PC,
  output [31:0] WB_PC,
  output [31:0] RDin,
  output [31:0] MDin,
  output [31:0] LedData
);

  wire Alu, AluEQ, and_1_out, and_2_out, and_3_out, and_4_out, and_5_out, and_6_out, and_7_out, and_8_out,
       and_9_out, and_10_out, and_11_out, and_12_out, and_13_out, and_14_out, bltu, Branchtaken, CLK,
       clock_1_out, clock_2_out, comparator_1_eq, comparator_2_eq, comparator_2_lt, comparator_3_gt,
       comparator_3_lt, d_ff_1_q, ecall, EX_ecall, EX_halt, exmem_1_out_19, exmem_1_out_20, exmem_1_out_21,
       exmem_1_out_22, exmem_1_out_23, exmem_1_out_26, exmem_1_out_27, flush, Go, halt, id_ex_1_out_30,
       id_ex_1_out_31, id_ex_1_out_33, id_ex_1_out_34, id_ex_1_out_37, id_ex_1_out_38, id_ex_1_out_39,
       id_ex_1_out_40, id_ex_1_out_43, id_ex_1_out_45, id_ex_1_out_48, IR1, IR2, IR3, JAL, mem_wb_1_out_19,
       mem_wb_1_out_20, mem_wb_1_out_21, mem_wb_1_out_22, mem_wb_1_out_23, mem_wb_1_out_27, nand_1_out,
       not_1_out, not_3_out, not_4_out, not_5_out, not_6_out, not_7_out, not_8_out, or_1_out, or_3_out,
       or_4_out, or_5_out, rs1_used, rs2_used, RST, S, stall, tunnel, W1, W2, W3, \单周期硬布线控制器_1_alu_src ,
       \单周期硬布线控制器_1_beq , \单周期硬布线控制器_1_bne , \单周期硬布线控制器_1_jalr , \单周期硬布线控制器_1_lb , \单周期硬布线控制器_1_lui ,
       \单周期硬布线控制器_1_memtoreg , \单周期硬布线控制器_1_memwrite , \单周期硬布线控制器_1_regwrite , \单周期硬布线控制器_1_uret ;
  wire [1:0] or_7_out, priority_encoder_1_out;
  wire [3:0] id_ex_1_out_47, \单周期硬布线控制器_1_alu_op ;
  wire [4:0] exmem_1_out_24, id_ex_1_out_49, multiplexer_2_out, multiplexer_3_out, WB_rd;
  wire [7:0] multiplexer_10_out;
  wire [12:0] CNT_num;
  wire [15:0] \LoadUse次数 , \总周期数 , \插入气泡数 , \无条件分支数 , \条件分支成功数 ;
  wire [31:0] adder_3_out, bit_extender_1_out, bit_extender_2_out, bit_extender_3_out, bit_extender_4_out,
       Calcuresult, EX_IR, exmem_1_out_28, exmem_1_out_29, exmem_1_out_31, id_ex_1_out_32, id_ex_1_out_36,
       id_ex_1_out_41, id_ex_1_out_46, id_ex_1_out_50, ID_IR, IF_IR, jaddr, LBDout, MEM_IR, mem_wb_1_out_28,
       mem_wb_1_out_31, multiplexer_1_out, multiplexer_4_out, multiplexer_5_out, multiplexer_6_out,
       multiplexer_9_out, PC_4, ram_1_data, regifile_1_r1, regifile_1_r2, shifter_1_out, shifter_2_out,
       WB_Dout, WB_IR;

  Button \u_总复位  (.out(RST));
  Button _1 (.out(IR1));
  Button _2 (.out(IR2));
  Button _3 (.out(IR3));
  // Probe on \总周期数 
  // Probe on \总周期数 
  Button \u_继续运行  (.out(Go));
  LED #(.active("true")) led_1 (.in(W1));
  LED #(.active("true")) led_2 (.in(W2));
  LED #(.active("true")) led_3 (.in(W3));
  Hex_Digit_Display hex_digit_display_1 (.value(LedData[31:28]));  // open: dp
  // Probe on IF_PC[19:0]
  // RiscV_Probe riscv_probe_1: pin names not known; wires that end beside it: IF_IR
  Hex_Digit_Display hex_digit_display_2 (.value(LedData[27:24]));  // open: dp
  Hex_Digit_Display hex_digit_display_3 (.value(LedData[23:20]));  // open: dp
  // Probe on ID_PC[19:0]
  // RiscV_Probe riscv_probe_2: pin names not known; wires that end beside it: ID_IR
  not not_1 (not_1_out, halt);
  and and_1 (and_1_out, not_1_out, stall);
  Counter #(.width(16), .max('hffff), .ongoal("wrap"), .trigger("rising"), .behavior("old")) counter_1 (
    .count(and_1_out), .Q(\插入气泡数 ), .clk(CLK));  // open: load, D, carry, clr, preset
  Hex_Digit_Display hex_digit_display_4 (.value(LedData[15:12]));  // open: dp
  Hex_Digit_Display hex_digit_display_5 (.value(LedData[19:16]));  // open: dp
  Counter #(.width(16), .max('hffff), .ongoal("wrap"), .trigger("rising"), .behavior("new")) counter_2 (
    .count(not_1_out), .Q(\总周期数 ), .clk(CLK));  // open: load, D, carry, clr, preset, down
  Hex_Digit_Display hex_digit_display_6 (.value(LedData[7:4]));  // open: dp
  Hex_Digit_Display hex_digit_display_7 (.value(LedData[11:8]));  // open: dp
  Clock #(.highDuration(1), .lowDuration(1)) clock_1 (.out(clock_1_out));
  // Probe on EX_PC[19:0]
  // RiscV_Probe riscv_probe_3: pin names not known; wires that end beside it: clock_1_out, EX_IR, CLK
  Multiplexer #(.select(2), .width(32), .disabled("Z"), .enable("false")) multiplexer_1 (
    .in0(PC_4), .in1(jaddr), .in2(Calcuresult), .out(multiplexer_1_out), .sel(priority_encoder_1_out));  // open: in3
  Hex_Digit_Display hex_digit_display_8 (.value(LedData[3:0]));  // open: dp
  and and_2 (and_2_out, ~stall, ~halt);  // AND_Gate
  // Probe on \总周期数 
  // Probe on M_PC[19:0]
  // RiscV_Probe riscv_probe_4: pin names not known; wires that end beside it: MEM_IR
  Register #(.width(32), .trigger("rising"), .Select("low")) PC (
    .D(multiplexer_1_out), .en(and_2_out), .Q(IF_PC), .clk(CLK), .clr(RST));
  // Probe on \总周期数 
  // Probe on \无条件分支数 
  // Probe on \条件分支成功数 
  // Probe on \插入气泡数 
  // Probe on \LoadUse次数 
  Adder #(.width(32)) adder_1 (.a(IF_PC), .b(32'h4), .out(PC_4));  // open: cin, cout
  // Probe on IF_PC[11:0]
  // Probe on WB_PC[19:0]
  // RiscV_Probe riscv_probe_5: pin names not known; wires that end beside it: WB_IR
  ROM #(.addrWidth(10), .dataWidth(32), .Select("high")) rom_1 (.addr(IF_PC[11:2]), .data(IF_IR));
  // Probe on ID_PC[11:0]
  // Probe on EX_PC[11:0]
  // RiscV_Probe riscv_probe_6: pin names not known; wires that end beside it: IF_IR
  // Probe on M_PC[11:0]
  D_Flip_Flop #(.trigger("high"), .Pre_Clr_Positions("LEGACY"), .NegatePresetClear("false"), .enable("true"), .NewFFLayout("false")) d_ff_1 (.Q(d_ff_1_q));  // open: clk, D, Qn, preset, en, reset
  // Probe on 13'hc
  not not_2 (tunnel, comparator_1_eq);
  Comparator #(.width(32), .mode("twosComplement")) comparator_1 (
    .a({32{1'b0}}), .b(ID_IR), .eq(comparator_1_eq));  // open: gt, lt
  and and_3 (and_3_out, ~stall, ~halt);  // AND_Gate
  // Probe on WB_PC[11:0]
  Comparator #(.width(13), .mode("twosComplement")) comparator_2 (
    .a(CNT_num), .b(13'hc), .eq(comparator_2_eq), .lt(comparator_2_lt));  // open: gt
  Clock #(.highDuration(1), .lowDuration(1)) clock_2 (.out(clock_2_out));
  IF_ID if_id_1 (
    .PC(IF_PC), .PC_2(ID_PC), .IR(IF_IR), .IR_2(ID_IR), .CLK(CLK), .e(and_3_out), .reset(RST),
    .bt(Branchtaken));
  nand nand_1 (nand_1_out, d_ff_1_q, comparator_2_eq);
  Counter #(.width(13), .max('h1fff), .ongoal("stay"), .trigger("rising"), .behavior("old")) counter_3 (
    .count(comparator_2_lt), .Q(CNT_num), .clk(clock_2_out));  // open: load, D, carry, clr, preset
  and and_4 (and_4_out, tunnel, \单周期硬布线控制器_1_lb );
  assign CLK = nand_1_out ? clock_2_out : 1'bz;  // Controlled_Buffer controlled_buffer_1
  Pull_Resistor #(.pull(1)) pull_resistor_1 (.node(CLK));
  \单周期硬布线控制器  \u_单周期硬布线控制器_1  (
    .Funct({ID_IR[30], ID_IR[25], ID_IR[14:12]}), .OP(ID_IR[6:2]), .ALU_OP(\单周期硬布线控制器_1_alu_op ),
    .MemToReg(\单周期硬布线控制器_1_memtoreg ), .MemWrite(\单周期硬布线控制器_1_memwrite ), .ALU_SRC(\单周期硬布线控制器_1_alu_src ),
    .RegWrite(\单周期硬布线控制器_1_regwrite ), .ecall(ecall), .S_type(S), .Jalr(\单周期硬布线控制器_1_jalr ),
    .Beq(\单周期硬布线控制器_1_beq ), .JAL(JAL), .Bne(\单周期硬布线控制器_1_bne ), .in_3(ID_IR[21]), .uret(\单周期硬布线控制器_1_uret ),
    .LUI(\单周期硬布线控制器_1_lui ), .lb(\单周期硬布线控制器_1_lb ), .bltu(bltu), .re2_used(rs2_used), .rs1_used(rs1_used));  // open: CSRRSI, CSRRCI, BGE, U_type
  Multiplexer #(.select(1), .width(5), .disabled("Z"), .enable("false")) multiplexer_2 (
    .in0(ID_IR[19:15]), .in1(5'b10001), .out(multiplexer_2_out), .sel(ecall));
  Multiplexer #(.select(1), .width(5), .disabled("Z"), .enable("false")) multiplexer_3 (
    .in0(ID_IR[24:20]), .in1(5'b01010), .out(multiplexer_3_out), .sel(ecall));
  and and_5 (and_5_out, tunnel, \单周期硬布线控制器_1_memtoreg );
  assign bit_extender_1_out = {{20{ID_IR[31]}}, ID_IR[31:20]};  // Bit_Extender bit_extender_1
  assign bit_extender_2_out = {{20{ID_IR[31]}}, {ID_IR[31:25], ID_IR[11:7]}};  // Bit_Extender bit_extender_2
  assign bit_extender_3_out = {{20{ID_IR[31]}}, {ID_IR[31], ID_IR[7], ID_IR[30:25], ID_IR[11:8]}};  // Bit_Extender bit_extender_3
  assign bit_extender_4_out = {{12{ID_IR[31]}}, {ID_IR[31], ID_IR[19:12], ID_IR[20], ID_IR[30:21]}};  // Bit_Extender bit_extender_4
  \气泡逻辑  \u_气泡逻辑_1  (
    .IR(ID_IR), .rs1_used(rs1_used), .rs2_used(rs2_used), .EX_rw(id_ex_1_out_37), .EX_rd(id_ex_1_out_49),
    .MEM_rw(exmem_1_out_26), .MEM_rd(exmem_1_out_24), .ecall(ecall), .BranchTaken(Branchtaken),
    .stall(stall), .flush(flush));
  not not_3 (not_3_out, CLK);
  Regifile regifile_1 (
    .Din(RDin), .Clk(not_3_out), .R1(regifile_1_r1), .R2(regifile_1_r2), .WE(RegWrite), .W_num(WB_rd),
    .R1_num(multiplexer_2_out), .R2_num(multiplexer_3_out));
  Multiplexer #(.select(1), .width(32), .disabled("Z"), .enable("false")) multiplexer_4 (
    .in0(bit_extender_3_out), .in1(bit_extender_4_out), .out(multiplexer_4_out), .sel(JAL));
  and and_6 (and_6_out, tunnel, \单周期硬布线控制器_1_alu_src );
  Multiplexer #(.select(1), .width(32), .disabled("Z"), .enable("false")) multiplexer_5 (
    .in0(bit_extender_1_out), .in1(bit_extender_2_out), .out(multiplexer_5_out), .sel(S));
  Shifter #(.width(32), .shift("ll")) shifter_1 (.in(multiplexer_4_out), .\dist (5'b00001), .out(shifter_1_out));
  and and_7 (and_7_out, tunnel, \单周期硬布线控制器_1_regwrite );
  ID_EX id_ex_1 (
    .in_1(and_4_out), .PC(ID_PC), .PC_2(EX_PC), .IR(ID_IR), .IR_2(EX_IR), .CLK(CLK), .e(not_4_out),
    .reset(RST), .flush(flush), .out_30(id_ex_1_out_30), .in_4(\单周期硬布线控制器_1_lui ), .out_33(id_ex_1_out_33),
    .in_6(\单周期硬布线控制器_1_uret ), .in_9(\单周期硬布线控制器_1_jalr ), .out_38(id_ex_1_out_38), .in_11(JAL),
    .out_40(id_ex_1_out_40), .in_14(\单周期硬布线控制器_1_beq ), .out_43(id_ex_1_out_43), .in_16(\单周期硬布线控制器_1_bne ),
    .out_45(id_ex_1_out_45), .in_19(and_5_out), .out_48(id_ex_1_out_48), .in_2(\单周期硬布线控制器_1_memwrite ),
    .out_31(id_ex_1_out_31), .in_5(and_6_out), .out_34(id_ex_1_out_34), .in_8(and_7_out),
    .out_37(id_ex_1_out_37), .in_10(bltu), .out_39(id_ex_1_out_39), .in_13(S), .in_15(ecall),
    .out_44(EX_ecall), .op(\单周期硬布线控制器_1_alu_op ), .out_47(id_ex_1_out_47), .rd(ID_IR[11:7]),
    .out_49(id_ex_1_out_49), .out_36(id_ex_1_out_36), .in_7(regifile_1_r2), .in_3(regifile_1_r1),
    .out_32(id_ex_1_out_32), .in_12(multiplexer_5_out), .out_41(id_ex_1_out_41), .in_17(shifter_1_out),
    .out_46(id_ex_1_out_46), .in_21({ID_IR[31:12], {12{1'b0}}}), .out_50(id_ex_1_out_50));  // open: out_35, out_42, in_28, out_53, in_29, out_54
  not not_4 (not_4_out, halt);
  not not_5 (not_5_out, halt);
  and and_8 (and_8_out, not_5_out, or_1_out);
  Counter #(.width(16), .max('hffff), .ongoal("wrap"), .trigger("rising"), .behavior("new")) counter_4 (
    .count(and_8_out), .Q(\无条件分支数 ), .clk(CLK));  // open: load, D, carry, clr, preset, down
  and and_9 (and_9_out, not_5_out, or_3_out);
  Priority_Encoder #(.select(2), .disabled("Z")) priority_encoder_1 (
    .in0(1'b1), .in1(or_4_out), .in2(id_ex_1_out_38), .out(priority_encoder_1_out));  // open: in3, gs, en_out, en_in
  or or_1 (or_1_out, id_ex_1_out_40, id_ex_1_out_38);
  Counter #(.width(16), .max('hffff), .ongoal("wrap"), .trigger("rising"), .behavior("new")) counter_5 (
    .count(and_9_out), .Q(\条件分支成功数 ), .clk(CLK));  // open: load, D, carry, clr, preset, down
  or or_2 (Branchtaken, id_ex_1_out_38, or_4_out);
  Multiplexer #(.select(1), .width(32), .disabled("Z"), .enable("false")) multiplexer_6 (
    .in0(id_ex_1_out_36), .in1(id_ex_1_out_41), .out(multiplexer_6_out), .sel(id_ex_1_out_34));
  Adder #(.width(32)) adder_2 (.a(id_ex_1_out_46), .b(EX_PC), .out(jaddr));  // open: cin, cout
  or or_3 (or_3_out, and_11_out, and_12_out, and_10_out);
  or or_4 (or_4_out, and_10_out, and_11_out, and_12_out, id_ex_1_out_40);
  ALU alu_1 (
    .X(id_ex_1_out_32), .Y(multiplexer_6_out), .AluOP(id_ex_1_out_47), .Equal(AluEQ), .Result(Calcuresult),
    .out_6(Alu));  // open: Result_2, out_4
  Comparator #(.width(32), .mode("twosComplement")) comparator_3 (
    .a(id_ex_1_out_32), .b(32'h22), .gt(comparator_3_gt), .lt(comparator_3_lt));  // open: eq
  and and_10 (and_10_out, id_ex_1_out_45, ~AluEQ);  // AND_Gate
  and and_11 (and_11_out, AluEQ, id_ex_1_out_43);
  and and_12 (and_12_out, Alu, id_ex_1_out_39);
  or or_5 (or_5_out, comparator_3_gt, comparator_3_lt);
  not not_6 (not_6_out, or_5_out);
  and and_13 (and_13_out, EX_ecall, or_5_out);
  and and_14 (and_14_out, not_6_out, EX_ecall);
  not not_7 (not_7_out, halt);
  D_Flip_Flop #(.trigger("falling"), .Pre_Clr_Positions("ABOVE_BELOW"), .NegatePresetClear("false"), .enable("true"), .NewFFLayout("true")) d_ff_2 (
    .clk(CLK), .D(1'b1), .Q(EX_halt), .en(and_13_out), .reset(Go));  // open: Qn, preset
  Register #(.width(32), .trigger("rising"), .Select("low")) register_1 (
    .D(id_ex_1_out_36), .en(and_14_out), .Q(LedData), .clk(CLK));  // open: clr
  EXMEM exmem_1 (
    .in_1(id_ex_1_out_30), .in_2(id_ex_1_out_33), .in_3(id_ex_1_out_38), .in_4(id_ex_1_out_40),
    .in_5(id_ex_1_out_48), .rd(id_ex_1_out_49), .in_7(id_ex_1_out_31), .in_8(id_ex_1_out_37), .in_9(EX_halt),
    .PC(EX_PC), .IR(EX_IR), .out_19(exmem_1_out_19), .out_20(exmem_1_out_20), .out_21(exmem_1_out_21),
    .out_22(exmem_1_out_22), .out_23(exmem_1_out_23), .out_24(exmem_1_out_24), .out_25(MemWrite),
    .out_26(exmem_1_out_26), .out_27(exmem_1_out_27), .out_28(exmem_1_out_28), .out_29(exmem_1_out_29),
    .PC_2(M_PC), .out_31(exmem_1_out_31), .IR_2(MEM_IR), .in_13(id_ex_1_out_50), .in_10(Calcuresult),
    .in_11(id_ex_1_out_36), .reset(RST), .bt(RST), .e(not_7_out), .CLK(CLK));
  Multiplexer #(.select(1), .width(32), .disabled("Z"), .enable("false")) multiplexer_7 (
    .in0(exmem_1_out_29), .in1(shifter_2_out), .out(MDin), .sel(exmem_1_out_28[1]));
  Shifter #(.width(32), .shift("ll")) shifter_2 (.in(exmem_1_out_29), .\dist (5'b10000), .out(shifter_2_out));
  RAM #(.addrWidth(10), .dataWidth(32), .bus("separate"), .Select("high")) ram_1 (
    .addr(exmem_1_out_28[11:2]), .din(MDin), .data(ram_1_data), .str(MemWrite), .sel(1'b1), .clk(CLK),
    .ld(1'b1), .clr(RST));
  not not_8 (not_8_out, halt);
  or or_6 (or_7_out[1], mem_wb_1_out_20, mem_wb_1_out_21, mem_wb_1_out_22);
  MEM_WB mem_wb_1 (
    .in_1(exmem_1_out_19), .in_2(exmem_1_out_20), .in_3(exmem_1_out_21), .in_4(exmem_1_out_22),
    .in_5(exmem_1_out_23), .rd(exmem_1_out_24), .in_7(MemWrite), .in_8(exmem_1_out_26),
    .in_9(exmem_1_out_27), .PC(M_PC), .IR(MEM_IR), .out_19(mem_wb_1_out_19), .out_20(mem_wb_1_out_20),
    .out_21(mem_wb_1_out_21), .out_22(mem_wb_1_out_22), .out_23(mem_wb_1_out_23), .out_24(WB_rd),
    .out_26(RegWrite), .out_27(mem_wb_1_out_27), .out_28(mem_wb_1_out_28), .out_29(WB_Dout), .PC_2(WB_PC),
    .out_31(mem_wb_1_out_31), .IR_2(WB_IR), .in_13(exmem_1_out_31), .in_10(exmem_1_out_28),
    .in_11(ram_1_data), .reset(RST), .bt(RST), .e(not_8_out), .CLK(CLK));  // open: out_25
  or or_7 (or_7_out[0], mem_wb_1_out_20, mem_wb_1_out_23);
  Adder #(.width(32)) adder_3 (.a(WB_PC), .b(32'h4), .out(adder_3_out));  // open: cin, cout
  Multiplexer #(.select(2), .width(32), .disabled("Z"), .enable("false")) multiplexer_8 (
    .in0(mem_wb_1_out_28), .in1(multiplexer_9_out), .in2(adder_3_out), .in3(mem_wb_1_out_31), .out(RDin),
    .sel(or_7_out));
  D_Flip_Flop #(.trigger("rising"), .Pre_Clr_Positions("ABOVE_BELOW"), .NegatePresetClear("false"), .enable("true"), .NewFFLayout("true")) d_ff_3 (
    .clk(mem_wb_1_out_27), .D(1'b1), .Q(halt), .en(1'b1), .reset(Go));  // open: Qn, preset
  Multiplexer #(.select(1), .width(32), .disabled("Z"), .enable("false")) multiplexer_9 (
    .in0(WB_Dout), .in1(LBDout), .out(multiplexer_9_out), .sel(mem_wb_1_out_19));
  Multiplexer #(.select(2), .width(8), .disabled("Z"), .enable("false")) multiplexer_10 (
    .in0(WB_Dout[7:0]), .in1(WB_Dout[15:8]), .in2(WB_Dout[23:16]), .in3(WB_Dout[31:24]),
    .out(multiplexer_10_out), .sel(mem_wb_1_out_28[1:0]));
  assign LBDout = {{24{multiplexer_10_out[7]}}, multiplexer_10_out};  // Bit_Extender bit_extender_5

  // Other names for the same wires on the sheet: rd[4:0] = ID_IR[11:7]; IR[31:0] = IF_IR; MEM_PC[31:0] = M_PC;
  //   PC[31:0] = IF_PC

  // Notes on the sheet:
  //   中断源
  //   时空图监测，可删除
  //   中断等待指示
  //   数码管输出
  //   指令存储器
  //   contents of rom_1 (hex, n*v repeats v):
  //   100493 100006f 100493 200913 300993 100006f 100493 200913 300993 100006f 100493 200913 300993
  //   100006f 100493 200913 300993 3f0000ef 100413 100493 1f49493 900533 2200893 73 24d493 48463 fedff06f
  //   900533 2200893 73 100493 249493 900533 2200893 73 48463 fedff06f 100493 1f49493 900533 2200893 73
  //   4034d493 900533 2200893 73 4044d493 900533 2200893 73 4044d493 900533 2200893 73 4044d493 900533
  //   2200893 73 4044d493 900533 2200893 73 4044d493 900533 2200893 73 4044d493 900533 2200893 73 4044d493
  //   900533 2200893 73 100413 1f41993 41f9d993 433 c00913 300b13 140413 f47413 800293 100313 499993
  //   89e9b3 1300533 2200893 73 406282b3 fe0294e3 140413 f00f93 1f47433 1c41413 800293 100313 49d993
  //   89e9b3 1300533 2200893 73 406282b3 fe0294e3 1c45413 406b0b33 b0463 f95ff06f 2b3 fff2c293 829293
  //   ff2e293 500533 2200893 73 fff00413 493 84a023 140413 448493 84a023 140413 448493 84a023 140413
  //   448493 84a023 140413 448493 84a023 140413 448493 84a023 140413 448493 84a023 140413 448493 84a023
  //   140413 448493 84a023 140413 448493 84a023 140413 448493 84a023 140413 448493 84a023 140413 448493
  //   84a023 140413 448493 84a023 140413 448493 84a023 140413 448493 84a023 140413 448493 140413 433
  //   3c00493 42983 4aa03 149a2b3 28663 134a023 1442023 ffc48493 fe9412e3 800533 2200893 73 440413 3c00493
  //   fc9416e3 3200893 73 100293 300313 800493 849493 7648493 1449493 900533 2200893 73 800e13 4054d4b3
  //   4064d4b3 900533 2200893 73 fffe0e13 fe0e14e3 a00893 73 800e13 fedc04b7 fff00413 1045413 84e4b3
  //   900533 2200893 73 ba984b7 900533 73 76544b7 900533 73 32104b7 900533 73 fffe0e13 fa0e1ee3 a00893 73
  //   313 1000e13 8400493 849493 8348493 400913 891913 490913 849493 8248493 849493 8148493 891913 490913
  //   891913 490913 932023 12484b3 430313 fffe0e13 fe0e18e3 2000e13 313 30483 900533 2200893 73 130313
  //   fffe0e13 fe0e14e3 a00893 73 ff100493 900533 2200893 73 148493 fe9068e3 900533 2200893 73 a00893 73
  //   a00893 73 413 140413 800533 2200893 73 240413 800533 2200893 73 340413 800533 2200893 73 440413
  //   800533 2200893 73 540413 800533 2200893 73 640413 800533 2200893 73 740413 800533 2200893 73 840413
  //   800533 2200893 2200893 73 8067
  //   控制位
  //   指令探针
  //   流水调试日志用
  //   暂停节拍，不能为0
  //   戳工具置1进入计数暂停模式，ctrl+k时钟自动运行到对应节拍暂停
  //   ctrl+k关闭时钟连续运行，将控制位置零，进入单步调试模式调试
  //   指令字
  //   可计数暂停的时钟源
  //   JAL
  //   JALR
  //   URET
  //   LUI
  //   lb
  //   Beq
  //   Bne
  //   MemToReg
  //   MemWrite
  //   AluOP
  //   AluSrcB
  //   RegWrite
  //   bltu
  //   S_type
  //   LUI
  //   stall
  //   为方便自动评测，需要输出流水线各段保存的PC值，注意是PC不是PC+4，另外ID段寄存器写入信息，Mem段内存写入信息也要输出
  //   IR
  //   rs2-used
  //   ecall
  //   rs1-used
  //   lb
  //   lui
  //   URET
  //   JALR
  //   JAL
  //   JAL
  //   Beq
  //   Beq
  //   Bne
  //   Bne
  //   MTR
  //   MW
  //   MW
  //   AluSrc
  //   AluSrcB
  //   RW
  //   bltu
  //   imm12
  //   imm12
  //   immj
  //   lui
  //   lb
  //   LUI
  //   URET
  //   MTR
  //   Rw
  //   s
  //   ecall
  //   r1
  //   r2
  //   r2
  //   flush
  //   result
  //   r2
  //   lui
  //   EX.RD
  //   EX.RW
  //   lb
  //   lui
  //   JALR
  //   JAL
  //   MTR
  //   MW
  //   RW
  //   lui
  //   MEM.rw
  //   MEM.rd
  //   数据存储器
  //   lb
  //   lb
  //   lui
  //   lui
  //   JALR
  //   JALR
  //   JAL
  //   JAL
  //   MTR
  //   MTR
  //   MTR
  //   MW
  //   MW
  //   RW
  //   RW
  //   halt
  //   halt
endmodule

module \重定向流水线  (
  output RegWrite,
  output MemWrite,
  output [31:0] IF_PC,
  output [31:0] ID_PC,
  output [31:0] EX_PC,
  output [31:0] M_PC,
  output [31:0] WB_PC,
  output [31:0] RDin,
  output [31:0] MDin,
  output [31:0] LedData
);

  wire Alu, AluEQ, and_1_out, and_2_out, and_3_out, and_4_out, and_5_out, and_6_out, and_7_out, and_8_out,
       and_9_out, and_10_out, and_11_out, and_12_out, and_13_out, and_14_out, bltu, Branchtaken, CLK,
       clock_1_out, clock_2_out, comparator_1_eq, comparator_2_eq, comparator_2_lt, comparator_3_gt,
       comparator_3_lt, d_ff_1_q, ecall, EX_ecall, EX_halt, exmem_1_out_19, exmem_1_out_20, exmem_1_out_21,
       exmem_1_out_22, exmem_1_out_23, exmem_1_out_26, exmem_1_out_27, Go, halt, id_ex_1_out_30,
       id_ex_1_out_31, id_ex_1_out_33, id_ex_1_out_34, id_ex_1_out_37, id_ex_1_out_38, id_ex_1_out_39,
       id_ex_1_out_40, id_ex_1_out_43, id_ex_1_out_45, id_ex_1_out_48, IR1, IR2, IR3, JAL, mem_wb_1_out_19,
       mem_wb_1_out_21, mem_wb_1_out_22, mem_wb_1_out_27, nand_1_out, not_1_out, not_2_out, not_4_out,
       not_5_out, not_6_out, not_7_out, not_8_out, not_9_out, not_10_out, or_1_out, or_3_out, or_4_out,
       or_5_out, rs1_used, rs2_used, RST, S, stall, tunnel, W1, W2, W3, \单周期硬布线控制器_1_alu_src ,
       \单周期硬布线控制器_1_beq , \单周期硬布线控制器_1_bne , \单周期硬布线控制器_1_jalr , \单周期硬布线控制器_1_lb , \单周期硬布线控制器_1_lui ,
       \单周期硬布线控制器_1_memtoreg , \单周期硬布线控制器_1_memwrite , \单周期硬布线控制器_1_regwrite , \单周期硬布线控制器_1_uret ,
       \重定向逻辑_1_flush ;
  wire [1:0] id_ex_1_out_53, id_ex_1_out_54, mem_wb_1_out_23, priority_encoder_1_out, \重定向逻辑_1_rs1forward ,
       \重定向逻辑_1_rs2forward ;
  wire [3:0] id_ex_1_out_47, \单周期硬布线控制器_1_alu_op ;
  wire [4:0] exmem_1_out_24, id_ex_1_out_49, multiplexer_2_out, multiplexer_3_out, WB_rd;
  wire [7:0] multiplexer_13_out;
  wire [12:0] CNT_num;
  wire [15:0] \LoadUse次数 , \总周期数 , \插入气泡数 , \无条件分支数 , \条件分支成功数 ;
  wire [31:0] adder_3_out, alu_1_result, bit_extender_1_out, bit_extender_2_out, bit_extender_3_out,
       bit_extender_4_out, Calcuresult, EX_IR, exmem_1_out_29, exmem_1_out_31, id_ex_1_out_32,
       id_ex_1_out_36, id_ex_1_out_41, id_ex_1_out_46, id_ex_1_out_50, ID_IR, IF_IR, jaddr, LBDout, MEM_IR,
       MEM_result, mem_wb_1_out_28, multiplexer_1_out, multiplexer_4_out, multiplexer_5_out,
       multiplexer_7_out, multiplexer_12_out, PC_4, r1, r2, ram_1_data, regifile_1_r1, regifile_1_r2,
       shifter_1_out, shifter_2_out, WB_Dout, WB_IR;

  Button \u_总复位  (.out(RST));
  Button _1 (.out(IR1));
  Button _2 (.out(IR2));
  Button _3 (.out(IR3));
  // Probe on \总周期数 
  // Probe on \总周期数 
  Button \u_继续运行  (.out(Go));
  LED #(.active("true")) led_1 (.in(W1));
  LED #(.active("true")) led_2 (.in(W2));
  LED #(.active("true")) led_3 (.in(W3));
  Hex_Digit_Display hex_digit_display_1 (.value(LedData[31:28]));  // open: dp
  // Probe on IF_PC[19:0]
  // RiscV_Probe riscv_probe_1: pin names not known; wires that end beside it: IF_IR
  Hex_Digit_Display hex_digit_display_2 (.value(LedData[23:20]));  // open: dp
  Hex_Digit_Display hex_digit_display_3 (.value(LedData[27:24]));  // open: dp
  // Probe on ID_PC[19:0]
  // RiscV_Probe riscv_probe_2: pin names not known; wires that end beside it: ID_IR
  not not_1 (not_1_out, halt);
  Hex_Digit_Display hex_digit_display_4 (.value(LedData[15:12]));  // open: dp
  Hex_Digit_Display hex_digit_display_5 (.value(LedData[19:16]));  // open: dp
  Counter #(.width(16), .max('hffff), .ongoal("wrap"), .trigger("rising"), .behavior("new")) counter_1 (
    .count(not_1_out), .Q(\总周期数 ), .clk(CLK));  // open: load, D, carry, clr, preset, down
  Hex_Digit_Display hex_digit_display_6 (.value(LedData[7:4]));  // open: dp
  Hex_Digit_Display hex_digit_display_7 (.value(LedData[11:8]));  // open: dp
  Clock #(.highDuration(1), .lowDuration(1)) clock_1 (.out(clock_1_out));
  // Probe on EX_PC[19:0]
  // RiscV_Probe riscv_probe_3: pin names not known; wires that end beside it: clock_1_out, EX_IR, CLK
  Multiplexer #(.select(2), .width(32), .disabled("Z"), .enable("false")) multiplexer_1 (
    .in0(PC_4), .in1(jaddr), .in2(Calcuresult), .out(multiplexer_1_out), .sel(priority_encoder_1_out));  // open: in3
  Hex_Digit_Display hex_digit_display_8 (.value(LedData[3:0]));  // open: dp
  and and_1 (and_1_out, ~stall, ~halt);  // AND_Gate
  // Probe on \总周期数 
  // Probe on M_PC[19:0]
  // RiscV_Probe riscv_probe_4: pin names not known; wires that end beside it: MEM_IR
  Register #(.width(32), .trigger("rising"), .Select("low")) PC (
    .D(multiplexer_1_out), .en(and_1_out), .Q(IF_PC), .clk(CLK), .clr(RST));
  // Probe on \总周期数 
  // Probe on \无条件分支数 
  // Probe on \条件分支成功数 
  // Probe on \插入气泡数 
  // Probe on \LoadUse次数 
  Adder #(.width(32)) adder_1 (.a(IF_PC), .b(32'h4), .out(PC_4));  // open: cin, cout
  // Probe on IF_PC[11:0]
  // Probe on WB_PC[19:0]
  // RiscV_Probe riscv_probe_5: pin names not known; wires that end beside it: WB_IR
  ROM #(.addrWidth(10), .dataWidth(32), .Select("high")) rom_1 (.addr(IF_PC[11:2]), .data(IF_IR));
  // Probe on EX_PC[11:0]
  // Probe on ID_PC[11:0]
  not not_2 (not_2_out, halt);
  // RiscV_Probe riscv_probe_6: pin names not known; wires that end beside it: IF_IR
  // Probe on M_PC[11:0]
  D_Flip_Flop #(.trigger("high"), .Pre_Clr_Positions("LEGACY"), .NegatePresetClear("false"), .enable("true"), .NewFFLayout("false")) d_ff_1 (.Q(d_ff_1_q));  // open: clk, D, Qn, preset, en, reset
  // Probe on 13'hc
  and and_2 (and_2_out, not_2_out, stall);
  Comparator #(.width(32), .mode("twosComplement")) comparator_1 (
    .a({32{1'b0}}), .b(ID_IR), .eq(comparator_1_eq));  // open: gt, lt
  not not_3 (tunnel, comparator_1_eq);
  and and_3 (and_3_out, ~stall, ~halt);  // AND_Gate
  // Probe on WB_PC[11:0]
  Comparator #(.width(13), .mode("twosComplement")) comparator_2 (
    .a(CNT_num), .b(13'hc), .eq(comparator_2_eq), .lt(comparator_2_lt));  // open: gt
  Clock #(.highDuration(1), .lowDuration(1)) clock_2 (.out(clock_2_out));
  Counter #(.width(16), .max('hffff), .ongoal("wrap"), .trigger("rising"), .behavior("new")) counter_2 (
    .count(and_2_out), .Q(\LoadUse次数 ), .clk(CLK));  // open: load, D, carry, clr, preset, down
  IF_ID if_id_1 (
    .PC(IF_PC), .PC_2(ID_PC), .IR(IF_IR), .IR_2(ID_IR), .CLK(CLK), .e(and_3_out), .reset(RST),
    .bt(Branchtaken));
  nand nand_1 (nand_1_out, d_ff_1_q, comparator_2_eq);
  Counter #(.width(13), .max('h1fff), .ongoal("stay"), .trigger("rising"), .behavior("old")) counter_3 (
    .count(comparator_2_lt), .Q(CNT_num), .clk(clock_2_out));  // open: load, D, carry, clr, preset
  not not_4 (not_4_out, halt);
  and and_4 (and_4_out, not_4_out, or_1_out);
  and and_5 (and_5_out, tunnel, \单周期硬布线控制器_1_lb );
  assign CLK = nand_1_out ? clock_2_out : 1'bz;  // Controlled_Buffer controlled_buffer_1
  Counter #(.width(16), .max('hffff), .ongoal("wrap"), .trigger("rising"), .behavior("new")) counter_4 (
    .count(and_4_out), .Q(\无条件分支数 ), .clk(CLK));  // open: load, D, carry, clr, preset, down
  Pull_Resistor #(.pull(1)) pull_resistor_1 (.node(CLK));
  \单周期硬布线控制器  \u_单周期硬布线控制器_1  (
    .Funct({ID_IR[30], ID_IR[25], ID_IR[14:12]}), .OP(ID_IR[6:2]), .ALU_OP(\单周期硬布线控制器_1_alu_op ),
    .MemToReg(\单周期硬布线控制器_1_memtoreg ), .MemWrite(\单周期硬布线控制器_1_memwrite ), .ALU_SRC(\单周期硬布线控制器_1_alu_src ),
    .RegWrite(\单周期硬布线控制器_1_regwrite ), .ecall(ecall), .S_type(S), .Jalr(\单周期硬布线控制器_1_jalr ),
    .Beq(\单周期硬布线控制器_1_beq ), .JAL(JAL), .Bne(\单周期硬布线控制器_1_bne ), .in_3(ID_IR[21]), .uret(\单周期硬布线控制器_1_uret ),
    .LUI(\单周期硬布线控制器_1_lui ), .lb(\单周期硬布线控制器_1_lb ), .bltu(bltu), .re2_used(rs2_used), .rs1_used(rs1_used));  // open: CSRRSI, CSRRCI, BGE, U_type
  Multiplexer #(.select(1), .width(5), .disabled("Z"), .enable("false")) multiplexer_2 (
    .in0(ID_IR[19:15]), .in1(5'b10001), .out(multiplexer_2_out), .sel(ecall));
  Multiplexer #(.select(1), .width(5), .disabled("Z"), .enable("false")) multiplexer_3 (
    .in0(ID_IR[24:20]), .in1(5'b01010), .out(multiplexer_3_out), .sel(ecall));
  and and_6 (and_6_out, tunnel, \单周期硬布线控制器_1_memtoreg );
  assign bit_extender_1_out = {{20{ID_IR[31]}}, ID_IR[31:20]};  // Bit_Extender bit_extender_1
  assign bit_extender_2_out = {{20{ID_IR[31]}}, {ID_IR[31:25], ID_IR[11:7]}};  // Bit_Extender bit_extender_2
  assign bit_extender_3_out = {{20{ID_IR[31]}}, {ID_IR[31], ID_IR[7], ID_IR[30:25], ID_IR[11:8]}};  // Bit_Extender bit_extender_3
  assign bit_extender_4_out = {{12{ID_IR[31]}}, {ID_IR[31], ID_IR[19:12], ID_IR[20], ID_IR[30:21]}};  // Bit_Extender bit_extender_4
  not not_5 (not_5_out, CLK);
  Regifile regifile_1 (
    .Din(RDin), .Clk(not_5_out), .R1(regifile_1_r1), .R2(regifile_1_r2), .WE(RegWrite), .W_num(WB_rd),
    .R1_num(multiplexer_2_out), .R2_num(multiplexer_3_out));
  Multiplexer #(.select(1), .width(32), .disabled("Z"), .enable("false")) multiplexer_4 (
    .in0(bit_extender_3_out), .in1(bit_extender_4_out), .out(multiplexer_4_out), .sel(JAL));
  or or_1 (or_1_out, id_ex_1_out_38, id_ex_1_out_40);
  and and_7 (and_7_out, tunnel, \单周期硬布线控制器_1_alu_src );
  Multiplexer #(.select(1), .width(32), .disabled("Z"), .enable("false")) multiplexer_5 (
    .in0(bit_extender_1_out), .in1(bit_extender_2_out), .out(multiplexer_5_out), .sel(S));
  Shifter #(.width(32), .shift("ll")) shifter_1 (.in(multiplexer_4_out), .\dist (5'b00001), .out(shifter_1_out));
  \重定向逻辑  \u_重定向逻辑_1  (
    .IR(ID_IR), .BranchTaken(Branchtaken), .ecall(ecall), .EX_rw(id_ex_1_out_37), .MEM_rw(exmem_1_out_26),
    .EX_rd(id_ex_1_out_49), .MEM_rd(exmem_1_out_24), .rs1_used(rs1_used), .rs2_used(rs2_used),
    .EX_MTR(id_ex_1_out_48), .stall(stall), .flush(\重定向逻辑_1_flush ), .rs1forward(\重定向逻辑_1_rs1forward ),
    .rs2forward(\重定向逻辑_1_rs2forward ));
  and and_8 (and_8_out, tunnel, \单周期硬布线控制器_1_regwrite );
  ID_EX id_ex_1 (
    .in_1(and_5_out), .PC(ID_PC), .PC_2(EX_PC), .IR(ID_IR), .IR_2(EX_IR), .CLK(CLK), .e(not_6_out),
    .reset(RST), .flush(\重定向逻辑_1_flush ), .out_30(id_ex_1_out_30), .in_4(\单周期硬布线控制器_1_lui ),
    .out_33(id_ex_1_out_33), .in_6(\单周期硬布线控制器_1_uret ), .in_9(\单周期硬布线控制器_1_jalr ), .out_38(id_ex_1_out_38),
    .in_11(JAL), .out_40(id_ex_1_out_40), .in_14(\单周期硬布线控制器_1_beq ), .out_43(id_ex_1_out_43),
    .in_16(\单周期硬布线控制器_1_bne ), .out_45(id_ex_1_out_45), .in_19(and_6_out), .out_48(id_ex_1_out_48),
    .in_2(\单周期硬布线控制器_1_memwrite ), .out_31(id_ex_1_out_31), .in_5(and_7_out), .out_34(id_ex_1_out_34),
    .in_8(and_8_out), .out_37(id_ex_1_out_37), .in_10(bltu), .out_39(id_ex_1_out_39), .in_13(S),
    .in_15(ecall), .out_44(EX_ecall), .op(\单周期硬布线控制器_1_alu_op ), .out_47(id_ex_1_out_47), .rd(ID_IR[11:7]),
    .out_49(id_ex_1_out_49), .out_36(id_ex_1_out_36), .in_7(regifile_1_r2), .in_3(regifile_1_r1),
    .out_32(id_ex_1_out_32), .in_12(multiplexer_5_out), .out_41(id_ex_1_out_41), .in_17(shifter_1_out),
    .out_46(id_ex_1_out_46), .in_21({ID_IR[31:12], {12{1'b0}}}), .out_50(id_ex_1_out_50),
    .in_28(\重定向逻辑_1_rs1forward ), .out_53(id_ex_1_out_53), .in_29(\重定向逻辑_1_rs2forward ),
    .out_54(id_ex_1_out_54));  // open: out_35, out_42
  not not_6 (not_6_out, halt);
  Priority_Encoder #(.select(2), .disabled("Z")) priority_encoder_1 (
    .in0(1'b1), .in1(or_3_out), .in2(id_ex_1_out_38), .out(priority_encoder_1_out));  // open: in3, gs, en_out, en_in
  Multiplexer #(.select(2), .width(32), .disabled("Z"), .enable("false")) multiplexer_6 (
    .in0(id_ex_1_out_36), .in1(RDin), .in2(MEM_result), .out(r2), .sel(id_ex_1_out_54));  // open: in3
  or or_2 (Branchtaken, id_ex_1_out_38, or_3_out);
  Multiplexer #(.select(1), .width(32), .disabled("Z"), .enable("false")) multiplexer_7 (
    .in0(r2), .in1(id_ex_1_out_41), .out(multiplexer_7_out), .sel(id_ex_1_out_34));
  Adder #(.width(32)) adder_2 (.a(id_ex_1_out_46), .b(EX_PC), .out(jaddr));  // open: cin, cout
  or or_3 (or_3_out, and_9_out, and_10_out, and_11_out, id_ex_1_out_40);
  ALU alu_1 (
    .X(r1), .Y(multiplexer_7_out), .AluOP(id_ex_1_out_47), .Equal(AluEQ), .Result(alu_1_result), .out_6(Alu));  // open: Result_2, out_4
  Comparator #(.width(32), .mode("twosComplement")) comparator_3 (
    .a(r1), .b(32'h22), .gt(comparator_3_gt), .lt(comparator_3_lt));  // open: eq
  Multiplexer #(.select(2), .width(32), .disabled("Z"), .enable("false")) multiplexer_8 (
    .in0(id_ex_1_out_32), .in1(RDin), .in2(MEM_result), .out(r1), .sel(id_ex_1_out_53));  // open: in3
  and and_9 (and_9_out, id_ex_1_out_45, ~AluEQ);  // AND_Gate
  and and_10 (and_10_out, AluEQ, id_ex_1_out_43);
  and and_11 (and_11_out, Alu, id_ex_1_out_39);
  or or_4 (or_4_out, comparator_3_gt, comparator_3_lt);
  not not_7 (not_7_out, or_4_out);
  Multiplexer #(.select(1), .width(32), .disabled("Z"), .enable("false")) multiplexer_9 (
    .in0(alu_1_result), .in1(id_ex_1_out_50), .out(Calcuresult), .sel(id_ex_1_out_33));
  and and_12 (and_12_out, EX_ecall, or_4_out);
  and and_13 (and_13_out, not_7_out, EX_ecall);
  not not_8 (not_8_out, halt);
  D_Flip_Flop #(.trigger("falling"), .Pre_Clr_Positions("ABOVE_BELOW"), .NegatePresetClear("false"), .enable("true"), .NewFFLayout("true")) d_ff_2 (
    .clk(CLK), .D(1'b1), .Q(EX_halt), .en(and_12_out), .reset(Go));  // open: Qn, preset
  Register #(.width(32), .trigger("rising"), .Select("low")) register_1 (
    .D(r2), .en(and_13_out), .Q(LedData), .clk(CLK));  // open: clr
  or or_5 (or_5_out, and_9_out, and_10_out, and_11_out);
  EXMEM exmem_1 (
    .in_1(id_ex_1_out_30), .in_2(id_ex_1_out_33), .in_3(id_ex_1_out_38), .in_4(id_ex_1_out_40),
    .in_5(id_ex_1_out_48), .rd(id_ex_1_out_49), .in_7(id_ex_1_out_31), .in_8(id_ex_1_out_37), .in_9(EX_halt),
    .PC(EX_PC), .IR(EX_IR), .out_19(exmem_1_out_19), .out_20(exmem_1_out_20), .out_21(exmem_1_out_21),
    .out_22(exmem_1_out_22), .out_23(exmem_1_out_23), .out_24(exmem_1_out_24), .out_25(MemWrite),
    .out_26(exmem_1_out_26), .out_27(exmem_1_out_27), .out_28(MEM_result), .out_29(exmem_1_out_29),
    .PC_2(M_PC), .out_31(exmem_1_out_31), .IR_2(MEM_IR), .in_13(id_ex_1_out_50), .in_10(Calcuresult),
    .in_11(r2), .reset(RST), .bt(RST), .e(not_8_out), .CLK(CLK));
  Multiplexer #(.select(1), .width(32), .disabled("Z"), .enable("false")) multiplexer_10 (
    .in0(exmem_1_out_29), .in1(shifter_2_out), .out(MDin), .sel(MEM_result[1]));
  Shifter #(.width(32), .shift("ll")) shifter_2 (.in(exmem_1_out_29), .\dist (5'b10000), .out(shifter_2_out));
  not not_9 (not_9_out, halt);
  and and_14 (and_14_out, not_9_out, or_5_out);
  RAM #(.addrWidth(10), .dataWidth(32), .bus("separate"), .Select("high")) ram_1 (
    .addr(MEM_result[11:2]), .din(MDin), .data(ram_1_data), .str(MemWrite), .sel(1'b1), .clk(CLK), .ld(1'b1),
    .clr(RST));
  not not_10 (not_10_out, halt);
  Counter #(.width(16), .max('hffff), .ongoal("wrap"), .trigger("rising"), .behavior("new")) counter_5 (
    .count(and_14_out), .Q(\条件分支成功数 ), .clk(CLK));  // open: load, D, carry, clr, preset, down
  or or_6 (mem_wb_1_out_23[1], mem_wb_1_out_21, mem_wb_1_out_22);
  MEM_WB mem_wb_1 (
    .in_1(exmem_1_out_19), .in_2(exmem_1_out_20), .in_3(exmem_1_out_21), .in_4(exmem_1_out_22),
    .in_5(exmem_1_out_23), .rd(exmem_1_out_24), .in_7(MemWrite), .in_8(exmem_1_out_26),
    .in_9(exmem_1_out_27), .PC(M_PC), .IR(MEM_IR), .out_19(mem_wb_1_out_19), .out_21(mem_wb_1_out_21),
    .out_22(mem_wb_1_out_22), .out_23(mem_wb_1_out_23[0]), .out_24(WB_rd), .out_26(RegWrite),
    .out_27(mem_wb_1_out_27), .out_28(mem_wb_1_out_28), .out_29(WB_Dout), .PC_2(WB_PC), .IR_2(WB_IR),
    .in_13(exmem_1_out_31), .in_10(MEM_result), .in_11(ram_1_data), .reset(RST), .bt(RST), .e(not_10_out),
    .CLK(CLK));  // open: out_20, out_25, out_31
  Adder #(.width(32)) adder_3 (.a(WB_PC), .b(32'h4), .out(adder_3_out));  // open: cin, cout
  Multiplexer #(.select(2), .width(32), .disabled("Z"), .enable("false")) multiplexer_11 (
    .in0(mem_wb_1_out_28), .in1(multiplexer_12_out), .in2(adder_3_out), .out(RDin), .sel(mem_wb_1_out_23));  // open: in3
  D_Flip_Flop #(.trigger("rising"), .Pre_Clr_Positions("ABOVE_BELOW"), .NegatePresetClear("false"), .enable("true"), .NewFFLayout("true")) d_ff_3 (
    .clk(mem_wb_1_out_27), .D(1'b1), .Q(halt), .en(1'b1), .reset(Go));  // open: Qn, preset
  Multiplexer #(.select(1), .width(32), .disabled("Z"), .enable("false")) multiplexer_12 (
    .in0(WB_Dout), .in1(LBDout), .out(multiplexer_12_out), .sel(mem_wb_1_out_19));
  Multiplexer #(.select(2), .width(8), .disabled("Z"), .enable("false")) multiplexer_13 (
    .in0(WB_Dout[7:0]), .in1(WB_Dout[15:8]), .in2(WB_Dout[23:16]), .in3(WB_Dout[31:24]),
    .out(multiplexer_13_out), .sel(mem_wb_1_out_28[1:0]));
  assign LBDout = {{24{multiplexer_13_out[7]}}, multiplexer_13_out};  // Bit_Extender bit_extender_5

  // Other names for the same wires on the sheet: rd[4:0] = ID_IR[11:7]; IR[31:0] = IF_IR; MEM_PC[31:0] = M_PC;
  //   PC[31:0] = IF_PC

  // Notes on the sheet:
  //   中断源
  //   时空图监测，可删除
  //   中断等待指示
  //   数码管输出
  //   指令存储器
  //   contents of rom_1 (hex, n*v repeats v):
  //   100493 100006f 100493 200913 300993 100006f 100493 200913 300993 100006f 100493 200913 300993
  //   100006f 100493 200913 300993 3f0000ef 100413 100493 1f49493 900533 2200893 73 24d493 48463 fedff06f
  //   900533 2200893 73 100493 249493 900533 2200893 73 48463 fedff06f 100493 1f49493 900533 2200893 73
  //   4034d493 900533 2200893 73 4044d493 900533 2200893 73 4044d493 900533 2200893 73 4044d493 900533
  //   2200893 73 4044d493 900533 2200893 73 4044d493 900533 2200893 73 4044d493 900533 2200893 73 4044d493
  //   900533 2200893 73 100413 1f41993 41f9d993 433 c00913 300b13 140413 f47413 800293 100313 499993
  //   89e9b3 1300533 2200893 73 406282b3 fe0294e3 140413 f00f93 1f47433 1c41413 800293 100313 49d993
  //   89e9b3 1300533 2200893 73 406282b3 fe0294e3 1c45413 406b0b33 b0463 f95ff06f 2b3 fff2c293 829293
  //   ff2e293 500533 2200893 73 fff00413 493 84a023 140413 448493 84a023 140413 448493 84a023 140413
  //   448493 84a023 140413 448493 84a023 140413 448493 84a023 140413 448493 84a023 140413 448493 84a023
  //   140413 448493 84a023 140413 448493 84a023 140413 448493 84a023 140413 448493 84a023 140413 448493
  //   84a023 140413 448493 84a023 140413 448493 84a023 140413 448493 84a023 140413 448493 140413 433
  //   3c00493 42983 4aa03 149a2b3 28663 134a023 1442023 ffc48493 fe9412e3 800533 2200893 73 440413 3c00493
  //   fc9416e3 3200893 73 100293 300313 800493 849493 7648493 1449493 900533 2200893 73 800e13 4054d4b3
  //   4064d4b3 900533 2200893 73 fffe0e13 fe0e14e3 a00893 73 800e13 fedc04b7 fff00413 1045413 84e4b3
  //   900533 2200893 73 ba984b7 900533 73 76544b7 900533 73 32104b7 900533 73 fffe0e13 fa0e1ee3 a00893 73
  //   313 1000e13 8400493 849493 8348493 400913 891913 490913 849493 8248493 849493 8148493 891913 490913
  //   891913 490913 932023 12484b3 430313 fffe0e13 fe0e18e3 2000e13 313 30483 900533 2200893 73 130313
  //   fffe0e13 fe0e14e3 a00893 73 ff100493 900533 2200893 73 148493 fe9068e3 900533 2200893 73 a00893 73
  //   a00893 73 413 140413 800533 2200893 73 240413 800533 2200893 73 340413 800533 2200893 73 440413
  //   800533 2200893 73 540413 800533 2200893 73 640413 800533 2200893 73 740413 800533 2200893 73 840413
  //   800533 2200893 2200893 73 8067
  //   控制位
  //   指令探针
  //   流水调试日志用
  //   暂停节拍，不能为0
  //   戳工具置1进入计数暂停模式，ctrl+k时钟自动运行到对应节拍暂停
  //   ctrl+k关闭时钟连续运行，将控制位置零，进入单步调试模式调试
  //   指令字
  //   可计数暂停的时钟源
  //   JAL
  //   JALR
  //   URET
  //   LUI
  //   lb
  //   Beq
  //   Bne
  //   MemToReg
  //   MemWrite
  //   AluOP
  //   AluSrcB
  //   RegWrite
  //   bltu
  //   S_type
  //   LUI
  //   为方便自动评测，需要输出流水线各段保存的PC值，注意是PC不是PC+4，另外ID段寄存器写入信息，Mem段内存写入信息也要输出
  //   stall
  //   IR
  //   lb
  //   lui
  //   URET
  //   JALR
  //   JAL
  //   JAL
  //   Beq
  //   Beq
  //   Bne
  //   Bne
  //   MTR
  //   MW
  //   MW
  //   AluSrc
  //   AluSrcB
  //   RW
  //   bltu
  //   imm12
  //   imm12
  //   immj
  //   lui
  //   rs1-used
  //   ecall
  //   lb
  //   LUI
  //   URET
  //   MTR
  //   Rw
  //   s
  //   ecall
  //   r1
  //   r2
  //   r2
  //   rs2-used
  //   flush
  //   result
  //   r2
  //   lui
  //   EX.RD
  //   EX.RW
  //   lb
  //   lui
  //   JALR
  //   JAL
  //   MTR
  //   MW
  //   RW
  //   lui
  //   MEM.rw
  //   MEM.rd
  //   数据存储器
  //   lb
  //   lb
  //   lui
  //   lui
  //   JALR
  //   JALR
  //   JAL
  //   JAL
  //   MTR
  //   MTR
  //   MTR
  //   MW
  //   MW
  //   RW
  //   RW
  //   halt
  //   halt
endmodule

module \中断按键参考电路  (
  input  \同步清零信号 ,
  output \与中断屏蔽位与 
);

  wire \_1号中断_out , and_1_out, clock_1_out, d_ff_1_q, or_1_out, or_2_out;

  Clock #(.highDuration(1), .lowDuration(1)) clock_1 (.out(clock_1_out));
  Button \_1号中断  (.out(\_1号中断_out ));
  or or_1 (or_1_out, \与中断屏蔽位与 , d_ff_1_q);
  LED #(.active("true")) \_1号中断等待指示灯  (.in(or_1_out));
  D_Flip_Flop #(.trigger("rising"), .Pre_Clr_Positions("LEGACY"), .NegatePresetClear("false"), .enable("true"), .NewFFLayout("false")) d_ff_1 (
    .clk(\_1号中断_out ), .D(1'b1), .Q(d_ff_1_q), .reset(\与中断屏蔽位与 ));  // open: Qn, preset, en
  or or_2 (or_2_out, d_ff_1_q, \与中断屏蔽位与 );
  and and_1 (and_1_out, or_2_out, ~\同步清零信号 );  // AND_Gate
  D_Flip_Flop #(.trigger("rising"), .Pre_Clr_Positions("LEGACY"), .NegatePresetClear("false"), .enable("true"), .NewFFLayout("false")) IR1 (
    .clk(clock_1_out), .D(and_1_out), .Q(\与中断屏蔽位与 ));  // open: Qn, preset, en, reset

  // Notes on the sheet:
  //   中断信号采样参考电路
  //   Reset 
endmodule

module \单周期_多级中断  (
  input  IR1,
  input  IR2,
  input  IR3,
  output RegWrite,
  output MemWrite,
  output [31:0] PC,
  output [31:0] IR,
  output [31:0] RDin,
  output [31:0] MDin,
  output [31:0] LedData
);

  wire Alu, AluEQ, AluSrcB, and_1_out, and_2_out, and_3_out, and_4_out, and_5_out, and_6_out, and_7_out,
       and_8_out, and_9_out, and_10_out, and_11_out, and_13_out, and_14_out, and_15_out, Beq, bltu, Bne, CLK,
       CLR1, CLR2, CLR3, comparator_1_eq, comparator_2_eq, comparator_3_eq, comparator_4_eq, comparator_5_eq,
       comparator_6_eq, CSRRCI, CSRRSI, d_ff_1_q, d_ff_2_q, d_ff_5_q, d_ff_6_q, d_ff_7_q, d_ff_8_q, d_ff_9_q,
       d_ff_10_q, decoder_1_out1, decoder_1_out2, decoder_1_out3, decoder_2_out1, decoder_2_out2,
       decoder_2_out3, ecall, ENINT, Go, halt, INTR, IR1_t, IR2_t, IR3_t, IRA, IRB, IRC, JAL, JALR, lb, LUI,
       MemToReg, not_1_out, not_2_out, not_3_out, not_4_out, not_5_out, or_1_out, or_2_out, or_5_out,
       or_7_out, or_8_out, or_9_out, or_10_out, or_15_out, or_16_out, or_17_out, register_1_q, register_2_q,
       register_3_q, RST, S, URET, W1, W2, W3, \中断请求 , \高级中断请求 ;
  wire [1:0] INT_N, INT_N_prime, priority_encoder_1_out;
  wire [1:1] or_11_out;
  wire [3:0] AluOP;
  wire [4:0] multiplexer_6_out, multiplexer_7_out;
  wire [7:0] multiplexer_14_out;
  wire [15:0] \总周期数 ;
  wire [31:0] adder_2_out, adder_3_out, bit_extender_1_out, bit_extender_2_out, bit_extender_3_out,
       bit_extender_4_out, Calcuresult, Dout, INT_PC, LBDout, mEPC_2_q, mEPC_3_q, mEPC_q, multiplexer_3_out,
       multiplexer_8_out, multiplexer_9_out, multiplexer_10_out, multiplexer_11_out, multiplexer_12_out,
       NEWPC, PC_4, regifile_1_r1, shifter_1_out, shifter_2_out, shifter_3_out, \断点地址 , \返回地址 ;

  Clock #(.highDuration(1), .lowDuration(1)) clock_1 (.out(CLK));
  Button _1 ();  // open: out
  Button _2 ();  // open: out
  Button _3 ();  // open: out
  Button \u_继续运行  (.out(Go));
  LED #(.active("true")) led_1 (.in(W1));
  LED #(.active("true")) led_2 (.in(W2));
  LED #(.active("true")) led_3 (.in(W3));
  Decoder #(.select(2), .tristate("false"), .disabled(0), .enable("false")) decoder_1 (
    .out1(decoder_1_out1), .out2(decoder_1_out2), .out3(decoder_1_out3), .sel(INT_N));  // open: out0
  Hex_Digit_Display hex_digit_display_1 (.value(LedData[31:28]));  // open: dp
  Comparator #(.width(16), .mode("twosComplement")) comparator_1 (
    .a(\总周期数 ), .b(16'h7), .eq(comparator_1_eq));  // open: gt, lt
  Comparator #(.width(16), .mode("twosComplement")) comparator_2 (
    .a(\总周期数 ), .b(16'h241), .eq(comparator_2_eq));  // open: gt, lt
  Hex_Digit_Display hex_digit_display_2 (.value(LedData[23:20]));  // open: dp
  Hex_Digit_Display hex_digit_display_3 (.value(LedData[27:24]));  // open: dp
  Comparator #(.width(16), .mode("twosComplement")) comparator_3 (
    .a(16'h258), .b(\总周期数 ), .eq(comparator_3_eq));  // open: gt, lt
  or or_1 (or_1_out, comparator_3_eq, comparator_4_eq);
  Comparator #(.width(16), .mode("twosComplement")) comparator_4 (
    .a(\总周期数 ), .b(16'h1), .eq(comparator_4_eq));  // open: gt, lt
  Comparator #(.width(16), .mode("twosComplement")) comparator_5 (
    .a(\总周期数 ), .b(16'h4), .eq(comparator_5_eq));  // open: gt, lt
  or or_2 (or_2_out, comparator_1_eq, comparator_2_eq);
  and and_1 (and_1_out, decoder_1_out1, \高级中断请求 );
  and and_2 (and_2_out, decoder_1_out2, \高级中断请求 );
  and and_3 (and_3_out, decoder_1_out3, \高级中断请求 );
  Hex_Digit_Display hex_digit_display_4 (.value(LedData[15:12]));  // open: dp
  Hex_Digit_Display hex_digit_display_5 (.value(LedData[19:16]));  // open: dp
  Pull_Resistor #(.pull(0)) pull_resistor_1 (.node(IRA));
  assign IRA = or_1_out ? ~CLK : 1'bz;  // Controlled_Inverter controlled_inverter_1
  Pull_Resistor #(.pull(0)) pull_resistor_2 (.node(IRB));
  assign IRB = comparator_5_eq ? ~CLK : 1'bz;  // Controlled_Inverter controlled_inverter_2
  Pull_Resistor #(.pull(0)) pull_resistor_3 (.node(IRC));
  assign IRC = or_2_out ? ~CLK : 1'bz;  // Controlled_Inverter controlled_inverter_3
  Hex_Digit_Display hex_digit_display_6 (.value(LedData[11:8]));  // open: dp
  Hex_Digit_Display hex_digit_display_7 (.value(LedData[7:4]));  // open: dp
  // Probe on \总周期数 
  Hex_Digit_Display hex_digit_display_8 (.value(LedData[3:0]));  // open: dp
  Register #(.width(32), .trigger("rising"), .Select("low")) mEPC (
    .D(\断点地址 ), .en(and_1_out), .Q(mEPC_q), .clk(CLK));  // open: clr
  Register #(.width(32), .trigger("rising"), .Select("low")) mEPC_2 (
    .D(\断点地址 ), .en(and_2_out), .Q(mEPC_2_q), .clk(CLK));  // open: clr
  Register #(.width(32), .trigger("rising"), .Select("low")) mEPC_3 (
    .D(\断点地址 ), .en(and_3_out), .Q(mEPC_3_q), .clk(CLK));  // open: clr
  or or_3 (IR1_t, IR1, IRA);
  Multiplexer #(.select(2), .width(32), .disabled("Z"), .enable("false")) multiplexer_1 (
    .in1(mEPC_q), .in2(mEPC_2_q), .in3(mEPC_3_q), .out(\返回地址 ), .sel(INT_N_prime));  // open: in0
  or or_4 (IR2_t, IR2, IRB);
  Decoder #(.select(2), .tristate("false"), .disabled(0), .enable("false")) decoder_2 (
    .out1(decoder_2_out1), .out2(decoder_2_out2), .out3(decoder_2_out3), .sel(INT_N));  // open: out0
  or or_5 (or_5_out, \中断请求 , URET);
  or or_6 (IR3_t, IR3, IRC);
  Priority_Encoder #(.select(2), .disabled("Z")) priority_encoder_1 (
    .in0(1'b1), .in1(JALR), .in2(JAL), .in3(or_7_out), .out(priority_encoder_1_out));  // open: gs, en_out, en_in
  or or_7 (or_7_out, or_8_out, and_4_out);
  Multiplexer #(.select(2), .width(32), .disabled("Z"), .enable("false")) multiplexer_2 (
    .in0(PC_4), .in1(Calcuresult), .in2(adder_3_out), .in3(adder_2_out), .out(\断点地址 ),
    .sel(priority_encoder_1_out));
  not not_1 (not_1_out, halt);
  not not_2 (not_2_out, halt);
  or or_8 (or_8_out, and_8_out, and_9_out);
  and and_4 (and_4_out, Alu, bltu);
  Multiplexer #(.select(1), .width(32), .disabled("Z"), .enable("false")) multiplexer_3 (
    .in0(NEWPC), .in1(INT_PC), .out(multiplexer_3_out), .sel(\中断请求 ));
  Register #(.width(32), .trigger("rising"), .Select("low")) u_PC (
    .D(multiplexer_3_out), .en(not_1_out), .Q(PC), .clk(CLK), .clr(RST));
  Adder #(.width(32)) adder_1 (.a(PC), .b(32'h4), .out(PC_4));  // open: cin, cout
  Counter #(.width(16), .max('hffff), .ongoal("wrap"), .trigger("rising"), .behavior("new")) counter_1 (
    .count(not_2_out), .Q(\总周期数 ), .clk(CLK));  // open: load, D, carry, clr, preset, down
  and and_5 (and_5_out, or_5_out, decoder_2_out1);
  and and_6 (and_6_out, or_5_out, decoder_2_out2);
  and and_7 (and_7_out, or_5_out, decoder_2_out3);
  and and_8 (and_8_out, Beq, AluEQ);
  and and_9 (and_9_out, ~AluEQ, Bne);  // AND_Gate
  Multiplexer #(.select(1), .width(32), .disabled("Z"), .enable("false")) multiplexer_4 (
    .in0(\断点地址 ), .in1(\返回地址 ), .out(NEWPC), .sel(URET));
  Multiplexer #(.select(2), .width(32), .disabled("Z"), .enable("false")) multiplexer_5 (
    .in1(32'h30ac), .in2(32'h3158), .in3(32'h3204), .out(INT_PC), .sel(INT_N));  // open: in0
  // RiscV_Probe riscv_probe_1: pin names not known; wires that end beside it: IR
  Register #(.width(1), .trigger("rising"), .Select("low")) register_1 (
    .D(not_3_out), .en(and_5_out), .Q(register_1_q), .clk(CLK));  // open: clr
  not not_3 (not_3_out, CLR1);
  not not_4 (not_4_out, CLR2);
  Register #(.width(1), .trigger("rising"), .Select("low")) register_2 (
    .D(not_4_out), .en(and_6_out), .Q(register_2_q), .clk(CLK));  // open: clr
  not not_5 (not_5_out, CLR3);
  Register #(.width(1), .trigger("rising"), .Select("low")) register_3 (
    .D(not_5_out), .en(and_7_out), .Q(register_3_q), .clk(CLK));  // open: clr
  ROM #(.addrWidth(10), .dataWidth(32), .Select("high")) rom_1 (.addr(PC[11:2]), .data(IR));
  Priority_Encoder #(.select(2), .disabled("Z")) priority_encoder_2 (
    .in0(1'b1), .in1(register_1_q), .in2(register_2_q), .in3(register_3_q), .out(INT_N_prime));  // open: gs, en_out, en_in
  \单周期硬布线控制器  \u_单周期硬布线控制器_1  (
    .Funct({IR[30], IR[25], IR[14:12]}), .OP(IR[6:2]), .ALU_OP(AluOP), .MemToReg(MemToReg),
    .MemWrite(MemWrite), .ALU_SRC(AluSrcB), .RegWrite(RegWrite), .ecall(ecall), .S_type(S), .Jalr(JALR),
    .Beq(Beq), .JAL(JAL), .Bne(Bne), .in_3(IR[21]), .uret(URET), .LUI(LUI), .lb(lb), .bltu(bltu),
    .CSRRSI(CSRRSI), .CSRRCI(CSRRCI));  // open: re2_used, rs1_used, BGE, U_type
  Multiplexer #(.select(1), .width(5), .disabled("Z"), .enable("false")) multiplexer_6 (
    .in0(IR[19:15]), .in1(5'b10001), .out(multiplexer_6_out), .sel(ecall));
  Multiplexer #(.select(1), .width(5), .disabled("Z"), .enable("false")) multiplexer_7 (
    .in0(IR[24:20]), .in1(5'b01010), .out(multiplexer_7_out), .sel(ecall));
  assign bit_extender_1_out = {{20{IR[31]}}, IR[31:20]};  // Bit_Extender bit_extender_1
  assign bit_extender_2_out = {{20{IR[31]}}, {IR[31:25], IR[11:7]}};  // Bit_Extender bit_extender_2
  assign bit_extender_3_out = {{20{IR[31]}}, {IR[31], IR[7], IR[30:25], IR[11:8]}};  // Bit_Extender bit_extender_3
  assign bit_extender_4_out = {{12{IR[31]}}, {IR[31], IR[19:12], IR[20], IR[30:21]}};  // Bit_Extender bit_extender_4
  Shifter #(.width(32), .shift("ll")) shifter_1 (.in(bit_extender_3_out), .\dist (5'b00001), .out(shifter_1_out));
  Shifter #(.width(32), .shift("ll")) shifter_2 (.in(bit_extender_4_out), .\dist (5'b00001), .out(shifter_2_out));
  Regifile regifile_1 (
    .Din(multiplexer_9_out), .Clk(CLK), .R1(regifile_1_r1), .R2(MDin), .WE(RegWrite), .W_num(IR[11:7]),
    .R1_num(multiplexer_6_out), .R2_num(multiplexer_7_out));
  Multiplexer #(.select(1), .width(32), .disabled("Z"), .enable("false")) multiplexer_8 (
    .in0(bit_extender_1_out), .in1(bit_extender_2_out), .out(multiplexer_8_out), .sel(S));
  Adder #(.width(32)) adder_2 (.a(shifter_1_out), .b(PC), .out(adder_2_out));  // open: cin, cout
  Adder #(.width(32)) adder_3 (.a(PC), .b(shifter_2_out), .out(adder_3_out));  // open: cin, cout
  Multiplexer #(.select(1), .width(32), .disabled("Z"), .enable("false")) multiplexer_9 (
    .in0(RDin), .in1({IR[31:12], {12{1'b0}}}), .out(multiplexer_9_out), .sel(LUI));
  D_Flip_Flop #(.trigger("rising"), .Pre_Clr_Positions("LEGACY"), .NegatePresetClear("false"), .enable("true"), .NewFFLayout("false")) d_ff_1 (
    .clk(CLK), .D(or_9_out), .Q(d_ff_1_q));  // open: Qn, preset, en, reset
  or or_9 (or_9_out, \中断请求 , CSRRCI);
  or or_10 (or_10_out, CSRRSI, URET);
  Multiplexer #(.select(1), .width(32), .disabled("Z"), .enable("false")) multiplexer_10 (
    .in0(MDin), .in1(multiplexer_8_out), .out(multiplexer_10_out), .sel(AluSrcB));
  D_Flip_Flop #(.trigger("rising"), .Pre_Clr_Positions("LEGACY"), .NegatePresetClear("false"), .enable("true"), .NewFFLayout("false")) d_ff_2 (
    .clk(CLK), .D(or_10_out), .Q(d_ff_2_q));  // open: Qn, preset, en, reset
  ALU alu_1 (
    .X(regifile_1_r1), .Y(multiplexer_10_out), .AluOP(AluOP), .Equal(AluEQ), .Result(Calcuresult), .out_6(Alu));  // open: Result_2, out_4
  Comparator #(.width(32), .mode("twosComplement")) comparator_6 (
    .a(regifile_1_r1), .b(32'h22), .eq(comparator_6_eq));  // open: gt, lt
  D_Flip_Flop #(.trigger("rising"), .Pre_Clr_Positions("LEGACY"), .NegatePresetClear("false"), .enable("true"), .NewFFLayout("false")) d_ff_3 (
    .Qn(ENINT), .preset(d_ff_1_q), .reset(d_ff_2_q));  // open: clk, D, Q, en
  Shifter #(.width(32), .shift("ll")) shifter_3 (.in(MDin), .\dist (5'b10000), .out(shifter_3_out));
  and and_10 (and_10_out, ~comparator_6_eq, ecall);  // AND_Gate
  and and_11 (and_11_out, comparator_6_eq, ecall);
  Multiplexer #(.select(1), .width(32), .disabled("Z"), .enable("false")) multiplexer_11 (
    .in0(MDin), .in1(shifter_3_out), .out(multiplexer_11_out), .sel(Calcuresult[1]));
  D_Flip_Flop #(.trigger("falling"), .Pre_Clr_Positions("ABOVE_BELOW"), .NegatePresetClear("false"), .enable("true"), .NewFFLayout("true")) d_ff_4 (
    .clk(CLK), .D(1'b1), .Q(halt), .en(and_10_out), .reset(Go));  // open: Qn, preset
  Register #(.width(32), .trigger("rising"), .Select("low")) register_4 (
    .D(MDin), .en(and_11_out), .Q(LedData), .clk(CLK));  // open: clr
  Multiplexer #(.select(1), .width(32), .disabled("Z"), .enable("false")) multiplexer_12 (
    .in0(Dout), .in1(LBDout), .out(multiplexer_12_out), .sel(lb));
  RAM #(.addrWidth(10), .dataWidth(32), .bus("separate"), .Select("high")) ram_1 (
    .addr(Calcuresult[11:2]), .din(multiplexer_11_out), .data(Dout), .str(MemWrite), .sel(1'b1), .clk(CLK),
    .ld(1'b1));  // open: clr
  or or_11 (or_11_out[1], JAL, JALR);
  Multiplexer #(.select(2), .width(32), .disabled("Z"), .enable("false")) multiplexer_13 (
    .in0(Calcuresult), .in1(multiplexer_12_out), .in2(PC_4), .in3(PC_4), .out(RDin),
    .sel({or_11_out[1], MemToReg}));
  Comparator #(.width(2), .mode("unsigned")) comparator_7 (.a(INT_N), .b(INT_N_prime), .gt(\高级中断请求 ));  // open: eq, lt
  and and_12 (\中断请求 , ENINT, \高级中断请求 );
  or or_12 (W1, d_ff_8_q, d_ff_5_q);
  or or_13 (W2, d_ff_9_q, d_ff_6_q);
  or or_14 (W3, d_ff_10_q, d_ff_7_q);
  D_Flip_Flop #(.trigger("rising"), .Pre_Clr_Positions("LEGACY"), .NegatePresetClear("false"), .enable("true"), .NewFFLayout("false")) d_ff_5 (
    .clk(IRA), .D(1'b1), .Q(d_ff_5_q), .reset(d_ff_8_q));  // open: Qn, preset, en
  D_Flip_Flop #(.trigger("rising"), .Pre_Clr_Positions("LEGACY"), .NegatePresetClear("false"), .enable("true"), .NewFFLayout("false")) d_ff_6 (
    .clk(IRB), .D(1'b1), .Q(d_ff_6_q), .reset(d_ff_9_q));  // open: Qn, preset, en
  D_Flip_Flop #(.trigger("rising"), .Pre_Clr_Positions("LEGACY"), .NegatePresetClear("false"), .enable("true"), .NewFFLayout("false")) d_ff_7 (
    .clk(IRC), .D(1'b1), .Q(d_ff_7_q), .reset(d_ff_10_q));  // open: Qn, preset, en
  or or_15 (or_15_out, d_ff_5_q, d_ff_8_q);
  or or_16 (or_16_out, d_ff_6_q, d_ff_9_q);
  or or_17 (or_17_out, d_ff_7_q, d_ff_10_q);
  Multiplexer #(.select(2), .width(8), .disabled("Z"), .enable("false")) multiplexer_14 (
    .in0(Dout[7:0]), .in1(Dout[15:8]), .in2(Dout[23:16]), .in3(Dout[31:24]), .out(multiplexer_14_out),
    .sel(Calcuresult[1:0]));
  and and_13 (and_13_out, or_15_out, ~CLR1);  // AND_Gate
  and and_14 (and_14_out, or_16_out, ~CLR2);  // AND_Gate
  and and_15 (and_15_out, or_17_out, ~CLR3);  // AND_Gate
  assign LBDout = {{24{multiplexer_14_out[7]}}, multiplexer_14_out};  // Bit_Extender bit_extender_5
  D_Flip_Flop #(.trigger("rising"), .Pre_Clr_Positions("LEGACY"), .NegatePresetClear("false"), .enable("true"), .NewFFLayout("false")) d_ff_8 (
    .clk(CLK), .D(and_13_out), .Q(d_ff_8_q));  // open: Qn, preset, en, reset
  D_Flip_Flop #(.trigger("rising"), .Pre_Clr_Positions("LEGACY"), .NegatePresetClear("false"), .enable("true"), .NewFFLayout("false")) d_ff_9 (
    .clk(CLK), .D(and_14_out), .Q(d_ff_9_q));  // open: Qn, preset, en, reset
  D_Flip_Flop #(.trigger("rising"), .Pre_Clr_Positions("LEGACY"), .NegatePresetClear("false"), .enable("true"), .NewFFLayout("false")) d_ff_10 (
    .clk(CLK), .D(and_15_out), .Q(d_ff_10_q));  // open: Qn, preset, en, reset
  Priority_Encoder #(.select(2), .disabled("Z")) priority_encoder_3 (
    .in0(1'b1), .in1(d_ff_8_q), .in2(d_ff_9_q), .in3(d_ff_10_q), .out(INT_N));  // open: gs, en_out, en_in
  Decoder #(.select(2), .tristate("false"), .disabled(0), .enable("true")) decoder_3 (
    .out1(CLR1), .out2(CLR2), .out3(CLR3), .sel(INT_N_prime), .en(URET));  // open: out0
  or or_18 (INTR, d_ff_10_q, d_ff_9_q, d_ff_8_q);

  // Notes on the sheet:
  //   中断源
  //   中断等待指示
  //   总复位信号应将除ROM以外所有存储组件全部清零
  //   多级中断测试信号模拟器
  //   数码管输出
  //   数码管输出应该用寄存器锁存，否则显示数据只能一闪而过
  //   为方便自动评测，需要输出PC，IR，寄存器堆写如数据RDin
  //   指令探针
  //   指令存储器
  //   RAM写使能MemWrite、RAM写入数据MDin等信号
  //   指令字
  //   contents of rom_1 (hex, n*v repeats v):
  //   7d000113 100413 1f41993 41f9d993 433 c00913 800b13 140413 f47413 800293 100313 499993 89e9b3 1300533
  //   2200893 73 406282b3 fe0294e3 140413 f00f93 1f47433 1c41413 800293 100313 49d993 89e9b3 1300533
  //   2200893 73 406282b3 fe0294e3 1c45413 406b0b33 b0463 f95ff06f 2b3 fff2c293 1029293 fff2e293 500533
  //   2200893 73 f5dff06f 1112023 410113 a12023 410113 812023 410113 1312023 410113 1412023 410113 1512023
  //   410113 1612023 410113 40e073 100b13 300a13 100a93 1600433 441413 14469b3 1300533 2200893 73 fe0416e3
  //   415a0a33 fe0a10e3 40f073 ffc10113 12b03 ffc10113 12a83 ffc10113 12a03 ffc10113 12983 ffc10113 12403
  //   ffc10113 12503 ffc10113 12883 200073 1112023 410113 a12023 410113 812023 410113 1312023 410113
  //   1412023 410113 1512023 410113 1612023 410113 40e073 200b13 300a13 100a93 1600433 441413 14469b3
  //   1300533 2200893 73 fe0416e3 415a0a33 fe0a10e3 40f073 ffc10113 12b03 ffc10113 12a83 ffc10113 12a03
  //   ffc10113 12983 ffc10113 12403 ffc10113 12503 ffc10113 12883 200073 1112023 410113 a12023 410113
  //   812023 410113 1312023 410113 1412023 410113 1512023 410113 1612023 410113 40e073 300b13 300a13
  //   100a93 1600433 441413 14469b3 1300533 2200893 73 fe0416e3 415a0a33 fe0a10e3 40f073 ffc10113 12b03
  //   ffc10113 12a83 ffc10113 12a03 ffc10113 12983 ffc10113 12403 ffc10113 12503 ffc10113 12883 200073
  //   JAL
  //   JALR
  //   URET
  //   LUI
  //   Beq
  //   Bne
  //   MemToReg
  //   MemWrite
  //   AluOP
  //   AluSrcB
  //   RegWrite
  //   LUI
  //   数据存储器
  //   用这个时钟源需要去掉电路中的其他时钟源
endmodule

module \封装正确性测试  (
);

  wire IR1, IR2, IR3, MemW, RegW;
  wire [31:0] EX_PC, ID_PC, IF_PC, IR, LED, MDin, MDinr, MEM_PC, PC, RDin, RDinr, WB_PC;

  \单周期RISC_V  \u_单周期risc_v_1  (
    .IR1(IR1), .IR2(IR2), .IR3(IR3), .RegWrite(RegW), .MemWrite(MemW), .PC(PC), .IR(IR), .RDin(RDin),
    .MDin(MDin), .LedData(LED));
  \气泡流水线  \u_气泡流水线_1  (
    .RegWrite(RegW), .MemWrite(MemW), .IF_PC(IF_PC), .ID_PC(ID_PC), .EX_PC(EX_PC), .M_PC(MEM_PC),
    .WB_PC(WB_PC), .RDin(RDinr), .MDin(MDinr), .LedData(LED));
  \单周期_单级中断  \u_单周期_单级中断_1  (
    .IR1(IR1), .IR2(IR2), .IR3(IR3), .RegWrite(RegW), .MemWrite(MemW), .PC(PC), .IR(IR), .RDin(RDin),
    .MDin(MDin), .LedData(LED));
  \理想流水线  \u_理想流水线_1  (
    .RegWrite(RegW), .MemWrite(MemW), .IF_PC(IF_PC), .ID_PC(ID_PC), .EX_PC(EX_PC), .M_PC(MEM_PC),
    .WB_PC(WB_PC), .RDin(RDinr), .MDin(MDinr), .LedData(LED));
  \重定向流水线  \u_重定向流水线_1  (
    .RegWrite(RegW), .MemWrite(MemW), .IF_PC(IF_PC), .ID_PC(ID_PC), .EX_PC(EX_PC), .M_PC(MEM_PC),
    .WB_PC(WB_PC), .RDin(RDinr), .MDin(MDinr), .LedData(LED));
  \单周期_多级中断  \u_单周期_多级中断_1  (
    .IR1(IR1), .IR2(IR2), .IR3(IR3), .RegWrite(RegW), .MemWrite(MemW), .PC(PC), .IR(IR), .RDin(RDin),
    .MDin(MDin), .LedData(LED));

  // Notes on the sheet:
  //   单周期封装测试
  //   气泡流水封装测试
  //   单周期+单级中断封装测试
  //   请检查上面封装有无位宽不匹配，引脚标签是否和连接的标签相对应，否则无法在educoder平台上正确测试
  //   理想流水封装测试
  //   重定向流水封装测试
  //   单周期+多级中断封装测试
endmodule

module ID_EX (
  input  in_1,
  input  in_2,
  input  [31:0] in_3,
  input  in_4,
  input  in_5,
  input  in_6,
  input  [31:0] in_7,
  input  in_8,
  input  in_9,
  input  in_10,
  input  in_11,
  input  [31:0] in_12,
  input  in_13,
  input  in_14,
  input  in_15,
  input  in_16,
  input  [31:0] in_17,
  input  [3:0] op,
  input  in_19,
  input  [4:0] rd,
  input  [31:0] in_21,
  input  [31:0] PC,
  input  [31:0] IR,
  input  CLK,
  input  e,
  input  reset,
  input  flush,
  input  [1:0] in_28,
  input  [1:0] in_29,
  output out_30,
  output out_31,
  output [31:0] out_32,
  output out_33,
  output out_34,
  output out_35,
  output [31:0] out_36,
  output out_37,
  output out_38,
  output out_39,
  output out_40,
  output [31:0] out_41,
  output out_42,
  output out_43,
  output out_44,
  output out_45,
  output [31:0] out_46,
  output [3:0] out_47,
  output out_48,
  output [4:0] out_49,
  output [31:0] out_50,
  output [31:0] PC_2,
  output [31:0] IR_2,
  output [1:0] out_53,
  output [1:0] out_54
);

  wire multiplexer_1_out, multiplexer_2_out, multiplexer_3_out, multiplexer_4_out, multiplexer_5_out,
       multiplexer_6_out, multiplexer_7_out, multiplexer_8_out, multiplexer_13_out, multiplexer_14_out,
       multiplexer_17_out, multiplexer_18_out, multiplexer_19_out, multiplexer_20_out, reset_t;
  wire [1:0] multiplexer_11_out, multiplexer_12_out;
  wire [3:0] multiplexer_15_out;
  wire [4:0] multiplexer_16_out;
  wire [31:0] multiplexer_9_out, multiplexer_10_out, multiplexer_21_out, multiplexer_22_out,
       multiplexer_23_out, multiplexer_24_out, multiplexer_25_out;

  Multiplexer #(.select(1), .width(1), .disabled("Z"), .enable("false")) multiplexer_1 (
    .in0(in_1), .in1(1'b0), .out(multiplexer_1_out), .sel(reset_t));
  Multiplexer #(.select(1), .width(1), .disabled("Z"), .enable("false")) multiplexer_2 (
    .in0(in_4), .in1(1'b0), .out(multiplexer_2_out), .sel(reset_t));
  Multiplexer #(.select(1), .width(1), .disabled("Z"), .enable("false")) multiplexer_3 (
    .in0(in_6), .in1(1'b0), .out(multiplexer_3_out), .sel(reset_t));
  Multiplexer #(.select(1), .width(1), .disabled("Z"), .enable("false")) multiplexer_4 (
    .in0(in_9), .in1(1'b0), .out(multiplexer_4_out), .sel(reset_t));
  Multiplexer #(.select(1), .width(1), .disabled("Z"), .enable("false")) multiplexer_5 (
    .in0(in_11), .in1(1'b0), .out(multiplexer_5_out), .sel(reset_t));
  Multiplexer #(.select(1), .width(1), .disabled("Z"), .enable("false")) multiplexer_6 (
    .in0(in_14), .in1(1'b0), .out(multiplexer_6_out), .sel(reset_t));
  Multiplexer #(.select(1), .width(1), .disabled("Z"), .enable("false")) multiplexer_7 (
    .in0(in_16), .in1(1'b0), .out(multiplexer_7_out), .sel(reset_t));
  Multiplexer #(.select(1), .width(1), .disabled("Z"), .enable("false")) multiplexer_8 (
    .in0(in_19), .in1(1'b0), .out(multiplexer_8_out), .sel(reset_t));
  Multiplexer #(.select(1), .width(32), .disabled("Z"), .enable("false")) multiplexer_9 (
    .in0(PC), .in1({32{1'b0}}), .out(multiplexer_9_out), .sel(reset_t));
  Multiplexer #(.select(1), .width(32), .disabled("Z"), .enable("false")) multiplexer_10 (
    .in0(IR), .in1({32{1'b0}}), .out(multiplexer_10_out), .sel(reset_t));
  Register #(.width(1), .trigger("rising"), .Select("low")) register_1 (
    .D(multiplexer_1_out), .en(e), .Q(out_30), .clk(CLK));  // open: clr
  Register #(.width(1), .trigger("rising"), .Select("low")) register_2 (
    .D(multiplexer_2_out), .en(e), .Q(out_33), .clk(CLK));  // open: clr
  Register #(.width(1), .trigger("rising"), .Select("low")) register_3 (
    .D(multiplexer_3_out), .en(e), .Q(out_35), .clk(CLK));  // open: clr
  Register #(.width(1), .trigger("rising"), .Select("low")) register_4 (
    .D(multiplexer_4_out), .en(e), .Q(out_38), .clk(CLK));  // open: clr
  Register #(.width(1), .trigger("rising"), .Select("low")) register_5 (
    .D(multiplexer_5_out), .en(e), .Q(out_40), .clk(CLK));  // open: clr
  Register #(.width(1), .trigger("rising"), .Select("low")) register_6 (
    .D(multiplexer_6_out), .en(e), .Q(out_43), .clk(CLK));  // open: clr
  Register #(.width(1), .trigger("rising"), .Select("low")) register_7 (
    .D(multiplexer_7_out), .en(e), .Q(out_45), .clk(CLK));  // open: clr
  Register #(.width(1), .trigger("rising"), .Select("low")) register_8 (
    .D(multiplexer_8_out), .en(e), .Q(out_48), .clk(CLK));  // open: clr
  or or_1 (reset_t, reset, flush);
  Multiplexer #(.select(1), .width(2), .disabled("Z"), .enable("false")) multiplexer_11 (
    .in0(in_28), .in1(2'b00), .out(multiplexer_11_out), .sel(reset_t));
  Multiplexer #(.select(1), .width(2), .disabled("Z"), .enable("false")) multiplexer_12 (
    .in0(in_29), .in1(2'b00), .out(multiplexer_12_out), .sel(reset_t));
  Register #(.width(2), .trigger("rising"), .Select("low")) register_9 (
    .D(multiplexer_11_out), .en(e), .Q(out_53), .clk(CLK));  // open: clr
  Register #(.width(2), .trigger("rising"), .Select("low")) register_10 (
    .D(multiplexer_12_out), .en(e), .Q(out_54), .clk(CLK));  // open: clr
  Register #(.width(32), .trigger("rising"), .Select("low")) register_11 (
    .D(multiplexer_9_out), .en(e), .Q(PC_2), .clk(CLK));  // open: clr
  Register #(.width(32), .trigger("rising"), .Select("low")) register_12 (
    .D(multiplexer_10_out), .en(e), .Q(IR_2), .clk(CLK));  // open: clr
  Multiplexer #(.select(1), .width(1), .disabled("Z"), .enable("false")) multiplexer_13 (
    .in0(in_13), .in1(1'b0), .out(multiplexer_13_out), .sel(reset_t));
  Multiplexer #(.select(1), .width(1), .disabled("Z"), .enable("false")) multiplexer_14 (
    .in0(in_15), .in1(1'b0), .out(multiplexer_14_out), .sel(reset_t));
  Multiplexer #(.select(1), .width(4), .disabled("Z"), .enable("false")) multiplexer_15 (
    .in0(op), .in1(4'b0000), .out(multiplexer_15_out), .sel(reset_t));
  Multiplexer #(.select(1), .width(5), .disabled("Z"), .enable("false")) multiplexer_16 (
    .in0(rd), .in1({5{1'b0}}), .out(multiplexer_16_out), .sel(reset_t));
  Multiplexer #(.select(1), .width(1), .disabled("Z"), .enable("false")) multiplexer_17 (
    .in0(in_2), .in1(1'b0), .out(multiplexer_17_out), .sel(reset_t));
  Multiplexer #(.select(1), .width(1), .disabled("Z"), .enable("false")) multiplexer_18 (
    .in0(in_5), .in1(1'b0), .out(multiplexer_18_out), .sel(reset_t));
  Multiplexer #(.select(1), .width(1), .disabled("Z"), .enable("false")) multiplexer_19 (
    .in0(in_8), .in1(1'b0), .out(multiplexer_19_out), .sel(reset_t));
  Multiplexer #(.select(1), .width(1), .disabled("Z"), .enable("false")) multiplexer_20 (
    .in0(in_10), .in1(1'b0), .out(multiplexer_20_out), .sel(reset_t));
  Register #(.width(1), .trigger("rising"), .Select("low")) register_13 (
    .D(multiplexer_13_out), .en(e), .Q(out_42), .clk(CLK));  // open: clr
  Register #(.width(1), .trigger("rising"), .Select("low")) register_14 (
    .D(multiplexer_14_out), .en(e), .Q(out_44), .clk(CLK));  // open: clr
  Register #(.width(4), .trigger("rising"), .Select("low")) register_15 (
    .D(multiplexer_15_out), .en(e), .Q(out_47), .clk(CLK));  // open: clr
  Register #(.width(5), .trigger("rising"), .Select("low")) register_16 (
    .D(multiplexer_16_out), .en(e), .Q(out_49), .clk(CLK));  // open: clr
  Register #(.width(1), .trigger("rising"), .Select("low")) register_17 (
    .D(multiplexer_17_out), .en(e), .Q(out_31), .clk(CLK));  // open: clr
  Register #(.width(1), .trigger("rising"), .Select("low")) register_18 (
    .D(multiplexer_18_out), .en(e), .Q(out_34), .clk(CLK));  // open: clr
  Register #(.width(1), .trigger("rising"), .Select("low")) register_19 (
    .D(multiplexer_19_out), .en(e), .Q(out_37), .clk(CLK));  // open: clr
  Register #(.width(1), .trigger("rising"), .Select("low")) register_20 (
    .D(multiplexer_20_out), .en(e), .Q(out_39), .clk(CLK));  // open: clr
  Multiplexer #(.select(1), .width(32), .disabled("Z"), .enable("false")) multiplexer_21 (
    .in0(in_3), .in1({32{1'b0}}), .out(multiplexer_21_out), .sel(reset_t));
  Multiplexer #(.select(1), .width(32), .disabled("Z"), .enable("false")) multiplexer_22 (
    .in0(in_7), .in1({32{1'b0}}), .out(multiplexer_22_out), .sel(reset_t));
  Multiplexer #(.select(1), .width(32), .disabled("Z"), .enable("false")) multiplexer_23 (
    .in0(in_12), .in1({32{1'b0}}), .out(multiplexer_23_out), .sel(reset_t));
  Multiplexer #(.select(1), .width(32), .disabled("Z"), .enable("false")) multiplexer_24 (
    .in0(in_17), .in1({32{1'b0}}), .out(multiplexer_24_out), .sel(reset_t));
  Multiplexer #(.select(1), .width(32), .disabled("Z"), .enable("false")) multiplexer_25 (
    .in0(in_21), .in1({32{1'b0}}), .out(multiplexer_25_out), .sel(reset_t));
  Register #(.width(32), .trigger("rising"), .Select("low")) register_21 (
    .D(multiplexer_21_out), .en(e), .Q(out_32), .clk(CLK));  // open: clr
  Register #(.width(32), .trigger("rising"), .Select("low")) register_22 (
    .D(multiplexer_22_out), .en(e), .Q(out_36), .clk(CLK));  // open: clr
  Register #(.width(32), .trigger("rising"), .Select("low")) register_23 (
    .D(multiplexer_23_out), .en(e), .Q(out_41), .clk(CLK));  // open: clr
  Register #(.width(32), .trigger("rising"), .Select("low")) register_24 (
    .D(multiplexer_24_out), .en(e), .Q(out_46), .clk(CLK));  // open: clr
  Register #(.width(32), .trigger("rising"), .Select("low")) register_25 (
    .D(multiplexer_25_out), .en(e), .Q(out_50), .clk(CLK));  // open: clr

  // Other names for the same wires on the sheet: enable = e
endmodule

module IF_ID (
  input  [31:0] PC,
  input  [31:0] IR,
  input  CLK,
  input  e,
  input  reset,
  input  bt,
  output [31:0] PC_2,
  output [31:0] IR_2
);

  wire or_1_out;
  wire [31:0] multiplexer_1_out, multiplexer_2_out;

  Multiplexer #(.select(1), .width(32), .disabled("Z"), .enable("false")) multiplexer_1 (
    .in0(PC), .in1({32{1'b0}}), .out(multiplexer_1_out), .sel(or_1_out));
  Multiplexer #(.select(1), .width(32), .disabled("Z"), .enable("false")) multiplexer_2 (
    .in0(IR), .in1({32{1'b0}}), .out(multiplexer_2_out), .sel(or_1_out));
  or or_1 (or_1_out, reset, bt);
  Register #(.width(32), .trigger("rising"), .Select("low")) register_1 (
    .D(multiplexer_1_out), .en(e), .Q(PC_2), .clk(CLK));  // open: clr
  Register #(.width(32), .trigger("rising"), .Select("low")) register_2 (
    .D(multiplexer_2_out), .en(e), .Q(IR_2), .clk(CLK));  // open: clr
endmodule

module EXMEM (
  input  in_1,
  input  in_2,
  input  in_3,
  input  in_4,
  input  in_5,
  input  [4:0] rd,
  input  in_7,
  input  in_8,
  input  in_9,
  input  [31:0] in_10,
  input  [31:0] in_11,
  input  [31:0] PC,
  input  [31:0] in_13,
  input  [31:0] IR,
  input  CLK,
  input  e,
  input  reset,
  input  bt,
  output out_19,
  output out_20,
  output out_21,
  output out_22,
  output out_23,
  output [4:0] out_24,
  output out_25,
  output out_26,
  output out_27,
  output [31:0] out_28,
  output [31:0] out_29,
  output [31:0] PC_2,
  output [31:0] out_31,
  output [31:0] IR_2
);

  wire multiplexer_7_out, multiplexer_8_out, multiplexer_9_out, multiplexer_10_out, multiplexer_11_out,
       multiplexer_12_out, multiplexer_13_out, multiplexer_14_out, reset_t;
  wire [4:0] multiplexer_1_out;
  wire [31:0] multiplexer_2_out, multiplexer_3_out, multiplexer_4_out, multiplexer_5_out, multiplexer_6_out;

  Multiplexer #(.select(1), .width(5), .disabled("Z"), .enable("false")) multiplexer_1 (
    .in0(rd), .in1({5{1'b0}}), .out(multiplexer_1_out), .sel(reset_t));
  Multiplexer #(.select(1), .width(32), .disabled("Z"), .enable("false")) multiplexer_2 (
    .in0(PC), .in1({32{1'b0}}), .out(multiplexer_2_out), .sel(reset_t));
  Multiplexer #(.select(1), .width(32), .disabled("Z"), .enable("false")) multiplexer_3 (
    .in0(IR), .in1({32{1'b0}}), .out(multiplexer_3_out), .sel(reset_t));
  Register #(.width(5), .trigger("rising"), .Select("low")) register_1 (
    .D(multiplexer_1_out), .en(e), .Q(out_24), .clk(CLK));  // open: clr
  or or_1 (reset_t, reset, bt);
  Register #(.width(32), .trigger("rising"), .Select("low")) register_2 (
    .D(multiplexer_2_out), .en(e), .Q(PC_2), .clk(CLK));  // open: clr
  Register #(.width(32), .trigger("rising"), .Select("low")) register_3 (
    .D(multiplexer_3_out), .en(e), .Q(IR_2), .clk(CLK));  // open: clr
  Multiplexer #(.select(1), .width(32), .disabled("Z"), .enable("false")) multiplexer_4 (
    .in0(in_13), .in1({32{1'b0}}), .out(multiplexer_4_out), .sel(reset_t));
  Multiplexer #(.select(1), .width(32), .disabled("Z"), .enable("false")) multiplexer_5 (
    .in0(in_10), .in1({32{1'b0}}), .out(multiplexer_5_out), .sel(reset_t));
  Multiplexer #(.select(1), .width(32), .disabled("Z"), .enable("false")) multiplexer_6 (
    .in0(in_11), .in1({32{1'b0}}), .out(multiplexer_6_out), .sel(reset_t));
  Register #(.width(32), .trigger("rising"), .Select("low")) register_4 (
    .D(multiplexer_4_out), .en(e), .Q(out_31), .clk(CLK));  // open: clr
  Register #(.width(32), .trigger("rising"), .Select("low")) register_5 (
    .D(multiplexer_5_out), .en(e), .Q(out_28), .clk(CLK));  // open: clr
  Register #(.width(32), .trigger("rising"), .Select("low")) register_6 (
    .D(multiplexer_6_out), .en(e), .Q(out_29), .clk(CLK));  // open: clr
  Multiplexer #(.select(1), .width(1), .disabled("Z"), .enable("false")) multiplexer_7 (
    .in0(in_1), .in1(1'b0), .out(multiplexer_7_out), .sel(reset_t));
  Multiplexer #(.select(1), .width(1), .disabled("Z"), .enable("false")) multiplexer_8 (
    .in0(in_2), .in1(1'b0), .out(multiplexer_8_out), .sel(reset_t));
  Multiplexer #(.select(1), .width(1), .disabled("Z"), .enable("false")) multiplexer_9 (
    .in0(in_3), .in1(1'b0), .out(multiplexer_9_out), .sel(reset_t));
  Multiplexer #(.select(1), .width(1), .disabled("Z"), .enable("false")) multiplexer_10 (
    .in0(in_4), .in1(1'b0), .out(multiplexer_10_out), .sel(reset_t));
  Multiplexer #(.select(1), .width(1), .disabled("Z"), .enable("false")) multiplexer_11 (
    .in0(in_5), .in1(1'b0), .out(multiplexer_11_out), .sel(reset_t));
  Multiplexer #(.select(1), .width(1), .disabled("Z"), .enable("false")) multiplexer_12 (
    .in0(in_7), .in1(1'b0), .out(multiplexer_12_out), .sel(reset_t));
  Multiplexer #(.select(1), .width(1), .disabled("Z"), .enable("false")) multiplexer_13 (
    .in0(in_8), .in1(1'b0), .out(multiplexer_13_out), .sel(reset_t));
  Multiplexer #(.select(1), .width(1), .disabled("Z"), .enable("false")) multiplexer_14 (
    .in0(in_9), .in1(1'b0), .out(multiplexer_14_out), .sel(reset_t));
  Register #(.width(1), .trigger("rising"), .Select("low")) register_7 (
    .D(multiplexer_7_out), .en(e), .Q(out_19), .clk(CLK));  // open: clr
  Register #(.width(1), .trigger("rising"), .Select("low")) register_8 (
    .D(multiplexer_8_out), .en(e), .Q(out_20), .clk(CLK));  // open: clr
  Register #(.width(1), .trigger("rising"), .Select("low")) register_9 (
    .D(multiplexer_9_out), .en(e), .Q(out_21), .clk(CLK));  // open: clr
  Register #(.width(1), .trigger("rising"), .Select("low")) register_10 (
    .D(multiplexer_10_out), .en(e), .Q(out_22), .clk(CLK));  // open: clr
  Register #(.width(1), .trigger("rising"), .Select("low")) register_11 (
    .D(multiplexer_11_out), .en(e), .Q(out_23), .clk(CLK));  // open: clr
  Register #(.width(1), .trigger("rising"), .Select("low")) register_12 (
    .D(multiplexer_12_out), .en(e), .Q(out_25), .clk(CLK));  // open: clr
  Register #(.width(1), .trigger("rising"), .Select("low")) register_13 (
    .D(multiplexer_13_out), .en(e), .Q(out_26), .clk(CLK));  // open: clr
  Register #(.width(1), .trigger("rising"), .Select("low")) register_14 (
    .D(multiplexer_14_out), .en(e), .Q(out_27), .clk(CLK));  // open: clr

  // Other names for the same wires on the sheet: enable = e
endmodule

module MEM_WB (
  input  in_1,
  input  in_2,
  input  in_3,
  input  in_4,
  input  in_5,
  input  [4:0] rd,
  input  in_7,
  input  in_8,
  input  in_9,
  input  [31:0] in_10,
  input  [31:0] in_11,
  input  [31:0] PC,
  input  [31:0] in_13,
  input  [31:0] IR,
  input  CLK,
  input  e,
  input  reset,
  input  bt,
  output out_19,
  output out_20,
  output out_21,
  output out_22,
  output out_23,
  output [4:0] out_24,
  output out_25,
  output out_26,
  output out_27,
  output [31:0] out_28,
  output [31:0] out_29,
  output [31:0] PC_2,
  output [31:0] out_31,
  output [31:0] IR_2
);

  wire multiplexer_7_out, multiplexer_8_out, multiplexer_9_out, multiplexer_10_out, multiplexer_11_out,
       multiplexer_12_out, multiplexer_13_out, multiplexer_14_out, reset_t;
  wire [4:0] multiplexer_1_out;
  wire [31:0] multiplexer_2_out, multiplexer_3_out, multiplexer_4_out, multiplexer_5_out, multiplexer_6_out;

  Multiplexer #(.select(1), .width(5), .disabled("Z"), .enable("false")) multiplexer_1 (
    .in0(rd), .in1({5{1'b0}}), .out(multiplexer_1_out), .sel(reset_t));
  Multiplexer #(.select(1), .width(32), .disabled("Z"), .enable("false")) multiplexer_2 (
    .in0(PC), .in1({32{1'b0}}), .out(multiplexer_2_out), .sel(reset_t));
  Multiplexer #(.select(1), .width(32), .disabled("Z"), .enable("false")) multiplexer_3 (
    .in0(IR), .in1({32{1'b0}}), .out(multiplexer_3_out), .sel(reset_t));
  Register #(.width(5), .trigger("rising"), .Select("low")) register_1 (
    .D(multiplexer_1_out), .en(e), .Q(out_24), .clk(CLK));  // open: clr
  or or_1 (reset_t, reset, bt);
  Register #(.width(32), .trigger("rising"), .Select("low")) register_2 (
    .D(multiplexer_2_out), .en(e), .Q(PC_2), .clk(CLK));  // open: clr
  Register #(.width(32), .trigger("rising"), .Select("low")) register_3 (
    .D(multiplexer_3_out), .en(e), .Q(IR_2), .clk(CLK));  // open: clr
  Multiplexer #(.select(1), .width(32), .disabled("Z"), .enable("false")) multiplexer_4 (
    .in0(in_13), .in1({32{1'b0}}), .out(multiplexer_4_out), .sel(reset_t));
  Multiplexer #(.select(1), .width(32), .disabled("Z"), .enable("false")) multiplexer_5 (
    .in0(in_10), .in1({32{1'b0}}), .out(multiplexer_5_out), .sel(reset_t));
  Multiplexer #(.select(1), .width(32), .disabled("Z"), .enable("false")) multiplexer_6 (
    .in0(in_11), .in1({32{1'b0}}), .out(multiplexer_6_out), .sel(reset_t));
  Register #(.width(32), .trigger("rising"), .Select("low")) register_4 (
    .D(multiplexer_4_out), .en(e), .Q(out_31), .clk(CLK));  // open: clr
  Register #(.width(32), .trigger("rising"), .Select("low")) register_5 (
    .D(multiplexer_5_out), .en(e), .Q(out_28), .clk(CLK));  // open: clr
  Register #(.width(32), .trigger("rising"), .Select("low")) register_6 (
    .D(multiplexer_6_out), .en(e), .Q(out_29), .clk(CLK));  // open: clr
  Multiplexer #(.select(1), .width(1), .disabled("Z"), .enable("false")) multiplexer_7 (
    .in0(in_1), .in1(1'b0), .out(multiplexer_7_out), .sel(reset_t));
  Multiplexer #(.select(1), .width(1), .disabled("Z"), .enable("false")) multiplexer_8 (
    .in0(in_2), .in1(1'b0), .out(multiplexer_8_out), .sel(reset_t));
  Multiplexer #(.select(1), .width(1), .disabled("Z"), .enable("false")) multiplexer_9 (
    .in0(in_3), .in1(1'b0), .out(multiplexer_9_out), .sel(reset_t));
  Multiplexer #(.select(1), .width(1), .disabled("Z"), .enable("false")) multiplexer_10 (
    .in0(in_4), .in1(1'b0), .out(multiplexer_10_out), .sel(reset_t));
  Multiplexer #(.select(1), .width(1), .disabled("Z"), .enable("false")) multiplexer_11 (
    .in0(in_5), .in1(1'b0), .out(multiplexer_11_out), .sel(reset_t));
  Multiplexer #(.select(1), .width(1), .disabled("Z"), .enable("false")) multiplexer_12 (
    .in0(in_7), .in1(1'b0), .out(multiplexer_12_out), .sel(reset_t));
  Multiplexer #(.select(1), .width(1), .disabled("Z"), .enable("false")) multiplexer_13 (
    .in0(in_8), .in1(1'b0), .out(multiplexer_13_out), .sel(reset_t));
  Multiplexer #(.select(1), .width(1), .disabled("Z"), .enable("false")) multiplexer_14 (
    .in0(in_9), .in1(1'b0), .out(multiplexer_14_out), .sel(reset_t));
  Register #(.width(1), .trigger("rising"), .Select("low")) register_7 (
    .D(multiplexer_7_out), .en(e), .Q(out_19), .clk(CLK));  // open: clr
  Register #(.width(1), .trigger("rising"), .Select("low")) register_8 (
    .D(multiplexer_8_out), .en(e), .Q(out_20), .clk(CLK));  // open: clr
  Register #(.width(1), .trigger("rising"), .Select("low")) register_9 (
    .D(multiplexer_9_out), .en(e), .Q(out_21), .clk(CLK));  // open: clr
  Register #(.width(1), .trigger("rising"), .Select("low")) register_10 (
    .D(multiplexer_10_out), .en(e), .Q(out_22), .clk(CLK));  // open: clr
  Register #(.width(1), .trigger("rising"), .Select("low")) register_11 (
    .D(multiplexer_11_out), .en(e), .Q(out_23), .clk(CLK));  // open: clr
  Register #(.width(1), .trigger("rising"), .Select("low")) register_12 (
    .D(multiplexer_12_out), .en(e), .Q(out_25), .clk(CLK));  // open: clr
  Register #(.width(1), .trigger("rising"), .Select("low")) register_13 (
    .D(multiplexer_13_out), .en(e), .Q(out_26), .clk(CLK));  // open: clr
  Register #(.width(1), .trigger("rising"), .Select("low")) register_14 (
    .D(multiplexer_14_out), .en(e), .Q(out_27), .clk(CLK));  // open: clr

  // Other names for the same wires on the sheet: enable = e
endmodule

module \气泡逻辑  (
  input  [31:0] IR,
  input  rs1_used,
  input  rs2_used,
  input  EX_rw,
  input  [4:0] EX_rd,
  input  MEM_rw,
  input  [4:0] MEM_rd,
  input  ecall,
  input  BranchTaken,
  output stall,
  output flush
);

  wire and_1_out, and_2_out, and_3_out, and_4_out, and_5_out, and_6_out, comparator_1_eq, comparator_2_eq,
       comparator_3_eq, comparator_4_eq, comparator_5_eq, comparator_6_eq, comparator_7_eq, comparator_8_eq,
       comparator_9_eq, comparator_10_eq, comparator_11_eq, comparator_12_eq, not_1_out, not_2_out,
       not_3_out, not_4_out, or_1_out, or_2_out;

  Comparator #(.width(5), .mode("twosComplement")) comparator_1 (
    .a({5{1'b0}}), .b(IR[24:20]), .eq(comparator_1_eq));  // open: gt, lt
  Comparator #(.width(5), .mode("twosComplement")) comparator_2 (
    .a(IR[24:20]), .b(MEM_rd), .eq(comparator_2_eq));  // open: gt, lt
  Comparator #(.width(5), .mode("twosComplement")) comparator_3 (
    .a({5{1'b0}}), .b(IR[19:15]), .eq(comparator_3_eq));  // open: gt, lt
  Comparator #(.width(5), .mode("twosComplement")) comparator_4 (
    .a(IR[19:15]), .b(MEM_rd), .eq(comparator_4_eq));  // open: gt, lt
  Comparator #(.width(5), .mode("twosComplement")) comparator_5 (
    .a(5'b01010), .b(MEM_rd), .eq(comparator_5_eq));  // open: gt, lt
  Comparator #(.width(5), .mode("twosComplement")) comparator_6 (
    .a(MEM_rd), .b(5'b10001), .eq(comparator_6_eq));  // open: gt, lt
  not not_1 (not_1_out, comparator_7_eq);
  Comparator #(.width(5), .mode("twosComplement")) comparator_7 (
    .a({5{1'b0}}), .b(IR[19:15]), .eq(comparator_7_eq));  // open: gt, lt
  Comparator #(.width(5), .mode("twosComplement")) comparator_8 (
    .a(IR[19:15]), .b(EX_rd), .eq(comparator_8_eq));  // open: gt, lt
  not not_2 (not_2_out, comparator_9_eq);
  Comparator #(.width(5), .mode("twosComplement")) comparator_9 (
    .a({5{1'b0}}), .b(IR[24:20]), .eq(comparator_9_eq));  // open: gt, lt
  Comparator #(.width(5), .mode("twosComplement")) comparator_10 (
    .a(IR[24:20]), .b(EX_rd), .eq(comparator_10_eq));  // open: gt, lt
  not not_3 (not_3_out, comparator_1_eq);
  not not_4 (not_4_out, comparator_3_eq);
  Comparator #(.width(5), .mode("twosComplement")) comparator_11 (
    .a(5'b01010), .b(EX_rd), .eq(comparator_11_eq));  // open: gt, lt
  Comparator #(.width(5), .mode("twosComplement")) comparator_12 (
    .a(EX_rd), .b(5'b10001), .eq(comparator_12_eq));  // open: gt, lt
  and and_1 (and_1_out, not_3_out, comparator_2_eq, MEM_rw, rs2_used);
  and and_2 (and_2_out, not_4_out, comparator_4_eq, MEM_rw, rs1_used);
  or or_1 (or_1_out, comparator_5_eq, comparator_6_eq);
  or or_2 (or_2_out, comparator_11_eq, comparator_12_eq);
  and and_3 (and_3_out, not_1_out, comparator_8_eq, EX_rw, rs1_used);
  and and_4 (and_4_out, not_2_out, comparator_10_eq, EX_rw, rs2_used);
  and and_5 (and_5_out, MEM_rw, or_1_out, ecall);
  and and_6 (and_6_out, EX_rw, or_2_out, ecall);
  or or_3 (stall, and_3_out, and_4_out, and_1_out, and_2_out, and_5_out, and_6_out);
  or or_4 (flush, stall, BranchTaken);

  // Other names for the same wires on the sheet: datastop = stall; rs1[4:0] = IR[19:15]; rs2[4:0] = IR[24:20]
endmodule
module \重定向逻辑  (
  input  [31:0] IR,
  input  BranchTaken,
  input  ecall,
  input  EX_rw,
  input  MEM_rw,
  input  [4:0] EX_rd,
  input  [4:0] MEM_rd,
  input  rs1_used,
  input  rs2_used,
  input  EX_MTR,
  output stall,
  output flush,
  output [1:0] rs1forward,
  output [1:0] rs2forward
);

  wire and_1_out, and_2_out, and_3_out, and_4_out, and_5_out, and_6_out, and_11_out, and_12_out, and_13_out,
       and_14_out, and_15_out, and_16_out, and_17_out, and_18_out, and_19_out, and_21_out, and_22_out,
       and_23_out, comparator_1_eq, comparator_2_eq, comparator_3_eq, comparator_4_eq, comparator_5_eq,
       comparator_6_eq, comparator_7_eq, comparator_8_eq, comparator_9_eq, comparator_10_eq,
       comparator_11_eq, comparator_12_eq, comparator_13_eq, comparator_14_eq, comparator_15_eq,
       comparator_16_eq, ecall1, ecall2, ecall3, ecall4, not_1_out, not_2_out, not_3_out, not_4_out,
       not_5_out, not_6_out, or_4_out, or_6_out;

  not not_1 (not_1_out, comparator_1_eq);
  Comparator #(.width(5), .mode("twosComplement")) comparator_1 (
    .a(IR[19:15]), .b({5{1'b0}}), .eq(comparator_1_eq));  // open: gt, lt
  Comparator #(.width(5), .mode("twosComplement")) comparator_2 (
    .a(IR[19:15]), .b(EX_rd), .eq(comparator_2_eq));  // open: gt, lt
  Comparator #(.width(5), .mode("twosComplement")) comparator_3 (
    .a(IR[24:20]), .b({5{1'b0}}), .eq(comparator_3_eq));  // open: gt, lt
  not not_2 (not_2_out, comparator_3_eq);
  Comparator #(.width(5), .mode("twosComplement")) comparator_4 (
    .a(IR[24:20]), .b(EX_rd), .eq(comparator_4_eq));  // open: gt, lt
  and and_1 (and_1_out, rs1_used, not_1_out);
  and and_2 (and_2_out, rs2_used, not_2_out);
  and and_3 (and_3_out, and_1_out, comparator_2_eq);
  and and_4 (and_4_out, and_2_out, comparator_4_eq);
  and and_5 (and_5_out, and_3_out, EX_MTR);
  and and_6 (and_6_out, EX_MTR, and_4_out);
  or or_1 (stall, and_5_out, and_6_out);
  or or_2 (flush, stall, BranchTaken);
  Comparator #(.width(5), .mode("twosComplement")) comparator_5 (
    .a(EX_rd), .b(5'b01010), .eq(comparator_5_eq));  // open: gt, lt
  Comparator #(.width(5), .mode("twosComplement")) comparator_6 (
    .a(MEM_rd), .b(5'b01010), .eq(comparator_6_eq));  // open: gt, lt
  Comparator #(.width(5), .mode("twosComplement")) comparator_7 (
    .a(EX_rd), .b(5'b10001), .eq(comparator_7_eq));  // open: gt, lt
  Comparator #(.width(5), .mode("twosComplement")) comparator_8 (
    .a(MEM_rd), .b(5'b10001), .eq(comparator_8_eq));  // open: gt, lt
  and and_7 (ecall1, ecall, EX_rw, comparator_7_eq);
  and and_8 (ecall2, ecall, comparator_8_eq, MEM_rw);
  and and_9 (ecall3, ecall, EX_rw, comparator_5_eq);
  and and_10 (ecall4, ecall, MEM_rw, comparator_6_eq);
  Comparator #(.width(5), .mode("twosComplement")) comparator_9 (
    .a(IR[19:15]), .b({5{1'b0}}), .eq(comparator_9_eq));  // open: gt, lt
  not not_3 (not_3_out, comparator_9_eq);
  Comparator #(.width(5), .mode("twosComplement")) comparator_10 (
    .a(EX_rd), .b(IR[19:15]), .eq(comparator_10_eq));  // open: gt, lt
  not not_4 (not_4_out, comparator_11_eq);
  Comparator #(.width(5), .mode("twosComplement")) comparator_11 (
    .a(IR[19:15]), .b({5{1'b0}}), .eq(comparator_11_eq));  // open: gt, lt
  Comparator #(.width(5), .mode("twosComplement")) comparator_12 (
    .a(MEM_rd), .b(IR[19:15]), .eq(comparator_12_eq));  // open: gt, lt
  and and_11 (and_11_out, rs1_used, not_3_out);
  and and_12 (and_12_out, rs1_used, not_4_out);
  and and_13 (and_13_out, and_11_out, comparator_10_eq);
  and and_14 (and_14_out, and_12_out, comparator_12_eq);
  Comparator #(.width(5), .mode("twosComplement")) comparator_13 (
    .a(IR[24:20]), .b({5{1'b0}}), .eq(comparator_13_eq));  // open: gt, lt
  Comparator #(.width(5), .mode("twosComplement")) comparator_14 (
    .a(EX_rd), .b(IR[24:20]), .eq(comparator_14_eq));  // open: gt, lt
  Comparator #(.width(5), .mode("twosComplement")) comparator_15 (
    .a(IR[24:20]), .b({5{1'b0}}), .eq(comparator_15_eq));  // open: gt, lt
  Comparator #(.width(5), .mode("twosComplement")) comparator_16 (
    .a(MEM_rd), .b(IR[24:20]), .eq(comparator_16_eq));  // open: gt, lt
  and and_15 (and_15_out, and_13_out, EX_rw);
  and and_16 (and_16_out, and_14_out, MEM_rw);
  not not_5 (not_5_out, comparator_13_eq);
  and and_17 (and_17_out, rs2_used, not_6_out);
  not not_6 (not_6_out, comparator_15_eq);
  or or_3 (rs1forward[1], and_15_out, ecall1);
  or or_4 (or_4_out, and_16_out, ecall2);
  and and_18 (and_18_out, rs2_used, not_5_out);
  and and_19 (and_19_out, and_17_out, comparator_16_eq);
  and and_20 (rs1forward[0], ~rs1forward[1], or_4_out);  // AND_Gate
  and and_21 (and_21_out, and_18_out, comparator_14_eq);
  and and_22 (and_22_out, and_21_out, EX_rw);
  and and_23 (and_23_out, and_19_out, MEM_rw);
  or or_5 (rs2forward[1], and_22_out, ecall3);
  and and_24 (rs2forward[0], ~rs2forward[1], or_6_out);  // AND_Gate
  or or_6 (or_6_out, and_23_out, ecall4);

  // Other names for the same wires on the sheet: rs1[4:0] = IR[19:15]; rs2[4:0] = IR[24:20]; Load_use = stall
endmodule

module \中断控制器  (
  input  IRA,
  input  IRB,
  input  IRC,
  input  CLK,
  input  CLR,
  output IRAW,
  output IRBW,
  output IRCW,
  output INTR,
  output [1:0] INT_N
);

  wire and_1_out, and_2_out, and_3_out, and_5_out, CLR1, CLR2, CLR3, d_ff_1_q, d_ff_2_q, d_ff_3_q, d_ff_4_q,
       d_ff_5_q, d_ff_6_q, ENINT, or_4_out, or_5_out, or_6_out, \中断请求 ;
  wire [1:0] INT_N_prime;

  or or_1 (IRAW, d_ff_4_q, d_ff_1_q);
  or or_2 (IRBW, d_ff_5_q, d_ff_2_q);
  or or_3 (IRCW, d_ff_6_q, d_ff_3_q);
  D_Flip_Flop #(.trigger("rising"), .Pre_Clr_Positions("LEGACY"), .NegatePresetClear("false"), .enable("true"), .NewFFLayout("false")) d_ff_1 (
    .clk(IRA), .D(1'b1), .Q(d_ff_1_q), .reset(d_ff_4_q));  // open: Qn, preset, en
  D_Flip_Flop #(.trigger("rising"), .Pre_Clr_Positions("LEGACY"), .NegatePresetClear("false"), .enable("true"), .NewFFLayout("false")) d_ff_2 (
    .clk(IRB), .D(1'b1), .Q(d_ff_2_q), .reset(d_ff_5_q));  // open: Qn, preset, en
  D_Flip_Flop #(.trigger("rising"), .Pre_Clr_Positions("LEGACY"), .NegatePresetClear("false"), .enable("true"), .NewFFLayout("false")) d_ff_3 (
    .clk(IRC), .D(1'b1), .Q(d_ff_3_q), .reset(d_ff_6_q));  // open: Qn, preset, en
  or or_4 (or_4_out, d_ff_1_q, d_ff_4_q);
  or or_5 (or_5_out, d_ff_2_q, d_ff_5_q);
  or or_6 (or_6_out, d_ff_3_q, d_ff_6_q);
  and and_1 (and_1_out, or_4_out, ~CLR1);  // AND_Gate
  and and_2 (and_2_out, or_5_out, ~CLR2);  // AND_Gate
  and and_3 (and_3_out, or_6_out, ~CLR3);  // AND_Gate
  D_Flip_Flop #(.trigger("rising"), .Pre_Clr_Positions("LEGACY"), .NegatePresetClear("false"), .enable("true"), .NewFFLayout("false")) d_ff_4 (
    .clk(CLK), .D(and_1_out), .Q(d_ff_4_q));  // open: Qn, preset, en, reset
  D_Flip_Flop #(.trigger("rising"), .Pre_Clr_Positions("LEGACY"), .NegatePresetClear("false"), .enable("true"), .NewFFLayout("false")) d_ff_5 (
    .clk(CLK), .D(and_2_out), .Q(d_ff_5_q));  // open: Qn, preset, en, reset
  D_Flip_Flop #(.trigger("rising"), .Pre_Clr_Positions("LEGACY"), .NegatePresetClear("false"), .enable("true"), .NewFFLayout("false")) d_ff_6 (
    .clk(CLK), .D(and_3_out), .Q(d_ff_6_q));  // open: Qn, preset, en, reset
  Decoder #(.select(2), .tristate("false"), .disabled(0), .enable("true")) decoder_1 (
    .out1(CLR1), .out2(CLR2), .out3(CLR3), .sel(INT_N_prime), .en(CLR));  // open: out0
  Priority_Encoder #(.select(2), .disabled("Z")) priority_encoder_1 (
    .in0(1'b1), .in1(d_ff_4_q), .in2(d_ff_5_q), .in3(d_ff_6_q), .out(INT_N));  // open: gs, en_out, en_in
  or or_7 (INTR, d_ff_6_q, d_ff_5_q, d_ff_4_q);
  Register #(.width(2), .trigger("rising"), .Select("low")) register_1 (
    .D(INT_N), .en(\中断请求 ), .Q(INT_N_prime), .clk(CLK));  // open: clr
  and and_4 (\中断请求 , ENINT, INTR);
  and and_5 (and_5_out, ~CLR, INTR);  // AND_Gate
  D_Flip_Flop #(.trigger("rising"), .Pre_Clr_Positions("LEGACY"), .NegatePresetClear("false"), .enable("true"), .NewFFLayout("false")) d_ff_7 (
    .clk(CLK), .D(and_5_out), .Qn(ENINT));  // open: Q, preset, en, reset
endmodule

module \气泡流水线_单级中断  (
  output RegWrite,
  output MemWrite,
  output [31:0] IF_PC,
  output [31:0] ID_PC,
  output [31:0] EX_PC,
  output [31:0] M_PC,
  output [31:0] WB_PC,
  output [31:0] RDin,
  output [31:0] MDin,
  output [31:0] LedData
);

  wire Alu, AluEQ, and_1_out, and_2_out, and_3_out, and_4_out, and_5_out, and_7_out, and_8_out, and_9_out,
       and_10_out, and_11_out, and_12_out, and_13_out, bltu, Branchtaken, CLK, clock_1_out, clock_2_out,
       comparator_1_eq, comparator_2_eq, comparator_3_eq, comparator_4_eq, comparator_5_eq, comparator_6_eq,
       comparator_6_lt, comparator_7_gt, comparator_7_lt, d_ff_1_q, ecall, ENINT, EX_ecall, EX_halt,
       exmem_1_out_19, exmem_1_out_20, exmem_1_out_21, exmem_1_out_22, exmem_1_out_23, exmem_1_out_26,
       exmem_1_out_27, Go, halt, id_ex_1_out_30, id_ex_1_out_31, id_ex_1_out_33, id_ex_1_out_34,
       id_ex_1_out_37, id_ex_1_out_38, id_ex_1_out_39, id_ex_1_out_40, id_ex_1_out_43, id_ex_1_out_45,
       id_ex_1_out_48, INTR, IR1, IR2, IR3, IRA, IRB, IRC, JAL, mem_wb_1_out_19, mem_wb_1_out_20,
       mem_wb_1_out_21, mem_wb_1_out_22, mem_wb_1_out_23, mem_wb_1_out_27, nand_1_out, not_1_out, not_3_out,
       not_4_out, not_5_out, not_6_out, not_7_out, or_1_out, or_2_out, or_4_out, or_5_out, rs1_used,
       rs2_used, RST, S, stall, tunnel, URET, W1, W2, W3, \中断请求 , \单周期硬布线控制器_1_alu_src , \单周期硬布线控制器_1_beq ,
       \单周期硬布线控制器_1_bne , \单周期硬布线控制器_1_jalr , \单周期硬布线控制器_1_lb , \单周期硬布线控制器_1_lui , \单周期硬布线控制器_1_memtoreg ,
       \单周期硬布线控制器_1_memwrite , \单周期硬布线控制器_1_regwrite , \气泡逻辑_1_flush ;
  wire [1:0] or_7_out, priority_encoder_1_out, \中断控制器_1_int_n ;
  wire [3:0] id_ex_1_out_47, \单周期硬布线控制器_1_alu_op ;
  wire [4:0] exmem_1_out_24, id_ex_1_out_49, multiplexer_5_out, multiplexer_6_out, WB_rd;
  wire [7:0] multiplexer_13_out;
  wire [12:0] CNT_num;
  wire [15:0] \LoadUse次数 , \总周期数 , \插入气泡数 , \无条件分支数 , \条件分支成功数 ;
  wire [31:0] adder_3_out, bit_extender_1_out, bit_extender_2_out, bit_extender_3_out, bit_extender_4_out,
       Calcuresult, EX_IR, exmem_1_out_28, exmem_1_out_29, exmem_1_out_31, id_ex_1_out_32, id_ex_1_out_36,
       id_ex_1_out_41, id_ex_1_out_46, id_ex_1_out_50, ID_IR, IF_IR, INT_PC, jaddr, LBDout, MEM_IR,
       mem_wb_1_out_28, mem_wb_1_out_31, mEPC_q, multiplexer_1_out, multiplexer_2_out, multiplexer_7_out,
       multiplexer_8_out, multiplexer_9_out, multiplexer_12_out, newPC, PC_4, ram_1_data, regifile_1_r1,
       regifile_1_r2, shifter_1_out, shifter_2_out, WB_Dout, WB_IR;

  Button \u_总复位  (.out(RST));
  Button _1 (.out(IR1));
  Button _2 (.out(IR2));
  Button _3 (.out(IR3));
  // Probe on \总周期数 
  // Probe on \总周期数 
  not not_1 (not_1_out, halt);
  Button \u_继续运行  (.out(Go));
  LED #(.active("true")) led_1 (.in(W1));
  LED #(.active("true")) led_2 (.in(W2));
  LED #(.active("true")) led_3 (.in(W3));
  Counter #(.width(16), .max('hffff), .ongoal("wrap"), .trigger("rising"), .behavior("new")) counter_1 (
    .count(not_1_out), .Q(\总周期数 ), .clk(CLK));  // open: load, D, carry, clr, preset, down
  Hex_Digit_Display hex_digit_display_1 (.value(LedData[31:28]));  // open: dp
  // Probe on IF_PC[19:0]
  // RiscV_Probe riscv_probe_1: pin names not known; wires that end beside it: IF_IR
  Comparator #(.width(16), .mode("twosComplement")) comparator_1 (
    .a(16'h23b), .b(\总周期数 ), .eq(comparator_1_eq));  // open: gt, lt
  Comparator #(.width(16), .mode("twosComplement")) comparator_2 (
    .a(\总周期数 ), .b(16'h1), .eq(comparator_2_eq));  // open: gt, lt
  Comparator #(.width(16), .mode("twosComplement")) comparator_3 (
    .a(\总周期数 ), .b(16'h4), .eq(comparator_3_eq));  // open: gt, lt
  Comparator #(.width(16), .mode("twosComplement")) comparator_4 (
    .a(\总周期数 ), .b(16'h7), .eq(comparator_4_eq));  // open: gt, lt
  Hex_Digit_Display hex_digit_display_2 (.value(LedData[27:24]));  // open: dp
  Hex_Digit_Display hex_digit_display_3 (.value(LedData[23:20]));  // open: dp
  // Probe on ID_PC[19:0]
  // RiscV_Probe riscv_probe_2: pin names not known; wires that end beside it: ID_IR
  or or_1 (or_1_out, comparator_1_eq, comparator_2_eq);
  assign IRA = or_1_out ? ~CLK : 1'bz;  // Controlled_Inverter controlled_inverter_1
  assign IRB = comparator_3_eq ? ~CLK : 1'bz;  // Controlled_Inverter controlled_inverter_2
  assign IRC = comparator_4_eq ? ~CLK : 1'bz;  // Controlled_Inverter controlled_inverter_3
  Hex_Digit_Display hex_digit_display_4 (.value(LedData[19:16]));  // open: dp
  Hex_Digit_Display hex_digit_display_5 (.value(LedData[15:12]));  // open: dp
  Pull_Resistor #(.pull(0)) pull_resistor_1 (.node(IRA));
  Pull_Resistor #(.pull(0)) pull_resistor_2 (.node(IRB));
  Pull_Resistor #(.pull(0)) pull_resistor_3 (.node(IRC));
  Multiplexer #(.select(1), .width(32), .disabled("Z"), .enable("false")) multiplexer_1 (
    .in0(newPC), .in1(INT_PC), .out(multiplexer_1_out), .sel(\中断请求 ));
  Hex_Digit_Display hex_digit_display_6 (.value(LedData[7:4]));  // open: dp
  Hex_Digit_Display hex_digit_display_7 (.value(LedData[11:8]));  // open: dp
  Clock #(.highDuration(1), .lowDuration(1)) clock_1 (.out(clock_1_out));
  // Probe on EX_PC[19:0]
  // RiscV_Probe riscv_probe_3: pin names not known; wires that end beside it: clock_1_out, EX_IR, CLK
  Multiplexer #(.select(2), .width(32), .disabled("Z"), .enable("false")) multiplexer_2 (
    .in0(PC_4), .in1(jaddr), .in2(Calcuresult), .out(multiplexer_2_out), .sel(priority_encoder_1_out));  // open: in3
  Hex_Digit_Display hex_digit_display_8 (.value(LedData[3:0]));  // open: dp
  or or_2 (or_2_out, and_1_out, \中断请求 );
  and and_1 (and_1_out, ~stall, ~halt);  // AND_Gate
  Register #(.width(32), .trigger("rising"), .Select("low")) mEPC (
    .D(multiplexer_2_out), .en(\中断请求 ), .Q(mEPC_q), .clk(CLK));  // open: clr
  // Probe on \总周期数 
  // Probe on M_PC[19:0]
  // RiscV_Probe riscv_probe_4: pin names not known; wires that end beside it: MEM_IR
  Register #(.width(32), .trigger("rising"), .Select("low")) PC (
    .D(multiplexer_1_out), .en(or_2_out), .Q(IF_PC), .clk(CLK), .clr(RST));
  Multiplexer #(.select(1), .width(32), .disabled("Z"), .enable("false")) multiplexer_3 (
    .in0(multiplexer_2_out), .in1(mEPC_q), .out(newPC), .sel(URET));
  // Probe on \总周期数 
  // Probe on \无条件分支数 
  // Probe on \条件分支成功数 
  // Probe on \插入气泡数 
  // Probe on \LoadUse次数 
  Adder #(.width(32)) adder_1 (.a(IF_PC), .b(32'h4), .out(PC_4));  // open: cin, cout
  \中断控制器  \u_中断控制器_1  (
    .IRA(IRA), .IRB(IRB), .IRC(IRC), .CLK(CLK), .CLR(URET), .IRAW(W1), .IRBW(W2), .IRCW(W3), .INTR(INTR),
    .INT_N(\中断控制器_1_int_n ));
  // Probe on IF_PC[11:0]
  // Probe on WB_PC[19:0]
  // RiscV_Probe riscv_probe_5: pin names not known; wires that end beside it: WB_IR
  ROM #(.addrWidth(10), .dataWidth(32), .Select("high")) rom_1 (.addr(IF_PC[11:2]), .data(IF_IR));
  // Probe on EX_PC[11:0]
  // Probe on ID_PC[11:0]
  // RiscV_Probe riscv_probe_6: pin names not known; wires that end beside it: IF_IR
  // Probe on M_PC[11:0]
  D_Flip_Flop #(.trigger("high"), .Pre_Clr_Positions("LEGACY"), .NegatePresetClear("false"), .enable("true"), .NewFFLayout("false")) d_ff_1 (.Q(d_ff_1_q));  // open: clk, D, Qn, preset, en, reset
  // Probe on 13'hc
  Comparator #(.width(32), .mode("twosComplement")) comparator_5 (
    .a({32{1'b0}}), .b(ID_IR), .eq(comparator_5_eq));  // open: gt, lt
  not not_2 (tunnel, comparator_5_eq);
  and and_2 (and_2_out, ~stall, ~halt);  // AND_Gate
  Multiplexer #(.select(2), .width(32), .disabled("Z"), .enable("false")) multiplexer_4 (
    .in1(32'h30ac), .in2(32'h3150), .in3(32'h31f4), .out(INT_PC), .sel(\中断控制器_1_int_n ));  // open: in0
  // Probe on WB_PC[11:0]
  Comparator #(.width(13), .mode("twosComplement")) comparator_6 (
    .a(CNT_num), .b(13'hc), .eq(comparator_6_eq), .lt(comparator_6_lt));  // open: gt
  Clock #(.highDuration(1), .lowDuration(1)) clock_2 (.out(clock_2_out));
  IF_ID if_id_1 (
    .PC(IF_PC), .PC_2(ID_PC), .IR(IF_IR), .IR_2(ID_IR), .CLK(CLK), .e(and_2_out), .reset(RST),
    .bt(Branchtaken));
  nand nand_1 (nand_1_out, d_ff_1_q, comparator_6_eq);
  Counter #(.width(13), .max('h1fff), .ongoal("stay"), .trigger("rising"), .behavior("old")) counter_2 (
    .count(comparator_6_lt), .Q(CNT_num), .clk(clock_2_out));  // open: load, D, carry, clr, preset
  and and_3 (and_3_out, tunnel, \单周期硬布线控制器_1_lb );
  assign CLK = nand_1_out ? clock_2_out : 1'bz;  // Controlled_Buffer controlled_buffer_1
  Pull_Resistor #(.pull(1)) pull_resistor_4 (.node(CLK));
  \单周期硬布线控制器  \u_单周期硬布线控制器_1  (
    .Funct({ID_IR[30], ID_IR[25], ID_IR[14:12]}), .OP(ID_IR[6:2]), .ALU_OP(\单周期硬布线控制器_1_alu_op ),
    .MemToReg(\单周期硬布线控制器_1_memtoreg ), .MemWrite(\单周期硬布线控制器_1_memwrite ), .ALU_SRC(\单周期硬布线控制器_1_alu_src ),
    .RegWrite(\单周期硬布线控制器_1_regwrite ), .ecall(ecall), .S_type(S), .Jalr(\单周期硬布线控制器_1_jalr ),
    .Beq(\单周期硬布线控制器_1_beq ), .JAL(JAL), .Bne(\单周期硬布线控制器_1_bne ), .in_3(ID_IR[21]), .uret(URET),
    .LUI(\单周期硬布线控制器_1_lui ), .lb(\单周期硬布线控制器_1_lb ), .bltu(bltu), .re2_used(rs2_used), .rs1_used(rs1_used));  // open: CSRRSI, CSRRCI, BGE, U_type
  Multiplexer #(.select(1), .width(5), .disabled("Z"), .enable("false")) multiplexer_5 (
    .in0(ID_IR[19:15]), .in1(5'b10001), .out(multiplexer_5_out), .sel(ecall));
  Multiplexer #(.select(1), .width(5), .disabled("Z"), .enable("false")) multiplexer_6 (
    .in0(ID_IR[24:20]), .in1(5'b01010), .out(multiplexer_6_out), .sel(ecall));
  and and_4 (and_4_out, tunnel, \单周期硬布线控制器_1_memtoreg );
  assign bit_extender_1_out = {{20{ID_IR[31]}}, ID_IR[31:20]};  // Bit_Extender bit_extender_1
  assign bit_extender_2_out = {{20{ID_IR[31]}}, {ID_IR[31:25], ID_IR[11:7]}};  // Bit_Extender bit_extender_2
  assign bit_extender_3_out = {{20{ID_IR[31]}}, {ID_IR[31], ID_IR[7], ID_IR[30:25], ID_IR[11:8]}};  // Bit_Extender bit_extender_3
  assign bit_extender_4_out = {{12{ID_IR[31]}}, {ID_IR[31], ID_IR[19:12], ID_IR[20], ID_IR[30:21]}};  // Bit_Extender bit_extender_4
  and and_5 (and_5_out, ~URET, INTR);  // AND_Gate
  and and_6 (\中断请求 , ENINT, INTR);
  \气泡逻辑  \u_气泡逻辑_1  (
    .IR(ID_IR), .rs1_used(rs1_used), .rs2_used(rs2_used), .EX_rw(id_ex_1_out_37), .EX_rd(id_ex_1_out_49),
    .MEM_rw(exmem_1_out_26), .MEM_rd(exmem_1_out_24), .ecall(ecall), .BranchTaken(Branchtaken),
    .stall(stall), .flush(\气泡逻辑_1_flush ));
  not not_3 (not_3_out, CLK);
  Regifile regifile_1 (
    .Din(RDin), .Clk(not_3_out), .R1(regifile_1_r1), .R2(regifile_1_r2), .WE(RegWrite), .W_num(WB_rd),
    .R1_num(multiplexer_5_out), .R2_num(multiplexer_6_out));
  Multiplexer #(.select(1), .width(32), .disabled("Z"), .enable("false")) multiplexer_7 (
    .in0(bit_extender_3_out), .in1(bit_extender_4_out), .out(multiplexer_7_out), .sel(JAL));
  D_Flip_Flop #(.trigger("rising"), .Pre_Clr_Positions("LEGACY"), .NegatePresetClear("false"), .enable("true"), .NewFFLayout("false")) d_ff_2 (
    .clk(CLK), .D(and_5_out), .Qn(ENINT));  // open: Q, preset, en, reset
  and and_7 (and_7_out, tunnel, \单周期硬布线控制器_1_alu_src );
  Multiplexer #(.select(1), .width(32), .disabled("Z"), .enable("false")) multiplexer_8 (
    .in0(bit_extender_1_out), .in1(bit_extender_2_out), .out(multiplexer_8_out), .sel(S));
  Shifter #(.width(32), .shift("ll")) shifter_1 (.in(multiplexer_7_out), .\dist (5'b00001), .out(shifter_1_out));
  and and_8 (and_8_out, tunnel, \单周期硬布线控制器_1_regwrite );
  ID_EX id_ex_1 (
    .in_1(and_3_out), .PC(ID_PC), .PC_2(EX_PC), .IR(ID_IR), .IR_2(EX_IR), .CLK(CLK), .e(not_4_out),
    .reset(RST), .flush(\气泡逻辑_1_flush ), .out_30(id_ex_1_out_30), .in_4(\单周期硬布线控制器_1_lui ),
    .out_33(id_ex_1_out_33), .in_6(URET), .in_9(\单周期硬布线控制器_1_jalr ), .out_38(id_ex_1_out_38), .in_11(JAL),
    .out_40(id_ex_1_out_40), .in_14(\单周期硬布线控制器_1_beq ), .out_43(id_ex_1_out_43), .in_16(\单周期硬布线控制器_1_bne ),
    .out_45(id_ex_1_out_45), .in_19(and_4_out), .out_48(id_ex_1_out_48), .in_2(\单周期硬布线控制器_1_memwrite ),
    .out_31(id_ex_1_out_31), .in_5(and_7_out), .out_34(id_ex_1_out_34), .in_8(and_8_out),
    .out_37(id_ex_1_out_37), .in_10(bltu), .out_39(id_ex_1_out_39), .in_13(S), .in_15(ecall),
    .out_44(EX_ecall), .op(\单周期硬布线控制器_1_alu_op ), .out_47(id_ex_1_out_47), .rd(ID_IR[11:7]),
    .out_49(id_ex_1_out_49), .out_36(id_ex_1_out_36), .in_7(regifile_1_r2), .in_3(regifile_1_r1),
    .out_32(id_ex_1_out_32), .in_12(multiplexer_8_out), .out_41(id_ex_1_out_41), .in_17(shifter_1_out),
    .out_46(id_ex_1_out_46), .in_21({ID_IR[31:12], {12{1'b0}}}), .out_50(id_ex_1_out_50));  // open: out_35, out_42, in_28, out_53, in_29, out_54
  not not_4 (not_4_out, halt);
  Priority_Encoder #(.select(2), .disabled("Z")) priority_encoder_1 (
    .in0(1'b1), .in1(or_4_out), .in2(id_ex_1_out_38), .out(priority_encoder_1_out));  // open: in3, gs, en_out, en_in
  or or_3 (Branchtaken, id_ex_1_out_38, or_4_out);
  Multiplexer #(.select(1), .width(32), .disabled("Z"), .enable("false")) multiplexer_9 (
    .in0(id_ex_1_out_36), .in1(id_ex_1_out_41), .out(multiplexer_9_out), .sel(id_ex_1_out_34));
  Adder #(.width(32)) adder_2 (.a(id_ex_1_out_46), .b(EX_PC), .out(jaddr));  // open: cin, cout
  or or_4 (or_4_out, and_9_out, and_10_out, and_11_out, id_ex_1_out_40);
  ALU alu_1 (
    .X(id_ex_1_out_32), .Y(multiplexer_9_out), .AluOP(id_ex_1_out_47), .Equal(AluEQ), .Result(Calcuresult),
    .out_6(Alu));  // open: Result_2, out_4
  Comparator #(.width(32), .mode("twosComplement")) comparator_7 (
    .a(id_ex_1_out_32), .b(32'h22), .gt(comparator_7_gt), .lt(comparator_7_lt));  // open: eq
  and and_9 (and_9_out, id_ex_1_out_45, ~AluEQ);  // AND_Gate
  and and_10 (and_10_out, AluEQ, id_ex_1_out_43);
  and and_11 (and_11_out, Alu, id_ex_1_out_39);
  or or_5 (or_5_out, comparator_7_gt, comparator_7_lt);
  not not_5 (not_5_out, or_5_out);
  and and_12 (and_12_out, EX_ecall, or_5_out);
  and and_13 (and_13_out, not_5_out, EX_ecall);
  not not_6 (not_6_out, halt);
  D_Flip_Flop #(.trigger("falling"), .Pre_Clr_Positions("ABOVE_BELOW"), .NegatePresetClear("false"), .enable("true"), .NewFFLayout("true")) d_ff_3 (
    .clk(CLK), .D(1'b1), .Q(EX_halt), .en(and_12_out), .reset(Go));  // open: Qn, preset
  Register #(.width(32), .trigger("rising"), .Select("low")) register_1 (
    .D(id_ex_1_out_36), .en(and_13_out), .Q(LedData), .clk(CLK));  // open: clr
  EXMEM exmem_1 (
    .in_1(id_ex_1_out_30), .in_2(id_ex_1_out_33), .in_3(id_ex_1_out_38), .in_4(id_ex_1_out_40),
    .in_5(id_ex_1_out_48), .rd(id_ex_1_out_49), .in_7(id_ex_1_out_31), .in_8(id_ex_1_out_37), .in_9(EX_halt),
    .PC(EX_PC), .IR(EX_IR), .out_19(exmem_1_out_19), .out_20(exmem_1_out_20), .out_21(exmem_1_out_21),
    .out_22(exmem_1_out_22), .out_23(exmem_1_out_23), .out_24(exmem_1_out_24), .out_25(MemWrite),
    .out_26(exmem_1_out_26), .out_27(exmem_1_out_27), .out_28(exmem_1_out_28), .out_29(exmem_1_out_29),
    .PC_2(M_PC), .out_31(exmem_1_out_31), .IR_2(MEM_IR), .in_13(id_ex_1_out_50), .in_10(Calcuresult),
    .in_11(id_ex_1_out_36), .reset(RST), .bt(RST), .e(not_6_out), .CLK(CLK));
  Multiplexer #(.select(1), .width(32), .disabled("Z"), .enable("false")) multiplexer_10 (
    .in0(exmem_1_out_29), .in1(shifter_2_out), .out(MDin), .sel(exmem_1_out_28[1]));
  Shifter #(.width(32), .shift("ll")) shifter_2 (.in(exmem_1_out_29), .\dist (5'b10000), .out(shifter_2_out));
  RAM #(.addrWidth(10), .dataWidth(32), .bus("separate"), .Select("high")) ram_1 (
    .addr(exmem_1_out_28[11:2]), .din(MDin), .data(ram_1_data), .str(MemWrite), .sel(1'b1), .clk(CLK),
    .ld(1'b1), .clr(RST));
  not not_7 (not_7_out, halt);
  or or_6 (or_7_out[1], mem_wb_1_out_20, mem_wb_1_out_21, mem_wb_1_out_22);
  MEM_WB mem_wb_1 (
    .in_1(exmem_1_out_19), .in_2(exmem_1_out_20), .in_3(exmem_1_out_21), .in_4(exmem_1_out_22),
    .in_5(exmem_1_out_23), .rd(exmem_1_out_24), .in_7(MemWrite), .in_8(exmem_1_out_26),
    .in_9(exmem_1_out_27), .PC(M_PC), .IR(MEM_IR), .out_19(mem_wb_1_out_19), .out_20(mem_wb_1_out_20),
    .out_21(mem_wb_1_out_21), .out_22(mem_wb_1_out_22), .out_23(mem_wb_1_out_23), .out_24(WB_rd),
    .out_26(RegWrite), .out_27(mem_wb_1_out_27), .out_28(mem_wb_1_out_28), .out_29(WB_Dout), .PC_2(WB_PC),
    .out_31(mem_wb_1_out_31), .IR_2(WB_IR), .in_13(exmem_1_out_31), .in_10(exmem_1_out_28),
    .in_11(ram_1_data), .reset(RST), .bt(RST), .e(not_7_out), .CLK(CLK));  // open: out_25
  or or_7 (or_7_out[0], mem_wb_1_out_20, mem_wb_1_out_23);
  Adder #(.width(32)) adder_3 (.a(WB_PC), .b(32'h4), .out(adder_3_out));  // open: cin, cout
  Multiplexer #(.select(2), .width(32), .disabled("Z"), .enable("false")) multiplexer_11 (
    .in0(mem_wb_1_out_28), .in1(multiplexer_12_out), .in2(adder_3_out), .in3(mem_wb_1_out_31), .out(RDin),
    .sel(or_7_out));
  D_Flip_Flop #(.trigger("rising"), .Pre_Clr_Positions("ABOVE_BELOW"), .NegatePresetClear("false"), .enable("true"), .NewFFLayout("true")) d_ff_4 (
    .clk(mem_wb_1_out_27), .D(1'b1), .Q(halt), .en(1'b1), .reset(Go));  // open: Qn, preset
  Multiplexer #(.select(1), .width(32), .disabled("Z"), .enable("false")) multiplexer_12 (
    .in0(WB_Dout), .in1(LBDout), .out(multiplexer_12_out), .sel(mem_wb_1_out_19));
  Multiplexer #(.select(2), .width(8), .disabled("Z"), .enable("false")) multiplexer_13 (
    .in0(WB_Dout[7:0]), .in1(WB_Dout[15:8]), .in2(WB_Dout[23:16]), .in3(WB_Dout[31:24]),
    .out(multiplexer_13_out), .sel(mem_wb_1_out_28[1:0]));
  assign LBDout = {{24{multiplexer_13_out[7]}}, multiplexer_13_out};  // Bit_Extender bit_extender_5

  // Other names for the same wires on the sheet: rd[4:0] = ID_IR[11:7]; IR[31:0] = IF_IR; MEM_PC[31:0] = M_PC;
  //   PC[31:0] = IF_PC

  // Notes on the sheet:
  //   中断源
  //   时空图监测，可删除
  //   中断等待指示
  //   单级中断测试信号模拟器
  //   数码管输出
  //   指令存储器
  //   contents of rom_1 (hex, n*v repeats v):
  //   7d000113 100413 1f41993 41f9d993 433 c00913 800b13 140413 f47413 800293 100313 499993 89e9b3 1300533
  //   2200893 73 406282b3 fe0294e3 140413 f00f93 1f47433 1c41413 800293 100313 49d993 89e9b3 1300533
  //   2200893 73 406282b3 fe0294e3 1c45413 406b0b33 b0463 f95ff06f 2b3 fff2c293 1029293 fff2e293 500533
  //   2200893 73 f5dff06f 1112023 410113 a12023 410113 812023 410113 1312023 410113 1412023 410113 1512023
  //   410113 1612023 410113 100b13 300a13 100a93 1600433 441413 14469b3 1300533 2200893 73 fe0416e3
  //   415a0a33 fe0a10e3 ffc10113 12b03 ffc10113 12a83 ffc10113 12a03 ffc10113 12983 ffc10113 12403
  //   ffc10113 12503 ffc10113 12883 200073 1112023 410113 a12023 410113 812023 410113 1312023 410113
  //   1412023 410113 1512023 410113 1612023 410113 200b13 300a13 100a93 1600433 441413 14469b3 1300533
  //   2200893 73 fe0416e3 415a0a33 fe0a10e3 ffc10113 12b03 ffc10113 12a83 ffc10113 12a03 ffc10113 12983
  //   ffc10113 12403 ffc10113 12503 ffc10113 12883 200073 1112023 410113 a12023 410113 812023 410113
  //   1312023 410113 1412023 410113 1512023 410113 1612023 410113 300b13 300a13 100a93 1600433 441413
  //   14469b3 1300533 2200893 73 fe0416e3 415a0a33 fe0a10e3 ffc10113 12b03 ffc10113 12a83 ffc10113 12a03
  //   ffc10113 12983 ffc10113 12403 ffc10113 12503 ffc10113 12883 200073
  //   控制位
  //   指令探针
  //   流水调试日志用
  //   暂停节拍，不能为0
  //   戳工具置1进入计数暂停模式，ctrl+k时钟自动运行到对应节拍暂停
  //   ctrl+k关闭时钟连续运行，将控制位置零，进入单步调试模式调试
  //   指令字
  //   可计数暂停的时钟源
  //   JAL
  //   JALR
  //   URET
  //   LUI
  //   lb
  //   Beq
  //   Bne
  //   MemToReg
  //   MemWrite
  //   AluOP
  //   AluSrcB
  //   RegWrite
  //   bltu
  //   S_type
  //   LUI
  //   stall
  //   为方便自动评测，需要输出流水线各段保存的PC值，注意是PC不是PC+4，另外ID段寄存器写入信息，Mem段内存写入信息也要输出
  //   IR
  //   rs2-used
  //   ecall
  //   rs1-used
  //   lb
  //   lui
  //   URET
  //   JALR
  //   JAL
  //   JAL
  //   Beq
  //   Beq
  //   Bne
  //   Bne
  //   MTR
  //   MW
  //   MW
  //   AluSrc
  //   AluSrcB
  //   RW
  //   bltu
  //   imm12
  //   imm12
  //   immj
  //   lui
  //   lb
  //   LUI
  //   URET
  //   MTR
  //   Rw
  //   s
  //   ecall
  //   r1
  //   r2
  //   r2
  //   flush
  //   result
  //   r2
  //   lui
  //   EX.RD
  //   EX.RW
  //   lb
  //   lui
  //   JALR
  //   JAL
  //   MTR
  //   MW
  //   RW
  //   lui
  //   MEM.rw
  //   MEM.rd
  //   数据存储器
  //   lb
  //   lb
  //   lui
  //   lui
  //   JALR
  //   JALR
  //   JAL
  //   JAL
  //   MTR
  //   MTR
  //   MTR
  //   MW
  //   MW
  //   RW
  //   RW
  //   halt
  //   halt
endmodule

module \中断输入  (
  input  IRA,
  input  IRB,
  input  IRC,
  input  CLK,
  input  CLR,
  input  IRD,
  input  IRE,
  input  IRF,
  input  IRG,
  input  IRH,
  input  IRI,
  input  IRJ,
  input  IRK,
  input  IRL,
  input  IRM,
  output IRAW,
  output IRBW,
  output IRCW,
  output INTR,
  output [3:0] INT_N,
  output IRDW,
  output IREW,
  output IRFW,
  output IRGW,
  output IRHW,
  output IRIW,
  output IRJW,
  output IRKW,
  output IRLW,
  output IRMW
);

  wire and_1_out, and_2_out, and_3_out, and_4_out, and_5_out, and_6_out, and_7_out, and_8_out, and_9_out,
       and_10_out, and_11_out, and_12_out, and_13_out, and_15_out, CLR1, CLR2, CLR3, CLR4, CLR5, CLR6, CLR7,
       CLR8, CLR9, CLR10, CLR11, CLR12, CLR13, d_ff_1_q, d_ff_2_q, d_ff_3_q, d_ff_4_q, d_ff_5_q, d_ff_6_q,
       d_ff_7_q, d_ff_8_q, d_ff_9_q, d_ff_10_q, d_ff_11_q, d_ff_12_q, d_ff_13_q, d_ff_14_q, d_ff_15_q,
       d_ff_16_q, d_ff_17_q, d_ff_18_q, d_ff_19_q, d_ff_20_q, d_ff_21_q, d_ff_22_q, d_ff_23_q, d_ff_24_q,
       ENINT, or_10_out, or_11_out, or_12_out, or_13_out, or_14_out, or_15_out, or_16_out, or_17_out,
       or_18_out, or_19_out, or_20_out, or_21_out, or_24_out, or_25_out, or_26_out, or_30_out, or_31_out,
       S12, S13, \中断请求 ;
  wire [3:0] INT_N_prime;

  or or_1 (IRAW, d_ff_10_q, d_ff_1_q);
  or or_2 (IRBW, d_ff_11_q, d_ff_2_q);
  or or_3 (IRCW, d_ff_12_q, d_ff_3_q);
  or or_4 (IRDW, d_ff_13_q, d_ff_4_q);
  or or_5 (IREW, d_ff_14_q, d_ff_5_q);
  or or_6 (IRFW, d_ff_15_q, d_ff_6_q);
  D_Flip_Flop #(.trigger("rising"), .Pre_Clr_Positions("LEGACY"), .NegatePresetClear("false"), .enable("true"), .NewFFLayout("false")) d_ff_1 (
    .clk(IRA), .D(1'b1), .Q(d_ff_1_q), .reset(d_ff_10_q));  // open: Qn, preset, en
  D_Flip_Flop #(.trigger("rising"), .Pre_Clr_Positions("LEGACY"), .NegatePresetClear("false"), .enable("true"), .NewFFLayout("false")) d_ff_2 (
    .clk(IRB), .D(1'b1), .Q(d_ff_2_q), .reset(d_ff_11_q));  // open: Qn, preset, en
  D_Flip_Flop #(.trigger("rising"), .Pre_Clr_Positions("LEGACY"), .NegatePresetClear("false"), .enable("true"), .NewFFLayout("false")) d_ff_3 (
    .clk(IRC), .D(1'b1), .Q(d_ff_3_q), .reset(d_ff_12_q));  // open: Qn, preset, en
  D_Flip_Flop #(.trigger("rising"), .Pre_Clr_Positions("LEGACY"), .NegatePresetClear("false"), .enable("true"), .NewFFLayout("false")) d_ff_4 (
    .clk(IRD), .D(1'b1), .Q(d_ff_4_q), .reset(d_ff_13_q));  // open: Qn, preset, en
  D_Flip_Flop #(.trigger("rising"), .Pre_Clr_Positions("LEGACY"), .NegatePresetClear("false"), .enable("true"), .NewFFLayout("false")) d_ff_5 (
    .clk(IRE), .D(1'b1), .Q(d_ff_5_q), .reset(d_ff_14_q));  // open: Qn, preset, en
  D_Flip_Flop #(.trigger("rising"), .Pre_Clr_Positions("LEGACY"), .NegatePresetClear("false"), .enable("true"), .NewFFLayout("false")) d_ff_6 (
    .clk(IRF), .D(1'b1), .Q(d_ff_6_q), .reset(d_ff_15_q));  // open: Qn, preset, en
  or or_7 (IRGW, d_ff_16_q, d_ff_7_q);
  or or_8 (IRHW, d_ff_17_q, d_ff_8_q);
  or or_9 (IRIW, d_ff_18_q, d_ff_9_q);
  or or_10 (or_10_out, d_ff_1_q, d_ff_10_q);
  or or_11 (or_11_out, d_ff_2_q, d_ff_11_q);
  or or_12 (or_12_out, d_ff_3_q, d_ff_12_q);
  or or_13 (or_13_out, d_ff_4_q, d_ff_13_q);
  or or_14 (or_14_out, d_ff_5_q, d_ff_14_q);
  or or_15 (or_15_out, d_ff_6_q, d_ff_15_q);
  D_Flip_Flop #(.trigger("rising"), .Pre_Clr_Positions("LEGACY"), .NegatePresetClear("false"), .enable("true"), .NewFFLayout("false")) d_ff_7 (
    .clk(IRG), .D(1'b1), .Q(d_ff_7_q), .reset(d_ff_16_q));  // open: Qn, preset, en
  D_Flip_Flop #(.trigger("rising"), .Pre_Clr_Positions("LEGACY"), .NegatePresetClear("false"), .enable("true"), .NewFFLayout("false")) d_ff_8 (
    .clk(IRH), .D(1'b1), .Q(d_ff_8_q), .reset(d_ff_17_q));  // open: Qn, preset, en
  D_Flip_Flop #(.trigger("rising"), .Pre_Clr_Positions("LEGACY"), .NegatePresetClear("false"), .enable("true"), .NewFFLayout("false")) d_ff_9 (
    .clk(IRI), .D(1'b1), .Q(d_ff_9_q), .reset(d_ff_18_q));  // open: Qn, preset, en
  and and_1 (and_1_out, or_10_out, ~CLR1);  // AND_Gate
  and and_2 (and_2_out, or_11_out, ~CLR2);  // AND_Gate
  and and_3 (and_3_out, or_12_out, ~CLR3);  // AND_Gate
  and and_4 (and_4_out, or_13_out, ~CLR4);  // AND_Gate
  and and_5 (and_5_out, or_14_out, ~CLR5);  // AND_Gate
  and and_6 (and_6_out, or_15_out, ~CLR6);  // AND_Gate
  or or_16 (or_16_out, d_ff_7_q, d_ff_16_q);
  or or_17 (or_17_out, d_ff_8_q, d_ff_17_q);
  or or_18 (or_18_out, d_ff_9_q, d_ff_18_q);
  D_Flip_Flop #(.trigger("rising"), .Pre_Clr_Positions("LEGACY"), .NegatePresetClear("false"), .enable("true"), .NewFFLayout("false")) d_ff_10 (
    .clk(CLK), .D(and_1_out), .Q(d_ff_10_q));  // open: Qn, preset, en, reset
  D_Flip_Flop #(.trigger("rising"), .Pre_Clr_Positions("LEGACY"), .NegatePresetClear("false"), .enable("true"), .NewFFLayout("false")) d_ff_11 (
    .clk(CLK), .D(and_2_out), .Q(d_ff_11_q));  // open: Qn, preset, en, reset
  D_Flip_Flop #(.trigger("rising"), .Pre_Clr_Positions("LEGACY"), .NegatePresetClear("false"), .enable("true"), .NewFFLayout("false")) d_ff_12 (
    .clk(CLK), .D(and_3_out), .Q(d_ff_12_q));  // open: Qn, preset, en, reset
  D_Flip_Flop #(.trigger("rising"), .Pre_Clr_Positions("LEGACY"), .NegatePresetClear("false"), .enable("true"), .NewFFLayout("false")) d_ff_13 (
    .clk(CLK), .D(and_4_out), .Q(d_ff_13_q));  // open: Qn, preset, en, reset
  D_Flip_Flop #(.trigger("rising"), .Pre_Clr_Positions("LEGACY"), .NegatePresetClear("false"), .enable("true"), .NewFFLayout("false")) d_ff_14 (
    .clk(CLK), .D(and_5_out), .Q(d_ff_14_q));  // open: Qn, preset, en, reset
  D_Flip_Flop #(.trigger("rising"), .Pre_Clr_Positions("LEGACY"), .NegatePresetClear("false"), .enable("true"), .NewFFLayout("false")) d_ff_15 (
    .clk(CLK), .D(and_6_out), .Q(d_ff_15_q));  // open: Qn, preset, en, reset
  and and_7 (and_7_out, or_16_out, ~CLR7);  // AND_Gate
  and and_8 (and_8_out, or_17_out, ~CLR8);  // AND_Gate
  and and_9 (and_9_out, or_18_out, ~CLR9);  // AND_Gate
  or or_19 (or_19_out, d_ff_13_q, d_ff_14_q, d_ff_15_q);
  D_Flip_Flop #(.trigger("rising"), .Pre_Clr_Positions("LEGACY"), .NegatePresetClear("false"), .enable("true"), .NewFFLayout("false")) d_ff_16 (
    .clk(CLK), .D(and_7_out), .Q(d_ff_16_q));  // open: Qn, preset, en, reset
  D_Flip_Flop #(.trigger("rising"), .Pre_Clr_Positions("LEGACY"), .NegatePresetClear("false"), .enable("true"), .NewFFLayout("false")) d_ff_17 (
    .clk(CLK), .D(and_8_out), .Q(d_ff_17_q));  // open: Qn, preset, en, reset
  D_Flip_Flop #(.trigger("rising"), .Pre_Clr_Positions("LEGACY"), .NegatePresetClear("false"), .enable("true"), .NewFFLayout("false")) d_ff_18 (
    .clk(CLK), .D(and_9_out), .Q(d_ff_18_q));  // open: Qn, preset, en, reset
  Priority_Encoder #(.select(4), .disabled("Z")) priority_encoder_1 (
    .in0(1'b1), .in1(d_ff_10_q), .in2(d_ff_11_q), .in3(d_ff_12_q), .in4(d_ff_13_q), .in5(d_ff_14_q),
    .in6(d_ff_15_q), .in7(d_ff_16_q), .in8(d_ff_17_q), .in9(d_ff_18_q), .in10(d_ff_22_q), .in11(d_ff_21_q),
    .in12(S12), .in13(S13), .out(INT_N));  // open: in14, in15, gs, en_out, en_in
  or or_20 (or_20_out, d_ff_12_q, d_ff_11_q, d_ff_10_q);
  or or_21 (or_21_out, d_ff_16_q, d_ff_17_q, d_ff_18_q);
  D_Flip_Flop #(.trigger("rising"), .Pre_Clr_Positions("LEGACY"), .NegatePresetClear("false"), .enable("true"), .NewFFLayout("false")) d_ff_19 (
    .clk(IRK), .D(1'b1), .Q(d_ff_19_q), .reset(d_ff_21_q));  // open: Qn, preset, en
  or or_22 (IRKW, d_ff_21_q, d_ff_19_q);
  or or_23 (IRJW, d_ff_22_q, d_ff_20_q);
  Register #(.width(4), .trigger("rising"), .Select("low")) register_1 (
    .D(INT_N), .en(\中断请求 ), .Q(INT_N_prime), .clk(CLK));  // open: clr
  D_Flip_Flop #(.trigger("rising"), .Pre_Clr_Positions("LEGACY"), .NegatePresetClear("false"), .enable("true"), .NewFFLayout("false")) d_ff_20 (
    .clk(IRJ), .D(1'b1), .Q(d_ff_20_q), .reset(d_ff_22_q));  // open: Qn, preset, en
  or or_24 (or_24_out, d_ff_19_q, d_ff_21_q);
  and and_10 (and_10_out, or_24_out, ~CLR11);  // AND_Gate
  or or_25 (or_25_out, d_ff_20_q, d_ff_22_q);
  and and_11 (and_11_out, or_25_out, ~CLR10);  // AND_Gate
  or or_26 (or_26_out, S12, d_ff_22_q, d_ff_21_q, S13);
  D_Flip_Flop #(.trigger("rising"), .Pre_Clr_Positions("LEGACY"), .NegatePresetClear("false"), .enable("true"), .NewFFLayout("false")) d_ff_21 (
    .clk(CLK), .D(and_10_out), .Q(d_ff_21_q));  // open: Qn, preset, en, reset
  D_Flip_Flop #(.trigger("rising"), .Pre_Clr_Positions("LEGACY"), .NegatePresetClear("false"), .enable("true"), .NewFFLayout("false")) d_ff_22 (
    .clk(CLK), .D(and_11_out), .Q(d_ff_22_q));  // open: Qn, preset, en, reset
  or or_27 (INTR, or_19_out, or_26_out, or_20_out, or_21_out);
  or or_28 (IRMW, S13, d_ff_23_q);
  or or_29 (IRLW, S12, d_ff_24_q);
  D_Flip_Flop #(.trigger("rising"), .Pre_Clr_Positions("LEGACY"), .NegatePresetClear("false"), .enable("true"), .NewFFLayout("false")) d_ff_23 (
    .clk(IRM), .D(1'b1), .Q(d_ff_23_q), .reset(S13));  // open: Qn, preset, en
  D_Flip_Flop #(.trigger("rising"), .Pre_Clr_Positions("LEGACY"), .NegatePresetClear("false"), .enable("true"), .NewFFLayout("false")) d_ff_24 (
    .clk(IRL), .D(1'b1), .Q(d_ff_24_q), .reset(S12));  // open: Qn, preset, en
  or or_30 (or_30_out, d_ff_23_q, S13);
  or or_31 (or_31_out, d_ff_24_q, S12);
  and and_12 (and_12_out, or_30_out, ~CLR13);  // AND_Gate
  Decoder #(.select(4), .tristate("false"), .disabled(0), .enable("true")) decoder_1 (
    .out1(CLR1), .out2(CLR2), .out3(CLR3), .out4(CLR4), .out5(CLR5), .out6(CLR6), .out7(CLR7), .out8(CLR8),
    .out9(CLR9), .out10(CLR10), .out11(CLR11), .out12(CLR12), .out13(CLR13), .sel(INT_N_prime), .en(CLR));  // open: out0, out14, out15
  and and_13 (and_13_out, or_31_out, ~CLR12);  // AND_Gate
  D_Flip_Flop #(.trigger("rising"), .Pre_Clr_Positions("LEGACY"), .NegatePresetClear("false"), .enable("true"), .NewFFLayout("false")) d_ff_25 (
    .clk(CLK), .D(and_12_out), .Q(S13));  // open: Qn, preset, en, reset
  D_Flip_Flop #(.trigger("rising"), .Pre_Clr_Positions("LEGACY"), .NegatePresetClear("false"), .enable("true"), .NewFFLayout("false")) d_ff_26 (
    .clk(CLK), .D(and_13_out), .Q(S12));  // open: Qn, preset, en, reset
  and and_14 (\中断请求 , ENINT, INTR);
  and and_15 (and_15_out, ~CLR, INTR);  // AND_Gate
  D_Flip_Flop #(.trigger("rising"), .Pre_Clr_Positions("LEGACY"), .NegatePresetClear("false"), .enable("true"), .NewFFLayout("false")) d_ff_27 (
    .clk(CLK), .D(and_15_out), .Qn(ENINT));  // open: Q, preset, en, reset

  // Notes on the sheet:
  //   当前处理的中断
endmodule

module \输出逻辑  (
  input  out,
  input  [31:0] \reg ,
  input  CLK,
  input  en,
  input  rst,
  output [31:0] D10,
  output [31:0] D0,
  output [31:0] D1,
  output [31:0] D2,
  output [31:0] D3,
  output [31:0] D4,
  output [31:0] D5,
  output [31:0] D6,
  output [31:0] D7,
  output [31:0] D8,
  output [31:0] D9,
  output [31:0] D11,
  output [31:0] D12,
  output [31:0] D13,
  output [31:0] D14,
  output [31:0] D15,
  output [31:0] D16,
  output [31:0] D17,
  output [31:0] D18,
  output [31:0] D19,
  output [31:0] D20,
  output [31:0] D22,
  output [31:0] D23,
  output [31:0] D24,
  output [31:0] D25,
  output [31:0] D26,
  output [31:0] D27,
  output [31:0] D28,
  output [31:0] D29,
  output [31:0] D30,
  output [31:0] D31,
  output [31:0] D21
);

  wire _10, _11, _12, _20, _21, _22, _30, _31, _32, _40, _41, _42, _50, _51, _52, _60, _61, _62, _70, _71,
       _72, _80, _81, _82, _90, _91, _92, and_1_out, and_2_out, and_3_out, and_4_out, and_5_out, and_6_out,
       and_7_out, and_8_out, and_9_out, and_10_out, and_11_out, and_12_out, and_13_out, and_14_out,
       and_15_out, and_16_out, and_17_out, and_18_out, and_19_out, and_20_out, and_21_out, and_22_out,
       and_23_out, and_24_out, and_25_out, and_26_out, and_27_out, and_28_out, and_29_out, and_30_out,
       and_31_out, and_32_out, and_33_out, and_34_out, and_35_out, and_36_out, and_37_out, and_38_out,
       and_39_out, and_40_out, and_41_out, and_42_out, and_43_out, and_44_out, and_45_out, and_46_out,
       and_47_out, and_48_out, and_49_out, and_50_out, and_51_out, and_52_out, and_53_out, and_54_out,
       and_55_out, and_56_out, and_57_out, and_58_out, and_59_out, and_60_out, and_61_out, and_62_out,
       and_63_out, and_64_out, and_65_out, and_66_out, and_67_out, and_68_out, and_69_out, and_70_out,
       and_71_out, and_72_out, and_73_out, and_74_out, and_75_out, and_76_out, and_77_out, and_78_out,
       and_79_out, and_80_out, and_81_out, comparator_1_eq, comparator_2_eq, comparator_3_eq,
       comparator_22_eq, comparator_23_eq, comparator_24_eq, comparator_34_eq, comparator_35_eq,
       comparator_36_eq, comparator_37_eq, comparator_38_eq, comparator_39_eq, comparator_40_eq,
       register_7_q, register_12_q, register_14_q, register_16_q, up;
  wire [7:0] cnt;
  wire [13:0] controlled_buffer_1_out, controlled_buffer_28_out, controlled_buffer_55_out, RAW1, RAW2, RAW3;
  wire [31:0] R1, R2, R3, R4, R5, R6, R7, R8, R9;

  ROM #(.addrWidth(14), .dataWidth(32), .Select("high")) rom_1 (.addr(RAW1), .data(D0));
  ROM #(.addrWidth(14), .dataWidth(32), .Select("high")) rom_2 (.addr(RAW1), .data(D1));
  ROM #(.addrWidth(14), .dataWidth(32), .Select("high")) rom_3 (.addr(RAW1), .data(D2));
  ROM #(.addrWidth(14), .dataWidth(32), .Select("high")) rom_4 (.addr(RAW1), .data(D3));
  ROM #(.addrWidth(14), .dataWidth(32), .Select("high")) rom_5 (.addr(RAW1), .data(D4));
  ROM #(.addrWidth(14), .dataWidth(32), .Select("high")) rom_6 (.addr(RAW1), .data(D5));
  ROM #(.addrWidth(14), .dataWidth(32), .Select("high")) rom_7 (.addr(RAW1), .data(D6));
  ROM #(.addrWidth(14), .dataWidth(32), .Select("high")) rom_8 (.addr(RAW1), .data(D7));
  ROM #(.addrWidth(14), .dataWidth(32), .Select("high")) rom_9 (.addr(RAW1), .data(D8));
  ROM #(.addrWidth(14), .dataWidth(32), .Select("high")) rom_10 (.addr(RAW1), .data(D9));
  ROM #(.addrWidth(14), .dataWidth(32), .Select("high")) rom_11 (.addr(RAW2), .data(D11));
  ROM #(.addrWidth(14), .dataWidth(32), .Select("high")) rom_12 (.addr(RAW2), .data(D12));
  ROM #(.addrWidth(14), .dataWidth(32), .Select("high")) rom_13 (.addr(RAW2), .data(D13));
  ROM #(.addrWidth(14), .dataWidth(32), .Select("high")) rom_14 (.addr(RAW2), .data(D14));
  ROM #(.addrWidth(14), .dataWidth(32), .Select("high")) rom_15 (.addr(RAW2), .data(D15));
  ROM #(.addrWidth(14), .dataWidth(32), .Select("high")) rom_16 (.addr(RAW2), .data(D16));
  ROM #(.addrWidth(14), .dataWidth(32), .Select("high")) rom_17 (.addr(RAW2), .data(D17));
  ROM #(.addrWidth(14), .dataWidth(32), .Select("high")) rom_18 (.addr(RAW2), .data(D18));
  ROM #(.addrWidth(14), .dataWidth(32), .Select("high")) rom_19 (.addr(RAW2), .data(D19));
  ROM #(.addrWidth(14), .dataWidth(32), .Select("high")) rom_20 (.addr(RAW2), .data(D20));
  ROM #(.addrWidth(14), .dataWidth(32), .Select("high")) rom_21 (.addr(RAW3), .data(D22));
  ROM #(.addrWidth(14), .dataWidth(32), .Select("high")) rom_22 (.addr(RAW3), .data(D23));
  ROM #(.addrWidth(14), .dataWidth(32), .Select("high")) rom_23 (.addr(RAW3), .data(D24));
  ROM #(.addrWidth(14), .dataWidth(32), .Select("high")) rom_24 (.addr(RAW3), .data(D25));
  ROM #(.addrWidth(14), .dataWidth(32), .Select("high")) rom_25 (.addr(RAW3), .data(D26));
  ROM #(.addrWidth(14), .dataWidth(32), .Select("high")) rom_26 (.addr(RAW3), .data(D27));
  ROM #(.addrWidth(14), .dataWidth(32), .Select("high")) rom_27 (.addr(RAW3), .data(D28));
  ROM #(.addrWidth(14), .dataWidth(32), .Select("high")) rom_28 (.addr(RAW3), .data(D29));
  ROM #(.addrWidth(14), .dataWidth(32), .Select("high")) rom_29 (.addr(RAW3), .data(D30));
  ROM #(.addrWidth(14), .dataWidth(32), .Select("high")) rom_30 (.addr(RAW3), .data(D31));
  DotMatrix #(.inputtype("row"), .matrixcols(32), .matrixrows(32), .persist(0), .dotshape("circle")) dotmatrix_1 (
    .row0(D0), .row1(D1), .row2(D2), .row3(D3), .row4(D4), .row5(D5), .row6(D6), .row7(D7), .row8(D8),
    .row9(D9), .row10({32{1'b1}}), .row11(D11), .row12(D12), .row13(D13), .row14(D14), .row15(D15),
    .row16(D16), .row17(D17), .row18(D18), .row19(D19), .row20(D20), .row21({32{1'b1}}), .row22(D22),
    .row23(D23), .row24(D24), .row25(D25), .row26(D26), .row27(D27), .row28(D28), .row29(D29), .row30(D30),
    .row31(D31));
  Comparator #(.width(8), .mode("twosComplement")) comparator_1 (
    .a(cnt), .b({8{1'b0}}), .eq(comparator_1_eq));  // open: gt, lt
  Comparator #(.width(8), .mode("twosComplement")) comparator_2 (
    .a(cnt), .b(8'h1), .eq(comparator_2_eq));  // open: gt, lt
  Comparator #(.width(8), .mode("twosComplement")) comparator_3 (
    .a(cnt), .b(8'h2), .eq(comparator_3_eq));  // open: gt, lt
  Comparator #(.width(32), .mode("twosComplement")) comparator_4 (.a({32{1'b0}}), .b(R1), .eq(_10));  // open: gt, lt
  Comparator #(.width(32), .mode("twosComplement")) comparator_5 (.a(32'h1), .b(R1), .eq(_11));  // open: gt, lt
  Comparator #(.width(32), .mode("twosComplement")) comparator_6 (.a({32{1'b1}}), .b(R1), .eq(_12));  // open: gt, lt
  Comparator #(.width(32), .mode("twosComplement")) comparator_7 (.a({32{1'b0}}), .b(R4), .eq(_40));  // open: gt, lt
  Comparator #(.width(32), .mode("twosComplement")) comparator_8 (.a(32'h1), .b(R4), .eq(_41));  // open: gt, lt
  Comparator #(.width(32), .mode("twosComplement")) comparator_9 (.a({32{1'b1}}), .b(R4), .eq(_42));  // open: gt, lt
  Comparator #(.width(32), .mode("twosComplement")) comparator_10 (.a({32{1'b0}}), .b(R7), .eq(_70));  // open: gt, lt
  Comparator #(.width(32), .mode("twosComplement")) comparator_11 (.a(32'h1), .b(R7), .eq(_71));  // open: gt, lt
  Comparator #(.width(32), .mode("twosComplement")) comparator_12 (.a({32{1'b1}}), .b(R7), .eq(_72));  // open: gt, lt
  Register #(.width(32), .trigger("rising"), .Select("low")) register_1 (
    .D(\reg ), .en(comparator_1_eq), .Q(R1), .clk(CLK));  // open: clr
  Register #(.width(32), .trigger("rising"), .Select("low")) register_2 (
    .D(\reg ), .en(comparator_2_eq), .Q(R2), .clk(CLK));  // open: clr
  Register #(.width(32), .trigger("rising"), .Select("low")) register_3 (
    .D(\reg ), .en(comparator_3_eq), .Q(R3), .clk(CLK));  // open: clr
  Comparator #(.width(32), .mode("twosComplement")) comparator_13 (.a({32{1'b0}}), .b(R2), .eq(_20));  // open: gt, lt
  Comparator #(.width(32), .mode("twosComplement")) comparator_14 (.a(32'h1), .b(R2), .eq(_21));  // open: gt, lt
  Comparator #(.width(32), .mode("twosComplement")) comparator_15 (.a({32{1'b1}}), .b(R2), .eq(_22));  // open: gt, lt
  Comparator #(.width(32), .mode("twosComplement")) comparator_16 (.a({32{1'b0}}), .b(R5), .eq(_50));  // open: gt, lt
  Comparator #(.width(32), .mode("twosComplement")) comparator_17 (.a(32'h1), .b(R5), .eq(_51));  // open: gt, lt
  Comparator #(.width(32), .mode("twosComplement")) comparator_18 (.a({32{1'b1}}), .b(R5), .eq(_52));  // open: gt, lt
  Comparator #(.width(32), .mode("twosComplement")) comparator_19 (.a({32{1'b0}}), .b(R8), .eq(_80));  // open: gt, lt
  Comparator #(.width(32), .mode("twosComplement")) comparator_20 (.a(32'h1), .b(R8), .eq(_81));  // open: gt, lt
  Comparator #(.width(32), .mode("twosComplement")) comparator_21 (.a({32{1'b1}}), .b(R8), .eq(_82));  // open: gt, lt
  Counter #(.width(8), .max('hff), .ongoal("wrap"), .trigger("rising"), .behavior("new")) counter_1 (
    .Q(cnt), .clk(up), .clr(comparator_34_eq));  // open: load, D, count, carry, preset, down
  Comparator #(.width(8), .mode("twosComplement")) comparator_22 (
    .a(cnt), .b(8'h3), .eq(comparator_22_eq));  // open: gt, lt
  Comparator #(.width(8), .mode("twosComplement")) comparator_23 (
    .a(cnt), .b(8'h4), .eq(comparator_23_eq));  // open: gt, lt
  Comparator #(.width(8), .mode("twosComplement")) comparator_24 (
    .a(cnt), .b(8'h5), .eq(comparator_24_eq));  // open: gt, lt
  Comparator #(.width(32), .mode("twosComplement")) comparator_25 (.a({32{1'b0}}), .b(R3), .eq(_30));  // open: gt, lt
  Comparator #(.width(32), .mode("twosComplement")) comparator_26 (.a(32'h1), .b(R3), .eq(_31));  // open: gt, lt
  Comparator #(.width(32), .mode("twosComplement")) comparator_27 (.a({32{1'b1}}), .b(R3), .eq(_32));  // open: gt, lt
  Comparator #(.width(32), .mode("twosComplement")) comparator_28 (.a({32{1'b0}}), .b(R6), .eq(_60));  // open: gt, lt
  Comparator #(.width(32), .mode("twosComplement")) comparator_29 (.a(32'h1), .b(R6), .eq(_61));  // open: gt, lt
  Comparator #(.width(32), .mode("twosComplement")) comparator_30 (.a({32{1'b1}}), .b(R6), .eq(_62));  // open: gt, lt
  Comparator #(.width(32), .mode("twosComplement")) comparator_31 (.a({32{1'b0}}), .b(R9), .eq(_90));  // open: gt, lt
  Comparator #(.width(32), .mode("twosComplement")) comparator_32 (.a(32'h1), .b(R9), .eq(_91));  // open: gt, lt
  Comparator #(.width(32), .mode("twosComplement")) comparator_33 (.a({32{1'b1}}), .b(R9), .eq(_92));  // open: gt, lt
  Register #(.width(32), .trigger("rising"), .Select("low")) register_4 (
    .D(\reg ), .en(comparator_22_eq), .Q(R4), .clk(CLK));  // open: clr
  Register #(.width(32), .trigger("rising"), .Select("low")) register_5 (
    .D(\reg ), .en(comparator_23_eq), .Q(R5), .clk(CLK));  // open: clr
  Register #(.width(32), .trigger("rising"), .Select("low")) register_6 (
    .D(\reg ), .en(comparator_24_eq), .Q(R6), .clk(CLK));  // open: clr
  Comparator #(.width(8), .mode("twosComplement")) comparator_34 (
    .a(8'h9), .b(cnt), .eq(comparator_34_eq));  // open: gt, lt
  Register #(.width(1), .trigger("rising"), .Select("low")) register_7 (
    .D(out), .Q(register_7_q), .clk(CLK));  // open: en, clr
  Register #(.width(1), .trigger("rising"), .Select("low")) register_8 (
    .D(register_7_q), .Q(up), .clk(CLK));  // open: en, clr
  Comparator #(.width(8), .mode("twosComplement")) comparator_35 (
    .a(cnt), .b(8'h6), .eq(comparator_35_eq));  // open: gt, lt
  Comparator #(.width(8), .mode("twosComplement")) comparator_36 (
    .a(cnt), .b(8'h7), .eq(comparator_36_eq));  // open: gt, lt
  Comparator #(.width(8), .mode("twosComplement")) comparator_37 (
    .a(cnt), .b(8'h8), .eq(comparator_37_eq));  // open: gt, lt
  Register #(.width(32), .trigger("rising"), .Select("low")) register_9 (
    .D(\reg ), .en(comparator_35_eq), .Q(R7), .clk(CLK));  // open: clr
  Register #(.width(32), .trigger("rising"), .Select("low")) register_10 (
    .D(\reg ), .en(comparator_36_eq), .Q(R8), .clk(CLK));  // open: clr
  Register #(.width(32), .trigger("rising"), .Select("low")) register_11 (
    .D(\reg ), .en(comparator_37_eq), .Q(R9), .clk(CLK));  // open: clr
  and and_1 (and_1_out, _10, _20, _30);
  and and_2 (and_2_out, _10, _20, _31);
  and and_3 (and_3_out, _10, _20, _32);
  and and_4 (and_4_out, _10, _21, _30);
  and and_5 (and_5_out, _10, _21, _31);
  and and_6 (and_6_out, _10, _21, _32);
  and and_7 (and_7_out, _10, _22, _30);
  and and_8 (and_8_out, _10, _22, _31);
  and and_9 (and_9_out, _10, _22, _32);
  and and_10 (and_10_out, _11, _20, _30);
  and and_11 (and_11_out, _11, _20, _31);
  and and_12 (and_12_out, _11, _20, _32);
  and and_13 (and_13_out, _11, _21, _30);
  and and_14 (and_14_out, _11, _21, _31);
  and and_15 (and_15_out, _11, _21, _32);
  and and_16 (and_16_out, _11, _22, _30);
  and and_17 (and_17_out, _11, _22, _31);
  and and_18 (and_18_out, _11, _22, _32);
  and and_19 (and_19_out, _12, _20, _30);
  and and_20 (and_20_out, _12, _20, _31);
  and and_21 (and_21_out, _12, _20, _32);
  and and_22 (and_22_out, _12, _21, _30);
  and and_23 (and_23_out, _12, _21, _31);
  and and_24 (and_24_out, _12, _21, _32);
  and and_25 (and_25_out, _12, _22, _30);
  and and_26 (and_26_out, _12, _22, _31);
  and and_27 (and_27_out, _12, _22, _32);
  assign controlled_buffer_1_out = and_1_out ? {14{1'b0}} : 14'bz;  // Controlled_Buffer controlled_buffer_1
  assign controlled_buffer_1_out = and_2_out ? 14'h1 : 14'bz;  // Controlled_Buffer controlled_buffer_2
  assign controlled_buffer_1_out = and_3_out ? 14'h2 : 14'bz;  // Controlled_Buffer controlled_buffer_3
  assign controlled_buffer_1_out = and_4_out ? 14'h3 : 14'bz;  // Controlled_Buffer controlled_buffer_4
  assign controlled_buffer_1_out = and_5_out ? 14'h4 : 14'bz;  // Controlled_Buffer controlled_buffer_5
  assign controlled_buffer_1_out = and_6_out ? 14'h5 : 14'bz;  // Controlled_Buffer controlled_buffer_6
  assign controlled_buffer_1_out = and_7_out ? 14'h6 : 14'bz;  // Controlled_Buffer controlled_buffer_7
  assign controlled_buffer_1_out = and_8_out ? 14'h7 : 14'bz;  // Controlled_Buffer controlled_buffer_8
  assign controlled_buffer_1_out = and_9_out ? 14'h8 : 14'bz;  // Controlled_Buffer controlled_buffer_9
  assign controlled_buffer_1_out = and_10_out ? 14'h9 : 14'bz;  // Controlled_Buffer controlled_buffer_10
  assign controlled_buffer_1_out = and_11_out ? 14'ha : 14'bz;  // Controlled_Buffer controlled_buffer_11
  assign controlled_buffer_1_out = and_12_out ? 14'hb : 14'bz;  // Controlled_Buffer controlled_buffer_12
  assign controlled_buffer_1_out = and_13_out ? 14'hc : 14'bz;  // Controlled_Buffer controlled_buffer_13
  assign controlled_buffer_1_out = and_14_out ? 14'hd : 14'bz;  // Controlled_Buffer controlled_buffer_14
  assign controlled_buffer_1_out = and_15_out ? 14'he : 14'bz;  // Controlled_Buffer controlled_buffer_15
  assign controlled_buffer_1_out = and_16_out ? 14'hf : 14'bz;  // Controlled_Buffer controlled_buffer_16
  assign controlled_buffer_1_out = and_17_out ? 14'h10 : 14'bz;  // Controlled_Buffer controlled_buffer_17
  assign controlled_buffer_1_out = and_18_out ? 14'h11 : 14'bz;  // Controlled_Buffer controlled_buffer_18
  assign controlled_buffer_1_out = and_19_out ? 14'h12 : 14'bz;  // Controlled_Buffer controlled_buffer_19
  assign controlled_buffer_1_out = and_20_out ? 14'h13 : 14'bz;  // Controlled_Buffer controlled_buffer_20
  assign controlled_buffer_1_out = and_21_out ? 14'h14 : 14'bz;  // Controlled_Buffer controlled_buffer_21
  assign controlled_buffer_1_out = and_22_out ? 14'h15 : 14'bz;  // Controlled_Buffer controlled_buffer_22
  assign controlled_buffer_1_out = and_23_out ? 14'h16 : 14'bz;  // Controlled_Buffer controlled_buffer_23
  assign controlled_buffer_1_out = and_24_out ? 14'h17 : 14'bz;  // Controlled_Buffer controlled_buffer_24
  assign controlled_buffer_1_out = and_25_out ? 14'h18 : 14'bz;  // Controlled_Buffer controlled_buffer_25
  assign controlled_buffer_1_out = and_26_out ? 14'h19 : 14'bz;  // Controlled_Buffer controlled_buffer_26
  assign controlled_buffer_1_out = and_27_out ? 14'h1a : 14'bz;  // Controlled_Buffer controlled_buffer_27
  Comparator #(.width(8), .mode("twosComplement")) comparator_38 (
    .a(cnt), .b(8'h2), .eq(comparator_38_eq));  // open: gt, lt
  Register #(.width(1), .trigger("rising"), .Select("low")) register_12 (
    .D(comparator_38_eq), .Q(register_12_q), .clk(CLK));  // open: en, clr
  Register #(.width(14), .trigger("rising"), .Select("low")) register_13 (
    .D(controlled_buffer_1_out), .en(register_12_q), .Q(RAW1), .clk(CLK));  // open: clr
  and and_28 (and_28_out, _40, _50, _60);
  and and_29 (and_29_out, _40, _50, _61);
  and and_30 (and_30_out, _40, _50, _62);
  and and_31 (and_31_out, _40, _51, _60);
  and and_32 (and_32_out, _40, _51, _61);
  and and_33 (and_33_out, _40, _51, _62);
  and and_34 (and_34_out, _40, _52, _60);
  and and_35 (and_35_out, _40, _52, _61);
  and and_36 (and_36_out, _40, _52, _62);
  and and_37 (and_37_out, _41, _50, _60);
  and and_38 (and_38_out, _41, _50, _61);
  and and_39 (and_39_out, _41, _50, _62);
  and and_40 (and_40_out, _41, _51, _60);
  and and_41 (and_41_out, _41, _51, _61);
  and and_42 (and_42_out, _41, _51, _62);
  and and_43 (and_43_out, _41, _52, _60);
  and and_44 (and_44_out, _41, _52, _61);
  and and_45 (and_45_out, _41, _52, _62);
  and and_46 (and_46_out, _42, _50, _60);
  and and_47 (and_47_out, _42, _50, _61);
  and and_48 (and_48_out, _42, _50, _62);
  and and_49 (and_49_out, _42, _51, _60);
  and and_50 (and_50_out, _42, _51, _61);
  and and_51 (and_51_out, _42, _51, _62);
  and and_52 (and_52_out, _42, _52, _60);
  and and_53 (and_53_out, _42, _52, _61);
  and and_54 (and_54_out, _42, _52, _62);
  assign controlled_buffer_28_out = and_28_out ? {14{1'b0}} : 14'bz;  // Controlled_Buffer controlled_buffer_28
  assign controlled_buffer_28_out = and_29_out ? 14'h1 : 14'bz;  // Controlled_Buffer controlled_buffer_29
  assign controlled_buffer_28_out = and_30_out ? 14'h2 : 14'bz;  // Controlled_Buffer controlled_buffer_30
  assign controlled_buffer_28_out = and_31_out ? 14'h3 : 14'bz;  // Controlled_Buffer controlled_buffer_31
  assign controlled_buffer_28_out = and_32_out ? 14'h4 : 14'bz;  // Controlled_Buffer controlled_buffer_32
  assign controlled_buffer_28_out = and_33_out ? 14'h5 : 14'bz;  // Controlled_Buffer controlled_buffer_33
  assign controlled_buffer_28_out = and_34_out ? 14'h6 : 14'bz;  // Controlled_Buffer controlled_buffer_34
  assign controlled_buffer_28_out = and_35_out ? 14'h7 : 14'bz;  // Controlled_Buffer controlled_buffer_35
  assign controlled_buffer_28_out = and_36_out ? 14'h8 : 14'bz;  // Controlled_Buffer controlled_buffer_36
  assign controlled_buffer_28_out = and_37_out ? 14'h9 : 14'bz;  // Controlled_Buffer controlled_buffer_37
  assign controlled_buffer_28_out = and_38_out ? 14'ha : 14'bz;  // Controlled_Buffer controlled_buffer_38
  assign controlled_buffer_28_out = and_39_out ? 14'hb : 14'bz;  // Controlled_Buffer controlled_buffer_39
  assign controlled_buffer_28_out = and_40_out ? 14'hc : 14'bz;  // Controlled_Buffer controlled_buffer_40
  assign controlled_buffer_28_out = and_41_out ? 14'hd : 14'bz;  // Controlled_Buffer controlled_buffer_41
  assign controlled_buffer_28_out = and_42_out ? 14'he : 14'bz;  // Controlled_Buffer controlled_buffer_42
  assign controlled_buffer_28_out = and_43_out ? 14'hf : 14'bz;  // Controlled_Buffer controlled_buffer_43
  assign controlled_buffer_28_out = and_44_out ? 14'h10 : 14'bz;  // Controlled_Buffer controlled_buffer_44
  assign controlled_buffer_28_out = and_45_out ? 14'h11 : 14'bz;  // Controlled_Buffer controlled_buffer_45
  assign controlled_buffer_28_out = and_46_out ? 14'h12 : 14'bz;  // Controlled_Buffer controlled_buffer_46
  assign controlled_buffer_28_out = and_47_out ? 14'h13 : 14'bz;  // Controlled_Buffer controlled_buffer_47
  assign controlled_buffer_28_out = and_48_out ? 14'h14 : 14'bz;  // Controlled_Buffer controlled_buffer_48
  assign controlled_buffer_28_out = and_49_out ? 14'h15 : 14'bz;  // Controlled_Buffer controlled_buffer_49
  assign controlled_buffer_28_out = and_50_out ? 14'h16 : 14'bz;  // Controlled_Buffer controlled_buffer_50
  assign controlled_buffer_28_out = and_51_out ? 14'h17 : 14'bz;  // Controlled_Buffer controlled_buffer_51
  assign controlled_buffer_28_out = and_52_out ? 14'h18 : 14'bz;  // Controlled_Buffer controlled_buffer_52
  assign controlled_buffer_28_out = and_53_out ? 14'h19 : 14'bz;  // Controlled_Buffer controlled_buffer_53
  assign controlled_buffer_28_out = and_54_out ? 14'h1a : 14'bz;  // Controlled_Buffer controlled_buffer_54
  Comparator #(.width(8), .mode("twosComplement")) comparator_39 (
    .a(cnt), .b(8'h5), .eq(comparator_39_eq));  // open: gt, lt
  Register #(.width(1), .trigger("rising"), .Select("low")) register_14 (
    .D(comparator_39_eq), .Q(register_14_q), .clk(CLK));  // open: en, clr
  Register #(.width(14), .trigger("rising"), .Select("low")) register_15 (
    .D(controlled_buffer_28_out), .en(register_14_q), .Q(RAW2), .clk(CLK));  // open: clr
  and and_55 (and_55_out, _70, _80, _90);
  and and_56 (and_56_out, _70, _80, _91);
  and and_57 (and_57_out, _70, _80, _92);
  and and_58 (and_58_out, _70, _81, _90);
  and and_59 (and_59_out, _70, _81, _91);
  and and_60 (and_60_out, _70, _81, _92);
  and and_61 (and_61_out, _70, _82, _90);
  and and_62 (and_62_out, _70, _82, _91);
  and and_63 (and_63_out, _70, _82, _92);
  and and_64 (and_64_out, _71, _80, _90);
  and and_65 (and_65_out, _71, _80, _91);
  and and_66 (and_66_out, _71, _80, _92);
  and and_67 (and_67_out, _71, _81, _90);
  and and_68 (and_68_out, _71, _81, _91);
  and and_69 (and_69_out, _71, _81, _92);
  and and_70 (and_70_out, _71, _82, _90);
  and and_71 (and_71_out, _71, _82, _91);
  and and_72 (and_72_out, _71, _82, _92);
  and and_73 (and_73_out, _72, _80, _90);
  and and_74 (and_74_out, _72, _80, _91);
  and and_75 (and_75_out, _72, _80, _92);
  and and_76 (and_76_out, _72, _81, _90);
  and and_77 (and_77_out, _72, _81, _91);
  and and_78 (and_78_out, _72, _81, _92);
  and and_79 (and_79_out, _72, _82, _90);
  and and_80 (and_80_out, _72, _82, _91);
  and and_81 (and_81_out, _72, _82, _92);
  assign controlled_buffer_55_out = and_55_out ? {14{1'b0}} : 14'bz;  // Controlled_Buffer controlled_buffer_55
  assign controlled_buffer_55_out = and_56_out ? 14'h1 : 14'bz;  // Controlled_Buffer controlled_buffer_56
  assign controlled_buffer_55_out = and_57_out ? 14'h2 : 14'bz;  // Controlled_Buffer controlled_buffer_57
  assign controlled_buffer_55_out = and_58_out ? 14'h3 : 14'bz;  // Controlled_Buffer controlled_buffer_58
  assign controlled_buffer_55_out = and_59_out ? 14'h4 : 14'bz;  // Controlled_Buffer controlled_buffer_59
  assign controlled_buffer_55_out = and_60_out ? 14'h5 : 14'bz;  // Controlled_Buffer controlled_buffer_60
  assign controlled_buffer_55_out = and_61_out ? 14'h6 : 14'bz;  // Controlled_Buffer controlled_buffer_61
  assign controlled_buffer_55_out = and_62_out ? 14'h7 : 14'bz;  // Controlled_Buffer controlled_buffer_62
  assign controlled_buffer_55_out = and_63_out ? 14'h8 : 14'bz;  // Controlled_Buffer controlled_buffer_63
  assign controlled_buffer_55_out = and_64_out ? 14'h9 : 14'bz;  // Controlled_Buffer controlled_buffer_64
  assign controlled_buffer_55_out = and_65_out ? 14'ha : 14'bz;  // Controlled_Buffer controlled_buffer_65
  assign controlled_buffer_55_out = and_66_out ? 14'hb : 14'bz;  // Controlled_Buffer controlled_buffer_66
  assign controlled_buffer_55_out = and_67_out ? 14'hc : 14'bz;  // Controlled_Buffer controlled_buffer_67
  assign controlled_buffer_55_out = and_68_out ? 14'hd : 14'bz;  // Controlled_Buffer controlled_buffer_68
  assign controlled_buffer_55_out = and_69_out ? 14'he : 14'bz;  // Controlled_Buffer controlled_buffer_69
  assign controlled_buffer_55_out = and_70_out ? 14'hf : 14'bz;  // Controlled_Buffer controlled_buffer_70
  assign controlled_buffer_55_out = and_71_out ? 14'h10 : 14'bz;  // Controlled_Buffer controlled_buffer_71
  assign controlled_buffer_55_out = and_72_out ? 14'h11 : 14'bz;  // Controlled_Buffer controlled_buffer_72
  assign controlled_buffer_55_out = and_73_out ? 14'h12 : 14'bz;  // Controlled_Buffer controlled_buffer_73
  assign controlled_buffer_55_out = and_74_out ? 14'h13 : 14'bz;  // Controlled_Buffer controlled_buffer_74
  assign controlled_buffer_55_out = and_75_out ? 14'h14 : 14'bz;  // Controlled_Buffer controlled_buffer_75
  assign controlled_buffer_55_out = and_76_out ? 14'h15 : 14'bz;  // Controlled_Buffer controlled_buffer_76
  assign controlled_buffer_55_out = and_77_out ? 14'h16 : 14'bz;  // Controlled_Buffer controlled_buffer_77
  assign controlled_buffer_55_out = and_78_out ? 14'h17 : 14'bz;  // Controlled_Buffer controlled_buffer_78
  assign controlled_buffer_55_out = and_79_out ? 14'h18 : 14'bz;  // Controlled_Buffer controlled_buffer_79
  assign controlled_buffer_55_out = and_80_out ? 14'h19 : 14'bz;  // Controlled_Buffer controlled_buffer_80
  assign controlled_buffer_55_out = and_81_out ? 14'h1a : 14'bz;  // Controlled_Buffer controlled_buffer_81
  Comparator #(.width(8), .mode("twosComplement")) comparator_40 (
    .a(cnt), .b(8'h8), .eq(comparator_40_eq));  // open: gt, lt
  Register #(.width(1), .trigger("rising"), .Select("low")) register_16 (
    .D(comparator_40_eq), .Q(register_16_q), .clk(CLK));  // open: en, clr
  Register #(.width(14), .trigger("rising"), .Select("low")) register_17 (
    .D(controlled_buffer_55_out), .en(register_16_q), .Q(RAW3), .clk(CLK));  // open: clr

  assign D10 = {32{1'b1}};
  assign D21 = {32{1'b1}};

  // Notes on the sheet:
  //   contents of rom_1 (hex, n*v repeats v):
  //   200400 200430 200601 218400 218430 218601 300c00 300c30 300e01 c200400 c200430 c200601 c218400
  //   c218430 c218601 c300c00 c300c30 c300e01 80600400 80600430 80600601 80618400 80618430 80618601
  //   80700c00 80700c30 80700e01
  //   contents of rom_2 (hex, n*v repeats v):
  //   200400 2004cc 200502 266400 2664cc 266502 281400 2814cc 281502 33200400 332004cc 33200502 33266400
  //   332664cc 33266502 33281400 332814cc 33281502 40a00400 40a004cc 40a00502 40a66400 40a664cc 40a66502
  //   40a81400 40a814cc 40a81502
  //   contents of rom_3 (hex, n*v repeats v):
  //   200400 200502 200484 281400 281502 281484 242400 242502 242484 40a00400 40a00502 40a00484 40a81400
  //   40a81502 40a81484 40a42400 40a42502 40a42484 21200400 21200502 21200484 21281400 21281502 21281484
  //   21242400 21242502 21242484
  //   contents of rom_4 (hex, n*v repeats v):
  //   200400 200502 200448 281400 281502 281448 224400 224502 224448 40a00400 40a00502 40a00448 40a81400
  //   40a81502 40a81448 40a24400 40a24502 40a24448 12200400 12200502 12200448 12281400 12281502 12281448
  //   12224400 12224502 12224448
  //   contents of rom_5 (hex, n*v repeats v):
  //   200400 200601 200430 300c00 300e01 300c30 218400 218601 218430 80600400 80600601 80600430 80700c00
  //   80700e01 80700c30 80618400 80618601 80618430 c200400 c200601 c200430 c300c00 c300e01 c300c30 c218400
  //   c218601 c218430
  //   contents of rom_6 (hex, n*v repeats v):
  //   200400 200601 200430 300c00 300e01 300c30 218400 218601 218430 80600400 80600601 80600430 80700c00
  //   80700e01 80700c30 80618400 80618601 80618430 c200400 c200601 c200430 c300c00 c300e01 c300c30 c218400
  //   c218601 c218430
  //   contents of rom_7 (hex, n*v repeats v):
  //   200400 200502 200448 281400 281502 281448 224400 224502 224448 40a00400 40a00502 40a00448 40a81400
  //   40a81502 40a81448 40a24400 40a24502 40a24448 12200400 12200502 12200448 12281400 12281502 12281448
  //   12224400 12224502 12224448
  //   contents of rom_8 (hex, n*v repeats v):
  //   200400 200502 200484 281400 281502 281484 242400 242502 242484 40a00400 40a00502 40a00484 40a81400
  //   40a81502 40a81484 40a42400 40a42502 40a42484 21200400 21200502 21200484 21281400 21281502 21281484
  //   21242400 21242502 21242484
  //   contents of rom_9 (hex, n*v repeats v):
  //   200400 2004cc 200502 266400 2664cc 266502 281400 2814cc 281502 33200400 332004cc 33200502 33266400
  //   332664cc 33266502 33281400 332814cc 33281502 40a00400 40a004cc 40a00502 40a66400 40a664cc 40a66502
  //   40a81400 40a814cc 40a81502
  //   contents of rom_10 (hex, n*v repeats v):
  //   200400 200430 200601 218400 218430 218601 300c00 300c30 300e01 c200400 c200430 c200601 c218400
  //   c218430 c218601 c300c00 c300c30 c300e01 80600400 80600430 80600601 80618400 80618430 80618601
  //   80700c00 80700c30 80700e01
  //   contents of rom_11 (hex, n*v repeats v):
  //   200400 200430 200601 218400 218430 218601 300c00 300c30 300e01 c200400 c200430 c200601 c218400
  //   c218430 c218601 c300c00 c300c30 c300e01 80600400 80600430 80600601 80618400 80618430 80618601
  //   80700c00 80700c30 80700e01
  //   contents of rom_12 (hex, n*v repeats v):
  //   200400 2004cc 200502 266400 2664cc 266502 281400 2814cc 281502 33200400 332004cc 33200502 33266400
  //   332664cc 33266502 33281400 332814cc 33281502 40a00400 40a004cc 40a00502 40a66400 40a664cc 40a66502
  //   40a81400 40a814cc 40a81502
  //   contents of rom_13 (hex, n*v repeats v):
  //   200400 200502 200484 281400 281502 281484 242400 242502 242484 40a00400 40a00502 40a00484 40a81400
  //   40a81502 40a81484 40a42400 40a42502 40a42484 21200400 21200502 21200484 21281400 21281502 21281484
  //   21242400 21242502 21242484
  //   contents of rom_14 (hex, n*v repeats v):
  //   200400 200502 200448 281400 281502 281448 224400 224502 224448 40a00400 40a00502 40a00448 40a81400
  //   40a81502 40a81448 40a24400 40a24502 40a24448 12200400 12200502 12200448 12281400 12281502 12281448
  //   12224400 12224502 12224448
  //   contents of rom_15 (hex, n*v repeats v):
  //   200400 200601 200430 300c00 300e01 300c30 218400 218601 218430 80600400 80600601 80600430 80700c00
  //   80700e01 80700c30 80618400 80618601 80618430 c200400 c200601 c200430 c300c00 c300e01 c300c30 c218400
  //   c218601 c218430
  //   contents of rom_16 (hex, n*v repeats v):
  //   200400 200601 200430 300c00 300e01 300c30 218400 218601 218430 80600400 80600601 80600430 80700c00
  //   80700e01 80700c30 80618400 80618601 80618430 c200400 c200601 c200430 c300c00 c300e01 c300c30 c218400
  //   c218601 c218430
  //   contents of rom_17 (hex, n*v repeats v):
  //   200400 200502 200448 281400 281502 281448 224400 224502 224448 40a00400 40a00502 40a00448 40a81400
  //   40a81502 40a81448 40a24400 40a24502 40a24448 12200400 12200502 12200448 12281400 12281502 12281448
  //   12224400 12224502 12224448
  //   contents of rom_18 (hex, n*v repeats v):
  //   200400 200502 200484 281400 281502 281484 242400 242502 242484 40a00400 40a00502 40a00484 40a81400
  //   40a81502 40a81484 40a42400 40a42502 40a42484 21200400 21200502 21200484 21281400 21281502 21281484
  //   21242400 21242502 21242484
  //   contents of rom_19 (hex, n*v repeats v):
  //   200400 2004cc 200502 266400 2664cc 266502 281400 2814cc 281502 33200400 332004cc 33200502 33266400
  //   332664cc 33266502 33281400 332814cc 33281502 40a00400 40a004cc 40a00502 40a66400 40a664cc 40a66502
  //   40a81400 40a814cc 40a81502
  //   contents of rom_20 (hex, n*v repeats v):
  //   200400 200430 200601 218400 218430 218601 300c00 300c30 300e01 c200400 c200430 c200601 c218400
  //   c218430 c218601 c300c00 c300c30 c300e01 80600400 80600430 80600601 80618400 80618430 80618601
  //   80700c00 80700c30 80700e01
  //   contents of rom_21 (hex, n*v repeats v):
  //   200400 200430 200601 218400 218430 218601 300c00 300c30 300e01 c200400 c200430 c200601 c218400
  //   c218430 c218601 c300c00 c300c30 c300e01 80600400 80600430 80600601 80618400 80618430 80618601
  //   80700c00 80700c30 80700e01
  //   contents of rom_22 (hex, n*v repeats v):
  //   200400 2004cc 200502 266400 2664cc 266502 281400 2814cc 281502 33200400 332004cc 33200502 33266400
  //   332664cc 33266502 33281400 332814cc 33281502 40a00400 40a004cc 40a00502 40a66400 40a664cc 40a66502
  //   40a81400 40a814cc 40a81502
  //   contents of rom_23 (hex, n*v repeats v):
  //   200400 200502 200484 281400 281502 281484 242400 242502 242484 40a00400 40a00502 40a00484 40a81400
  //   40a81502 40a81484 40a42400 40a42502 40a42484 21200400 21200502 21200484 21281400 21281502 21281484
  //   21242400 21242502 21242484
  //   contents of rom_24 (hex, n*v repeats v):
  //   200400 200502 200448 281400 281502 281448 224400 224502 224448 40a00400 40a00502 40a00448 40a81400
  //   40a81502 40a81448 40a24400 40a24502 40a24448 12200400 12200502 12200448 12281400 12281502 12281448
  //   12224400 12224502 12224448
  //   contents of rom_25 (hex, n*v repeats v):
  //   200400 200601 200430 300c00 300e01 300c30 218400 218601 218430 80600400 80600601 80600430 80700c00
  //   80700e01 80700c30 80618400 80618601 80618430 c200400 c200601 c200430 c300c00 c300e01 c300c30 c218400
  //   c218601 c218430
  //   contents of rom_26 (hex, n*v repeats v):
  //   200400 200601 200430 300c00 300e01 300c30 218400 218601 218430 80600400 80600601 80600430 80700c00
  //   80700e01 80700c30 80618400 80618601 80618430 c200400 c200601 c200430 c300c00 c300e01 c300c30 c218400
  //   c218601 c218430
  //   contents of rom_27 (hex, n*v repeats v):
  //   200400 200502 200448 281400 281502 281448 224400 224502 224448 40a00400 40a00502 40a00448 40a81400
  //   40a81502 40a81448 40a24400 40a24502 40a24448 12200400 12200502 12200448 12281400 12281502 12281448
  //   12224400 12224502 12224448
  //   contents of rom_28 (hex, n*v repeats v):
  //   200400 200502 200484 281400 281502 281484 242400 242502 242484 40a00400 40a00502 40a00484 40a81400
  //   40a81502 40a81484 40a42400 40a42502 40a42484 21200400 21200502 21200484 21281400 21281502 21281484
  //   21242400 21242502 21242484
  //   contents of rom_29 (hex, n*v repeats v):
  //   200400 2004cc 200502 266400 2664cc 266502 281400 2814cc 281502 33200400 332004cc 33200502 33266400
  //   332664cc 33266502 33281400 332814cc 33281502 40a00400 40a004cc 40a00502 40a66400 40a664cc 40a66502
  //   40a81400 40a814cc 40a81502
  //   contents of rom_30 (hex, n*v repeats v):
  //   200400 200430 200601 218400 218430 218601 300c00 300c30 300e01 c200400 c200430 c200601 c218400
  //   c218430 c218601 c300c00 c300c30 c300e01 80600400 80600430 80600601 80618400 80618430 80618601
  //   80700c00 80700c30 80700e01
  //   第一行
  //   第二行
  //   第三行
endmodule
